// Logisim project cpu24.circ as structural Verilog: 29 circuits, main circuit ◇单周期MIPS
module \单周期MIPS  (
  input  IR1,
  input  IR2,
  input  IR3,
  output RegWrite,
  output MemWrite,
  output [31:0] PC,
  output [31:0] IR,
  output [31:0] RDin,
  output [31:0] MDin,
  output [31:0] LedData
);

  wire AluSrcB, and_1_out, and_2_out, and_4_out, Beq, Bne, CLK, clock_2_out, comparator_1_eq,
       comparator_2_eq, comparator_2_lt, controlled_buffer_1_out, d_ff_1_q, Go, halt, IR1_t, IR2_t, IR3_t,
       IRA, IRB, IRC, JAL, JMP, JR, MemToReg, mips_alu_1_equal, multiplexer_3_out, nand_1_out, or_1_out,
       RegDst, SignedExt, Syscall, W1, W2, W3;
  wire [3:0] mips_probe_1_p5;
  wire [4:0] multiplexer_4_out, multiplexer_5_out, multiplexer_6_out, multiplexer_7_out;
  wire [12:0] CNT_num;
  wire [15:0] \总周期数 ;
  wire [27:0] adder_1_out;
  wire [31:0] adder_2_out, bit_extender_1_out, bit_extender_2_out, mips_alu_1_result, multiplexer_1_out,
       multiplexer_2_out, multiplexer_9_out, multiplexer_10_out, multiplexer_11_out, R1, ram_1_data,
       shifter_1_out, shifter_2_out;

  Clock #(.highDuration(1), .lowDuration(1)) clock_1 (.out(CLK));
  Button _1 (.out(IRA));
  Button _2 (.out(IRB));
  Button _3 (.out(IRC));
  Button \u_继续运行  (.out(Go));
  LED #(.active("true")) led_1 (.in(W1));
  LED #(.active("true")) led_2 (.in(W2));
  LED #(.active("true")) led_3 (.in(W3));
  and and_1 (and_1_out, mips_alu_1_equal, Beq);
  and and_2 (and_2_out, Bne, ~mips_alu_1_equal);  // AND_Gate
  or or_1 (or_1_out, and_2_out, and_1_out);
  Multiplexer #(.select(1), .width(32), .disabled("Z"), .enable("false")) multiplexer_1 (
    .in0({shifter_1_out[31:28], adder_1_out}), .in1(adder_2_out), .out(multiplexer_1_out), .sel(or_1_out));
  Hex_Digit_Display hex_digit_display_1 (.value(LedData[31:28]));  // open: dp
  Multiplexer #(.select(2), .width(32), .disabled("Z"), .enable("false")) multiplexer_2 (
    .in0(multiplexer_1_out), .in1(shifter_1_out), .in2(shifter_1_out), .in3(R1), .out(multiplexer_2_out),
    .sel({JMP, JR}));
  Multiplexer #(.select(1), .width(1), .disabled("Z"), .enable("false")) multiplexer_3 (
    .in0(1'b1), .in1(Go), .out(multiplexer_3_out), .sel(halt));
  Hex_Digit_Display hex_digit_display_2 (.value(LedData[23:20]));  // open: dp
  Hex_Digit_Display hex_digit_display_3 (.value(LedData[27:24]));  // open: dp
  Register #(.width(32), .trigger("rising"), .Select("low")) u_PC (
    .D(multiplexer_2_out), .en(multiplexer_3_out), .Q(PC), .clk(CLK));  // open: clr
  Counter #(.width(16), .max('hffff), .ongoal("wrap"), .trigger("rising"), .behavior("old")) counter_1 (
    .load(1'b0), .count(multiplexer_3_out), .Q(\总周期数 ), .clk(CLK));  // open: D, carry, clr, preset
  Hex_Digit_Display hex_digit_display_4 (.value(LedData[19:16]));  // open: dp
  Hex_Digit_Display hex_digit_display_5 (.value(LedData[15:12]));  // open: dp
  Adder #(.width(32)) adder_1 (.a(PC), .b(32'h4), .out({shifter_1_out[31:28], adder_1_out}));  // open: cin, cout
  Hex_Digit_Display hex_digit_display_6 (.value(LedData[11:8]));  // open: dp
  Hex_Digit_Display hex_digit_display_7 (.value(LedData[7:4]));  // open: dp
  // Probe on \总周期数 
  Hex_Digit_Display hex_digit_display_8 (.value(LedData[3:0]));  // open: dp
  ROM #(.addrWidth(10), .dataWidth(32), .Select("high")) rom_1 (.addr(PC[11:2]), .data(IR));
  // Mips_Probe mips_probe_1: pin names not known; wires that end beside it: IR, Bne, MemToReg, MemWrite, mips_probe_1_p5
  or or_2 (IR1_t, IR1, IRA);
  Multiplexer #(.select(1), .width(5), .disabled("Z"), .enable("false")) multiplexer_4 (
    .in0(IR[20:16]), .in1(IR[15:11]), .out(multiplexer_4_out), .sel(RegDst));
  assign bit_extender_1_out = {{16{1'b0}}, IR[15:0]};  // Bit_Extender bit_extender_1
  assign bit_extender_2_out = {{16{IR[15]}}, IR[15:0]};  // Bit_Extender bit_extender_2
  Shifter #(.width(28), .shift("ll")) shifter_1 (.in(IR[27:0]), .\dist (5'b00010), .out(shifter_1_out[27:0]));
  or or_3 (IR2_t, IR2, IRB);
  \单周期硬布线控制器  \u_单周期硬布线控制器_1  (
    .Func(IR[5:0]), .OP(IR[31:26]), .ALU_OP(mips_probe_1_p5), .MemToReg(MemToReg), .MemWrite(MemWrite),
    .ALU_SRC(AluSrcB), .RegWrite(RegWrite), .SysCALL(Syscall), .SignedExt(SignedExt), .RegDst(RegDst),
    .JR(JR), .JMP(JMP), .Beq(Beq), .JAL(JAL), .Bne(Bne));
  Multiplexer #(.select(1), .width(5), .disabled("Z"), .enable("false")) multiplexer_5 (
    .in0(IR[25:21]), .in1(5'b00010), .out(multiplexer_5_out), .sel(Syscall));
  Multiplexer #(.select(1), .width(5), .disabled("Z"), .enable("false")) multiplexer_6 (
    .in0(IR[20:16]), .in1(5'b00100), .out(multiplexer_6_out), .sel(Syscall));
  Multiplexer #(.select(1), .width(5), .disabled("Z"), .enable("false")) multiplexer_7 (
    .in0(multiplexer_4_out), .in1({5{1'b1}}), .out(multiplexer_7_out), .sel(JAL));
  Multiplexer #(.select(1), .width(32), .disabled("Z"), .enable("false")) multiplexer_8 (
    .in0(multiplexer_11_out), .in1({shifter_1_out[31:28], adder_1_out}), .out(RDin), .sel(JAL));
  Multiplexer #(.select(1), .width(32), .disabled("Z"), .enable("false")) multiplexer_9 (
    .in0(bit_extender_1_out), .in1(bit_extender_2_out), .out(multiplexer_9_out), .sel(SignedExt));
  or or_4 (IR3_t, IR3, IRC);
  MIPS_Regifile mips_regifile_1 (
    .Din(RDin), .Clk(CLK), .R1(R1), .R2(MDin), .WE(RegWrite), .W_num(multiplexer_7_out),
    .R1_num(multiplexer_5_out), .R2_num(multiplexer_6_out));
  Multiplexer #(.select(1), .width(32), .disabled("Z"), .enable("false")) multiplexer_10 (
    .in0(MDin), .in1(multiplexer_9_out), .out(multiplexer_10_out), .sel(AluSrcB));
  Shifter #(.width(32), .shift("ll")) shifter_2 (.in(multiplexer_9_out), .\dist (5'b00010), .out(shifter_2_out));
  MIPS_ALU mips_alu_1 (
    .X(R1), .Y(multiplexer_10_out), .AluOP(mips_probe_1_p5), .Equal(mips_alu_1_equal),
    .Result(mips_alu_1_result), .shamt(IR[10:6]));  // open: Result_2
  Adder #(.width(32)) adder_2 (
    .a(shifter_2_out), .b({shifter_1_out[31:28], adder_1_out}), .out(adder_2_out));  // open: cin, cout
  Comparator #(.width(32), .mode("twosComplement")) comparator_1 (
    .a(R1), .b(32'h22), .eq(comparator_1_eq));  // open: gt, lt
  and and_3 (halt, ~comparator_1_eq, Syscall);  // AND_Gate
  and and_4 (and_4_out, comparator_1_eq, Syscall);
  RAM #(.addrWidth(10), .dataWidth(32), .bus("separate"), .Select("high")) ram_1 (
    .addr(mips_alu_1_result[11:2]), .din(MDin), .data(ram_1_data), .str(MemWrite), .clk(CLK));  // open: sel, ld, clr
  Register #(.width(32), .trigger("rising"), .Select("low")) register_1 (
    .D(MDin), .en(and_4_out), .Q(LedData), .clk(CLK));  // open: clr
  Multiplexer #(.select(1), .width(32), .disabled("Z"), .enable("false")) multiplexer_11 (
    .in0(mips_alu_1_result), .in1(ram_1_data), .out(multiplexer_11_out), .sel(MemToReg));
  D_Flip_Flop #(.trigger("high"), .Pre_Clr_Positions("LEGACY"), .NegatePresetClear("false"), .enable("true"), .NewFFLayout("false")) d_ff_1 (.Q(d_ff_1_q));  // open: clk, D, Qn, preset, en, reset
  // Probe on 13'hc
  Clock #(.highDuration(1), .lowDuration(1)) clock_2 (.out(clock_2_out));
  Comparator #(.width(13), .mode("twosComplement")) comparator_2 (
    .a(CNT_num), .b(13'hc), .eq(comparator_2_eq), .lt(comparator_2_lt));  // open: gt
  nand nand_1 (nand_1_out, d_ff_1_q, comparator_2_eq);
  Counter #(.width(13), .max('h1fff), .ongoal("stay"), .trigger("rising"), .behavior("old")) counter_2 (
    .count(comparator_2_lt), .Q(CNT_num), .clk(clock_2_out));  // open: load, D, carry, clr, preset
  assign controlled_buffer_1_out = nand_1_out ? clock_2_out : 1'bz;  // Controlled_Buffer controlled_buffer_1
  Pull_Resistor #(.pull(1)) pull_resistor_1 (.node(controlled_buffer_1_out));

  // Other names for the same wires on the sheet: R2[31:0] = MDin

  // Notes on the sheet:
  //   中断源
  //   中断等待指示
  //   总复位信号应将除ROM以外所有存储组件全部清零
  //   数码管输出
  //   数码管输出应该用寄存器锁存，否则显示数据只能一闪而过
  //   指令存储器
  //   PC+4
  //   指令字
  //   contents of rom_1 (hex, n*v repeats v):
  //   20110001 8000c05 20110001 20120002 20130003 8000c09 20110001 20120002 20130003 8000c0d 20110001
  //   20120002 20130003 8000c11 20110001 20120002 20130003 c000cb8 20100001 20110001 118fc0 112020
  //   20020022 c 118882 12200001 8000c15 112020 20020022 c 20110001 118880 112020 20020022 c 12200001
  //   8000c1f 20110001 118fc0 112020 20020022 c 1188c3 112020 20020022 c 118903 112020 20020022 c 118903
  //   112020 20020022 c 118903 112020 20020022 c 118903 112020 20020022 c 118903 112020 20020022 c 118903
  //   112020 20020022 c 118903 112020 20020022 c 20100001 109fc0 139fc3 8021 2012000c 24160003 26100001
  //   3210000f 20080008 20090001 139900 2709825 132020 20020022 c 1094022 1500fff9 22100001 2018000f
  //   2188024 108700 20080008 20090001 139902 2709825 132021 20020022 c 1094022 1500fff9 108702 2c9b022
  //   12c00001 8000c50 4020 1084027 84400 3508ffff 82021 20020022 c 2010ffff 20110000 ae300000 22100001
  //   22310004 ae300000 22100001 22310004 ae300000 22100001 22310004 ae300000 22100001 22310004 ae300000
  //   22100001 22310004 ae300000 22100001 22310004 ae300000 22100001 22310004 ae300000 22100001 22310004
  //   ae300000 22100001 22310004 ae300000 22100001 22310004 ae300000 22100001 22310004 ae300000 22100001
  //   22310004 ae300000 22100001 22310004 ae300000 22100001 22310004 ae300000 22100001 22310004 ae300000
  //   22100001 22310004 22100001 8020 2011003c 8e130000 8e340000 274402a 11000002 ae330000 ae140000
  //   2231fffc 1611fff8 102020 20020022 c 22100004 2011003c 1611fff2 20020032 c 20100000 22100001 102020
  //   20020022 c 22100002 102020 20020022 c 22100003 102020 20020022 c 22100004 102020 20020022 c 22100005
  //   102020 20020022 c 22100006 102020 20020022 c 22100007 102020 20020022 c 22100008 102020 20020022
  //   20020022 c 3e00008
  //   OP
  //   Func
  //   rs
  //   rt
  //   rd
  //   JMP
  //   JR
  //   OP
  //   Func
  //   Beq
  //   Bne
  //   MemToReg
  //   MemWrite
  //   AluOP
  //   AluSrcB
  //   RegWrite
  //   JAL
  //   RegDst
  //   Syscall
  //   为方便自动评测，需要输出PC，IR，寄存器堆写如数据RDin
  //   PCBranch
  //   RAM写使能MemWrite、RAM写入数据MDin等信号
  //   控制位
  //   暂停节拍，不能为0
  //   戳工具置1进入计数暂停模式，ctrl+k时钟自动运行到对应节拍暂停
  //   ctrl+k关闭时钟连续运行，将控制位置零，进入单步调试模式调试
  //   用这个时钟源需要去掉电路中的其他时钟源
  //   可计数暂停的时钟源
endmodule

// 单周期硬布线控制器
module \单周期硬布线控制器  (
  input  [5:0] OP,
  input  [5:0] Func,
  output [3:0] ALU_OP,
  output MemToReg,
  output MemWrite,
  output ALU_SRC,
  output RegWrite,
  output SysCALL,
  output SignedExt,
  output RegDst,
  output Beq,
  output Bne,
  output JR,
  output JMP,
  output JAL
);

  \运算控制器自动生成  \u_运算控制器自动生成_1  (
    .OP0(OP[0]), .OP1(OP[1]), .OP2(OP[2]), .OP3(OP[3]), .OP4(OP[4]), .OP5(OP[5]), .F0(Func[0]), .F1(Func[1]),
    .F2(Func[2]), .F3(Func[3]), .F4(Func[4]), .F5(Func[5]), .S0(ALU_OP[0]), .S1(ALU_OP[1]), .S2(ALU_OP[2]),
    .S3(ALU_OP[3]));
  \控制信号自动生成  \u_控制信号自动生成_1  (
    .OP0(OP[0]), .OP1(OP[1]), .OP2(OP[2]), .OP3(OP[3]), .OP4(OP[4]), .OP5(OP[5]), .F0(Func[0]), .F1(Func[1]),
    .F2(Func[2]), .F3(Func[3]), .F4(Func[4]), .F5(Func[5]), .MemToReg(MemToReg), .MemWrite(MemWrite),
    .ALU_SRC(ALU_SRC), .RegWrite(RegWrite), .SysCALL(SysCALL), .SignedExt(SignedExt), .RegDst(RegDst),
    .BEQ(Beq), .BNE(Bne), .JR(JR), .JUMP(JMP), .JAL(JAL));

  // Other names for the same wires on the sheet: OP_CODE[5:0] = OP

  // Notes on the sheet:
  //   运算器控制器，根据指令生成运算器功能选择信号
  //   控制信号生成，产生数据通路需要的其他控制信号
endmodule

// 运算器控制器
module \运算控制器自动生成  (
  input  OP0,
  input  OP1,
  input  OP2,
  input  OP3,
  input  OP4,
  input  OP5,
  input  F0,
  input  F1,
  input  F2,
  input  F3,
  input  F4,
  input  F5,
  output S0,
  output S1,
  output S2,
  output S3
);

  wire and_1_out, and_2_out, and_3_out, and_4_out, and_5_out, and_6_out, and_7_out, and_8_out, and_9_out,
       and_10_out, and_11_out, and_12_out, and_13_out, and_14_out, and_15_out, and_16_out, and_17_out,
       and_18_out, and_19_out, and_20_out, and_21_out, and_22_out, and_23_out, and_24_out, and_25_out,
       and_26_out, and_27_out, and_28_out, and_29_out, and_30_out, and_31_out, and_32_out, and_33_out,
       and_34_out, not_1_out, not_2_out, not_3_out, not_4_out, not_5_out, not_6_out, not_7_out, not_8_out,
       not_9_out, not_10_out, not_11_out, not_12_out, not_13_out, not_14_out, not_15_out, not_16_out,
       not_17_out, not_18_out, not_19_out, not_20_out, not_21_out, not_22_out, not_23_out, not_24_out,
       not_25_out, not_26_out, not_27_out, not_28_out, not_29_out, not_30_out, not_31_out, not_32_out,
       not_33_out, not_34_out, not_35_out, not_36_out, not_37_out, not_38_out, not_39_out, not_40_out,
       not_41_out, not_42_out, not_43_out, not_44_out, not_45_out, not_46_out, not_47_out, not_48_out,
       not_49_out, not_50_out, not_51_out, not_52_out, not_53_out, not_54_out, not_55_out, not_56_out,
       not_57_out, not_58_out, not_59_out, not_60_out, not_61_out, not_62_out, not_63_out, not_64_out,
       not_65_out, not_66_out, not_67_out, not_68_out, not_69_out, not_70_out, not_71_out, not_72_out,
       not_73_out, not_74_out, not_75_out, not_76_out, not_77_out, not_78_out, not_79_out, not_80_out,
       not_81_out, not_82_out, not_83_out, not_84_out, not_85_out, not_86_out, not_87_out, not_88_out,
       not_89_out, not_90_out, not_91_out, not_92_out, not_93_out, not_94_out, not_95_out, not_96_out,
       not_97_out, not_98_out, not_99_out, not_100_out, not_101_out, not_102_out, not_103_out, not_104_out,
       not_105_out, not_106_out, not_107_out, not_108_out, not_109_out, not_110_out, not_111_out,
       not_112_out, not_113_out, not_114_out, not_115_out, not_116_out, not_117_out, not_118_out,
       not_119_out, not_120_out, not_121_out, not_122_out, not_123_out, not_124_out, not_125_out,
       not_126_out, not_127_out, not_128_out, not_129_out, not_130_out, not_131_out, not_132_out,
       not_133_out, not_134_out, not_135_out, not_136_out, not_137_out, not_138_out, not_139_out,
       not_140_out, not_141_out, not_142_out, not_143_out, not_144_out, not_145_out, not_146_out,
       not_147_out, not_148_out, not_149_out, not_150_out, not_151_out, not_152_out, not_153_out,
       not_154_out, not_155_out, not_156_out, not_157_out, not_158_out, not_159_out, not_160_out,
       not_161_out, not_162_out, not_163_out, not_164_out, not_165_out, not_166_out, not_167_out,
       not_168_out, not_169_out, not_170_out, not_171_out, not_172_out, not_173_out, not_174_out,
       not_175_out, not_176_out, not_177_out, not_178_out, not_179_out, not_180_out, not_181_out,
       not_182_out, not_183_out, not_184_out, not_185_out, not_186_out, not_187_out, not_188_out,
       not_189_out, not_190_out, not_191_out, not_192_out, not_193_out, not_194_out, not_195_out,
       not_196_out, not_197_out, not_198_out, not_199_out, not_200_out, not_201_out, not_202_out,
       not_203_out, not_204_out, not_205_out, not_206_out, not_207_out, not_208_out, not_209_out,
       not_210_out, not_211_out, not_212_out, not_213_out, not_214_out, not_215_out, not_216_out,
       not_217_out, not_218_out, not_219_out, not_220_out, not_221_out, not_222_out, not_223_out,
       not_224_out, not_225_out, not_226_out, not_227_out, not_228_out, not_229_out, not_230_out,
       not_231_out, not_232_out, not_233_out, not_234_out, not_235_out, not_236_out;

  not not_1 (not_1_out, OP5);
  not not_2 (not_2_out, OP4);
  not not_3 (not_3_out, OP3);
  not not_4 (not_4_out, OP2);
  not not_5 (not_5_out, OP1);
  not not_6 (not_6_out, OP0);
  not not_7 (not_7_out, F5);
  not not_8 (not_8_out, F4);
  not not_9 (not_9_out, F3);
  not not_10 (not_10_out, F2);
  not not_11 (not_11_out, OP5);
  not not_12 (not_12_out, OP4);
  not not_13 (not_13_out, OP3);
  not not_14 (not_14_out, OP2);
  not not_15 (not_15_out, OP1);
  not not_16 (not_16_out, OP0);
  not not_17 (not_17_out, F4);
  not not_18 (not_18_out, F3);
  not not_19 (not_19_out, F2);
  not not_20 (not_20_out, F1);
  not not_21 (not_21_out, F0);
  not not_22 (not_22_out, OP5);
  not not_23 (not_23_out, OP4);
  not not_24 (not_24_out, OP3);
  not not_25 (not_25_out, OP2);
  not not_26 (not_26_out, OP1);
  not not_27 (not_27_out, OP0);
  not not_28 (not_28_out, F4);
  not not_29 (not_29_out, F3);
  not not_30 (not_30_out, F2);
  not not_31 (not_31_out, F1);
  not not_32 (not_32_out, OP5);
  not not_33 (not_33_out, OP4);
  not not_34 (not_34_out, OP3);
  not not_35 (not_35_out, OP2);
  not not_36 (not_36_out, OP1);
  not not_37 (not_37_out, OP0);
  not not_38 (not_38_out, F4);
  not not_39 (not_39_out, F3);
  not not_40 (not_40_out, F1);
  not not_41 (not_41_out, F0);
  not not_42 (not_42_out, OP5);
  not not_43 (not_43_out, OP4);
  not not_44 (not_44_out, OP3);
  not not_45 (not_45_out, OP2);
  not not_46 (not_46_out, OP1);
  not not_47 (not_47_out, OP0);
  not not_48 (not_48_out, F4);
  not not_49 (not_49_out, F2);
  not not_50 (not_50_out, F0);
  not not_51 (not_51_out, OP5);
  not not_52 (not_52_out, OP4);
  not not_53 (not_53_out, OP2);
  not not_54 (not_54_out, OP1);
  not not_55 (not_55_out, OP0);
  not not_56 (not_56_out, OP5);
  not not_57 (not_57_out, OP4);
  not not_58 (not_58_out, OP1);
  not not_59 (not_59_out, OP0);
  not not_60 (not_60_out, OP5);
  not not_61 (not_61_out, OP4);
  not not_62 (not_62_out, OP2);
  not not_63 (not_63_out, OP1);
  not not_64 (not_64_out, OP5);
  not not_65 (not_65_out, OP4);
  not not_66 (not_66_out, OP2);
  not not_67 (not_67_out, OP0);
  not not_68 (not_68_out, OP4);
  not not_69 (not_69_out, OP3);
  not not_70 (not_70_out, OP2);
  not not_71 (not_71_out, OP4);
  not not_72 (not_72_out, OP2);
  not not_73 (not_73_out, OP5);
  not not_74 (not_74_out, OP4);
  not not_75 (not_75_out, OP3);
  not not_76 (not_76_out, OP2);
  not not_77 (not_77_out, OP1);
  not not_78 (not_78_out, OP0);
  not not_79 (not_79_out, F5);
  not not_80 (not_80_out, F4);
  not not_81 (not_81_out, F3);
  not not_82 (not_82_out, F2);
  not not_83 (not_83_out, F0);
  not not_84 (not_84_out, OP5);
  not not_85 (not_85_out, OP4);
  not not_86 (not_86_out, OP3);
  not not_87 (not_87_out, OP2);
  not not_88 (not_88_out, OP1);
  not not_89 (not_89_out, OP0);
  not not_90 (not_90_out, F4);
  not not_91 (not_91_out, F3);
  not not_92 (not_92_out, F2);
  not not_93 (not_93_out, F0);
  not not_94 (not_94_out, OP5);
  not not_95 (not_95_out, OP4);
  not not_96 (not_96_out, OP3);
  not not_97 (not_97_out, OP2);
  not not_98 (not_98_out, OP1);
  not not_99 (not_99_out, OP0);
  not not_100 (not_100_out, F4);
  not not_101 (not_101_out, F3);
  not not_102 (not_102_out, F1);
  not not_103 (not_103_out, F0);
  not not_104 (not_104_out, OP5);
  not not_105 (not_105_out, OP4);
  not not_106 (not_106_out, OP3);
  not not_107 (not_107_out, OP2);
  not not_108 (not_108_out, OP1);
  not not_109 (not_109_out, OP0);
  not not_110 (not_110_out, F4);
  not not_111 (not_111_out, F3);
  not not_112 (not_112_out, OP5);
  not not_113 (not_113_out, OP4);
  not not_114 (not_114_out, OP3);
  not not_115 (not_115_out, OP2);
  not not_116 (not_116_out, OP1);
  not not_117 (not_117_out, OP0);
  not not_118 (not_118_out, F4);
  not not_119 (not_119_out, F2);
  not not_120 (not_120_out, F0);
  not not_121 (not_121_out, OP5);
  not not_122 (not_122_out, OP4);
  not not_123 (not_123_out, OP1);
  not not_124 (not_124_out, OP0);
  not not_125 (not_125_out, OP5);
  not not_126 (not_126_out, OP4);
  not not_127 (not_127_out, OP2);
  not not_128 (not_128_out, OP0);
  not not_129 (not_129_out, OP5);
  not not_130 (not_130_out, OP4);
  not not_131 (not_131_out, OP3);
  not not_132 (not_132_out, OP2);
  not not_133 (not_133_out, OP1);
  not not_134 (not_134_out, OP0);
  not not_135 (not_135_out, F4);
  not not_136 (not_136_out, F3);
  not not_137 (not_137_out, F2);
  not not_138 (not_138_out, F1);
  not not_139 (not_139_out, F0);
  not not_140 (not_140_out, OP5);
  not not_141 (not_141_out, OP4);
  not not_142 (not_142_out, OP3);
  not not_143 (not_143_out, OP2);
  not not_144 (not_144_out, OP1);
  not not_145 (not_145_out, OP0);
  not not_146 (not_146_out, F4);
  not not_147 (not_147_out, F3);
  not not_148 (not_148_out, F2);
  not not_149 (not_149_out, F1);
  not not_150 (not_150_out, OP5);
  not not_151 (not_151_out, OP4);
  not not_152 (not_152_out, OP3);
  not not_153 (not_153_out, OP2);
  not not_154 (not_154_out, OP1);
  not not_155 (not_155_out, OP0);
  not not_156 (not_156_out, F4);
  not not_157 (not_157_out, F3);
  not not_158 (not_158_out, F2);
  not not_159 (not_159_out, F0);
  not not_160 (not_160_out, OP5);
  not not_161 (not_161_out, OP4);
  not not_162 (not_162_out, OP3);
  not not_163 (not_163_out, OP2);
  not not_164 (not_164_out, OP1);
  not not_165 (not_165_out, OP0);
  not not_166 (not_166_out, F4);
  not not_167 (not_167_out, F3);
  not not_168 (not_168_out, F1);
  not not_169 (not_169_out, F0);
  not not_170 (not_170_out, OP5);
  not not_171 (not_171_out, OP4);
  not not_172 (not_172_out, OP3);
  not not_173 (not_173_out, OP2);
  not not_174 (not_174_out, OP1);
  not not_175 (not_175_out, OP0);
  not not_176 (not_176_out, F4);
  not not_177 (not_177_out, F2);
  not not_178 (not_178_out, OP5);
  not not_179 (not_179_out, OP4);
  not not_180 (not_180_out, OP2);
  not not_181 (not_181_out, OP1);
  not not_182 (not_182_out, OP0);
  not not_183 (not_183_out, OP5);
  not not_184 (not_184_out, OP4);
  not not_185 (not_185_out, OP1);
  not not_186 (not_186_out, OP0);
  not not_187 (not_187_out, OP5);
  not not_188 (not_188_out, OP4);
  not not_189 (not_189_out, OP2);
  not not_190 (not_190_out, OP1);
  not not_191 (not_191_out, OP4);
  not not_192 (not_192_out, OP3);
  not not_193 (not_193_out, OP2);
  not not_194 (not_194_out, OP4);
  not not_195 (not_195_out, OP2);
  not not_196 (not_196_out, OP5);
  not not_197 (not_197_out, OP4);
  not not_198 (not_198_out, OP3);
  not not_199 (not_199_out, OP2);
  not not_200 (not_200_out, OP1);
  not not_201 (not_201_out, OP0);
  not not_202 (not_202_out, F4);
  not not_203 (not_203_out, F3);
  not not_204 (not_204_out, F1);
  not not_205 (not_205_out, OP5);
  not not_206 (not_206_out, OP4);
  not not_207 (not_207_out, OP3);
  not not_208 (not_208_out, OP2);
  not not_209 (not_209_out, OP1);
  not not_210 (not_210_out, OP0);
  not not_211 (not_211_out, F4);
  not not_212 (not_212_out, F3);
  not not_213 (not_213_out, OP5);
  not not_214 (not_214_out, OP4);
  not not_215 (not_215_out, OP3);
  not not_216 (not_216_out, OP2);
  not not_217 (not_217_out, OP1);
  not not_218 (not_218_out, OP0);
  not not_219 (not_219_out, F4);
  not not_220 (not_220_out, F2);
  not not_221 (not_221_out, F0);
  not not_222 (not_222_out, OP5);
  not not_223 (not_223_out, OP4);
  not not_224 (not_224_out, OP3);
  not not_225 (not_225_out, OP2);
  not not_226 (not_226_out, OP1);
  not not_227 (not_227_out, OP0);
  not not_228 (not_228_out, F4);
  not not_229 (not_229_out, F2);
  not not_230 (not_230_out, OP5);
  not not_231 (not_231_out, OP4);
  not not_232 (not_232_out, OP2);
  not not_233 (not_233_out, OP0);
  not not_234 (not_234_out, OP5);
  not not_235 (not_235_out, OP4);
  not not_236 (not_236_out, OP1);
  and and_1 (and_1_out, not_1_out, not_2_out, not_3_out, not_4_out, not_5_out, not_6_out, not_7_out, not_8_out, not_9_out, not_10_out, F1, F0);
  and and_2 (and_2_out, not_11_out, not_12_out, not_13_out, not_14_out, not_15_out, not_16_out, F5, not_17_out, not_18_out, not_19_out, not_20_out, not_21_out);
  and and_3 (and_3_out, not_22_out, not_23_out, not_24_out, not_25_out, not_26_out, not_27_out, F5, not_28_out, not_29_out, not_30_out, not_31_out, F0);
  and and_4 (and_4_out, not_32_out, not_33_out, not_34_out, not_35_out, not_36_out, not_37_out, F5, not_38_out, not_39_out, F2, not_40_out, not_41_out);
  and and_5 (and_5_out, not_42_out, not_43_out, not_44_out, not_45_out, not_46_out, not_47_out, F5, not_48_out, F3, not_49_out, F1, not_50_out);
  and and_6 (and_6_out, not_51_out, not_52_out, OP3, not_53_out, not_54_out, not_55_out);
  and and_7 (and_7_out, not_56_out, not_57_out, OP3, OP2, not_58_out, not_59_out);
  and and_8 (and_8_out, not_60_out, not_61_out, OP3, not_62_out, not_63_out, OP0);
  and and_9 (and_9_out, not_64_out, not_65_out, OP3, not_66_out, OP1, not_67_out);
  and and_10 (and_10_out, OP5, not_68_out, not_69_out, not_70_out, OP1, OP0);
  and and_11 (and_11_out, OP5, not_71_out, OP3, not_72_out, OP1, OP0);
  and and_12 (and_12_out, not_73_out, not_74_out, not_75_out, not_76_out, not_77_out, not_78_out, not_79_out, not_80_out, not_81_out, not_82_out, F1, not_83_out);
  and and_13 (and_13_out, not_84_out, not_85_out, not_86_out, not_87_out, not_88_out, not_89_out, F5, not_90_out, not_91_out, not_92_out, F1, not_93_out);
  and and_14 (and_14_out, not_94_out, not_95_out, not_96_out, not_97_out, not_98_out, not_99_out, F5, not_100_out, not_101_out, F2, not_102_out, not_103_out);
  and and_15 (and_15_out, not_104_out, not_105_out, not_106_out, not_107_out, not_108_out, not_109_out, F5, not_110_out, not_111_out, F2, F1, F0);
  and and_16 (and_16_out, not_112_out, not_113_out, not_114_out, not_115_out, not_116_out, not_117_out, F5, not_118_out, F3, not_119_out, F1, not_120_out);
  and and_17 (and_17_out, not_121_out, not_122_out, OP3, OP2, not_123_out, not_124_out);
  and and_18 (and_18_out, not_125_out, not_126_out, OP3, not_127_out, OP1, not_128_out);
  and and_19 (and_19_out, not_129_out, not_130_out, not_131_out, not_132_out, not_133_out, not_134_out, F5, not_135_out, not_136_out, not_137_out, not_138_out, not_139_out);
  and and_20 (and_20_out, not_140_out, not_141_out, not_142_out, not_143_out, not_144_out, not_145_out, F5, not_146_out, not_147_out, not_148_out, not_149_out, F0);
  and and_21 (and_21_out, not_150_out, not_151_out, not_152_out, not_153_out, not_154_out, not_155_out, F5, not_156_out, not_157_out, not_158_out, F1, not_159_out);
  and and_22 (and_22_out, not_160_out, not_161_out, not_162_out, not_163_out, not_164_out, not_165_out, F5, not_166_out, not_167_out, F2, not_168_out, not_169_out);
  and and_23 (and_23_out, not_170_out, not_171_out, not_172_out, not_173_out, not_174_out, not_175_out, F5, not_176_out, F3, not_177_out, F1, F0);
  and and_24 (and_24_out, not_178_out, not_179_out, OP3, not_180_out, not_181_out, not_182_out);
  and and_25 (and_25_out, not_183_out, not_184_out, OP3, OP2, not_185_out, not_186_out);
  and and_26 (and_26_out, not_187_out, not_188_out, OP3, not_189_out, not_190_out, OP0);
  and and_27 (and_27_out, OP5, not_191_out, not_192_out, not_193_out, OP1, OP0);
  and and_28 (and_28_out, OP5, not_194_out, OP3, not_195_out, OP1, OP0);
  and and_29 (and_29_out, not_196_out, not_197_out, not_198_out, not_199_out, not_200_out, not_201_out, F5, not_202_out, not_203_out, F2, not_204_out, F0);
  and and_30 (and_30_out, not_205_out, not_206_out, not_207_out, not_208_out, not_209_out, not_210_out, F5, not_211_out, not_212_out, F2, F1, F0);
  and and_31 (and_31_out, not_213_out, not_214_out, not_215_out, not_216_out, not_217_out, not_218_out, F5, not_219_out, F3, not_220_out, F1, not_221_out);
  and and_32 (and_32_out, not_222_out, not_223_out, not_224_out, not_225_out, not_226_out, not_227_out, F5, not_228_out, F3, not_229_out, F1, F0);
  and and_33 (and_33_out, not_230_out, not_231_out, OP3, not_232_out, OP1, not_233_out);
  and and_34 (and_34_out, not_234_out, not_235_out, OP3, OP2, not_236_out, OP0);
  or or_1 (S0, and_1_out, and_2_out, and_3_out, and_4_out, and_5_out, and_6_out, and_7_out, and_8_out, and_9_out, and_10_out, and_11_out);
  or or_2 (S1, and_12_out, and_13_out, and_14_out, and_15_out, and_16_out, and_17_out, and_18_out);
  or or_3 (S2, and_19_out, and_20_out, and_21_out, and_22_out, and_23_out, and_24_out, and_25_out, and_26_out, and_27_out, and_28_out);
  or or_4 (S3, and_29_out, and_30_out, and_31_out, and_32_out, and_33_out, and_34_out);
endmodule

// 控制信号生成
module \控制信号自动生成  (
  input  OP0,
  input  OP1,
  input  OP2,
  input  OP3,
  input  OP4,
  input  OP5,
  input  F0,
  input  F1,
  input  F2,
  input  F3,
  input  F4,
  input  F5,
  output MemToReg,
  output MemWrite,
  output ALU_SRC,
  output RegWrite,
  output SysCALL,
  output SignedExt,
  output RegDst,
  output BEQ,
  output BNE,
  output JR,
  output JUMP,
  output JAL
);

  wire and_3_out, and_4_out, and_5_out, and_6_out, and_7_out, and_8_out, and_9_out, and_10_out, and_11_out,
       and_12_out, and_13_out, and_14_out, and_15_out, and_16_out, and_17_out, and_18_out, and_19_out,
       and_20_out, and_21_out, and_22_out, and_23_out, and_24_out, and_25_out, and_26_out, and_27_out,
       and_29_out, and_30_out, and_31_out, and_32_out, and_33_out, and_34_out, and_35_out, and_36_out,
       and_37_out, and_38_out, and_39_out, and_40_out, and_41_out, and_42_out, and_43_out, and_44_out,
       and_45_out, and_46_out, and_50_out, and_51_out, and_52_out, not_1_out, not_2_out, not_3_out,
       not_4_out, not_5_out, not_6_out, not_7_out, not_8_out, not_9_out, not_10_out, not_11_out, not_12_out,
       not_13_out, not_14_out, not_15_out, not_16_out, not_17_out, not_18_out, not_19_out, not_20_out,
       not_21_out, not_22_out, not_23_out, not_24_out, not_25_out, not_26_out, not_27_out, not_28_out,
       not_29_out, not_30_out, not_31_out, not_32_out, not_33_out, not_34_out, not_35_out, not_36_out,
       not_37_out, not_38_out, not_39_out, not_40_out, not_41_out, not_42_out, not_43_out, not_44_out,
       not_45_out, not_46_out, not_47_out, not_48_out, not_49_out, not_50_out, not_51_out, not_52_out,
       not_53_out, not_54_out, not_55_out, not_56_out, not_57_out, not_58_out, not_59_out, not_60_out,
       not_61_out, not_62_out, not_63_out, not_64_out, not_65_out, not_66_out, not_67_out, not_68_out,
       not_69_out, not_70_out, not_71_out, not_72_out, not_73_out, not_74_out, not_75_out, not_76_out,
       not_77_out, not_78_out, not_79_out, not_80_out, not_81_out, not_82_out, not_83_out, not_84_out,
       not_85_out, not_86_out, not_87_out, not_88_out, not_89_out, not_90_out, not_91_out, not_92_out,
       not_93_out, not_94_out, not_95_out, not_96_out, not_97_out, not_98_out, not_99_out, not_100_out,
       not_101_out, not_102_out, not_103_out, not_104_out, not_105_out, not_106_out, not_107_out,
       not_108_out, not_109_out, not_110_out, not_111_out, not_112_out, not_113_out, not_114_out,
       not_115_out, not_116_out, not_117_out, not_118_out, not_119_out, not_120_out, not_121_out,
       not_122_out, not_123_out, not_124_out, not_125_out, not_126_out, not_127_out, not_128_out,
       not_129_out, not_130_out, not_131_out, not_132_out, not_133_out, not_134_out, not_135_out,
       not_136_out, not_137_out, not_138_out, not_139_out, not_140_out, not_141_out, not_142_out,
       not_143_out, not_144_out, not_145_out, not_146_out, not_147_out, not_148_out, not_149_out,
       not_150_out, not_151_out, not_152_out, not_153_out, not_154_out, not_155_out, not_156_out,
       not_157_out, not_158_out, not_159_out, not_160_out, not_161_out, not_162_out, not_163_out,
       not_164_out, not_165_out, not_166_out, not_167_out, not_168_out, not_169_out, not_170_out,
       not_171_out, not_172_out, not_173_out, not_174_out, not_175_out, not_176_out, not_177_out,
       not_178_out, not_179_out, not_180_out, not_181_out, not_182_out, not_183_out, not_184_out,
       not_185_out, not_186_out, not_187_out, not_188_out, not_189_out, not_190_out, not_191_out,
       not_192_out, not_193_out, not_194_out, not_195_out, not_196_out, not_197_out, not_198_out,
       not_199_out, not_200_out, not_201_out, not_202_out, not_203_out, not_204_out, not_205_out,
       not_206_out, not_207_out, not_208_out, not_209_out, not_210_out, not_211_out, not_212_out,
       not_213_out, not_214_out, not_215_out, not_216_out, not_217_out, not_218_out, not_219_out,
       not_220_out, not_221_out, not_222_out, not_223_out, not_224_out, not_225_out, not_226_out,
       not_227_out, not_228_out, not_229_out, not_230_out, not_231_out, not_232_out, not_233_out,
       not_234_out, not_235_out, not_236_out, not_237_out, not_238_out, not_239_out, not_240_out,
       not_241_out, not_242_out, not_243_out, not_244_out, not_245_out, not_246_out, not_247_out,
       not_248_out, not_249_out, not_250_out, not_251_out, not_252_out, not_253_out, not_254_out,
       not_255_out, not_256_out, not_257_out, not_258_out, not_259_out, not_260_out, not_261_out,
       not_262_out, not_263_out, not_264_out, not_265_out, not_266_out, not_267_out, not_268_out,
       not_269_out, not_270_out, not_271_out, not_272_out, not_273_out, not_274_out, not_275_out,
       not_276_out, not_277_out, not_278_out, not_279_out, not_280_out, not_281_out, not_282_out,
       not_283_out, not_284_out, not_285_out, not_286_out, not_287_out, not_288_out, not_289_out,
       not_290_out, not_291_out, not_292_out, not_293_out, not_294_out, not_295_out, not_296_out,
       not_297_out, not_298_out, not_299_out, not_300_out, not_301_out, not_302_out, not_303_out,
       not_304_out, not_305_out, not_306_out, not_307_out, not_308_out, not_309_out, not_310_out,
       not_311_out, not_312_out, not_313_out, not_314_out, not_315_out, not_316_out, not_317_out,
       not_318_out, not_319_out, not_320_out, not_321_out, not_322_out, not_323_out, not_324_out,
       not_325_out, not_326_out, not_327_out, not_328_out, not_329_out, not_330_out, not_331_out,
       not_332_out, not_333_out, not_334_out, not_335_out, not_336_out, not_337_out, not_338_out,
       not_339_out, not_340_out, not_341_out, not_342_out, not_343_out, not_344_out, not_345_out,
       not_346_out, not_347_out, not_348_out, not_349_out, not_350_out, not_351_out, not_352_out,
       not_353_out, not_354_out;

  not not_1 (not_1_out, OP4);
  not not_2 (not_2_out, OP3);
  not not_3 (not_3_out, OP2);
  not not_4 (not_4_out, OP4);
  not not_5 (not_5_out, OP2);
  not not_6 (not_6_out, OP5);
  not not_7 (not_7_out, OP4);
  not not_8 (not_8_out, OP2);
  not not_9 (not_9_out, OP1);
  not not_10 (not_10_out, OP0);
  not not_11 (not_11_out, OP5);
  not not_12 (not_12_out, OP4);
  not not_13 (not_13_out, OP1);
  not not_14 (not_14_out, OP0);
  not not_15 (not_15_out, OP5);
  not not_16 (not_16_out, OP4);
  not not_17 (not_17_out, OP2);
  not not_18 (not_18_out, OP1);
  not not_19 (not_19_out, OP5);
  not not_20 (not_20_out, OP4);
  not not_21 (not_21_out, OP2);
  not not_22 (not_22_out, OP0);
  not not_23 (not_23_out, OP5);
  not not_24 (not_24_out, OP4);
  not not_25 (not_25_out, OP1);
  not not_26 (not_26_out, OP4);
  not not_27 (not_27_out, OP3);
  not not_28 (not_28_out, OP2);
  not not_29 (not_29_out, OP4);
  not not_30 (not_30_out, OP2);
  not not_31 (not_31_out, OP5);
  not not_32 (not_32_out, OP4);
  not not_33 (not_33_out, OP3);
  not not_34 (not_34_out, OP2);
  not not_35 (not_35_out, OP1);
  not not_36 (not_36_out, OP0);
  not not_37 (not_37_out, F5);
  not not_38 (not_38_out, F4);
  not not_39 (not_39_out, F3);
  not not_40 (not_40_out, F2);
  not not_41 (not_41_out, F1);
  not not_42 (not_42_out, F0);
  not not_43 (not_43_out, OP5);
  not not_44 (not_44_out, OP4);
  not not_45 (not_45_out, OP3);
  not not_46 (not_46_out, OP2);
  not not_47 (not_47_out, OP1);
  not not_48 (not_48_out, OP0);
  not not_49 (not_49_out, F5);
  not not_50 (not_50_out, F4);
  not not_51 (not_51_out, F3);
  not not_52 (not_52_out, F2);
  not not_53 (not_53_out, OP5);
  not not_54 (not_54_out, OP4);
  not not_55 (not_55_out, OP3);
  not not_56 (not_56_out, OP2);
  not not_57 (not_57_out, OP1);
  not not_58 (not_58_out, OP0);
  not not_59 (not_59_out, F5);
  not not_60 (not_60_out, F4);
  not not_61 (not_61_out, F3);
  not not_62 (not_62_out, F2);
  not not_63 (not_63_out, F0);
  not not_64 (not_64_out, OP5);
  not not_65 (not_65_out, OP4);
  not not_66 (not_66_out, OP3);
  not not_67 (not_67_out, OP2);
  not not_68 (not_68_out, OP1);
  not not_69 (not_69_out, OP0);
  not not_70 (not_70_out, F4);
  not not_71 (not_71_out, F3);
  not not_72 (not_72_out, F2);
  not not_73 (not_73_out, F1);
  not not_74 (not_74_out, F0);
  not not_75 (not_75_out, OP5);
  not not_76 (not_76_out, OP4);
  not not_77 (not_77_out, OP3);
  not not_78 (not_78_out, OP2);
  not not_79 (not_79_out, OP1);
  not not_80 (not_80_out, OP0);
  not not_81 (not_81_out, F4);
  not not_82 (not_82_out, F3);
  not not_83 (not_83_out, F2);
  not not_84 (not_84_out, F1);
  not not_85 (not_85_out, OP5);
  not not_86 (not_86_out, OP4);
  not not_87 (not_87_out, OP3);
  not not_88 (not_88_out, OP2);
  not not_89 (not_89_out, OP1);
  not not_90 (not_90_out, OP0);
  not not_91 (not_91_out, F4);
  not not_92 (not_92_out, F3);
  not not_93 (not_93_out, F2);
  not not_94 (not_94_out, F0);
  not not_95 (not_95_out, OP5);
  not not_96 (not_96_out, OP4);
  not not_97 (not_97_out, OP3);
  not not_98 (not_98_out, OP2);
  not not_99 (not_99_out, OP1);
  not not_100 (not_100_out, OP0);
  not not_101 (not_101_out, F4);
  not not_102 (not_102_out, F3);
  not not_103 (not_103_out, F1);
  not not_104 (not_104_out, F0);
  not not_105 (not_105_out, OP5);
  not not_106 (not_106_out, OP4);
  not not_107 (not_107_out, OP3);
  not not_108 (not_108_out, OP2);
  not not_109 (not_109_out, OP1);
  not not_110 (not_110_out, OP0);
  not not_111 (not_111_out, F4);
  not not_112 (not_112_out, F3);
  not not_113 (not_113_out, F1);
  not not_114 (not_114_out, OP5);
  not not_115 (not_115_out, OP4);
  not not_116 (not_116_out, OP3);
  not not_117 (not_117_out, OP2);
  not not_118 (not_118_out, OP1);
  not not_119 (not_119_out, OP0);
  not not_120 (not_120_out, F4);
  not not_121 (not_121_out, F3);
  not not_122 (not_122_out, OP5);
  not not_123 (not_123_out, OP4);
  not not_124 (not_124_out, OP3);
  not not_125 (not_125_out, OP2);
  not not_126 (not_126_out, OP1);
  not not_127 (not_127_out, OP0);
  not not_128 (not_128_out, F4);
  not not_129 (not_129_out, F2);
  not not_130 (not_130_out, F0);
  not not_131 (not_131_out, OP5);
  not not_132 (not_132_out, OP4);
  not not_133 (not_133_out, OP3);
  not not_134 (not_134_out, OP2);
  not not_135 (not_135_out, OP1);
  not not_136 (not_136_out, OP0);
  not not_137 (not_137_out, F4);
  not not_138 (not_138_out, F2);
  not not_139 (not_139_out, OP5);
  not not_140 (not_140_out, OP4);
  not not_141 (not_141_out, OP3);
  not not_142 (not_142_out, OP2);
  not not_143 (not_143_out, OP5);
  not not_144 (not_144_out, OP4);
  not not_145 (not_145_out, OP2);
  not not_146 (not_146_out, OP1);
  not not_147 (not_147_out, OP0);
  not not_148 (not_148_out, OP5);
  not not_149 (not_149_out, OP4);
  not not_150 (not_150_out, OP1);
  not not_151 (not_151_out, OP0);
  not not_152 (not_152_out, OP5);
  not not_153 (not_153_out, OP4);
  not not_154 (not_154_out, OP2);
  not not_155 (not_155_out, OP1);
  not not_156 (not_156_out, OP5);
  not not_157 (not_157_out, OP4);
  not not_158 (not_158_out, OP2);
  not not_159 (not_159_out, OP0);
  not not_160 (not_160_out, OP5);
  not not_161 (not_161_out, OP4);
  not not_162 (not_162_out, OP1);
  not not_163 (not_163_out, OP4);
  not not_164 (not_164_out, OP3);
  not not_165 (not_165_out, OP2);
  not not_166 (not_166_out, OP5);
  not not_167 (not_167_out, OP4);
  not not_168 (not_168_out, OP3);
  not not_169 (not_169_out, OP2);
  not not_170 (not_170_out, OP1);
  not not_171 (not_171_out, OP0);
  not not_172 (not_172_out, F5);
  not not_173 (not_173_out, F4);
  not not_174 (not_174_out, F1);
  not not_175 (not_175_out, F0);
  not not_176 (not_176_out, OP5);
  not not_177 (not_177_out, OP4);
  not not_178 (not_178_out, OP3);
  not not_179 (not_179_out, OP1);
  not not_180 (not_180_out, OP0);
  not not_181 (not_181_out, OP5);
  not not_182 (not_182_out, OP4);
  not not_183 (not_183_out, OP3);
  not not_184 (not_184_out, OP1);
  not not_185 (not_185_out, OP5);
  not not_186 (not_186_out, OP4);
  not not_187 (not_187_out, OP2);
  not not_188 (not_188_out, OP1);
  not not_189 (not_189_out, OP0);
  not not_190 (not_190_out, OP5);
  not not_191 (not_191_out, OP4);
  not not_192 (not_192_out, OP2);
  not not_193 (not_193_out, OP1);
  not not_194 (not_194_out, OP5);
  not not_195 (not_195_out, OP4);
  not not_196 (not_196_out, OP2);
  not not_197 (not_197_out, OP0);
  not not_198 (not_198_out, OP4);
  not not_199 (not_199_out, OP3);
  not not_200 (not_200_out, OP2);
  not not_201 (not_201_out, OP4);
  not not_202 (not_202_out, OP2);
  not not_203 (not_203_out, OP5);
  not not_204 (not_204_out, OP4);
  not not_205 (not_205_out, OP3);
  not not_206 (not_206_out, OP2);
  not not_207 (not_207_out, OP1);
  not not_208 (not_208_out, OP0);
  not not_209 (not_209_out, F5);
  not not_210 (not_210_out, F4);
  not not_211 (not_211_out, F3);
  not not_212 (not_212_out, F2);
  not not_213 (not_213_out, F1);
  not not_214 (not_214_out, F0);
  not not_215 (not_215_out, OP5);
  not not_216 (not_216_out, OP4);
  not not_217 (not_217_out, OP3);
  not not_218 (not_218_out, OP2);
  not not_219 (not_219_out, OP1);
  not not_220 (not_220_out, OP0);
  not not_221 (not_221_out, F5);
  not not_222 (not_222_out, F4);
  not not_223 (not_223_out, F3);
  not not_224 (not_224_out, F2);
  not not_225 (not_225_out, OP5);
  not not_226 (not_226_out, OP4);
  not not_227 (not_227_out, OP3);
  not not_228 (not_228_out, OP2);
  not not_229 (not_229_out, OP1);
  not not_230 (not_230_out, OP0);
  not not_231 (not_231_out, F5);
  not not_232 (not_232_out, F4);
  not not_233 (not_233_out, F3);
  not not_234 (not_234_out, F2);
  not not_235 (not_235_out, F0);
  not not_236 (not_236_out, OP5);
  not not_237 (not_237_out, OP4);
  not not_238 (not_238_out, OP3);
  not not_239 (not_239_out, OP2);
  not not_240 (not_240_out, OP1);
  not not_241 (not_241_out, OP0);
  not not_242 (not_242_out, F4);
  not not_243 (not_243_out, F3);
  not not_244 (not_244_out, F2);
  not not_245 (not_245_out, F1);
  not not_246 (not_246_out, F0);
  not not_247 (not_247_out, OP5);
  not not_248 (not_248_out, OP4);
  not not_249 (not_249_out, OP3);
  not not_250 (not_250_out, OP2);
  not not_251 (not_251_out, OP1);
  not not_252 (not_252_out, OP0);
  not not_253 (not_253_out, F4);
  not not_254 (not_254_out, F3);
  not not_255 (not_255_out, F2);
  not not_256 (not_256_out, F1);
  not not_257 (not_257_out, OP5);
  not not_258 (not_258_out, OP4);
  not not_259 (not_259_out, OP3);
  not not_260 (not_260_out, OP2);
  not not_261 (not_261_out, OP1);
  not not_262 (not_262_out, OP0);
  not not_263 (not_263_out, F4);
  not not_264 (not_264_out, F3);
  not not_265 (not_265_out, F2);
  not not_266 (not_266_out, F0);
  not not_267 (not_267_out, OP5);
  not not_268 (not_268_out, OP4);
  not not_269 (not_269_out, OP3);
  not not_270 (not_270_out, OP2);
  not not_271 (not_271_out, OP1);
  not not_272 (not_272_out, OP0);
  not not_273 (not_273_out, F4);
  not not_274 (not_274_out, F3);
  not not_275 (not_275_out, F1);
  not not_276 (not_276_out, F0);
  not not_277 (not_277_out, OP5);
  not not_278 (not_278_out, OP4);
  not not_279 (not_279_out, OP3);
  not not_280 (not_280_out, OP2);
  not not_281 (not_281_out, OP1);
  not not_282 (not_282_out, OP0);
  not not_283 (not_283_out, F4);
  not not_284 (not_284_out, F3);
  not not_285 (not_285_out, F1);
  not not_286 (not_286_out, OP5);
  not not_287 (not_287_out, OP4);
  not not_288 (not_288_out, OP3);
  not not_289 (not_289_out, OP2);
  not not_290 (not_290_out, OP1);
  not not_291 (not_291_out, OP0);
  not not_292 (not_292_out, F4);
  not not_293 (not_293_out, F3);
  not not_294 (not_294_out, OP5);
  not not_295 (not_295_out, OP4);
  not not_296 (not_296_out, OP3);
  not not_297 (not_297_out, OP2);
  not not_298 (not_298_out, OP1);
  not not_299 (not_299_out, OP0);
  not not_300 (not_300_out, F4);
  not not_301 (not_301_out, F2);
  not not_302 (not_302_out, F0);
  not not_303 (not_303_out, OP5);
  not not_304 (not_304_out, OP4);
  not not_305 (not_305_out, OP3);
  not not_306 (not_306_out, OP2);
  not not_307 (not_307_out, OP1);
  not not_308 (not_308_out, OP0);
  not not_309 (not_309_out, F4);
  not not_310 (not_310_out, F2);
  not not_311 (not_311_out, OP5);
  not not_312 (not_312_out, OP4);
  not not_313 (not_313_out, OP3);
  not not_314 (not_314_out, OP1);
  not not_315 (not_315_out, OP0);
  not not_316 (not_316_out, OP5);
  not not_317 (not_317_out, OP4);
  not not_318 (not_318_out, OP3);
  not not_319 (not_319_out, OP1);
  not not_320 (not_320_out, OP5);
  not not_321 (not_321_out, OP4);
  not not_322 (not_322_out, OP3);
  not not_323 (not_323_out, OP2);
  not not_324 (not_324_out, OP1);
  not not_325 (not_325_out, OP0);
  not not_326 (not_326_out, F5);
  not not_327 (not_327_out, F4);
  not not_328 (not_328_out, F2);
  not not_329 (not_329_out, F1);
  not not_330 (not_330_out, F0);
  not not_331 (not_331_out, OP5);
  not not_332 (not_332_out, OP4);
  not not_333 (not_333_out, OP3);
  not not_334 (not_334_out, OP2);
  not not_335 (not_335_out, OP1);
  not not_336 (not_336_out, OP0);
  not not_337 (not_337_out, F5);
  not not_338 (not_338_out, F4);
  not not_339 (not_339_out, F2);
  not not_340 (not_340_out, F1);
  not not_341 (not_341_out, F0);
  not not_342 (not_342_out, OP5);
  not not_343 (not_343_out, OP4);
  not not_344 (not_344_out, OP3);
  not not_345 (not_345_out, OP2);
  not not_346 (not_346_out, OP0);
  not not_347 (not_347_out, OP5);
  not not_348 (not_348_out, OP4);
  not not_349 (not_349_out, OP3);
  not not_350 (not_350_out, OP2);
  not not_351 (not_351_out, OP5);
  not not_352 (not_352_out, OP4);
  not not_353 (not_353_out, OP3);
  not not_354 (not_354_out, OP2);
  and and_1 (MemToReg, OP5, not_1_out, not_2_out, not_3_out, OP1, OP0);
  and and_2 (MemWrite, OP5, not_4_out, OP3, not_5_out, OP1, OP0);
  and and_3 (and_3_out, not_6_out, not_7_out, OP3, not_8_out, not_9_out, not_10_out);
  and and_4 (and_4_out, not_11_out, not_12_out, OP3, OP2, not_13_out, not_14_out);
  and and_5 (and_5_out, not_15_out, not_16_out, OP3, not_17_out, not_18_out, OP0);
  and and_6 (and_6_out, not_19_out, not_20_out, OP3, not_21_out, OP1, not_22_out);
  and and_7 (and_7_out, not_23_out, not_24_out, OP3, OP2, not_25_out, OP0);
  and and_8 (and_8_out, OP5, not_26_out, not_27_out, not_28_out, OP1, OP0);
  and and_9 (and_9_out, OP5, not_29_out, OP3, not_30_out, OP1, OP0);
  and and_10 (and_10_out, not_31_out, not_32_out, not_33_out, not_34_out, not_35_out, not_36_out, not_37_out, not_38_out, not_39_out, not_40_out, not_41_out, not_42_out);
  and and_11 (and_11_out, not_43_out, not_44_out, not_45_out, not_46_out, not_47_out, not_48_out, not_49_out, not_50_out, not_51_out, not_52_out, F1, F0);
  and and_12 (and_12_out, not_53_out, not_54_out, not_55_out, not_56_out, not_57_out, not_58_out, not_59_out, not_60_out, not_61_out, not_62_out, F1, not_63_out);
  and and_13 (and_13_out, not_64_out, not_65_out, not_66_out, not_67_out, not_68_out, not_69_out, F5, not_70_out, not_71_out, not_72_out, not_73_out, not_74_out);
  and and_14 (and_14_out, not_75_out, not_76_out, not_77_out, not_78_out, not_79_out, not_80_out, F5, not_81_out, not_82_out, not_83_out, not_84_out, F0);
  and and_15 (and_15_out, not_85_out, not_86_out, not_87_out, not_88_out, not_89_out, not_90_out, F5, not_91_out, not_92_out, not_93_out, F1, not_94_out);
  and and_16 (and_16_out, not_95_out, not_96_out, not_97_out, not_98_out, not_99_out, not_100_out, F5, not_101_out, not_102_out, F2, not_103_out, not_104_out);
  and and_17 (and_17_out, not_105_out, not_106_out, not_107_out, not_108_out, not_109_out, not_110_out, F5, not_111_out, not_112_out, F2, not_113_out, F0);
  and and_18 (and_18_out, not_114_out, not_115_out, not_116_out, not_117_out, not_118_out, not_119_out, F5, not_120_out, not_121_out, F2, F1, F0);
  and and_19 (and_19_out, not_122_out, not_123_out, not_124_out, not_125_out, not_126_out, not_127_out, F5, not_128_out, F3, not_129_out, F1, not_130_out);
  and and_20 (and_20_out, not_131_out, not_132_out, not_133_out, not_134_out, not_135_out, not_136_out, F5, not_137_out, F3, not_138_out, F1, F0);
  and and_21 (and_21_out, not_139_out, not_140_out, not_141_out, not_142_out, OP1, OP0);
  and and_22 (and_22_out, not_143_out, not_144_out, OP3, not_145_out, not_146_out, not_147_out);
  and and_23 (and_23_out, not_148_out, not_149_out, OP3, OP2, not_150_out, not_151_out);
  and and_24 (and_24_out, not_152_out, not_153_out, OP3, not_154_out, not_155_out, OP0);
  and and_25 (and_25_out, not_156_out, not_157_out, OP3, not_158_out, OP1, not_159_out);
  and and_26 (and_26_out, not_160_out, not_161_out, OP3, OP2, not_162_out, OP0);
  and and_27 (and_27_out, OP5, not_163_out, not_164_out, not_165_out, OP1, OP0);
  and and_28 (SysCALL, not_166_out, not_167_out, not_168_out, not_169_out, not_170_out, not_171_out, not_172_out, not_173_out, F3, F2, not_174_out, not_175_out);
  and and_29 (and_29_out, not_176_out, not_177_out, not_178_out, OP2, not_179_out, not_180_out);
  and and_30 (and_30_out, not_181_out, not_182_out, not_183_out, OP2, not_184_out, OP0);
  and and_31 (and_31_out, not_185_out, not_186_out, OP3, not_187_out, not_188_out, not_189_out);
  and and_32 (and_32_out, not_190_out, not_191_out, OP3, not_192_out, not_193_out, OP0);
  and and_33 (and_33_out, not_194_out, not_195_out, OP3, not_196_out, OP1, not_197_out);
  and and_34 (and_34_out, OP5, not_198_out, not_199_out, not_200_out, OP1, OP0);
  and and_35 (and_35_out, OP5, not_201_out, OP3, not_202_out, OP1, OP0);
  and and_36 (and_36_out, not_203_out, not_204_out, not_205_out, not_206_out, not_207_out, not_208_out, not_209_out, not_210_out, not_211_out, not_212_out, not_213_out, not_214_out);
  and and_37 (and_37_out, not_215_out, not_216_out, not_217_out, not_218_out, not_219_out, not_220_out, not_221_out, not_222_out, not_223_out, not_224_out, F1, F0);
  and and_38 (and_38_out, not_225_out, not_226_out, not_227_out, not_228_out, not_229_out, not_230_out, not_231_out, not_232_out, not_233_out, not_234_out, F1, not_235_out);
  and and_39 (and_39_out, not_236_out, not_237_out, not_238_out, not_239_out, not_240_out, not_241_out, F5, not_242_out, not_243_out, not_244_out, not_245_out, not_246_out);
  and and_40 (and_40_out, not_247_out, not_248_out, not_249_out, not_250_out, not_251_out, not_252_out, F5, not_253_out, not_254_out, not_255_out, not_256_out, F0);
  and and_41 (and_41_out, not_257_out, not_258_out, not_259_out, not_260_out, not_261_out, not_262_out, F5, not_263_out, not_264_out, not_265_out, F1, not_266_out);
  and and_42 (and_42_out, not_267_out, not_268_out, not_269_out, not_270_out, not_271_out, not_272_out, F5, not_273_out, not_274_out, F2, not_275_out, not_276_out);
  and and_43 (and_43_out, not_277_out, not_278_out, not_279_out, not_280_out, not_281_out, not_282_out, F5, not_283_out, not_284_out, F2, not_285_out, F0);
  and and_44 (and_44_out, not_286_out, not_287_out, not_288_out, not_289_out, not_290_out, not_291_out, F5, not_292_out, not_293_out, F2, F1, F0);
  and and_45 (and_45_out, not_294_out, not_295_out, not_296_out, not_297_out, not_298_out, not_299_out, F5, not_300_out, F3, not_301_out, F1, not_302_out);
  and and_46 (and_46_out, not_303_out, not_304_out, not_305_out, not_306_out, not_307_out, not_308_out, F5, not_309_out, F3, not_310_out, F1, F0);
  and and_47 (BEQ, not_311_out, not_312_out, not_313_out, OP2, not_314_out, not_315_out);
  and and_48 (BNE, not_316_out, not_317_out, not_318_out, OP2, not_319_out, OP0);
  and and_49 (JR, not_320_out, not_321_out, not_322_out, not_323_out, not_324_out, not_325_out, not_326_out, not_327_out, F3, not_328_out, not_329_out, not_330_out);
  and and_50 (and_50_out, not_331_out, not_332_out, not_333_out, not_334_out, not_335_out, not_336_out, not_337_out, not_338_out, F3, not_339_out, not_340_out, not_341_out);
  and and_51 (and_51_out, not_342_out, not_343_out, not_344_out, not_345_out, OP1, not_346_out);
  and and_52 (and_52_out, not_347_out, not_348_out, not_349_out, not_350_out, OP1, OP0);
  and and_53 (JAL, not_351_out, not_352_out, not_353_out, not_354_out, OP1, OP0);
  or or_1 (ALU_SRC, and_3_out, and_4_out, and_5_out, and_6_out, and_7_out, and_8_out, and_9_out);
  or or_2 (SignedExt, and_29_out, and_30_out, and_31_out, and_32_out, and_33_out, and_34_out, and_35_out);
  or or_3 (RegDst, and_36_out, and_37_out, and_38_out, and_39_out, and_40_out, and_41_out, and_42_out, and_43_out, and_44_out, and_45_out, and_46_out);
  or or_4 (JUMP, and_50_out, and_51_out, and_52_out);
  or or_5 (RegWrite, and_10_out, and_11_out, and_12_out, and_13_out, and_14_out, and_15_out, and_16_out, and_17_out, and_18_out, and_19_out, and_20_out, and_21_out, and_22_out, and_23_out, and_24_out, and_25_out, and_26_out, and_27_out);
endmodule

// ALU
module MIPS_ALU (
  input  [4:0] shamt,
  input  [31:0] X,
  input  [31:0] Y,
  input  [3:0] AluOP,
  output Equal,
  output [31:0] Result,
  output [31:0] Result_2
);

  wire [0:0] comparator_1_lt, comparator_2_lt;
  wire [31:0] adder_1_out, AND_out, divider_1_out, divider_1_rem, multiplier_1_cout, multiplier_1_out,
       NOR_out, OR_out, shifter_1_out, shifter_2_out, shifter_3_out, subtractor_1_out, XOR_out;

  assign AND_out = X & Y;  // AND_Gate AND, 32 bits wide
  assign OR_out = X | Y;  // OR_Gate OR, 32 bits wide
  Shifter #(.width(32), .shift("ll")) shifter_1 (.in(Y), .\dist (shamt), .out(shifter_1_out));
  Shifter #(.width(32), .shift("ar")) shifter_2 (.in(Y), .\dist (shamt), .out(shifter_2_out));
  Shifter #(.width(32), .shift("lr")) shifter_3 (.in(Y), .\dist (shamt), .out(shifter_3_out));
  Multiplier #(.width(32)) multiplier_1 (.a(X), .b(Y), .out(multiplier_1_out), .cout(multiplier_1_cout));  // open: cin
  Divider #(.width(32)) divider_1 (.a(X), .b(Y), .out(divider_1_out), .rem(divider_1_rem));  // open: upper
  Adder #(.width(32)) adder_1 (.a(X), .b(Y), .out(adder_1_out));  // open: cin, cout
  Subtractor #(.width(32)) subtractor_1 (.a(X), .b(Y), .out(subtractor_1_out));  // open: bin, bout
  assign XOR_out = X ^ Y;  // XOR_Gate XOR, 32 bits wide
  assign NOR_out = ~(X | Y);  // NOR_Gate NOR, 32 bits wide
  Comparator #(.width(32), .mode("twosComplement")) comparator_1 (
    .a(X), .b(Y), .eq(Equal), .lt(comparator_1_lt[0]));  // open: gt
  Comparator #(.width(32), .mode("unsigned")) comparator_2 (.a(X), .b(Y), .lt(comparator_2_lt[0]));  // open: gt, eq
  Multiplexer #(.select(4), .width(32), .disabled("Z"), .enable("false")) multiplexer_1 (
    .in0(shifter_1_out), .in1(shifter_2_out), .in2(shifter_3_out), .in3(multiplier_1_out),
    .in4(divider_1_out), .in5(adder_1_out), .in6(subtractor_1_out), .in7(AND_out), .in8(OR_out),
    .in9(XOR_out), .in10(NOR_out), .in11({{31{1'b0}}, comparator_1_lt[0]}),
    .in12({{31{1'b0}}, comparator_2_lt[0]}), .in13({32{1'b0}}), .in14({32{1'b0}}), .in15({32{1'b0}}),
    .out(Result), .sel(AluOP));
  Multiplexer #(.select(4), .width(32), .disabled("Z"), .enable("false")) multiplexer_2 (
    .in0({32{1'b0}}), .in1({32{1'b0}}), .in2({32{1'b0}}), .in3(multiplier_1_cout), .in4(divider_1_rem),
    .in5({32{1'b0}}), .in6({32{1'b0}}), .in7({32{1'b0}}), .in8({32{1'b0}}), .in9({32{1'b0}}),
    .in10({32{1'b0}}), .in11({32{1'b0}}), .in12({32{1'b0}}), .in13({32{1'b0}}), .in14({32{1'b0}}),
    .in15({32{1'b0}}), .out(Result_2), .sel(AluOP));

  // Other names for the same wires on the sheet: Result2[31:0] = Result_2; S[3:0] = AluOP

  // Notes on the sheet:
  //   不要改变此引脚区域内容，也不要改变ALU封装形式
  //   输入引脚
  //   输出引脚
endmodule

module MIPS_Regifile (
  input  [31:0] Din,
  input  Clk,
  input  WE,
  input  [4:0] R1_num,
  input  [4:0] W_num,
  input  [4:0] R2_num,
  output [31:0] R1,
  output [31:0] R2
);

  // RegisterFile registerfile_1: pin names not known; wires that end beside it: Din, Clk, WE, W_num, R1_num, R2_num, R1, R2
endmodule

module \理想流水线  (
  output RegWrite,
  output MemWrite,
  output [31:0] IF_PC,
  output [31:0] ID_PC,
  output [31:0] EX_PC,
  output [31:0] M_PC,
  output [31:0] WB_PC,
  output [31:0] RDin,
  output [31:0] MDin,
  output [31:0] LedData
);

  wire AluSrcB, and_1_out, and_2_out, Beq, Bne, CLK, clock_2_out, comparator_1_eq, comparator_1_lt,
       controlled_buffer_1_out, d_ff_1_q, equal, ex_mem_1_equal_out, ex_mem_1_jal_out, ex_mem_1_memtoreg_out,
       ex_mem_1_regdst_out, ex_mem_1_regwrite_out, ex_mem_1_syscall_out, Go, halt, id_ex_1_jal_out,
       id_ex_1_memtoreg_out, id_ex_1_memwrite_out, id_ex_1_regdst_out, id_ex_1_regwrite_out, IR1, IR2, IR3,
       JMP, LED, mem_wb_1_equal_out, mem_wb_1_jal_out, mem_wb_1_memtoreg_out, mem_wb_1_syscall_out,
       multiplexer_3_out, nand_2_out, not_1_out, or_1_out, RegDst, RST, SignedExt, Syscall, W1, W2, W3,
       Write, \单周期硬布线控制器_1_alu_src , \单周期硬布线控制器_1_beq , \单周期硬布线控制器_1_bne , \单周期硬布线控制器_1_jal ,
       \单周期硬布线控制器_1_jmp , \单周期硬布线控制器_1_jr , \单周期硬布线控制器_1_memtoreg , \单周期硬布线控制器_1_memwrite ,
       \单周期硬布线控制器_1_regdst , \单周期硬布线控制器_1_regwrite , \单周期硬布线控制器_1_syscall ;
  wire [3:0] id_ex_1_aluop_out, \单周期硬布线控制器_1_alu_op ;
  wire [4:0] if_id_1_ir_out_2, if_id_1_ir_out_3, if_id_1_ir_out_4, multiplexer_4_out, multiplexer_5_out,
       multiplexer_9_out, w_num;
  wire [5:0] if_id_1_ir_out_5;
  wire [10:0] if_id_1_ir_out;
  wire [12:0] CNT_num;
  wire [15:0] \LoadUse次数 , \总周期数 , \插入气泡数 , \无条件分支数 , \条件分支成功数 ;
  wire [27:0] shifter_1_out;
  wire [31:0] adder_1_out, bit_extender_1_out, bit_extender_2_out, EX_IR, ex_mem_1_aluout_out,
       ex_mem_1_ir_out, ex_mem_1_pc_out, ID_IR, if_id_1_pc_out, IF_IR, imme, IR, MEM_IR, mem_wb_1_aluout_out,
       mem_wb_1_ir_out, mem_wb_1_memout_out, mem_wb_1_pc_out, mips_alu_1_result, mips_regifile_1_r1,
       mips_regifile_1_r2, multiplexer_1_out, multiplexer_2_out, multiplexer_6_out, multiplexer_7_out,
       multiplexer_8_out, multiplexer_11_out, PC_4, PCBranch, R1, R2, ram_1_data, rom_1_data, shifter_2_out,
       WB_IR;

  Button \u_总复位  (.out(RST));
  Button _1 (.out(IR1));
  Button _2 (.out(IR2));
  Button _3 (.out(IR3));
  // Probe on \总周期数 
  // Probe on \总周期数 
  Button \u_继续运行  (.out(Go));
  LED #(.active("true")) led_1 (.in(W1));
  LED #(.active("true")) led_2 (.in(W2));
  LED #(.active("true")) led_3 (.in(W3));
  Hex_Digit_Display hex_digit_display_1 (.value(LedData[31:28]));  // open: dp
  // Probe on IF_PC[19:0]
  // Mips_Probe mips_probe_1: pin names not known; wires that end beside it: IF_IR
  and and_1 (and_1_out, Bne, ~equal);  // AND_Gate
  Hex_Digit_Display hex_digit_display_2 (.value(LedData[27:24]));  // open: dp
  Hex_Digit_Display hex_digit_display_3 (.value(LedData[23:20]));  // open: dp
  // Probe on ID_PC[19:0]
  // Mips_Probe mips_probe_2: pin names not known; wires that end beside it: ID_IR
  and and_2 (and_2_out, equal, Beq);
  or or_1 (or_1_out, and_1_out, and_2_out);
  Multiplexer #(.select(1), .width(32), .disabled("Z"), .enable("false")) multiplexer_1 (
    .in0(adder_1_out), .in1(PCBranch), .out(multiplexer_1_out), .sel(or_1_out));
  Shifter #(.width(28), .shift("ll")) shifter_1 (.in(IR[27:0]), .\dist (5'b00010), .out(shifter_1_out));
  Hex_Digit_Display hex_digit_display_4 (.value(LedData[15:12]));  // open: dp
  Hex_Digit_Display hex_digit_display_5 (.value(LedData[19:16]));  // open: dp
  Multiplexer #(.select(2), .width(32), .disabled("Z"), .enable("false")) multiplexer_2 (
    .in0(multiplexer_1_out), .in1(R1), .in2({PC_4[31:28], shifter_1_out}), .in3(R1), .out(multiplexer_2_out),
    .sel({2{JMP}}));
  Multiplexer #(.select(1), .width(1), .disabled("Z"), .enable("false")) multiplexer_3 (
    .in0(1'b1), .in1(Go), .out(multiplexer_3_out), .sel(halt));
  Hex_Digit_Display hex_digit_display_6 (.value(LedData[7:4]));  // open: dp
  Hex_Digit_Display hex_digit_display_7 (.value(LedData[11:8]));  // open: dp
  Clock #(.highDuration(1), .lowDuration(1)) clock_1 (.out(CLK));
  // Probe on EX_PC[19:0]
  // Mips_Probe mips_probe_3: pin names not known; wires that end beside it: EX_IR
  Register #(.width(32), .trigger("rising"), .Select("low")) PC (
    .D(multiplexer_2_out), .en(multiplexer_3_out), .Q(IF_PC), .clk(CLK));  // open: clr
  Counter #(.width(16), .max('hffff), .ongoal("wrap"), .trigger("rising"), .behavior("old")) counter_1 (
    .load(1'b0), .count(multiplexer_3_out), .Q(\总周期数 ), .clk(CLK));  // open: D, carry, clr, preset
  not not_1 (not_1_out, Go);
  nand nand_1 (Write, not_1_out, halt);
  Hex_Digit_Display hex_digit_display_8 (.value(LedData[3:0]));  // open: dp
  Adder #(.width(32)) adder_1 (.a(IF_PC), .b(32'h4), .out(adder_1_out));  // open: cin, cout
  // Probe on \总周期数 
  // Probe on M_PC[19:0]
  // Mips_Probe mips_probe_4: pin names not known; wires that end beside it: MEM_IR
  // Probe on \总周期数 
  // Probe on \无条件分支数 
  // Probe on \条件分支成功数 
  // Probe on \插入气泡数 
  // Probe on \LoadUse次数 
  ROM #(.addrWidth(10), .dataWidth(32), .Select("high")) rom_1 (.addr(IF_PC[11:2]), .data(rom_1_data));
  // Probe on IF_PC[11:0]
  // Probe on WB_PC[19:0]
  // Mips_Probe mips_probe_5: pin names not known; wires that end beside it: WB_IR
  // Mips_Probe mips_probe_6: pin names not known; wires that end beside it: rom_1_data
  // Probe on ID_PC[11:0]
  // Probe on EX_PC[11:0]
  IF_ID if_id_1 (
    .IR_in(rom_1_data), .OldPC_in(IF_PC), .PC_in(adder_1_out),
    .IR_out({if_id_1_ir_out_5, if_id_1_ir_out_4, if_id_1_ir_out_3, if_id_1_ir_out_2, if_id_1_ir_out}),
    .OldPC_out(ID_PC), .PC_out(if_id_1_pc_out), .\气泡高电平有效 (1'b0), .\使能 (Write), .Clk(CLK), .Clr(RST));  // open: PredJmp_in, PredJmp_out
  // Probe on M_PC[11:0]
  D_Flip_Flop #(.trigger("high"), .Pre_Clr_Positions("LEGACY"), .NegatePresetClear("false"), .enable("true"), .NewFFLayout("false")) d_ff_1 (.Q(d_ff_1_q));  // open: clk, D, Qn, preset, en, reset
  // Probe on 13'hc
  // Probe on WB_PC[11:0]
  Comparator #(.width(13), .mode("twosComplement")) comparator_1 (
    .a(CNT_num), .b(13'hc), .eq(comparator_1_eq), .lt(comparator_1_lt));  // open: gt
  Clock #(.highDuration(1), .lowDuration(1)) clock_2 (.out(clock_2_out));
  nand nand_2 (nand_2_out, d_ff_1_q, comparator_1_eq);
  Counter #(.width(13), .max('h1fff), .ongoal("stay"), .trigger("rising"), .behavior("old")) counter_2 (
    .count(comparator_1_lt), .Q(CNT_num), .clk(clock_2_out));  // open: load, D, carry, clr, preset
  assign bit_extender_1_out = {{16{1'b0}}, {if_id_1_ir_out_2, if_id_1_ir_out}};  // Bit_Extender bit_extender_1
  assign bit_extender_2_out = {{16{if_id_1_ir_out_2[4]}}, {if_id_1_ir_out_2, if_id_1_ir_out}};  // Bit_Extender bit_extender_2
  assign controlled_buffer_1_out = nand_2_out ? clock_2_out : 1'bz;  // Controlled_Buffer controlled_buffer_1
  \单周期硬布线控制器  \u_单周期硬布线控制器_1  (
    .Func(if_id_1_ir_out[5:0]), .OP(if_id_1_ir_out_5), .ALU_OP(\单周期硬布线控制器_1_alu_op ),
    .MemToReg(\单周期硬布线控制器_1_memtoreg ), .MemWrite(\单周期硬布线控制器_1_memwrite ), .ALU_SRC(\单周期硬布线控制器_1_alu_src ),
    .RegWrite(\单周期硬布线控制器_1_regwrite ), .SysCALL(\单周期硬布线控制器_1_syscall ), .SignedExt(SignedExt),
    .RegDst(\单周期硬布线控制器_1_regdst ), .JR(\单周期硬布线控制器_1_jr ), .JMP(\单周期硬布线控制器_1_jmp ), .Beq(\单周期硬布线控制器_1_beq ),
    .JAL(\单周期硬布线控制器_1_jal ), .Bne(\单周期硬布线控制器_1_bne ));
  Multiplexer #(.select(1), .width(5), .disabled("Z"), .enable("false")) multiplexer_4 (
    .in0(if_id_1_ir_out_4), .in1(5'b00010), .out(multiplexer_4_out), .sel(\单周期硬布线控制器_1_syscall ));
  Multiplexer #(.select(1), .width(5), .disabled("Z"), .enable("false")) multiplexer_5 (
    .in0(if_id_1_ir_out_3), .in1(5'b00100), .out(multiplexer_5_out), .sel(\单周期硬布线控制器_1_syscall ));
  Multiplexer #(.select(1), .width(32), .disabled("Z"), .enable("false")) multiplexer_6 (
    .in0(bit_extender_1_out), .in1(bit_extender_2_out), .out(multiplexer_6_out), .sel(SignedExt));
  Pull_Resistor #(.pull(1)) pull_resistor_1 (.node(controlled_buffer_1_out));
  MIPS_Regifile mips_regifile_1 (
    .Din(RDin), .Clk(CLK), .R1(mips_regifile_1_r1), .R2(mips_regifile_1_r2), .WE(RegWrite), .W_num(w_num),
    .R1_num(multiplexer_4_out), .R2_num(multiplexer_5_out));
  ID_EX id_ex_1 (
    .Beq_in(\单周期硬布线控制器_1_beq ), .Bne_in(\单周期硬布线控制器_1_bne ), .MemToReg_in(\单周期硬布线控制器_1_memtoreg ),
    .MemWrite_in(\单周期硬布线控制器_1_memwrite ), .AluSrcB_in(\单周期硬布线控制器_1_alu_src ),
    .RegWrite_in(\单周期硬布线控制器_1_regwrite ), .JAL_in(\单周期硬布线控制器_1_jal ), .RegDst_in(\单周期硬布线控制器_1_regdst ),
    .JMP_in(\单周期硬布线控制器_1_jmp ), .JR_in(\单周期硬布线控制器_1_jr ), .SignedExt_in(SignedExt),
    .AluOP_in(\单周期硬布线控制器_1_alu_op ),
    .IR_in({if_id_1_ir_out_5, if_id_1_ir_out_4, if_id_1_ir_out_3, if_id_1_ir_out_2, if_id_1_ir_out}),
    .OldPC_in(ID_PC), .PC_in(if_id_1_pc_out), .R1_in(mips_regifile_1_r1), .R2_in(mips_regifile_1_r2),
    .imm_in(multiplexer_6_out), .Beq_out(Beq), .Bne_out(Bne), .MemToReg_out(id_ex_1_memtoreg_out),
    .MemWrite_out(id_ex_1_memwrite_out), .AluSrcB_out(AluSrcB), .RegWrite_out(id_ex_1_regwrite_out),
    .JAL_out(id_ex_1_jal_out), .RegDst_out(id_ex_1_regdst_out), .JMP_out(JMP), .JR_out(JMP),
    .AluOP_out(id_ex_1_aluop_out), .IR_out(IR), .OldPC_out(EX_PC), .PC_out(PC_4), .R1_out(R1), .R2_out(R2),
    .imm_out(imme), .\气泡高电平有效 (1'b0), .\使能 (Write), .Clk(CLK), .Clr(RST), .Syscall_in(\单周期硬布线控制器_1_syscall ),
    .Syscall_out(Syscall));  // open: SignedExt_out, BGTZ, BGTZ_2, LHU, LHU_2, PredJmp_in_Eret_in, PredJmp_out_Eret_in
  Register #(.width(32), .trigger("rising"), .Select("low")) register_1 (
    .D(R2), .Q(LedData), .clk(LED), .clr(RST));  // open: en
  Multiplexer #(.select(1), .width(32), .disabled("Z"), .enable("false")) multiplexer_7 (
    .in0(R2), .in1(imme), .out(multiplexer_7_out), .sel(AluSrcB));
  Shifter #(.width(32), .shift("ll")) shifter_2 (.in(imme), .\dist (5'b00010), .out(shifter_2_out));
  Multiplexer #(.select(1), .width(32), .disabled("Z"), .enable("false")) multiplexer_8 (
    .in0(multiplexer_7_out), .in1(32'h22), .out(multiplexer_8_out), .sel(Syscall));
  Adder #(.width(32)) adder_2 (.a(shifter_2_out), .b(PC_4), .out(PCBranch));  // open: cin, cout
  MIPS_ALU mips_alu_1 (
    .X(R1), .Y(multiplexer_8_out), .AluOP(id_ex_1_aluop_out), .Equal(equal), .Result(mips_alu_1_result),
    .shamt(IR[10:6]));  // open: Result_2
  EX_MEM ex_mem_1 (
    .Syscall_in(Syscall), .MemToReg_in(id_ex_1_memtoreg_out), .MemWrite_in(id_ex_1_memwrite_out),
    .RegWrite_in(id_ex_1_regwrite_out), .JAL_in(id_ex_1_jal_out), .RegDst_in(id_ex_1_regdst_out),
    .equal_in(equal), .IR_in(IR), .OldPC_in(EX_PC), .PC_in(PC_4), .AluOut_in(mips_alu_1_result), .R2_in(R2),
    .Syscall_out(ex_mem_1_syscall_out), .MemToReg_out(ex_mem_1_memtoreg_out), .MemWrite_out(MemWrite),
    .RegWrite_out(ex_mem_1_regwrite_out), .JAL_out(ex_mem_1_jal_out), .RegDst_out(ex_mem_1_regdst_out),
    .equal_out(ex_mem_1_equal_out), .IR_out(ex_mem_1_ir_out), .OldPC_out(M_PC), .PC_out(ex_mem_1_pc_out),
    .AluOut_out(ex_mem_1_aluout_out), .R2_out(MDin), .\气泡高电平有效 (1'b0), .\使能 (Write), .Clk(CLK), .Clr(RST));  // open: LHU_2, LHU, pause_in, pause_out, Eret_in, Eret_in_2
  RAM #(.addrWidth(10), .dataWidth(32), .bus("separate"), .Select("high")) ram_1 (
    .addr(ex_mem_1_aluout_out[11:2]), .din(MDin), .data(ram_1_data), .str(MemWrite), .clk(CLK), .clr(RST));  // open: sel, ld
  MEM_WB mem_wb_1 (
    .Syscall_in(ex_mem_1_syscall_out), .MemToReg_in(ex_mem_1_memtoreg_out), .MemWrite_in(MemWrite),
    .RegWrite_in(ex_mem_1_regwrite_out), .JAL_in(ex_mem_1_jal_out), .RegDst_in(ex_mem_1_regdst_out),
    .equal_in(ex_mem_1_equal_out), .IR_in(ex_mem_1_ir_out), .OldPC_in(M_PC), .PC_in(ex_mem_1_pc_out),
    .AluOut_in(ex_mem_1_aluout_out), .MemOut_in(ram_1_data), .Syscall_out(mem_wb_1_syscall_out),
    .MemToReg_out(mem_wb_1_memtoreg_out), .RegWrite_out(RegWrite), .JAL_out(mem_wb_1_jal_out),
    .RegDst_out(RegDst), .equal_out(mem_wb_1_equal_out), .IR_out(mem_wb_1_ir_out), .OldPC_out(WB_PC),
    .PC_out(mem_wb_1_pc_out), .AluOut_out(mem_wb_1_aluout_out), .MemOut_out(mem_wb_1_memout_out),
    .\气泡高电平有效 (1'b0), .\使能 (Write), .Clk(CLK), .Clr(RST));  // open: MemWrite_out, LHU_2, LHU, pause_in, pause_out, Eret_in, Eret_out
  Multiplexer #(.select(1), .width(5), .disabled("Z"), .enable("false")) multiplexer_9 (
    .in0(mem_wb_1_ir_out[20:16]), .in1(mem_wb_1_ir_out[15:11]), .out(multiplexer_9_out), .sel(RegDst));
  Multiplexer #(.select(1), .width(5), .disabled("Z"), .enable("false")) multiplexer_10 (
    .in0(multiplexer_9_out), .in1({5{1'b1}}), .out(w_num), .sel(mem_wb_1_jal_out));
  Multiplexer #(.select(1), .width(32), .disabled("Z"), .enable("false")) multiplexer_11 (
    .in0(mem_wb_1_aluout_out), .in1(mem_wb_1_memout_out), .out(multiplexer_11_out),
    .sel(mem_wb_1_memtoreg_out));
  Multiplexer #(.select(1), .width(32), .disabled("Z"), .enable("false")) multiplexer_12 (
    .in0(multiplexer_11_out), .in1(mem_wb_1_pc_out), .out(RDin), .sel(mem_wb_1_jal_out));
  and and_3 (halt, ~mem_wb_1_equal_out, mem_wb_1_syscall_out);  // AND_Gate
  and and_4 (LED, mem_wb_1_equal_out, Syscall);

  // Other names for the same wires on the sheet: JR = JMP; MEM_PC[31:0] = M_PC; PC[31:0] = IF_PC

  // Notes on the sheet:
  //   中断源
  //   时空图监测，可删除
  //   中断等待指示
  //   数码管输出
  //   指令存储器
  //   PC+4
  //   contents of rom_1 (hex, n*v repeats v):
  //   20100000 20110000 20120000 20130000 36100000 36310001 36520002 36730003 ae100000 ae110004 ae120008
  //   ae13000c 2002000a 20110000 20120000 20130000 c
  //   控制位
  //   流水调试日志用
  //   暂停节拍，不能为0
  //   指令字
  //   戳工具置1进入计数暂停模式，ctrl+k时钟自动运行到对应节拍暂停
  //   ctrl+k关闭时钟连续运行，将控制位置零，进入单步调试模式调试
  //   用这个时钟源需要去掉电路中的其他时钟源
  //   OP
  //   Func
  //   rs
  //   rt
  //   rd
  //   JMP
  //   JR
  //   OP
  //   Func
  //   可计数暂停的时钟源
  //   Beq
  //   Bne
  //   MemToReg
  //   MemWrite
  //   AluOP
  //   AluSrcB
  //   RegWrite
  //   JAL
  //   RegDst
  //   Syscall
  //   为方便自动评测，需要输出流水线各段保存的PC值，注意是PC不是PC+4，另外ID段寄存器写入信息，Mem段内存写入信息也要输出
  //   PCBranch
  //   rt
  //   rd
endmodule

module \气泡流水线  (
  output RegWrite,
  output MemWrite,
  output [31:0] IF_PC,
  output [31:0] ID_PC,
  output [31:0] EX_PC,
  output [31:0] M_PC,
  output [31:0] WB_PC,
  output [31:0] RDin,
  output [31:0] MDin,
  output [31:0] LedData
);

  wire AluSrcB, and_1_out, and_2_out, and_4_out, and_5_out, and_6_out, Beq, BGTZ, BGTZ_flag, Bne, CLK,
       clock_2_out, comparator_1_gt, comparator_2_eq, comparator_2_lt, controlled_buffer_1_out, d_ff_1_q,
       equal, ex_mem_1_equal_out, ex_mem_1_jal_out, ex_mem_1_lhu_2, ex_mem_1_memtoreg_out,
       ex_mem_1_regdst_out, ex_mem_1_syscall_out, EX_RegWrite, Go, halt, id_ex_1_jal_out, id_ex_1_lhu_2,
       id_ex_1_memtoreg_out, id_ex_1_memwrite_out, id_ex_1_regdst_out, IR1, IR2, IR3, J, JMP, jmp_flag, JR,
       LED, LHU, MEM_RegWrite, mem_wb_1_equal_out, mem_wb_1_jal_out, mem_wb_1_memtoreg_out,
       mem_wb_1_syscall_out, multiplexer_4_out, nand_2_out, not_1_out, or_2_out, or_4_out, RegDst, RST,
       SignedExt, Syscall, W1, W2, W3, Write, \单周期硬布线控制器_差异化_1_alu_src , \单周期硬布线控制器_差异化_1_beq ,
       \单周期硬布线控制器_差异化_1_bgtz , \单周期硬布线控制器_差异化_1_bne , \单周期硬布线控制器_差异化_1_jal , \单周期硬布线控制器_差异化_1_jmp ,
       \单周期硬布线控制器_差异化_1_jr , \单周期硬布线控制器_差异化_1_lhu , \单周期硬布线控制器_差异化_1_memtoreg , \单周期硬布线控制器_差异化_1_memwrite ,
       \单周期硬布线控制器_差异化_1_regdst , \单周期硬布线控制器_差异化_1_regwrite , \单周期硬布线控制器_差异化_1_syscall , \数据相关 ;
  wire [3:0] id_ex_1_aluop_out, \单周期硬布线控制器_差异化_1_alu_op ;
  wire [4:0] EX_WriteReg_num, ID_ReadReg1_num, ID_ReadReg2_num, MEM_WriteReg_num, multiplexer_10_out,
       multiplexer_12_out, multiplexer_14_out, w_num;
  wire [5:0] Func, OP;
  wire [12:0] CNT_num;
  wire [15:0] \LoadUse次数 , multiplexer_16_out, \总周期数 , \插入气泡数 , \无条件分支数 , \条件分支成功数 ;
  wire [25:6] if_id_1_ir_out;
  wire [27:0] shifter_1_out;
  wire [31:0] adder_1_out, bit_extender_1_out, bit_extender_2_out, bit_extender_3_out, EX_IR,
       ex_mem_1_aluout_out, ex_mem_1_ir_out, ex_mem_1_pc_out, ID_IR, if_id_1_pc_out, IF_IR, imme, IR, MEM_IR,
       mem_wb_1_aluout_out, mem_wb_1_ir_out, mem_wb_1_memout_out, mem_wb_1_pc_out, mips_alu_1_result,
       \mips_regfile_下降沿_1_r1 , \mips_regfile_下降沿_1_r2 , multiplexer_1_out, multiplexer_2_out,
       multiplexer_3_out, multiplexer_7_out, multiplexer_8_out, multiplexer_9_out, multiplexer_17_out,
       multiplexer_18_out, PC_4, PCBranch, R1, R2, ram_1_data, rom_1_data, shifter_2_out, WB_IR;

  Button \u_总复位  (.out(RST));
  Button _1 (.out(IR1));
  Button _2 (.out(IR2));
  Button _3 (.out(IR3));
  // Probe on \总周期数 
  // Probe on \总周期数 
  Button \u_继续运行  (.out(Go));
  LED #(.active("true")) led_1 (.in(W1));
  LED #(.active("true")) led_2 (.in(W2));
  LED #(.active("true")) led_3 (.in(W3));
  not not_1 (not_1_out, Go);
  Hex_Digit_Display hex_digit_display_1 (.value(LedData[31:28]));  // open: dp
  // Probe on IF_PC[19:0]
  // Mips_Probe mips_probe_1: pin names not known; wires that end beside it: IF_IR
  nand nand_1 (Write, not_1_out, halt);
  Hex_Digit_Display hex_digit_display_2 (.value(LedData[27:24]));  // open: dp
  Hex_Digit_Display hex_digit_display_3 (.value(LedData[23:20]));  // open: dp
  // Probe on ID_PC[19:0]
  // Mips_Probe mips_probe_2: pin names not known; wires that end beside it: ID_IR
  and and_1 (and_1_out, Bne, ~equal);  // AND_Gate
  and and_2 (and_2_out, equal, Beq);
  or or_1 (jmp_flag, and_1_out, and_2_out);
  Multiplexer #(.select(1), .width(32), .disabled("Z"), .enable("false")) multiplexer_1 (
    .in0(adder_1_out), .in1(PCBranch), .out(multiplexer_1_out), .sel(jmp_flag));
  Shifter #(.width(28), .shift("ll")) shifter_1 (.in(IR[27:0]), .\dist (5'b00010), .out(shifter_1_out));
  or or_2 (or_2_out, BGTZ_flag, jmp_flag);
  Hex_Digit_Display hex_digit_display_4 (.value(LedData[15:12]));  // open: dp
  Hex_Digit_Display hex_digit_display_5 (.value(LedData[19:16]));  // open: dp
  Multiplexer #(.select(2), .width(32), .disabled("Z"), .enable("false")) multiplexer_2 (
    .in0(multiplexer_1_out), .in1(R1), .in2({PC_4[31:28], shifter_1_out}), .in3(R1), .out(multiplexer_2_out),
    .sel({JMP, JR}));
  Hex_Digit_Display hex_digit_display_6 (.value(LedData[11:8]));  // open: dp
  Hex_Digit_Display hex_digit_display_7 (.value(LedData[7:4]));  // open: dp
  Clock #(.highDuration(1), .lowDuration(1)) clock_1 (.out(CLK));
  // Probe on EX_PC[19:0]
  // Mips_Probe mips_probe_3: pin names not known; wires that end beside it: EX_IR
  Register #(.width(32), .trigger("rising"), .Select("low")) register_1 (
    .D(R2), .Q(LedData), .clk(LED), .clr(RST));  // open: en
  Comparator #(.width(32), .mode("twosComplement")) comparator_1 (
    .a(R1), .b({32{1'b0}}), .gt(comparator_1_gt));  // open: eq, lt
  and and_3 (BGTZ_flag, BGTZ, comparator_1_gt);
  Multiplexer #(.select(1), .width(32), .disabled("Z"), .enable("false")) multiplexer_3 (
    .in0(multiplexer_2_out), .in1(PCBranch), .out(multiplexer_3_out), .sel(BGTZ_flag));
  and and_4 (and_4_out, Write, \数据相关 );
  Counter #(.width(16), .max('hffff), .ongoal("wrap"), .trigger("rising"), .behavior("old")) counter_1 (
    .load(1'b0), .count(JMP), .Q(\无条件分支数 ), .clk(CLK), .clr(RST));  // open: D, carry, preset
  Counter #(.width(16), .max('hffff), .ongoal("wrap"), .trigger("rising"), .behavior("old")) counter_2 (
    .load(1'b0), .count(or_2_out), .Q(\条件分支成功数 ), .clk(CLK), .clr(RST));  // open: D, carry, preset
  or or_3 (J, or_2_out, JMP, JR);
  Hex_Digit_Display hex_digit_display_8 (.value(LedData[3:0]));  // open: dp
  and and_5 (and_5_out, ~\数据相关 , multiplexer_4_out);  // AND_Gate
  Multiplexer #(.select(1), .width(1), .disabled("Z"), .enable("false")) multiplexer_4 (
    .in0(1'b1), .in1(Go), .out(multiplexer_4_out), .sel(halt));
  Counter #(.width(16), .max('hffff), .ongoal("wrap"), .trigger("rising"), .behavior("old")) counter_3 (
    .load(1'b0), .count(and_4_out), .Q(\插入气泡数 ), .clk(CLK), .clr(RST));  // open: D, carry, preset
  // Probe on \总周期数 
  // Probe on M_PC[19:0]
  // Mips_Probe mips_probe_4: pin names not known; wires that end beside it: MEM_IR
  Register #(.width(32), .trigger("rising"), .Select("low")) PC (
    .D(multiplexer_3_out), .en(and_5_out), .Q(IF_PC), .clk(CLK), .clr(RST));
  Counter #(.width(16), .max('hffff), .ongoal("wrap"), .trigger("rising"), .behavior("old")) counter_4 (
    .load(1'b0), .count(multiplexer_4_out), .Q(\总周期数 ), .clk(CLK), .clr(RST));  // open: D, carry, preset
  // Probe on \总周期数 
  // Probe on \无条件分支数 
  // Probe on \条件分支成功数 
  // Probe on \插入气泡数 
  // Probe on \LoadUse次数 
  Adder #(.width(32)) adder_1 (.a(IF_PC), .b(32'h4), .out(adder_1_out));  // open: cin, cout
  // Probe on IF_PC[11:0]
  // Probe on WB_PC[19:0]
  // Mips_Probe mips_probe_5: pin names not known; wires that end beside it: WB_IR
  // Probe on ID_PC[11:0]
  // Probe on EX_PC[11:0]
  ROM #(.addrWidth(10), .dataWidth(32), .Select("high")) rom_1 (.addr(IF_PC[11:2]), .data(rom_1_data));
  // Probe on M_PC[11:0]
  D_Flip_Flop #(.trigger("high"), .Pre_Clr_Positions("LEGACY"), .NegatePresetClear("false"), .enable("true"), .NewFFLayout("false")) d_ff_1 (.Q(d_ff_1_q));  // open: clk, D, Qn, preset, en, reset
  // Probe on 13'hc
  // Mips_Probe mips_probe_6: pin names not known; wires that end beside it: rom_1_data
  and and_6 (and_6_out, Write, ~\数据相关 );  // AND_Gate
  \数据相关检测逻辑  \u_数据相关检测逻辑_1  (
    .EX_WriteReg_num(EX_WriteReg_num), .OP(OP), .EX_RegWrite(EX_RegWrite),
    .MEM_WriteReg_num(MEM_WriteReg_num), .Func(Func), .MEM_RegWrite(MEM_RegWrite),
    .ID_ReadReg1_num(ID_ReadReg1_num), .ID_ReadReg2_num(ID_ReadReg2_num), .\数据相关 (\数据相关 ));
  // Probe on WB_PC[11:0]
  Comparator #(.width(13), .mode("twosComplement")) comparator_2 (
    .a(CNT_num), .b(13'hc), .eq(comparator_2_eq), .lt(comparator_2_lt));  // open: gt
  Clock #(.highDuration(1), .lowDuration(1)) clock_2 (.out(clock_2_out));
  IF_ID if_id_1 (
    .IR_in(rom_1_data), .OldPC_in(IF_PC), .PC_in(adder_1_out), .IR_out({OP, if_id_1_ir_out, Func}),
    .OldPC_out(ID_PC), .PC_out(if_id_1_pc_out), .\气泡高电平有效 (J), .\使能 (and_6_out), .Clk(CLK), .Clr(RST));  // open: PredJmp_in, PredJmp_out
  nand nand_2 (nand_2_out, d_ff_1_q, comparator_2_eq);
  Counter #(.width(13), .max('h1fff), .ongoal("stay"), .trigger("rising"), .behavior("old")) counter_5 (
    .count(comparator_2_lt), .Q(CNT_num), .clk(clock_2_out));  // open: load, D, carry, clr, preset
  assign controlled_buffer_1_out = nand_2_out ? clock_2_out : 1'bz;  // Controlled_Buffer controlled_buffer_1
  Pull_Resistor #(.pull(1)) pull_resistor_1 (.node(controlled_buffer_1_out));
  assign bit_extender_1_out = {{16{1'b0}}, {if_id_1_ir_out[15:6], Func}};  // Bit_Extender bit_extender_1
  assign bit_extender_2_out = {{16{if_id_1_ir_out[15]}}, {if_id_1_ir_out[15:6], Func}};  // Bit_Extender bit_extender_2
  \单周期硬布线控制器_差异化  \u_单周期硬布线控制器_差异化_1  (
    .OP(OP), .Func(Func), .ALU_OP(\单周期硬布线控制器_差异化_1_alu_op ), .MemToReg(\单周期硬布线控制器_差异化_1_memtoreg ),
    .MemWrite(\单周期硬布线控制器_差异化_1_memwrite ), .ALU_SRC(\单周期硬布线控制器_差异化_1_alu_src ),
    .RegWrite(\单周期硬布线控制器_差异化_1_regwrite ), .SysCALL(\单周期硬布线控制器_差异化_1_syscall ), .SignedExt(SignedExt),
    .RegDst(\单周期硬布线控制器_差异化_1_regdst ), .Beq(\单周期硬布线控制器_差异化_1_beq ), .Bne(\单周期硬布线控制器_差异化_1_bne ),
    .JR(\单周期硬布线控制器_差异化_1_jr ), .JMP(\单周期硬布线控制器_差异化_1_jmp ), .JAL(\单周期硬布线控制器_差异化_1_jal ),
    .BGTZ(\单周期硬布线控制器_差异化_1_bgtz ), .LHU(\单周期硬布线控制器_差异化_1_lhu ));
  Multiplexer #(.select(1), .width(5), .disabled("Z"), .enable("false")) multiplexer_5 (
    .in0(if_id_1_ir_out[25:21]), .in1(5'b00010), .out(ID_ReadReg1_num), .sel(\单周期硬布线控制器_差异化_1_syscall ));
  Multiplexer #(.select(1), .width(5), .disabled("Z"), .enable("false")) multiplexer_6 (
    .in0(if_id_1_ir_out[20:16]), .in1(5'b00100), .out(ID_ReadReg2_num), .sel(\单周期硬布线控制器_差异化_1_syscall ));
  Multiplexer #(.select(1), .width(32), .disabled("Z"), .enable("false")) multiplexer_7 (
    .in0(bit_extender_1_out), .in1(bit_extender_2_out), .out(multiplexer_7_out), .sel(SignedExt));
  \MIPS_Regfile_下降沿  \mips_regfile_下降沿_1  (
    .Din(RDin), .Clk(CLK), .R1(\mips_regfile_下降沿_1_r1 ), .R2(\mips_regfile_下降沿_1_r2 ), .WE(RegWrite),
    .W_num(w_num), .R1_num(ID_ReadReg1_num), .R2_num(ID_ReadReg2_num));
  or or_4 (or_4_out, J, \数据相关 );
  ID_EX id_ex_1 (
    .Beq_in(\单周期硬布线控制器_差异化_1_beq ), .Bne_in(\单周期硬布线控制器_差异化_1_bne ), .MemToReg_in(\单周期硬布线控制器_差异化_1_memtoreg ),
    .MemWrite_in(\单周期硬布线控制器_差异化_1_memwrite ), .AluSrcB_in(\单周期硬布线控制器_差异化_1_alu_src ),
    .RegWrite_in(\单周期硬布线控制器_差异化_1_regwrite ), .JAL_in(\单周期硬布线控制器_差异化_1_jal ),
    .RegDst_in(\单周期硬布线控制器_差异化_1_regdst ), .JMP_in(\单周期硬布线控制器_差异化_1_jmp ), .JR_in(\单周期硬布线控制器_差异化_1_jr ),
    .SignedExt_in(SignedExt), .AluOP_in(\单周期硬布线控制器_差异化_1_alu_op ), .IR_in({OP, if_id_1_ir_out, Func}),
    .OldPC_in(ID_PC), .PC_in(if_id_1_pc_out), .R1_in(\mips_regfile_下降沿_1_r1 ),
    .R2_in(\mips_regfile_下降沿_1_r2 ), .imm_in(multiplexer_7_out), .Beq_out(Beq), .Bne_out(Bne),
    .MemToReg_out(id_ex_1_memtoreg_out), .MemWrite_out(id_ex_1_memwrite_out), .AluSrcB_out(AluSrcB),
    .RegWrite_out(EX_RegWrite), .JAL_out(id_ex_1_jal_out), .RegDst_out(id_ex_1_regdst_out), .JMP_out(JMP),
    .JR_out(JR), .AluOP_out(id_ex_1_aluop_out), .IR_out(IR), .OldPC_out(EX_PC), .PC_out(PC_4), .R1_out(R1),
    .R2_out(R2), .imm_out(imme), .\气泡高电平有效 (or_4_out), .\使能 (Write), .Clk(CLK), .Clr(RST),
    .Syscall_in(\单周期硬布线控制器_差异化_1_syscall ), .Syscall_out(Syscall), .BGTZ(\单周期硬布线控制器_差异化_1_bgtz ),
    .BGTZ_2(BGTZ), .LHU(\单周期硬布线控制器_差异化_1_lhu ), .LHU_2(id_ex_1_lhu_2));  // open: SignedExt_out, PredJmp_in_Eret_in, PredJmp_out_Eret_in
  Multiplexer #(.select(1), .width(32), .disabled("Z"), .enable("false")) multiplexer_8 (
    .in0(R2), .in1(imme), .out(multiplexer_8_out), .sel(AluSrcB));
  Shifter #(.width(32), .shift("ll")) shifter_2 (.in(imme), .\dist (5'b00010), .out(shifter_2_out));
  Multiplexer #(.select(1), .width(32), .disabled("Z"), .enable("false")) multiplexer_9 (
    .in0(multiplexer_8_out), .in1(32'h22), .out(multiplexer_9_out), .sel(Syscall));
  Multiplexer #(.select(1), .width(5), .disabled("Z"), .enable("false")) multiplexer_10 (
    .in0(IR[20:16]), .in1(IR[15:11]), .out(multiplexer_10_out), .sel(id_ex_1_regdst_out));
  Multiplexer #(.select(1), .width(5), .disabled("Z"), .enable("false")) multiplexer_11 (
    .in0(multiplexer_10_out), .in1({5{1'b1}}), .out(EX_WriteReg_num), .sel(id_ex_1_jal_out));
  Adder #(.width(32)) adder_2 (.a(shifter_2_out), .b(PC_4), .out(PCBranch));  // open: cin, cout
  MIPS_ALU mips_alu_1 (
    .X(R1), .Y(multiplexer_9_out), .AluOP(id_ex_1_aluop_out), .Equal(equal), .Result(mips_alu_1_result),
    .shamt(IR[10:6]));  // open: Result_2
  EX_MEM ex_mem_1 (
    .Syscall_in(Syscall), .MemToReg_in(id_ex_1_memtoreg_out), .MemWrite_in(id_ex_1_memwrite_out),
    .RegWrite_in(EX_RegWrite), .JAL_in(id_ex_1_jal_out), .RegDst_in(id_ex_1_regdst_out), .equal_in(equal),
    .IR_in(IR), .OldPC_in(EX_PC), .PC_in(PC_4), .AluOut_in(mips_alu_1_result), .R2_in(R2),
    .Syscall_out(ex_mem_1_syscall_out), .MemToReg_out(ex_mem_1_memtoreg_out), .MemWrite_out(MemWrite),
    .RegWrite_out(MEM_RegWrite), .JAL_out(ex_mem_1_jal_out), .RegDst_out(ex_mem_1_regdst_out),
    .equal_out(ex_mem_1_equal_out), .IR_out(ex_mem_1_ir_out), .OldPC_out(M_PC), .PC_out(ex_mem_1_pc_out),
    .AluOut_out(ex_mem_1_aluout_out), .R2_out(MDin), .\气泡高电平有效 (1'b0), .\使能 (Write), .Clk(CLK), .Clr(RST),
    .LHU_2(ex_mem_1_lhu_2), .LHU(id_ex_1_lhu_2));  // open: pause_in, pause_out, Eret_in, Eret_in_2
  Multiplexer #(.select(1), .width(5), .disabled("Z"), .enable("false")) multiplexer_12 (
    .in0(ex_mem_1_ir_out[20:16]), .in1(ex_mem_1_ir_out[15:11]), .out(multiplexer_12_out),
    .sel(ex_mem_1_regdst_out));
  Multiplexer #(.select(1), .width(5), .disabled("Z"), .enable("false")) multiplexer_13 (
    .in0(multiplexer_12_out), .in1({5{1'b1}}), .out(MEM_WriteReg_num), .sel(ex_mem_1_jal_out));
  RAM #(.addrWidth(10), .dataWidth(32), .bus("separate"), .Select("high")) ram_1 (
    .addr(ex_mem_1_aluout_out[11:2]), .din(MDin), .data(ram_1_data), .str(MemWrite), .clk(CLK), .clr(RST));  // open: sel, ld
  MEM_WB mem_wb_1 (
    .Syscall_in(ex_mem_1_syscall_out), .MemToReg_in(ex_mem_1_memtoreg_out), .MemWrite_in(MemWrite),
    .RegWrite_in(MEM_RegWrite), .JAL_in(ex_mem_1_jal_out), .RegDst_in(ex_mem_1_regdst_out),
    .equal_in(ex_mem_1_equal_out), .IR_in(ex_mem_1_ir_out), .OldPC_in(M_PC), .PC_in(ex_mem_1_pc_out),
    .AluOut_in(ex_mem_1_aluout_out), .MemOut_in(ram_1_data), .Syscall_out(mem_wb_1_syscall_out),
    .MemToReg_out(mem_wb_1_memtoreg_out), .RegWrite_out(RegWrite), .JAL_out(mem_wb_1_jal_out),
    .RegDst_out(RegDst), .equal_out(mem_wb_1_equal_out), .IR_out(mem_wb_1_ir_out), .OldPC_out(WB_PC),
    .PC_out(mem_wb_1_pc_out), .AluOut_out(mem_wb_1_aluout_out), .MemOut_out(mem_wb_1_memout_out),
    .\气泡高电平有效 (1'b0), .\使能 (Write), .Clk(CLK), .Clr(RST), .LHU_2(LHU), .LHU(ex_mem_1_lhu_2));  // open: MemWrite_out, pause_in, pause_out, Eret_in, Eret_out
  Multiplexer #(.select(1), .width(5), .disabled("Z"), .enable("false")) multiplexer_14 (
    .in0(mem_wb_1_ir_out[20:16]), .in1(mem_wb_1_ir_out[15:11]), .out(multiplexer_14_out), .sel(RegDst));
  Multiplexer #(.select(1), .width(5), .disabled("Z"), .enable("false")) multiplexer_15 (
    .in0(multiplexer_14_out), .in1({5{1'b1}}), .out(w_num), .sel(mem_wb_1_jal_out));
  Multiplexer #(.select(1), .width(16), .disabled("Z"), .enable("false")) multiplexer_16 (
    .in0(mem_wb_1_memout_out[15:0]), .in1(mem_wb_1_memout_out[31:16]), .out(multiplexer_16_out),
    .sel(mem_wb_1_aluout_out[1]));
  Multiplexer #(.select(1), .width(32), .disabled("Z"), .enable("false")) multiplexer_17 (
    .in0(mem_wb_1_aluout_out), .in1(mem_wb_1_memout_out), .out(multiplexer_17_out),
    .sel(mem_wb_1_memtoreg_out));
  assign bit_extender_3_out = {{16{1'b0}}, multiplexer_16_out};  // Bit_Extender bit_extender_3
  Multiplexer #(.select(1), .width(32), .disabled("Z"), .enable("false")) multiplexer_18 (
    .in0(multiplexer_17_out), .in1(bit_extender_3_out), .out(multiplexer_18_out), .sel(LHU));
  Multiplexer #(.select(1), .width(32), .disabled("Z"), .enable("false")) multiplexer_19 (
    .in0(multiplexer_18_out), .in1(mem_wb_1_pc_out), .out(RDin), .sel(mem_wb_1_jal_out));
  and and_7 (halt, ~mem_wb_1_equal_out, mem_wb_1_syscall_out);  // AND_Gate
  and and_8 (LED, mem_wb_1_equal_out, Syscall);

  // Other names for the same wires on the sheet: MEM_PC[31:0] = M_PC; PC[31:0] = IF_PC

  // Notes on the sheet:
  //   中断源
  //   时空图监测，可删除
  //   中断等待指示
  //   数码管输出
  //   指令存储器
  //   PC+4
  //   控制位
  //   contents of rom_1 (hex, n*v repeats v):
  //   2011000f 112020 20020022 c 2231ffff 1e20fffb 2002000a c
  //   流水调试日志用
  //   暂停节拍，不能为0
  //   戳工具置1进入计数暂停模式，ctrl+k时钟自动运行到对应节拍暂停
  //   ctrl+k关闭时钟连续运行，将控制位置零，进入单步调试模式调试
  //   指令字
  //   可计数暂停的时钟源
  //   OP
  //   Func
  //   rs
  //   rt
  //   rd
  //   JMP
  //   JR
  //   OP
  //   Func
  //   Beq
  //   Bne
  //   MemToReg
  //   MemWrite
  //   AluOP
  //   AluSrcB
  //   RegWrite
  //   JAL
  //   RegDst
  //   Syscall
  //   为方便自动评测，需要输出流水线各段保存的PC值，注意是PC不是PC+4，另外ID段寄存器写入信息，Mem段内存写入信息也要输出
  //   PCBranch
  //   rt
  //   rd
endmodule
module \重定向流水线  (
  output RegWrite,
  output MemWrite,
  output [31:0] IF_PC,
  output [31:0] ID_PC,
  output [31:0] EX_PC,
  output [31:0] M_PC,
  output [31:0] WB_PC,
  output [31:0] RDin,
  output [31:0] MDin,
  output [31:0] LedData
);

  wire AluSrcB, and_1_out, and_2_out, and_4_out, and_5_out, and_6_out, Beq, BGTZ, BGTZ_flag, Bne, CLK,
       clock_2_out, comparator_1_gt, comparator_2_eq, comparator_2_lt, controlled_buffer_1_out, d_ff_1_q,
       equal, ex_mem_1_equal_out, ex_mem_1_jal_out, ex_mem_1_lhu_2, ex_mem_1_pause_out, ex_mem_1_regdst_out,
       ex_mem_1_syscall_out, EX_RegWrite, Go, halt, id_ex_1_jal_out, id_ex_1_lhu_2, id_ex_1_memtoreg_out,
       id_ex_1_memwrite_out, id_ex_1_regdst_out, IR1, IR2, IR3, J, JMP, jmp_flag, JR, LED, LHU, load_use,
       MEM_RegWrite, mem_wb_1_jal_out, mem_wb_1_memtoreg_out, MemToReg, multiplexer_4_out, nand_1_out,
       not_1_out, or_2_out, or_4_out, or_5_out, pause, RegDst, RST, SignedExt, Syscall, V034, W1, W2, W3,
       Write, \单周期硬布线控制器_差异化_1_alu_src , \单周期硬布线控制器_差异化_1_beq , \单周期硬布线控制器_差异化_1_bgtz ,
       \单周期硬布线控制器_差异化_1_bne , \单周期硬布线控制器_差异化_1_jal , \单周期硬布线控制器_差异化_1_jmp , \单周期硬布线控制器_差异化_1_jr ,
       \单周期硬布线控制器_差异化_1_lhu , \单周期硬布线控制器_差异化_1_memtoreg , \单周期硬布线控制器_差异化_1_memwrite ,
       \单周期硬布线控制器_差异化_1_regdst , \单周期硬布线控制器_差异化_1_regwrite , \单周期硬布线控制器_差异化_1_syscall ;
  wire [1:0] Forward1, Forward2, ForwardRD1, ForwardRD2, multiplexer_11_out, multiplexer_12_out;
  wire [3:0] id_ex_1_aluop_out, \单周期硬布线控制器_差异化_1_alu_op ;
  wire [4:0] EX_WriteReg_num, ID_ReadReg1_num, ID_ReadReg2_num, MEM_WriteReg_num, multiplexer_9_out,
       multiplexer_13_out, multiplexer_17_out, w_num;
  wire [5:0] Func, OP;
  wire [12:0] CNT_num;
  wire [15:0] \LoadUse次数 , multiplexer_20_out, \总周期数 , \插入气泡数 , \无条件分支数 , \条件分支成功数 ;
  wire [25:6] if_id_1_ir_out;
  wire [27:0] shifter_1_out;
  wire [31:0] adder_1_out, bit_extender_1_out, bit_extender_2_out, bit_extender_3_out, EX_IR,
       ex_mem_1_ir_out, ex_mem_1_pc_out, ID_IR, if_id_1_pc_out, IF_IR, imme, IR, MEM_AluOut, MEM_IR,
       Mem_MemData, mem_wb_1_ir_out, mem_wb_1_pc_out, mips_alu_1_result, \mips_regfile_下降沿_1_r1 ,
       \mips_regfile_下降沿_1_r2 , multiplexer_1_out, multiplexer_2_out, multiplexer_3_out, multiplexer_7_out,
       multiplexer_8_out, multiplexer_19_out, NewR1, NewR2, PC_4, PCBranch, R1, R2, ram_1_data, rom_1_data,
       shifter_2_out, WB_AluOut, WB_IR, WB_MemOut;

  Button \u_总复位  (.out(RST));
  Button _1 (.out(IR1));
  Button _2 (.out(IR2));
  Button _3 (.out(IR3));
  // Probe on \总周期数 
  // Probe on \总周期数 
  Button \u_继续运行  (.out(Go));
  LED #(.active("true")) led_1 (.in(W1));
  LED #(.active("true")) led_2 (.in(W2));
  LED #(.active("true")) led_3 (.in(W3));
  Hex_Digit_Display hex_digit_display_1 (.value(LedData[31:28]));  // open: dp
  // Probe on IF_PC[19:0]
  // Mips_Probe mips_probe_1: pin names not known; wires that end beside it: IF_IR
  Hex_Digit_Display hex_digit_display_2 (.value(LedData[23:20]));  // open: dp
  Hex_Digit_Display hex_digit_display_3 (.value(LedData[27:24]));  // open: dp
  // Probe on ID_PC[19:0]
  // Mips_Probe mips_probe_2: pin names not known; wires that end beside it: ID_IR
  and and_1 (and_1_out, equal, Beq);
  and and_2 (and_2_out, Bne, ~equal);  // AND_Gate
  or or_1 (jmp_flag, and_2_out, and_1_out);
  Multiplexer #(.select(1), .width(32), .disabled("Z"), .enable("false")) multiplexer_1 (
    .in0(adder_1_out), .in1(PCBranch), .out(multiplexer_1_out), .sel(jmp_flag));
  Shifter #(.width(28), .shift("ll")) shifter_1 (.in(IR[27:0]), .\dist (5'b00010), .out(shifter_1_out));
  Hex_Digit_Display hex_digit_display_4 (.value(LedData[19:16]));  // open: dp
  Hex_Digit_Display hex_digit_display_5 (.value(LedData[15:12]));  // open: dp
  Multiplexer #(.select(2), .width(32), .disabled("Z"), .enable("false")) multiplexer_2 (
    .in0(multiplexer_1_out), .in1(NewR1), .in2({PC_4[31:28], shifter_1_out}), .in3(NewR1),
    .out(multiplexer_2_out), .sel({JMP, JR}));
  Hex_Digit_Display hex_digit_display_6 (.value(LedData[7:4]));  // open: dp
  Hex_Digit_Display hex_digit_display_7 (.value(LedData[11:8]));  // open: dp
  Clock #(.highDuration(1), .lowDuration(1)) clock_1 (.out(CLK));
  // Probe on EX_PC[19:0]
  // Mips_Probe mips_probe_3: pin names not known; wires that end beside it: EX_IR
  Register #(.width(32), .trigger("rising"), .Select("low")) register_1 (
    .D(NewR2), .Q(LedData), .clk(LED), .clr(RST));  // open: en
  Comparator #(.width(32), .mode("twosComplement")) comparator_1 (
    .a(NewR1), .b({32{1'b0}}), .gt(comparator_1_gt));  // open: eq, lt
  and and_3 (BGTZ_flag, BGTZ, comparator_1_gt);
  Multiplexer #(.select(1), .width(32), .disabled("Z"), .enable("false")) multiplexer_3 (
    .in0(multiplexer_2_out), .in1(PCBranch), .out(multiplexer_3_out), .sel(BGTZ_flag));
  Hex_Digit_Display hex_digit_display_8 (.value(LedData[3:0]));  // open: dp
  and and_4 (and_4_out, ~load_use, multiplexer_4_out);  // AND_Gate
  Multiplexer #(.select(1), .width(1), .disabled("Z"), .enable("false")) multiplexer_4 (
    .in0(1'b1), .in1(Go), .out(multiplexer_4_out), .sel(halt));
  // Probe on \总周期数 
  // Probe on M_PC[19:0]
  // Mips_Probe mips_probe_4: pin names not known; wires that end beside it: MEM_IR
  Register #(.width(32), .trigger("rising"), .Select("low")) PC (
    .D(multiplexer_3_out), .en(and_4_out), .Q(IF_PC), .clk(CLK), .clr(RST));
  Counter #(.width(16), .max('hffff), .ongoal("wrap"), .trigger("rising"), .behavior("old")) counter_1 (
    .load(1'b0), .count(multiplexer_4_out), .Q(\总周期数 ), .clk(CLK), .clr(RST));  // open: D, carry, preset
  // Probe on \总周期数 
  // Probe on \无条件分支数 
  // Probe on \条件分支成功数 
  // Probe on \插入气泡数 
  // Probe on \LoadUse次数 
  Adder #(.width(32)) adder_1 (.a(IF_PC), .b(32'h4), .out(adder_1_out));  // open: cin, cout
  // Probe on IF_PC[11:0]
  // Probe on WB_PC[19:0]
  // Mips_Probe mips_probe_5: pin names not known; wires that end beside it: WB_IR
  // Probe on ID_PC[11:0]
  // Probe on EX_PC[11:0]
  ROM #(.addrWidth(10), .dataWidth(32), .Select("high")) rom_1 (.addr(IF_PC[11:2]), .data(rom_1_data));
  // Probe on M_PC[11:0]
  D_Flip_Flop #(.trigger("high"), .Pre_Clr_Positions("LEGACY"), .NegatePresetClear("false"), .enable("true"), .NewFFLayout("false")) d_ff_1 (.Q(d_ff_1_q));  // open: clk, D, Qn, preset, en, reset
  // Probe on 13'h377
  // Mips_Probe mips_probe_6: pin names not known; wires that end beside it: rom_1_data
  and and_5 (and_5_out, Write, ~load_use);  // AND_Gate
  or or_2 (or_2_out, BGTZ_flag, jmp_flag);
  // Probe on WB_PC[11:0]
  Comparator #(.width(13), .mode("twosComplement")) comparator_2 (
    .a(CNT_num), .b(13'h377), .eq(comparator_2_eq), .lt(comparator_2_lt));  // open: gt
  Clock #(.highDuration(1), .lowDuration(1)) clock_2 (.out(clock_2_out));
  IF_ID if_id_1 (
    .IR_in(rom_1_data), .OldPC_in(IF_PC), .PC_in(adder_1_out), .IR_out({OP, if_id_1_ir_out, Func}),
    .OldPC_out(ID_PC), .PC_out(if_id_1_pc_out), .\气泡高电平有效 (J), .\使能 (and_5_out), .Clk(CLK), .Clr(RST));  // open: PredJmp_in, PredJmp_out
  not not_1 (not_1_out, Go);
  nand nand_1 (nand_1_out, d_ff_1_q, comparator_2_eq);
  Counter #(.width(13), .max('h1fff), .ongoal("stay"), .trigger("rising"), .behavior("old")) counter_2 (
    .count(comparator_2_lt), .Q(CNT_num), .clk(clock_2_out));  // open: load, D, carry, clr, preset
  nand nand_2 (Write, not_1_out, halt);
  Counter #(.width(16), .max('hffff), .ongoal("wrap"), .trigger("rising"), .behavior("old")) counter_3 (
    .load(1'b0), .count(JMP), .Q(\无条件分支数 ), .clk(CLK), .clr(RST));  // open: D, carry, preset
  Counter #(.width(16), .max('hffff), .ongoal("wrap"), .trigger("rising"), .behavior("old")) counter_4 (
    .load(1'b0), .count(or_2_out), .Q(\条件分支成功数 ), .clk(CLK), .clr(RST));  // open: D, carry, preset
  or or_3 (J, or_2_out, JMP, JR);
  assign controlled_buffer_1_out = nand_1_out ? clock_2_out : 1'bz;  // Controlled_Buffer controlled_buffer_1
  Pull_Resistor #(.pull(1)) pull_resistor_1 (.node(controlled_buffer_1_out));
  assign bit_extender_1_out = {{16{1'b0}}, {if_id_1_ir_out[15:6], Func}};  // Bit_Extender bit_extender_1
  assign bit_extender_2_out = {{16{if_id_1_ir_out[15]}}, {if_id_1_ir_out[15:6], Func}};  // Bit_Extender bit_extender_2
  \单周期硬布线控制器_差异化  \u_单周期硬布线控制器_差异化_1  (
    .OP(OP), .Func(Func), .ALU_OP(\单周期硬布线控制器_差异化_1_alu_op ), .MemToReg(\单周期硬布线控制器_差异化_1_memtoreg ),
    .MemWrite(\单周期硬布线控制器_差异化_1_memwrite ), .ALU_SRC(\单周期硬布线控制器_差异化_1_alu_src ),
    .RegWrite(\单周期硬布线控制器_差异化_1_regwrite ), .SysCALL(\单周期硬布线控制器_差异化_1_syscall ), .SignedExt(SignedExt),
    .RegDst(\单周期硬布线控制器_差异化_1_regdst ), .Beq(\单周期硬布线控制器_差异化_1_beq ), .Bne(\单周期硬布线控制器_差异化_1_bne ),
    .JR(\单周期硬布线控制器_差异化_1_jr ), .JMP(\单周期硬布线控制器_差异化_1_jmp ), .JAL(\单周期硬布线控制器_差异化_1_jal ),
    .BGTZ(\单周期硬布线控制器_差异化_1_bgtz ), .LHU(\单周期硬布线控制器_差异化_1_lhu ));
  Multiplexer #(.select(1), .width(5), .disabled("Z"), .enable("false")) multiplexer_5 (
    .in0(if_id_1_ir_out[25:21]), .in1(5'b00010), .out(ID_ReadReg1_num), .sel(\单周期硬布线控制器_差异化_1_syscall ));
  Multiplexer #(.select(1), .width(5), .disabled("Z"), .enable("false")) multiplexer_6 (
    .in0(if_id_1_ir_out[20:16]), .in1(5'b00100), .out(ID_ReadReg2_num), .sel(\单周期硬布线控制器_差异化_1_syscall ));
  Multiplexer #(.select(1), .width(32), .disabled("Z"), .enable("false")) multiplexer_7 (
    .in0(bit_extender_1_out), .in1(bit_extender_2_out), .out(multiplexer_7_out), .sel(SignedExt));
  \MIPS_Regfile_下降沿  \mips_regfile_下降沿_1  (
    .Din(RDin), .Clk(CLK), .R1(\mips_regfile_下降沿_1_r1 ), .R2(\mips_regfile_下降沿_1_r2 ), .WE(RegWrite),
    .W_num(w_num), .R1_num(ID_ReadReg1_num), .R2_num(ID_ReadReg2_num));
  and and_6 (and_6_out, load_use, Write);
  \重定向控制逻辑  \u_重定向控制逻辑_1  (
    .OP(OP), .EX_WriteReg_num(EX_WriteReg_num), .EX_RegWrite(EX_RegWrite), .FUNC(Func),
    .MEM_WriteReg_num(MEM_WriteReg_num), .MEM_RegWrite(MEM_RegWrite), .EX_OP(IR[31:26]),
    .ID_R1_num(ID_ReadReg1_num), .MemToReg(MemToReg), .ID_R2_num(ID_ReadReg2_num), .load_use(load_use),
    .Forward1(Forward1), .Forward2(Forward2));
  Counter #(.width(16), .max('hffff), .ongoal("wrap"), .trigger("rising"), .behavior("old")) counter_5 (
    .load(1'b0), .count(and_6_out), .Q(\LoadUse次数 ), .clk(CLK), .clr(RST));  // open: D, carry, preset
  or or_4 (or_4_out, J, load_use);
  ID_EX id_ex_1 (
    .Beq_in(\单周期硬布线控制器_差异化_1_beq ), .Bne_in(\单周期硬布线控制器_差异化_1_bne ), .MemToReg_in(\单周期硬布线控制器_差异化_1_memtoreg ),
    .MemWrite_in(\单周期硬布线控制器_差异化_1_memwrite ), .AluSrcB_in(\单周期硬布线控制器_差异化_1_alu_src ),
    .RegWrite_in(\单周期硬布线控制器_差异化_1_regwrite ), .JAL_in(\单周期硬布线控制器_差异化_1_jal ),
    .RegDst_in(\单周期硬布线控制器_差异化_1_regdst ), .JMP_in(\单周期硬布线控制器_差异化_1_jmp ), .JR_in(\单周期硬布线控制器_差异化_1_jr ),
    .SignedExt_in(SignedExt), .AluOP_in(\单周期硬布线控制器_差异化_1_alu_op ), .IR_in({OP, if_id_1_ir_out, Func}),
    .OldPC_in(ID_PC), .PC_in(if_id_1_pc_out), .R1_in(\mips_regfile_下降沿_1_r1 ),
    .R2_in(\mips_regfile_下降沿_1_r2 ), .imm_in(multiplexer_7_out), .Beq_out(Beq), .Bne_out(Bne),
    .MemToReg_out(id_ex_1_memtoreg_out), .MemWrite_out(id_ex_1_memwrite_out), .AluSrcB_out(AluSrcB),
    .RegWrite_out(EX_RegWrite), .JAL_out(id_ex_1_jal_out), .RegDst_out(id_ex_1_regdst_out), .JMP_out(JMP),
    .JR_out(JR), .AluOP_out(id_ex_1_aluop_out), .IR_out(IR), .OldPC_out(EX_PC), .PC_out(PC_4), .R1_out(R1),
    .R2_out(R2), .imm_out(imme), .\气泡高电平有效 (or_4_out), .\使能 (Write), .Clk(CLK), .Clr(RST),
    .Syscall_in(\单周期硬布线控制器_差异化_1_syscall ), .Syscall_out(Syscall), .BGTZ(\单周期硬布线控制器_差异化_1_bgtz ),
    .BGTZ_2(BGTZ), .LHU(\单周期硬布线控制器_差异化_1_lhu ), .LHU_2(id_ex_1_lhu_2));  // open: SignedExt_out, PredJmp_in_Eret_in, PredJmp_out_Eret_in
  Shifter #(.width(32), .shift("ll")) shifter_2 (.in(imme), .\dist (5'b00010), .out(shifter_2_out));
  Multiplexer #(.select(1), .width(32), .disabled("Z"), .enable("false")) multiplexer_8 (
    .in0(NewR2), .in1(imme), .out(multiplexer_8_out), .sel(AluSrcB));
  Multiplexer #(.select(1), .width(5), .disabled("Z"), .enable("false")) multiplexer_9 (
    .in0(IR[20:16]), .in1(IR[15:11]), .out(multiplexer_9_out), .sel(id_ex_1_regdst_out));
  Multiplexer #(.select(1), .width(5), .disabled("Z"), .enable("false")) multiplexer_10 (
    .in0(multiplexer_9_out), .in1({5{1'b1}}), .out(EX_WriteReg_num), .sel(id_ex_1_jal_out));
  Adder #(.width(32)) adder_2 (.a(shifter_2_out), .b(PC_4), .out(PCBranch));  // open: cin, cout
  or or_5 (or_5_out, load_use, J);
  MIPS_ALU mips_alu_1 (
    .X(NewR1), .Y(multiplexer_8_out), .AluOP(id_ex_1_aluop_out), .Equal(equal), .Result(mips_alu_1_result),
    .shamt(IR[10:6]));  // open: Result_2
  Multiplexer #(.select(1), .width(2), .disabled("Z"), .enable("false")) multiplexer_11 (
    .in0(Forward1), .in1(2'b00), .out(multiplexer_11_out), .sel(or_5_out));
  Multiplexer #(.select(1), .width(2), .disabled("Z"), .enable("false")) multiplexer_12 (
    .in0(Forward2), .in1(2'b00), .out(multiplexer_12_out), .sel(or_5_out));
  Register #(.width(2), .trigger("rising"), .Select("low")) register_2 (
    .D(multiplexer_11_out), .en(Write), .Q(ForwardRD1), .clk(CLK), .clr(RST));
  Register #(.width(2), .trigger("rising"), .Select("low")) register_3 (
    .D(multiplexer_12_out), .en(Write), .Q(ForwardRD2), .clk(CLK), .clr(RST));
  EX_MEM ex_mem_1 (
    .Syscall_in(Syscall), .MemToReg_in(id_ex_1_memtoreg_out), .MemWrite_in(id_ex_1_memwrite_out),
    .RegWrite_in(EX_RegWrite), .JAL_in(id_ex_1_jal_out), .RegDst_in(id_ex_1_regdst_out), .equal_in(equal),
    .IR_in(IR), .OldPC_in(EX_PC), .PC_in(PC_4), .AluOut_in(mips_alu_1_result), .R2_in(NewR2),
    .Syscall_out(ex_mem_1_syscall_out), .MemToReg_out(MemToReg), .MemWrite_out(MemWrite),
    .RegWrite_out(MEM_RegWrite), .JAL_out(ex_mem_1_jal_out), .RegDst_out(ex_mem_1_regdst_out),
    .equal_out(ex_mem_1_equal_out), .IR_out(ex_mem_1_ir_out), .OldPC_out(M_PC), .PC_out(ex_mem_1_pc_out),
    .AluOut_out(MEM_AluOut), .R2_out(MDin), .\气泡高电平有效 (1'b0), .\使能 (Write), .Clk(CLK), .Clr(RST),
    .LHU_2(ex_mem_1_lhu_2), .LHU(id_ex_1_lhu_2), .pause_in(pause), .pause_out(ex_mem_1_pause_out));  // open: Eret_in, Eret_in_2
  Multiplexer #(.select(1), .width(5), .disabled("Z"), .enable("false")) multiplexer_13 (
    .in0(ex_mem_1_ir_out[20:16]), .in1(ex_mem_1_ir_out[15:11]), .out(multiplexer_13_out),
    .sel(ex_mem_1_regdst_out));
  Multiplexer #(.select(2), .width(32), .disabled("Z"), .enable("false")) multiplexer_14 (
    .in0(R1), .in1(MEM_AluOut), .in2(WB_AluOut), .in3(Mem_MemData), .out(NewR1), .sel(ForwardRD1));
  Multiplexer #(.select(2), .width(32), .disabled("Z"), .enable("false")) multiplexer_15 (
    .in0(R2), .in1(MEM_AluOut), .in2(WB_AluOut), .in3(Mem_MemData), .out(NewR2), .sel(ForwardRD2));
  Multiplexer #(.select(1), .width(5), .disabled("Z"), .enable("false")) multiplexer_16 (
    .in0(multiplexer_13_out), .in1({5{1'b1}}), .out(MEM_WriteReg_num), .sel(ex_mem_1_jal_out));
  RAM #(.addrWidth(10), .dataWidth(32), .bus("separate"), .Select("high")) ram_1 (
    .addr(MEM_AluOut[11:2]), .din(MDin), .data(ram_1_data), .str(MemWrite), .clk(CLK), .clr(RST));  // open: sel, ld
  MEM_WB mem_wb_1 (
    .Syscall_in(ex_mem_1_syscall_out), .MemToReg_in(MemToReg), .MemWrite_in(MemWrite),
    .RegWrite_in(MEM_RegWrite), .JAL_in(ex_mem_1_jal_out), .RegDst_in(ex_mem_1_regdst_out),
    .equal_in(ex_mem_1_equal_out), .IR_in(ex_mem_1_ir_out), .OldPC_in(M_PC), .PC_in(ex_mem_1_pc_out),
    .AluOut_in(MEM_AluOut), .MemOut_in(ram_1_data), .MemToReg_out(mem_wb_1_memtoreg_out),
    .RegWrite_out(RegWrite), .JAL_out(mem_wb_1_jal_out), .RegDst_out(RegDst), .IR_out(mem_wb_1_ir_out),
    .OldPC_out(WB_PC), .PC_out(mem_wb_1_pc_out), .AluOut_out(WB_AluOut), .MemOut_out(WB_MemOut),
    .\气泡高电平有效 (1'b0), .\使能 (Write), .Clk(CLK), .Clr(RST), .LHU_2(LHU), .LHU(ex_mem_1_lhu_2),
    .pause_in(ex_mem_1_pause_out), .pause_out(halt));  // open: Syscall_out, MemWrite_out, equal_out, Eret_in, Eret_out
  Comparator #(.width(32), .mode("twosComplement")) comparator_3 (.a(NewR1), .b(32'h22), .eq(V034));  // open: gt, lt
  Multiplexer #(.select(1), .width(5), .disabled("Z"), .enable("false")) multiplexer_17 (
    .in0(mem_wb_1_ir_out[20:16]), .in1(mem_wb_1_ir_out[15:11]), .out(multiplexer_17_out), .sel(RegDst));
  Multiplexer #(.select(1), .width(5), .disabled("Z"), .enable("false")) multiplexer_18 (
    .in0(multiplexer_17_out), .in1({5{1'b1}}), .out(w_num), .sel(mem_wb_1_jal_out));
  and and_7 (pause, ~V034, Syscall);  // AND_Gate
  and and_8 (LED, V034, Syscall);
  Multiplexer #(.select(1), .width(32), .disabled("Z"), .enable("false")) multiplexer_19 (
    .in0(WB_AluOut), .in1(Mem_MemData), .out(multiplexer_19_out), .sel(mem_wb_1_memtoreg_out));
  Multiplexer #(.select(1), .width(16), .disabled("Z"), .enable("false")) multiplexer_20 (
    .in0(WB_MemOut[15:0]), .in1(WB_MemOut[31:16]), .out(multiplexer_20_out), .sel(WB_AluOut[1]));
  assign bit_extender_3_out = {{16{1'b0}}, multiplexer_20_out};  // Bit_Extender bit_extender_3
  Multiplexer #(.select(1), .width(32), .disabled("Z"), .enable("false")) multiplexer_21 (
    .in0(multiplexer_19_out), .in1(mem_wb_1_pc_out), .out(RDin), .sel(mem_wb_1_jal_out));
  Multiplexer #(.select(1), .width(32), .disabled("Z"), .enable("false")) multiplexer_22 (
    .in0(WB_MemOut), .in1(bit_extender_3_out), .out(Mem_MemData), .sel(LHU));

  // Other names for the same wires on the sheet: MEM_PC[31:0] = M_PC; PC[31:0] = IF_PC

  // Notes on the sheet:
  //   中断源
  //   时空图监测，可删除
  //   中断等待指示
  //   数码管输出
  //   指令存储器
  //   PC+4
  //   控制位
  //   contents of rom_1 (hex, n*v repeats v):
  //   20110001 8000c05 20110001 20120002 20130003 8000c09 20110001 20120002 20130003 8000c0d 20110001
  //   20120002 20130003 8000c11 20110001 20120002 20130003 c000cb8 20100001 20110001 118fc0 112020
  //   20020022 c 118882 12200001 8000c15 112020 20020022 c 20110001 118880 112020 20020022 c 12200001
  //   8000c1f 20110001 118fc0 112020 20020022 c 1188c3 112020 20020022 c 118903 112020 20020022 c 118903
  //   112020 20020022 c 118903 112020 20020022 c 118903 112020 20020022 c 118903 112020 20020022 c 118903
  //   112020 20020022 c 118903 112020 20020022 c 20100001 109fc0 139fc3 8021 2012000c 24160003 26100001
  //   3210000f 20080008 20090001 139900 2709825 132020 20020022 c 1094022 1500fff9 22100001 2018000f
  //   2188024 108700 20080008 20090001 139902 2709825 132021 20020022 c 1094022 1500fff9 108702 2c9b022
  //   12c00001 8000c50 4020 1084027 84400 3508ffff 82021 20020022 c 2010ffff 20110000 ae300000 22100001
  //   22310004 ae300000 22100001 22310004 ae300000 22100001 22310004 ae300000 22100001 22310004 ae300000
  //   22100001 22310004 ae300000 22100001 22310004 ae300000 22100001 22310004 ae300000 22100001 22310004
  //   ae300000 22100001 22310004 ae300000 22100001 22310004 ae300000 22100001 22310004 ae300000 22100001
  //   22310004 ae300000 22100001 22310004 ae300000 22100001 22310004 ae300000 22100001 22310004 ae300000
  //   22100001 22310004 22100001 8020 2011003c 8e130000 8e340000 274402a 11000002 ae330000 ae140000
  //   2231fffc 1611fff8 102020 20020022 c 22100004 2011003c 1611fff2 20020032 c 20100000 22100001 102020
  //   20020022 c 22100002 102020 20020022 c 22100003 102020 20020022 c 22100004 102020 20020022 c 22100005
  //   102020 20020022 c 22100006 102020 20020022 c 22100007 102020 20020022 c 22100008 102020 20020022
  //   20020022 c 3e00008
  //   流水调试日志用
  //   暂停节拍，不能为0
  //   戳工具置1进入计数暂停模式，ctrl+k时钟自动运行到对应节拍暂停
  //   ctrl+k关闭时钟连续运行，将控制位置零，进入单步调试模式调试
  //   指令字
  //   可计数暂停的时钟源
  //   OP
  //   Func
  //   rs
  //   rt
  //   rd
  //   JMP
  //   JR
  //   OP
  //   Func
  //   Beq
  //   Bne
  //   MemToReg
  //   MemWrite
  //   AluOP
  //   AluSrcB
  //   RegWrite
  //   JAL
  //   RegDst
  //   Syscall
  //   为方便自动评测，需要输出流水线各段保存的PC值，注意是PC不是PC+4，另外ID段寄存器写入信息，Mem段内存写入信息也要输出
  //   PCBranch
  //   rt
  //   rd
endmodule

module \单周期MIPS_单级中断  (
  input  IR1,
  input  IR2,
  input  IR3,
  output RegWrite,
  output MemWrite,
  output [31:0] PC,
  output [31:0] IR,
  output [31:0] RDin,
  output [31:0] MDin,
  output [31:0] LedData
);

  wire AluSrcB, and_1_out, and_2_out, and_3_out, and_4_out, and_5_out, and_8_out, Beq, Bne, CLK, clock_2_out,
       clock_3_out, clock_4_out, comparator_1_eq, comparator_3_eq, comparator_4_eq, comparator_5_eq,
       comparator_6_eq, comparator_7_eq, controlled_inverter_1_out, controlled_inverter_2_out,
       controlled_inverter_3_out, d_ff_1_q, d_ff_2_q, d_ff_3_q, Eret, Go, halt, IE, Interrupt, IR1_2_q,
       IR1_3_q, IR1_q, IR1_t, IR1reset, IR2_t, IR2reset, IR3_t, IR3reset, IRA, IRB, IRC, JAL, JMP, JR,
       MemToReg, mips_alu_1_equal, multiplexer_5_out, not_1_out, or_1_out, or_2_out, or_9_out, or_10_out,
       or_11_out, or_12_out, priority_encoder_1_gs, RegDst, SignedExt, Syscall, W1, W2, W3;
  wire [1:0] IRnumber, register_2_q;
  wire [3:0] mips_probe_1_p5;
  wire [4:0] multiplexer_6_out, multiplexer_7_out, multiplexer_8_out, multiplexer_9_out;
  wire [15:0] \总周期数 ;
  wire [27:0] adder_1_out;
  wire [31:0] adder_1_out_2, adder_2_out, bit_extender_1_out, bit_extender_2_out, EPC, IRaddress,
       mips_alu_1_result, multiplexer_1_out, multiplexer_3_out, multiplexer_4_out, multiplexer_11_out,
       multiplexer_12_out, multiplexer_14_out, PCnxt, R1, ram_1_data, shifter_2_out;

  Clock #(.highDuration(1), .lowDuration(1)) clock_1 (.out(CLK));
  Button _1 (.out(IRA));
  Button _2 (.out(IRB));
  Button _3 (.out(IRC));
  Button \u_继续运行  (.out(Go));
  LED #(.active("true")) led_1 (.in(W1));
  LED #(.active("true")) led_2 (.in(W2));
  LED #(.active("true")) led_3 (.in(W3));
  and and_1 (and_1_out, mips_alu_1_equal, Beq);
  and and_2 (and_2_out, Bne, ~mips_alu_1_equal);  // AND_Gate
  or or_1 (or_1_out, and_2_out, and_1_out);
  Multiplexer #(.select(1), .width(32), .disabled("Z"), .enable("false")) multiplexer_1 (
    .in0({adder_1_out_2[31:28], adder_1_out}), .in1(adder_2_out), .out(multiplexer_1_out), .sel(or_1_out));
  Comparator #(.width(16), .mode("twosComplement")) comparator_1 (
    .a(\总周期数 ), .b({16{1'b0}}), .eq(comparator_1_eq));  // open: gt, lt
  Hex_Digit_Display hex_digit_display_1 (.value(LedData[31:28]));  // open: dp
  Multiplexer #(.select(2), .width(32), .disabled("Z"), .enable("false")) multiplexer_2 (
    .in0(multiplexer_1_out), .in1(adder_1_out_2), .in2(adder_1_out_2), .in3(R1), .out(PCnxt), .sel({JMP, JR}));
  not not_1 (not_1_out, Interrupt);
  or or_2 (or_2_out, Interrupt, Eret, comparator_1_eq);
  Comparator #(.width(32), .mode("twosComplement")) comparator_2 (.a(IR), .b(32'h42000018), .eq(Eret));  // open: gt, lt
  Hex_Digit_Display hex_digit_display_2 (.value(LedData[27:24]));  // open: dp
  Hex_Digit_Display hex_digit_display_3 (.value(LedData[23:20]));  // open: dp
  Register #(.width(1), .trigger("rising"), .Select("low")) register_1 (
    .D(not_1_out), .en(or_2_out), .Q(IE), .clk(CLK));  // open: clr
  Hex_Digit_Display hex_digit_display_4 (.value(LedData[19:16]));  // open: dp
  Hex_Digit_Display hex_digit_display_5 (.value(LedData[15:12]));  // open: dp
  Multiplexer #(.select(1), .width(32), .disabled("Z"), .enable("false")) multiplexer_3 (
    .in0(PCnxt), .in1(IRaddress), .out(multiplexer_3_out), .sel(Interrupt));
  Multiplexer #(.select(1), .width(32), .disabled("Z"), .enable("false")) multiplexer_4 (
    .in0(multiplexer_3_out), .in1(EPC), .out(multiplexer_4_out), .sel(Eret));
  Hex_Digit_Display hex_digit_display_6 (.value(LedData[11:8]));  // open: dp
  Hex_Digit_Display hex_digit_display_7 (.value(LedData[7:4]));  // open: dp
  // Probe on \总周期数 
  Multiplexer #(.select(1), .width(1), .disabled("Z"), .enable("false")) multiplexer_5 (
    .in0(1'b1), .in1(Go), .out(multiplexer_5_out), .sel(halt));
  Hex_Digit_Display hex_digit_display_8 (.value(LedData[3:0]));  // open: dp
  Register #(.width(32), .trigger("rising"), .Select("low")) u_PC (
    .D(multiplexer_4_out), .en(multiplexer_5_out), .Q(PC), .clk(CLK));  // open: clr
  Counter #(.width(16), .max('hffff), .ongoal("wrap"), .trigger("rising"), .behavior("old")) counter_1 (
    .load(1'b0), .count(multiplexer_5_out), .Q(\总周期数 ), .clk(CLK));  // open: D, carry, clr, preset
  Demultiplexer #(.select(2), .width(1), .tristate("false"), .disabled("Z"), .enable("false")) demultiplexer_1 (
    .out1(IR1reset), .out2(IR2reset), .out3(IR3reset), .in(Eret), .sel(register_2_q));  // open: out0
  Register #(.width(2), .trigger("rising"), .Select("low")) register_2 (
    .D(IRnumber), .en(Interrupt), .Q(register_2_q), .clk(CLK));  // open: clr
  Register #(.width(32), .trigger("rising"), .Select("low")) u_EPC (
    .D(PCnxt), .en(Interrupt), .Q(EPC), .clk(CLK));  // open: clr
  Adder #(.width(32)) adder_1 (.a(PC), .b(32'h4), .out({adder_1_out_2[31:28], adder_1_out}));  // open: cin, cout
  or or_3 (IR1_t, IR1, IRA);
  or or_4 (IR2_t, IR2, IRB);
  // Mips_Probe mips_probe_1: pin names not known; wires that end beside it: IR, Bne, MemToReg, MemWrite, mips_probe_1_p5
  ROM #(.addrWidth(10), .dataWidth(32), .Select("high")) rom_1 (.addr(PC[11:2]), .data(IR));
  Clock #(.highDuration(1), .lowDuration(1)) clock_2 (.out(clock_2_out));
  LED #(.active("true")) \_1号中断等待指示灯  (.in(W1));
  Clock #(.highDuration(1), .lowDuration(1)) clock_3 (.out(clock_3_out));
  LED #(.active("true")) \_2号中断等待指示灯  (.in(W2));
  Clock #(.highDuration(1), .lowDuration(1)) clock_4 (.out(clock_4_out));
  LED #(.active("true")) \_3号中断等待指示灯  (.in(W3));
  D_Flip_Flop #(.trigger("rising"), .Pre_Clr_Positions("LEGACY"), .NegatePresetClear("false"), .enable("true"), .NewFFLayout("false")) d_ff_1 (
    .clk(IR1_t), .D(1'b1), .Q(d_ff_1_q), .reset(IR1_q));  // open: Qn, preset, en
  or or_5 (W1, IR1_q, d_ff_1_q);
  D_Flip_Flop #(.trigger("rising"), .Pre_Clr_Positions("LEGACY"), .NegatePresetClear("false"), .enable("true"), .NewFFLayout("false")) d_ff_2 (
    .clk(IR2_t), .D(1'b1), .Q(d_ff_2_q), .reset(IR1_2_q));  // open: Qn, preset, en
  or or_6 (W2, IR1_2_q, d_ff_2_q);
  D_Flip_Flop #(.trigger("rising"), .Pre_Clr_Positions("LEGACY"), .NegatePresetClear("false"), .enable("true"), .NewFFLayout("false")) d_ff_3 (
    .clk(IR3_t), .D(1'b1), .Q(d_ff_3_q), .reset(IR1_3_q));  // open: Qn, preset, en
  or or_7 (W3, IR1_3_q, d_ff_3_q);
  or or_8 (IR3_t, IR3, IRC);
  \单周期硬布线控制器  \u_单周期硬布线控制器_1  (
    .Func(IR[5:0]), .OP(IR[31:26]), .ALU_OP(mips_probe_1_p5), .MemToReg(MemToReg), .MemWrite(MemWrite),
    .ALU_SRC(AluSrcB), .RegWrite(RegWrite), .SysCALL(Syscall), .SignedExt(SignedExt), .RegDst(RegDst),
    .JR(JR), .JMP(JMP), .Beq(Beq), .JAL(JAL), .Bne(Bne));
  Multiplexer #(.select(1), .width(5), .disabled("Z"), .enable("false")) multiplexer_6 (
    .in0(IR[25:21]), .in1(5'b00010), .out(multiplexer_6_out), .sel(Syscall));
  Multiplexer #(.select(1), .width(5), .disabled("Z"), .enable("false")) multiplexer_7 (
    .in0(IR[20:16]), .in1(5'b00100), .out(multiplexer_7_out), .sel(Syscall));
  Multiplexer #(.select(1), .width(5), .disabled("Z"), .enable("false")) multiplexer_8 (
    .in0(IR[20:16]), .in1(IR[15:11]), .out(multiplexer_8_out), .sel(RegDst));
  assign bit_extender_1_out = {{16{1'b0}}, IR[15:0]};  // Bit_Extender bit_extender_1
  assign bit_extender_2_out = {{16{IR[15]}}, IR[15:0]};  // Bit_Extender bit_extender_2
  Shifter #(.width(28), .shift("ll")) shifter_1 (.in(IR[27:0]), .\dist (5'b00010), .out(adder_1_out_2[27:0]));
  or or_9 (or_9_out, d_ff_1_q, IR1_q);
  or or_10 (or_10_out, d_ff_2_q, IR1_2_q);
  or or_11 (or_11_out, d_ff_3_q, IR1_3_q);
  Multiplexer #(.select(1), .width(5), .disabled("Z"), .enable("false")) multiplexer_9 (
    .in0(multiplexer_8_out), .in1({5{1'b1}}), .out(multiplexer_9_out), .sel(JAL));
  Multiplexer #(.select(1), .width(32), .disabled("Z"), .enable("false")) multiplexer_10 (
    .in0(multiplexer_14_out), .in1({adder_1_out_2[31:28], adder_1_out}), .out(RDin), .sel(JAL));
  Multiplexer #(.select(1), .width(32), .disabled("Z"), .enable("false")) multiplexer_11 (
    .in0(bit_extender_1_out), .in1(bit_extender_2_out), .out(multiplexer_11_out), .sel(SignedExt));
  and and_3 (and_3_out, or_9_out, ~IR1reset);  // AND_Gate
  Pull_Resistor #(.pull(0)) pull_resistor_1 (.node(IR1reset));
  and and_4 (and_4_out, or_10_out, ~IR2reset);  // AND_Gate
  Pull_Resistor #(.pull(0)) pull_resistor_2 (.node(IR2reset));
  and and_5 (and_5_out, or_11_out, ~IR3reset);  // AND_Gate
  Pull_Resistor #(.pull(0)) pull_resistor_3 (.node(IR3reset));
  MIPS_Regifile mips_regifile_1 (
    .Din(RDin), .Clk(CLK), .R1(R1), .R2(MDin), .WE(RegWrite), .W_num(multiplexer_9_out),
    .R1_num(multiplexer_6_out), .R2_num(multiplexer_7_out));
  D_Flip_Flop #(.trigger("rising"), .Pre_Clr_Positions("LEGACY"), .NegatePresetClear("false"), .enable("true"), .NewFFLayout("false")) u_IR1 (
    .clk(clock_2_out), .D(and_3_out), .Q(IR1_q));  // open: Qn, preset, en, reset
  D_Flip_Flop #(.trigger("rising"), .Pre_Clr_Positions("LEGACY"), .NegatePresetClear("false"), .enable("true"), .NewFFLayout("false")) IR1_2 (
    .clk(clock_3_out), .D(and_4_out), .Q(IR1_2_q));  // open: Qn, preset, en, reset
  D_Flip_Flop #(.trigger("rising"), .Pre_Clr_Positions("LEGACY"), .NegatePresetClear("false"), .enable("true"), .NewFFLayout("false")) IR1_3 (
    .clk(clock_4_out), .D(and_5_out), .Q(IR1_3_q));  // open: Qn, preset, en, reset
  Multiplexer #(.select(1), .width(32), .disabled("Z"), .enable("false")) multiplexer_12 (
    .in0(MDin), .in1(multiplexer_11_out), .out(multiplexer_12_out), .sel(AluSrcB));
  Shifter #(.width(32), .shift("ll")) shifter_2 (.in(multiplexer_11_out), .\dist (5'b00010), .out(shifter_2_out));
  MIPS_ALU mips_alu_1 (
    .X(R1), .Y(multiplexer_12_out), .AluOP(mips_probe_1_p5), .Equal(mips_alu_1_equal),
    .Result(mips_alu_1_result), .shamt(IR[10:6]));  // open: Result_2
  Priority_Encoder #(.select(2), .disabled("Z")) priority_encoder_1 (
    .in1(IR1_q), .in2(IR1_2_q), .in3(IR1_3_q), .out(IRnumber), .gs(priority_encoder_1_gs));  // open: in0, en_out, en_in
  Adder #(.width(32)) adder_2 (
    .a(shifter_2_out), .b({adder_1_out_2[31:28], adder_1_out}), .out(adder_2_out));  // open: cin, cout
  Multiplexer #(.select(2), .width(32), .disabled("Z"), .enable("false")) multiplexer_13 (
    .in1(32'h30ac), .in2(32'h3150), .in3(32'h31f4), .out(IRaddress), .sel(IRnumber));  // open: in0
  and and_6 (Interrupt, priority_encoder_1_gs, IE);
  Comparator #(.width(32), .mode("twosComplement")) comparator_3 (
    .a(R1), .b(32'h22), .eq(comparator_3_eq));  // open: gt, lt
  RAM #(.addrWidth(10), .dataWidth(32), .bus("separate"), .Select("high")) ram_1 (
    .addr(mips_alu_1_result[9:0]), .din(MDin), .data(ram_1_data), .str(MemWrite), .clk(CLK));  // open: sel, ld, clr
  and and_7 (halt, ~comparator_3_eq, Syscall);  // AND_Gate
  and and_8 (and_8_out, comparator_3_eq, Syscall);
  Register #(.width(32), .trigger("rising"), .Select("low")) register_3 (
    .D(MDin), .en(and_8_out), .Q(LedData), .clk(CLK));  // open: clr
  Multiplexer #(.select(1), .width(32), .disabled("Z"), .enable("false")) multiplexer_14 (
    .in0(mips_alu_1_result), .in1(ram_1_data), .out(multiplexer_14_out), .sel(MemToReg));
  Comparator #(.width(16), .mode("twosComplement")) comparator_4 (
    .a(16'h23b), .b(\总周期数 ), .eq(comparator_4_eq));  // open: gt, lt
  Comparator #(.width(16), .mode("twosComplement")) comparator_5 (
    .a(\总周期数 ), .b(16'h1), .eq(comparator_5_eq));  // open: gt, lt
  Comparator #(.width(16), .mode("twosComplement")) comparator_6 (
    .a(\总周期数 ), .b(16'h4), .eq(comparator_6_eq));  // open: gt, lt
  Comparator #(.width(16), .mode("twosComplement")) comparator_7 (
    .a(\总周期数 ), .b(16'h7), .eq(comparator_7_eq));  // open: gt, lt
  or or_12 (or_12_out, comparator_4_eq, comparator_5_eq);
  assign controlled_inverter_1_out = or_12_out ? ~CLK : 1'bz;  // Controlled_Inverter controlled_inverter_1
  assign controlled_inverter_2_out = comparator_6_eq ? ~CLK : 1'bz;  // Controlled_Inverter controlled_inverter_2
  assign controlled_inverter_3_out = comparator_7_eq ? ~CLK : 1'bz;  // Controlled_Inverter controlled_inverter_3
  Pull_Resistor #(.pull(0)) pull_resistor_4 (.node(controlled_inverter_1_out));
  Pull_Resistor #(.pull(0)) pull_resistor_5 (.node(controlled_inverter_2_out));
  Pull_Resistor #(.pull(0)) pull_resistor_6 (.node(controlled_inverter_3_out));

  // Other names for the same wires on the sheet: R2[31:0] = MDin

  // Notes on the sheet:
  //   中断源
  //   中断等待指示
  //   总复位信号应将除ROM以外所有存储组件全部清零
  //   IE
  //   数码管输出
  //   数码管输出应该用寄存器锁存，否则显示数据只能一闪而过
  //   PC+4
  //   指令存储器
  //   指令字
  //   contents of rom_1 (hex, n*v repeats v):
  //   201d07d0 20100001 109fc0 139fc3 8021 2012000c 24160008 26100001 3210000f 20080008 20090001 139900
  //   2709825 132020 20020022 c 1094022 1500fff9 22100001 2018000f 2188024 108700 20080008 20090001 139902
  //   2709825 132021 20020022 c 1094022 1500fff9 108702 2c9b022 12c00001 8000c07 4020 1084027 84400
  //   3508ffff 82021 20020022 c 8000c01 afa20000 23bd0004 afa40000 23bd0004 afb00000 23bd0004 afb30000
  //   23bd0004 afb40000 23bd0004 afb50000 23bd0004 afb60000 23bd0004 20160001 20140003 20150001 168020
  //   108100 2149825 132020 20020022 c 1600fffa 295a022 1680fff7 23bdfffc 8fb60000 23bdfffc 8fb50000
  //   23bdfffc 8fb40000 23bdfffc 8fb30000 23bdfffc 8fb00000 23bdfffc 8fa40000 23bdfffc 8fa20000 42000018
  //   afa20000 23bd0004 afa40000 23bd0004 afb00000 23bd0004 afb30000 23bd0004 afb40000 23bd0004 afb50000
  //   23bd0004 afb60000 23bd0004 20160002 20140003 20150001 168020 108100 2149825 132020 20020022 c
  //   1600fffa 295a022 1680fff7 23bdfffc 8fb60000 23bdfffc 8fb50000 23bdfffc 8fb40000 23bdfffc 8fb30000
  //   23bdfffc 8fb00000 23bdfffc 8fa40000 23bdfffc 8fa20000 42000018 afa20000 23bd0004 afa40000 23bd0004
  //   afb00000 23bd0004 afb30000 23bd0004 afb40000 23bd0004 afb50000 23bd0004 afb60000 23bd0004 20160003
  //   20140003 20150001 168020 108100 2149825 132020 20020022 c 1600fffa 295a022 1680fff7 23bdfffc
  //   8fb60000 23bdfffc 8fb50000 23bdfffc 8fb40000 23bdfffc 8fb30000 23bdfffc 8fb00000 23bdfffc 8fa40000
  //   23bdfffc 8fa20000 42000018
  //   OP
  //   Func
  //   rs
  //   rt
  //   rd
  //   JMP
  //   JR
  //   OP
  //   Func
  //   Syscall
  //   Beq
  //   Bne
  //   MemToReg
  //   MemWrite
  //   AluOP
  //   AluSrcB
  //   RegWrite
  //   JAL
  //   RegDst
  //   Reset 
  //   Reset 
  //   Reset 
  //   为方便自动评测，需要输出PC，IR，寄存器堆写如数据RDin
  //   RAM写使能MemWrite、RAM写入数据MDin等信号
  //   PCBranch
  //   单级中断测试信号模拟器
endmodule

module \中断按键参考电路  (
  input  \同步清零信号 ,
  output \与中断屏蔽位与 
);

  wire \_1号中断_out , and_1_out, clock_1_out, d_ff_1_q, or_1_out, or_2_out;

  Clock #(.highDuration(1), .lowDuration(1)) clock_1 (.out(clock_1_out));
  Button \_1号中断  (.out(\_1号中断_out ));
  or or_1 (or_1_out, \与中断屏蔽位与 , d_ff_1_q);
  LED #(.active("true")) \_1号中断等待指示灯  (.in(or_1_out));
  D_Flip_Flop #(.trigger("rising"), .Pre_Clr_Positions("LEGACY"), .NegatePresetClear("false"), .enable("true"), .NewFFLayout("false")) d_ff_1 (
    .clk(\_1号中断_out ), .D(1'b1), .Q(d_ff_1_q), .reset(\与中断屏蔽位与 ));  // open: Qn, preset, en
  or or_2 (or_2_out, d_ff_1_q, \与中断屏蔽位与 );
  and and_1 (and_1_out, or_2_out, ~\同步清零信号 );  // AND_Gate
  D_Flip_Flop #(.trigger("rising"), .Pre_Clr_Positions("LEGACY"), .NegatePresetClear("false"), .enable("true"), .NewFFLayout("false")) IR1 (
    .clk(clock_1_out), .D(and_1_out), .Q(\与中断屏蔽位与 ));  // open: Qn, preset, en, reset
  \单周期硬布线控制器  \u_单周期硬布线控制器_1  ();  // open: Func, OP, ALU_OP, MemToReg, MemWrite, ALU_SRC, RegWrite, SysCALL, SignedExt, RegDst, JR, JMP, Beq, JAL, Bne

  // Notes on the sheet:
  //   中断信号采样参考电路
  //   Reset 
endmodule

module \单周期MIPS_多级中断  (
  input  IR1,
  input  IR2,
  input  IR3,
  output RegWrite,
  output MemWrite,
  output [31:0] PC,
  output [31:0] IR,
  output [31:0] RDin,
  output [31:0] MDin,
  output [31:0] LedData
);

  wire AluSrcB, and_1_out, and_2_out, and_5_out, and_6_out, and_7_out, and_8_out, and_9_out, and_10_out,
       and_12_out, and_13_out, and_14_out, and_15_out, Beq, Bne, CLK, clock_2_out, clock_3_out, clock_4_out,
       comparator_2_eq, comparator_3_eq, comparator_4_eq, comparator_5_eq, comparator_6_eq, comparator_7_eq,
       comparator_8_eq, comparator_9_eq, comparator_10_eq, comparator_12_eq, controlled_inverter_1_out,
       controlled_inverter_2_out, controlled_inverter_3_out, d_ff_1_q, d_ff_2_q, d_ff_3_q, decoder_1_out0,
       decoder_1_out1, decoder_1_out2, decoder_2_out2, decoder_2_out3, Eret, Go, halt, high_pri, IE,
       Interrupt, IR1_2_q, IR1_3_q, IR1_4_q, IR1_t, IR1reset, IR2_t, IR2reset, IR3_t, IR3reset, IRA, IRB,
       IRC, JAL, JMP, JR, MemToReg, mfc0, mips_alu_1_equal, mtc0, multiplexer_6_out, not_1_out, or_1_out,
       or_2_out, or_3_out, or_4_out, or_5_out, or_6_out, or_13_out, or_14_out, or_15_out,
       priority_encoder_1_gs, pull_resistor_4_node, RegDst, SignedExt, Syscall, W1, W2, W3;
  wire [1:0] adder_1_out, IR1_q, IR2_q, IR3_q, IRnow, IRnumber, multiplexer_1_out, StackTop;
  wire [3:0] mips_probe_1_p5;
  wire [4:0] multiplexer_7_out, multiplexer_9_out, multiplexer_10_out, multiplexer_11_out;
  wire [15:0] \总周期数 ;
  wire [27:0] shifter_1_out;
  wire [31:0] adder_2_out, adder_3_out, bit_extender_1_out, bit_extender_2_out, EPC, EPC1_q, EPC2_q, EPC3_q,
       IRaddress, mips_alu_1_result, multiplexer_2_out, multiplexer_4_out, multiplexer_5_out,
       multiplexer_13_out, multiplexer_15_out, multiplexer_16_out, PCnxt, R1, ram_1_data, shifter_2_out;

  Clock #(.highDuration(1), .lowDuration(1)) clock_1 (.out(CLK));
  Button _1 (.out(IRA));
  Button _2 (.out(IRB));
  Button _3 (.out(IRC));
  Button \u_继续运行  (.out(Go));
  LED #(.active("true")) led_1 (.in(W1));
  LED #(.active("true")) led_2 (.in(W2));
  LED #(.active("true")) led_3 (.in(W3));
  and and_1 (and_1_out, Bne, ~mips_alu_1_equal);  // AND_Gate
  Multiplexer #(.select(1), .width(2), .disabled("Z"), .enable("false")) multiplexer_1 (
    .in0(2'b11), .in1(2'b01), .out(multiplexer_1_out), .sel(Interrupt));
  Hex_Digit_Display hex_digit_display_1 (.value(LedData[31:28]));  // open: dp
  and and_2 (and_2_out, mips_alu_1_equal, Beq);
  or or_1 (or_1_out, and_1_out, and_2_out);
  Multiplexer #(.select(1), .width(32), .disabled("Z"), .enable("false")) multiplexer_2 (
    .in0(adder_2_out), .in1(adder_3_out), .out(multiplexer_2_out), .sel(or_1_out));
  Comparator #(.width(32), .mode("twosComplement")) comparator_1 (.a(IR), .b(32'h42000018), .eq(Eret));  // open: gt, lt
  Comparator #(.width(6), .mode("twosComplement")) comparator_2 (
    .a(IR[31:26]), .b(6'b010000), .eq(comparator_2_eq));  // open: gt, lt
  Comparator #(.width(5), .mode("twosComplement")) comparator_3 (
    .a(IR[25:21]), .b({5{1'b0}}), .eq(comparator_3_eq));  // open: gt, lt
  Comparator #(.width(5), .mode("twosComplement")) comparator_4 (
    .a(IR[25:21]), .b(5'b00100), .eq(comparator_4_eq));  // open: gt, lt
  Adder #(.width(2)) adder_1 (.a(StackTop), .b(multiplexer_1_out), .out(adder_1_out));  // open: cin, cout
  or or_2 (or_2_out, Interrupt, Eret);
  Comparator #(.width(16), .mode("twosComplement")) comparator_5 (
    .a(16'h258), .b(\总周期数 ), .eq(comparator_5_eq));  // open: gt, lt
  Comparator #(.width(16), .mode("twosComplement")) comparator_6 (
    .a(\总周期数 ), .b(16'h1), .eq(comparator_6_eq));  // open: gt, lt
  Comparator #(.width(16), .mode("twosComplement")) comparator_7 (
    .a(\总周期数 ), .b(16'h4), .eq(comparator_7_eq));  // open: gt, lt
  Comparator #(.width(16), .mode("twosComplement")) comparator_8 (
    .a(\总周期数 ), .b(16'h7), .eq(comparator_8_eq));  // open: gt, lt
  Comparator #(.width(16), .mode("twosComplement")) comparator_9 (
    .a(\总周期数 ), .b(16'h241), .eq(comparator_9_eq));  // open: gt, lt
  Hex_Digit_Display hex_digit_display_2 (.value(LedData[27:24]));  // open: dp
  Hex_Digit_Display hex_digit_display_3 (.value(LedData[23:20]));  // open: dp
  Multiplexer #(.select(2), .width(32), .disabled("Z"), .enable("false")) multiplexer_3 (
    .in0(multiplexer_2_out), .in1({adder_2_out[31:28], shifter_1_out}),
    .in2({adder_2_out[31:28], shifter_1_out}), .in3(R1), .out(PCnxt), .sel({JMP, JR}));
  and and_3 (mfc0, comparator_2_eq, comparator_3_eq);
  and and_4 (mtc0, comparator_2_eq, comparator_4_eq);
  Register #(.width(2), .trigger("rising"), .Select("low")) register_1 (
    .D(adder_1_out), .en(or_2_out), .Q(StackTop), .clk(CLK));  // open: clr
  or or_3 (or_3_out, comparator_5_eq, comparator_6_eq);
  assign controlled_inverter_1_out = or_3_out ? ~CLK : 1'bz;  // Controlled_Inverter controlled_inverter_1
  assign controlled_inverter_2_out = comparator_7_eq ? ~CLK : 1'bz;  // Controlled_Inverter controlled_inverter_2
  or or_4 (or_4_out, comparator_8_eq, comparator_9_eq);
  assign controlled_inverter_3_out = or_4_out ? ~CLK : 1'bz;  // Controlled_Inverter controlled_inverter_3
  Hex_Digit_Display hex_digit_display_4 (.value(LedData[15:12]));  // open: dp
  Hex_Digit_Display hex_digit_display_5 (.value(LedData[19:16]));  // open: dp
  Multiplexer #(.select(1), .width(32), .disabled("Z"), .enable("false")) multiplexer_4 (
    .in0(PCnxt), .in1(IRaddress), .out(multiplexer_4_out), .sel(Interrupt));
  Pull_Resistor #(.pull(0)) pull_resistor_1 (.node(controlled_inverter_1_out));
  Pull_Resistor #(.pull(0)) pull_resistor_2 (.node(controlled_inverter_2_out));
  Pull_Resistor #(.pull(0)) pull_resistor_3 (.node(controlled_inverter_3_out));
  Hex_Digit_Display hex_digit_display_6 (.value(LedData[11:8]));  // open: dp
  Hex_Digit_Display hex_digit_display_7 (.value(LedData[7:4]));  // open: dp
  // Probe on \总周期数 
  Multiplexer #(.select(1), .width(32), .disabled("Z"), .enable("false")) multiplexer_5 (
    .in0(multiplexer_4_out), .in1(EPC), .out(multiplexer_5_out), .sel(Eret));
  Multiplexer #(.select(1), .width(1), .disabled("Z"), .enable("false")) multiplexer_6 (
    .in0(1'b1), .in1(Go), .out(multiplexer_6_out), .sel(halt));
  Hex_Digit_Display hex_digit_display_8 (.value(LedData[3:0]));  // open: dp
  Demultiplexer #(.select(2), .width(1), .tristate("false"), .disabled("Z"), .enable("false")) demultiplexer_1 (
    .out1(IR1reset), .out2(IR2reset), .out3(IR3reset), .in(Eret), .sel(IRnumber));  // open: out0
  or or_5 (or_5_out, Interrupt, mtc0);
  Comparator #(.width(16), .mode("twosComplement")) comparator_10 (
    .a(\总周期数 ), .b({16{1'b0}}), .eq(comparator_10_eq));  // open: gt, lt
  Decoder #(.select(2), .tristate("false"), .disabled("Z"), .enable("false")) decoder_1 (
    .out0(decoder_1_out0), .out1(decoder_1_out1), .out2(decoder_1_out2), .sel(StackTop));  // open: out3
  Register #(.width(32), .trigger("rising"), .Select("low")) u_PC (
    .D(multiplexer_5_out), .en(multiplexer_6_out), .Q(PC), .clk(CLK));  // open: clr
  Counter #(.width(16), .max('hffff), .ongoal("wrap"), .trigger("rising"), .behavior("old")) counter_1 (
    .load(1'b0), .count(multiplexer_6_out), .Q(\总周期数 ), .clk(CLK));  // open: D, carry, clr, preset
  not not_1 (not_1_out, or_5_out);
  or or_6 (or_6_out, Interrupt, Eret, mfc0, mtc0, comparator_10_eq);
  or or_7 (IR1_t, IR1, IRA);
  Adder #(.width(32)) adder_2 (.a(PC), .b(32'h4), .out(adder_2_out));  // open: cin, cout
  Register #(.width(1), .trigger("rising"), .Select("low")) register_2 (
    .D(not_1_out), .en(or_6_out), .Q(IE), .clk(CLK));  // open: clr
  and and_5 (and_5_out, Interrupt, decoder_1_out0);
  and and_6 (and_6_out, Interrupt, decoder_1_out1);
  and and_7 (and_7_out, Interrupt, decoder_1_out2);
  or or_8 (IR2_t, IR2, IRB);
  ROM #(.addrWidth(10), .dataWidth(32), .Select("high")) rom_1 (.addr(PC[11:2]), .data(IR));
  Register #(.width(2), .trigger("rising"), .Select("low")) u_IR1 (
    .D(IRnumber), .en(and_5_out), .Q(IR1_q), .clk(CLK));  // open: clr
  Register #(.width(2), .trigger("rising"), .Select("low")) u_IR2 (
    .D(IRnumber), .en(and_6_out), .Q(IR2_q), .clk(CLK));  // open: clr
  Register #(.width(2), .trigger("rising"), .Select("low")) u_IR3 (
    .D(IRnumber), .en(and_7_out), .Q(IR3_q), .clk(CLK));  // open: clr
  // Mips_Probe mips_probe_1: pin names not known; wires that end beside it: IR, Bne, MemToReg, MemWrite, mips_probe_1_p5
  Pull_Resistor #(.pull(0)) pull_resistor_4 (.node(pull_resistor_4_node));
  Decoder #(.select(2), .tristate("false"), .disabled("Z"), .enable("false")) decoder_2 (
    .out1(pull_resistor_4_node), .out2(decoder_2_out2), .out3(decoder_2_out3), .sel(IRnumber));  // open: out0
  Pull_Resistor #(.pull(0)) pull_resistor_5 (.node(decoder_2_out2));
  Pull_Resistor #(.pull(0)) pull_resistor_6 (.node(decoder_2_out3));
  or or_9 (IR3_t, IR3, IRC);
  Multiplexer #(.select(1), .width(5), .disabled("Z"), .enable("false")) multiplexer_7 (
    .in0(IR[20:16]), .in1(IR[15:11]), .out(multiplexer_7_out), .sel(RegDst));
  assign bit_extender_1_out = {{16{1'b0}}, IR[15:0]};  // Bit_Extender bit_extender_1
  assign bit_extender_2_out = {{16{IR[15]}}, IR[15:0]};  // Bit_Extender bit_extender_2
  Shifter #(.width(28), .shift("ll")) shifter_1 (.in(IR[27:0]), .\dist (5'b00010), .out(shifter_1_out));
  and and_8 (and_8_out, Interrupt, pull_resistor_4_node);
  and and_9 (and_9_out, Interrupt, decoder_2_out2);
  and and_10 (and_10_out, Interrupt, decoder_2_out3);
  Multiplexer #(.select(2), .width(2), .disabled("Z"), .enable("false")) multiplexer_8 (
    .in1(IR1_q), .in2(IR2_q), .in3(IR3_q), .out(IRnow), .sel(StackTop));  // open: in0
  \单周期硬布线控制器  \u_单周期硬布线控制器_1  (
    .Func(IR[5:0]), .OP(IR[31:26]), .ALU_OP(mips_probe_1_p5), .MemToReg(MemToReg), .MemWrite(MemWrite),
    .ALU_SRC(AluSrcB), .RegWrite(RegWrite), .SysCALL(Syscall), .SignedExt(SignedExt), .RegDst(RegDst),
    .JR(JR), .JMP(JMP), .Beq(Beq), .JAL(JAL), .Bne(Bne));
  Multiplexer #(.select(1), .width(5), .disabled("Z"), .enable("false")) multiplexer_9 (
    .in0(IR[25:21]), .in1(5'b00010), .out(multiplexer_9_out), .sel(Syscall));
  Multiplexer #(.select(1), .width(5), .disabled("Z"), .enable("false")) multiplexer_10 (
    .in0(IR[20:16]), .in1(5'b00100), .out(multiplexer_10_out), .sel(Syscall));
  Multiplexer #(.select(1), .width(5), .disabled("Z"), .enable("false")) multiplexer_11 (
    .in0(multiplexer_7_out), .in1({5{1'b1}}), .out(multiplexer_11_out), .sel(JAL));
  Multiplexer #(.select(1), .width(32), .disabled("Z"), .enable("false")) multiplexer_12 (
    .in0(multiplexer_16_out), .in1(adder_2_out), .out(RDin), .sel(JAL));
  Multiplexer #(.select(1), .width(32), .disabled("Z"), .enable("false")) multiplexer_13 (
    .in0(bit_extender_1_out), .in1(bit_extender_2_out), .out(multiplexer_13_out), .sel(SignedExt));
  Register #(.width(32), .trigger("rising"), .Select("low")) EPC1 (
    .D(PCnxt), .en(and_8_out), .Q(EPC1_q), .clk(CLK));  // open: clr
  Register #(.width(32), .trigger("rising"), .Select("low")) EPC2 (
    .D(PCnxt), .en(and_9_out), .Q(EPC2_q), .clk(CLK));  // open: clr
  Register #(.width(32), .trigger("rising"), .Select("low")) EPC3 (
    .D(PCnxt), .en(and_10_out), .Q(EPC3_q), .clk(CLK));  // open: clr
  Comparator #(.width(2), .mode("unsigned")) comparator_11 (.a(IRnow), .b(IRnumber), .lt(high_pri));  // open: gt, eq
  Pull_Resistor #(.pull(1)) pull_resistor_7 (.node(high_pri));
  MIPS_Regifile mips_regifile_1 (
    .Din(RDin), .Clk(CLK), .R1(R1), .R2(MDin), .WE(RegWrite), .W_num(multiplexer_11_out),
    .R1_num(multiplexer_9_out), .R2_num(multiplexer_10_out));
  Multiplexer #(.select(2), .width(32), .disabled("Z"), .enable("false")) multiplexer_14 (
    .in1(EPC1_q), .in2(EPC2_q), .in3(EPC3_q), .out(EPC), .sel(IRnow));  // open: in0
  Multiplexer #(.select(1), .width(32), .disabled("Z"), .enable("false")) multiplexer_15 (
    .in0(MDin), .in1(multiplexer_13_out), .out(multiplexer_15_out), .sel(AluSrcB));
  Shifter #(.width(32), .shift("ll")) shifter_2 (.in(multiplexer_13_out), .\dist (5'b00010), .out(shifter_2_out));
  MIPS_ALU mips_alu_1 (
    .X(R1), .Y(multiplexer_15_out), .AluOP(mips_probe_1_p5), .Equal(mips_alu_1_equal),
    .Result(mips_alu_1_result), .shamt(IR[10:6]));  // open: Result_2
  Adder #(.width(32)) adder_3 (.a(shifter_2_out), .b(adder_2_out), .out(adder_3_out));  // open: cin, cout
  Comparator #(.width(32), .mode("twosComplement")) comparator_12 (
    .a(R1), .b(32'h22), .eq(comparator_12_eq));  // open: gt, lt
  Clock #(.highDuration(1), .lowDuration(1)) clock_2 (.out(clock_2_out));
  or or_10 (W1, IR1_2_q, d_ff_1_q);
  LED #(.active("true")) \_1号中断等待指示灯  (.in(W1));
  Clock #(.highDuration(1), .lowDuration(1)) clock_3 (.out(clock_3_out));
  or or_11 (W2, IR1_3_q, d_ff_2_q);
  LED #(.active("true")) \_2号中断等待指示灯  (.in(W2));
  Clock #(.highDuration(1), .lowDuration(1)) clock_4 (.out(clock_4_out));
  or or_12 (W3, IR1_4_q, d_ff_3_q);
  LED #(.active("true")) \_3号中断等待指示灯  (.in(W3));
  and and_11 (halt, ~comparator_12_eq, Syscall);  // AND_Gate
  and and_12 (and_12_out, comparator_12_eq, Syscall);
  RAM #(.addrWidth(10), .dataWidth(32), .bus("separate"), .Select("high")) ram_1 (
    .addr(mips_alu_1_result[9:0]), .din(MDin), .data(ram_1_data), .str(MemWrite), .clk(CLK));  // open: sel, ld, clr
  D_Flip_Flop #(.trigger("rising"), .Pre_Clr_Positions("LEGACY"), .NegatePresetClear("false"), .enable("true"), .NewFFLayout("false")) d_ff_1 (
    .clk(IR1_t), .D(1'b1), .Q(d_ff_1_q), .reset(IR1_2_q));  // open: Qn, preset, en
  D_Flip_Flop #(.trigger("rising"), .Pre_Clr_Positions("LEGACY"), .NegatePresetClear("false"), .enable("true"), .NewFFLayout("false")) d_ff_2 (
    .clk(IR2_t), .D(1'b1), .Q(d_ff_2_q), .reset(IR1_3_q));  // open: Qn, preset, en
  D_Flip_Flop #(.trigger("rising"), .Pre_Clr_Positions("LEGACY"), .NegatePresetClear("false"), .enable("true"), .NewFFLayout("false")) d_ff_3 (
    .clk(IR3_t), .D(1'b1), .Q(d_ff_3_q), .reset(IR1_4_q));  // open: Qn, preset, en
  Register #(.width(32), .trigger("rising"), .Select("low")) register_3 (
    .D(MDin), .en(and_12_out), .Q(LedData), .clk(CLK));  // open: clr
  Multiplexer #(.select(1), .width(32), .disabled("Z"), .enable("false")) multiplexer_16 (
    .in0(mips_alu_1_result), .in1(ram_1_data), .out(multiplexer_16_out), .sel(MemToReg));
  or or_13 (or_13_out, d_ff_1_q, IR1_2_q);
  Pull_Resistor #(.pull(0)) pull_resistor_8 (.node(IR1reset));
  or or_14 (or_14_out, d_ff_2_q, IR1_3_q);
  Pull_Resistor #(.pull(0)) pull_resistor_9 (.node(IR2reset));
  or or_15 (or_15_out, d_ff_3_q, IR1_4_q);
  Pull_Resistor #(.pull(0)) pull_resistor_10 (.node(IR3reset));
  and and_13 (and_13_out, or_13_out, ~IR1reset);  // AND_Gate
  and and_14 (and_14_out, or_14_out, ~IR2reset);  // AND_Gate
  and and_15 (and_15_out, or_15_out, ~IR3reset);  // AND_Gate
  D_Flip_Flop #(.trigger("rising"), .Pre_Clr_Positions("LEGACY"), .NegatePresetClear("false"), .enable("true"), .NewFFLayout("false")) IR1_2 (
    .clk(clock_2_out), .D(and_13_out), .Q(IR1_2_q));  // open: Qn, preset, en, reset
  D_Flip_Flop #(.trigger("rising"), .Pre_Clr_Positions("LEGACY"), .NegatePresetClear("false"), .enable("true"), .NewFFLayout("false")) IR1_3 (
    .clk(clock_3_out), .D(and_14_out), .Q(IR1_3_q));  // open: Qn, preset, en, reset
  D_Flip_Flop #(.trigger("rising"), .Pre_Clr_Positions("LEGACY"), .NegatePresetClear("false"), .enable("true"), .NewFFLayout("false")) IR1_4 (
    .clk(clock_4_out), .D(and_15_out), .Q(IR1_4_q));  // open: Qn, preset, en, reset
  Priority_Encoder #(.select(2), .disabled("Z")) priority_encoder_1 (
    .in1(IR1_2_q), .in2(IR1_3_q), .in3(IR1_4_q), .out(IRnumber), .gs(priority_encoder_1_gs));  // open: in0, en_out, en_in
  Multiplexer #(.select(2), .width(32), .disabled("Z"), .enable("false")) multiplexer_17 (
    .in1(32'h30ac), .in2(32'h3158), .in3(32'h3204), .out(IRaddress), .sel(IRnumber));  // open: in0
  and and_16 (Interrupt, priority_encoder_1_gs, IE, high_pri);

  // Other names for the same wires on the sheet: rs[4:0] = IR[25:21]; OP[5:0] = IR[31:26]; R2[31:0] = MDin

  // Notes on the sheet:
  //   中断源
  //   中断等待指示
  //   总复位信号应将除ROM以外所有存储组件全部清零
  //   多级中断测试信号模拟器
  //   数码管输出
  //   数码管输出应该用寄存器锁存，否则显示数据只能一闪而过
  //   IE
  //   指令存储器
  //   PC+4
  //   contents of rom_1 (hex, n*v repeats v):
  //   201d07d0 20100001 109fc0 139fc3 8021 2012000c 24160008 26100001 3210000f 20080008 20090001 139900
  //   2709825 132020 20020022 c 1094022 1500fff9 22100001 2018000f 2188024 108700 20080008 20090001 139902
  //   2709825 132021 20020022 c 1094022 1500fff9 108702 2c9b022 12c00001 8000c07 4020 1084027 84400
  //   3508ffff 82021 20020022 c 8000c01 afa20000 23bd0004 afa40000 23bd0004 afb00000 23bd0004 afb30000
  //   23bd0004 afb40000 23bd0004 afb50000 23bd0004 afb60000 23bd0004 40000000 20160001 20140003 20150001
  //   168020 108100 2149825 132020 20020022 c 1600fffa 295a022 1680fff7 40800000 23bdfffc 8fb60000
  //   23bdfffc 8fb50000 23bdfffc 8fb40000 23bdfffc 8fb30000 23bdfffc 8fb00000 23bdfffc 8fa40000 23bdfffc
  //   8fa20000 42000018 afa20000 23bd0004 afa40000 23bd0004 afb00000 23bd0004 afb30000 23bd0004 afb40000
  //   23bd0004 afb50000 23bd0004 afb60000 23bd0004 40000000 20160002 20140003 20150001 168020 108100
  //   2149825 132020 20020022 c 1600fffa 295a022 1680fff7 40800000 23bdfffc 8fb60000 23bdfffc 8fb50000
  //   23bdfffc 8fb40000 23bdfffc 8fb30000 23bdfffc 8fb00000 23bdfffc 8fa40000 23bdfffc 8fa20000 42000018
  //   afa20000 23bd0004 afa40000 23bd0004 afb00000 23bd0004 afb30000 23bd0004 afb40000 23bd0004 afb50000
  //   23bd0004 afb60000 23bd0004 40000000 20160003 20140003 20150001 168020 108100 2149825 132020 20020022
  //   c 1600fffa 295a022 1680fff7 40800000 23bdfffc 8fb60000 23bdfffc 8fb50000 23bdfffc 8fb40000 23bdfffc
  //   8fb30000 23bdfffc 8fb00000 23bdfffc 8fa40000 23bdfffc 8fa20000 42000018
  //   OP
  //   Func
  //   rs
  //   指令字
  //   rt
  //   rd
  //   JMP
  //   JR
  //   OP
  //   Func
  //   Beq
  //   Bne
  //   MemToReg
  //   MemWrite
  //   AluOP
  //   AluSrcB
  //   RegWrite
  //   JAL
  //   RegDst
  //   Syscall
  //   为方便自动评测，需要输出PC，IR，寄存器堆写如数据RDin
  //   RAM写使能MemWrite、RAM写入数据MDin等信号
  //   PCBranch
  //   Reset 
  //   Reset 
  //   Reset 
endmodule

module \封装正确性测试  (
);

  wire IR1, IR2, IR3, MemW, RegW;
  wire [31:0] EX_PC, ID_PC, IF_PC, IR, LED, MDin, MDinr, MEM_PC, PC, RDin, RDinr, WB_PC;

  \单周期MIPS  \u_单周期mips_1  (
    .RegWrite(RegW), .MemWrite(MemW), .PC(PC), .IR(IR), .RDin(RDin), .MDin(MDin), .LedData(LED));  // open: IR1, IR2, IR3
  \气泡流水线  \u_气泡流水线_1  (
    .RegWrite(RegW), .MemWrite(MemW), .IF_PC(IF_PC), .ID_PC(ID_PC), .EX_PC(EX_PC), .M_PC(MEM_PC),
    .WB_PC(WB_PC), .RDin(RDinr), .MDin(MDinr), .LedData(LED));
  \单周期MIPS_单级中断  \u_单周期mips_单级中断_1  (
    .IR1(IR1), .IR2(IR2), .IR3(IR3), .RegWrite(RegW), .MemWrite(MemW), .PC(PC), .IR(IR), .RDin(RDin),
    .MDin(MDin), .LedData(LED));
  \理想流水线  \u_理想流水线_1  (
    .RegWrite(RegW), .MemWrite(MemW), .IF_PC(IF_PC), .ID_PC(ID_PC), .EX_PC(EX_PC), .M_PC(MEM_PC),
    .WB_PC(WB_PC), .RDin(RDinr), .MDin(MDinr), .LedData(LED));
  \重定向流水线  \u_重定向流水线_1  (
    .RegWrite(RegW), .MemWrite(MemW), .IF_PC(IF_PC), .ID_PC(ID_PC), .EX_PC(EX_PC), .M_PC(MEM_PC),
    .WB_PC(WB_PC), .RDin(RDinr), .MDin(MDinr), .LedData(LED));
  \单周期MIPS_多级中断  \u_单周期mips_多级中断_1  (
    .IR1(IR1), .IR2(IR2), .IR3(IR3), .RegWrite(RegW), .MemWrite(MemW), .PC(PC), .IR(IR), .RDin(RDin),
    .MDin(MDin), .LedData(LED));

  // Notes on the sheet:
  //   单周期封装测试
  //   气泡流水封装测试
  //   单周期+单级中断封装测试
  //   请检查上面封装有无位宽不匹配，引脚标签是否和连接的标签相对应，否则无法在educoder平台上正确测试
  //   理想流水封装测试
  //   重定向流水封装测试
  //   单周期+多级中断封装测试
endmodule

module IF_ID (
  input  [31:0] IR_in,
  input  [31:0] OldPC_in,
  input  [31:0] PC_in,
  input  PredJmp_in,
  input  \气泡高电平有效 ,
  input  \使能 ,
  input  Clk,
  input  Clr,
  output [31:0] IR_out,
  output [31:0] OldPC_out,
  output [31:0] PC_out,
  output PredJmp_out
);

  wire multiplexer_1_out;
  wire [31:0] multiplexer_2_out, multiplexer_3_out, multiplexer_4_out;

  Multiplexer #(.select(1), .width(1), .disabled("Z"), .enable("false")) multiplexer_1 (
    .in0(PredJmp_in), .in1(1'b0), .out(multiplexer_1_out), .sel(\气泡高电平有效 ));
  Multiplexer #(.select(1), .width(32), .disabled("Z"), .enable("false")) multiplexer_2 (
    .in0(IR_in), .in1({32{1'b0}}), .out(multiplexer_2_out), .sel(\气泡高电平有效 ));
  Multiplexer #(.select(1), .width(32), .disabled("Z"), .enable("false")) multiplexer_3 (
    .in0(OldPC_in), .in1({32{1'b0}}), .out(multiplexer_3_out), .sel(\气泡高电平有效 ));
  Multiplexer #(.select(1), .width(32), .disabled("Z"), .enable("false")) multiplexer_4 (
    .in0(PC_in), .in1({32{1'b0}}), .out(multiplexer_4_out), .sel(\气泡高电平有效 ));
  Register #(.width(32), .trigger("rising"), .Select("low")) register_1 (
    .D(multiplexer_2_out), .en(\使能 ), .Q(IR_out), .clk(Clk), .clr(Clr));
  Register #(.width(32), .trigger("rising"), .Select("low")) register_2 (
    .D(multiplexer_3_out), .en(\使能 ), .Q(OldPC_out), .clk(Clk), .clr(Clr));
  Register #(.width(32), .trigger("rising"), .Select("low")) register_3 (
    .D(multiplexer_4_out), .en(\使能 ), .Q(PC_out), .clk(Clk), .clr(Clr));
  Register #(.width(1), .trigger("rising"), .Select("low")) register_4 (
    .D(multiplexer_1_out), .en(\使能 ), .Q(PredJmp_out), .clk(Clk), .clr(Clr));
endmodule

module ID_EX (
  input  Syscall_in,
  input  Beq_in,
  input  Bne_in,
  input  MemToReg_in,
  input  MemWrite_in,
  input  AluSrcB_in,
  input  RegWrite_in,
  input  JAL_in,
  input  RegDst_in,
  input  JMP_in,
  input  JR_in,
  input  SignedExt_in,
  input  [3:0] AluOP_in,
  input  [31:0] IR_in,
  input  [31:0] OldPC_in,
  input  [31:0] PC_in,
  input  [31:0] R1_in,
  input  [31:0] R2_in,
  input  [31:0] imm_in,
  input  BGTZ,
  input  LHU,
  input  PredJmp_in_Eret_in,
  input  \气泡高电平有效 ,
  input  \使能 ,
  input  Clk,
  input  Clr,
  output Syscall_out,
  output Beq_out,
  output Bne_out,
  output MemToReg_out,
  output MemWrite_out,
  output AluSrcB_out,
  output RegWrite_out,
  output JAL_out,
  output RegDst_out,
  output JMP_out,
  output JR_out,
  output SignedExt_out,
  output [3:0] AluOP_out,
  output [31:0] IR_out,
  output [31:0] OldPC_out,
  output [31:0] PC_out,
  output [31:0] R1_out,
  output [31:0] R2_out,
  output [31:0] imm_out,
  output BGTZ_2,
  output LHU_2,
  output PredJmp_out_Eret_in
);

  wire multiplexer_1_out, multiplexer_2_out, multiplexer_3_out, multiplexer_4_out, multiplexer_5_out,
       multiplexer_6_out, multiplexer_7_out, multiplexer_8_out, multiplexer_9_out, multiplexer_10_out,
       multiplexer_11_out, multiplexer_12_out, multiplexer_20_out, multiplexer_21_out, multiplexer_22_out;
  wire [3:0] multiplexer_13_out;
  wire [31:0] multiplexer_14_out, multiplexer_15_out, multiplexer_16_out, multiplexer_17_out,
       multiplexer_18_out, multiplexer_19_out;

  Multiplexer #(.select(1), .width(1), .disabled("Z"), .enable("false")) multiplexer_1 (
    .in0(Syscall_in), .in1(1'b0), .out(multiplexer_1_out), .sel(\气泡高电平有效 ));
  Multiplexer #(.select(1), .width(1), .disabled("Z"), .enable("false")) multiplexer_2 (
    .in0(Beq_in), .in1(1'b0), .out(multiplexer_2_out), .sel(\气泡高电平有效 ));
  Multiplexer #(.select(1), .width(1), .disabled("Z"), .enable("false")) multiplexer_3 (
    .in0(Bne_in), .in1(1'b0), .out(multiplexer_3_out), .sel(\气泡高电平有效 ));
  Multiplexer #(.select(1), .width(1), .disabled("Z"), .enable("false")) multiplexer_4 (
    .in0(MemToReg_in), .in1(1'b0), .out(multiplexer_4_out), .sel(\气泡高电平有效 ));
  Multiplexer #(.select(1), .width(1), .disabled("Z"), .enable("false")) multiplexer_5 (
    .in0(MemWrite_in), .in1(1'b0), .out(multiplexer_5_out), .sel(\气泡高电平有效 ));
  Multiplexer #(.select(1), .width(1), .disabled("Z"), .enable("false")) multiplexer_6 (
    .in0(AluSrcB_in), .in1(1'b0), .out(multiplexer_6_out), .sel(\气泡高电平有效 ));
  Multiplexer #(.select(1), .width(1), .disabled("Z"), .enable("false")) multiplexer_7 (
    .in0(RegWrite_in), .in1(1'b0), .out(multiplexer_7_out), .sel(\气泡高电平有效 ));
  Multiplexer #(.select(1), .width(1), .disabled("Z"), .enable("false")) multiplexer_8 (
    .in0(JAL_in), .in1(1'b0), .out(multiplexer_8_out), .sel(\气泡高电平有效 ));
  Multiplexer #(.select(1), .width(1), .disabled("Z"), .enable("false")) multiplexer_9 (
    .in0(RegDst_in), .in1(1'b0), .out(multiplexer_9_out), .sel(\气泡高电平有效 ));
  Multiplexer #(.select(1), .width(1), .disabled("Z"), .enable("false")) multiplexer_10 (
    .in0(JMP_in), .in1(1'b0), .out(multiplexer_10_out), .sel(\气泡高电平有效 ));
  Multiplexer #(.select(1), .width(1), .disabled("Z"), .enable("false")) multiplexer_11 (
    .in0(JR_in), .in1(1'b0), .out(multiplexer_11_out), .sel(\气泡高电平有效 ));
  Multiplexer #(.select(1), .width(1), .disabled("Z"), .enable("false")) multiplexer_12 (
    .in0(SignedExt_in), .in1(1'b0), .out(multiplexer_12_out), .sel(\气泡高电平有效 ));
  Multiplexer #(.select(1), .width(4), .disabled("Z"), .enable("false")) multiplexer_13 (
    .in0(AluOP_in), .in1(4'b0000), .out(multiplexer_13_out), .sel(\气泡高电平有效 ));
  Multiplexer #(.select(1), .width(32), .disabled("Z"), .enable("false")) multiplexer_14 (
    .in0(IR_in), .in1({32{1'b0}}), .out(multiplexer_14_out), .sel(\气泡高电平有效 ));
  Multiplexer #(.select(1), .width(32), .disabled("Z"), .enable("false")) multiplexer_15 (
    .in0(OldPC_in), .in1({32{1'b0}}), .out(multiplexer_15_out), .sel(\气泡高电平有效 ));
  Multiplexer #(.select(1), .width(32), .disabled("Z"), .enable("false")) multiplexer_16 (
    .in0(PC_in), .in1({32{1'b0}}), .out(multiplexer_16_out), .sel(\气泡高电平有效 ));
  Multiplexer #(.select(1), .width(32), .disabled("Z"), .enable("false")) multiplexer_17 (
    .in0(R1_in), .in1({32{1'b0}}), .out(multiplexer_17_out), .sel(\气泡高电平有效 ));
  Multiplexer #(.select(1), .width(32), .disabled("Z"), .enable("false")) multiplexer_18 (
    .in0(R2_in), .in1({32{1'b0}}), .out(multiplexer_18_out), .sel(\气泡高电平有效 ));
  Multiplexer #(.select(1), .width(32), .disabled("Z"), .enable("false")) multiplexer_19 (
    .in0(imm_in), .in1({32{1'b0}}), .out(multiplexer_19_out), .sel(\气泡高电平有效 ));
  Multiplexer #(.select(1), .width(1), .disabled("Z"), .enable("false")) multiplexer_20 (
    .in0(BGTZ), .in1(1'b0), .out(multiplexer_20_out), .sel(\气泡高电平有效 ));
  Multiplexer #(.select(1), .width(1), .disabled("Z"), .enable("false")) multiplexer_21 (
    .in0(LHU), .in1(1'b0), .out(multiplexer_21_out), .sel(\气泡高电平有效 ));
  Multiplexer #(.select(1), .width(1), .disabled("Z"), .enable("false")) multiplexer_22 (
    .in0(PredJmp_in_Eret_in), .in1(1'b0), .out(multiplexer_22_out), .sel(\气泡高电平有效 ));
  Register #(.width(1), .trigger("rising"), .Select("low")) register_1 (
    .D(multiplexer_1_out), .en(\使能 ), .Q(Syscall_out), .clk(Clk), .clr(Clr));
  Register #(.width(1), .trigger("rising"), .Select("low")) register_2 (
    .D(multiplexer_2_out), .en(\使能 ), .Q(Beq_out), .clk(Clk), .clr(Clr));
  Register #(.width(1), .trigger("rising"), .Select("low")) register_3 (
    .D(multiplexer_3_out), .en(\使能 ), .Q(Bne_out), .clk(Clk), .clr(Clr));
  Register #(.width(1), .trigger("rising"), .Select("low")) register_4 (
    .D(multiplexer_4_out), .en(\使能 ), .Q(MemToReg_out), .clk(Clk), .clr(Clr));
  Register #(.width(1), .trigger("rising"), .Select("low")) register_5 (
    .D(multiplexer_5_out), .en(\使能 ), .Q(MemWrite_out), .clk(Clk), .clr(Clr));
  Register #(.width(1), .trigger("rising"), .Select("low")) register_6 (
    .D(multiplexer_6_out), .en(\使能 ), .Q(AluSrcB_out), .clk(Clk), .clr(Clr));
  Register #(.width(1), .trigger("rising"), .Select("low")) register_7 (
    .D(multiplexer_7_out), .en(\使能 ), .Q(RegWrite_out), .clk(Clk), .clr(Clr));
  Register #(.width(1), .trigger("rising"), .Select("low")) register_8 (
    .D(multiplexer_8_out), .en(\使能 ), .Q(JAL_out), .clk(Clk), .clr(Clr));
  Register #(.width(1), .trigger("rising"), .Select("low")) register_9 (
    .D(multiplexer_9_out), .en(\使能 ), .Q(RegDst_out), .clk(Clk), .clr(Clr));
  Register #(.width(1), .trigger("rising"), .Select("low")) register_10 (
    .D(multiplexer_10_out), .en(\使能 ), .Q(JMP_out), .clk(Clk), .clr(Clr));
  Register #(.width(1), .trigger("rising"), .Select("low")) register_11 (
    .D(multiplexer_11_out), .en(\使能 ), .Q(JR_out), .clk(Clk), .clr(Clr));
  Register #(.width(1), .trigger("rising"), .Select("low")) register_12 (
    .D(multiplexer_12_out), .en(\使能 ), .Q(SignedExt_out), .clk(Clk), .clr(Clr));
  Register #(.width(4), .trigger("rising"), .Select("low")) register_13 (
    .D(multiplexer_13_out), .en(\使能 ), .Q(AluOP_out), .clk(Clk), .clr(Clr));
  Register #(.width(32), .trigger("rising"), .Select("low")) register_14 (
    .D(multiplexer_14_out), .en(\使能 ), .Q(IR_out), .clk(Clk), .clr(Clr));
  Register #(.width(32), .trigger("rising"), .Select("low")) register_15 (
    .D(multiplexer_15_out), .en(\使能 ), .Q(OldPC_out), .clk(Clk), .clr(Clr));
  Register #(.width(32), .trigger("rising"), .Select("low")) register_16 (
    .D(multiplexer_16_out), .en(\使能 ), .Q(PC_out), .clk(Clk), .clr(Clr));
  Register #(.width(32), .trigger("rising"), .Select("low")) register_17 (
    .D(multiplexer_17_out), .en(\使能 ), .Q(R1_out), .clk(Clk), .clr(Clr));
  Register #(.width(32), .trigger("rising"), .Select("low")) register_18 (
    .D(multiplexer_18_out), .en(\使能 ), .Q(R2_out), .clk(Clk), .clr(Clr));
  Register #(.width(32), .trigger("rising"), .Select("low")) register_19 (
    .D(multiplexer_19_out), .en(\使能 ), .Q(imm_out), .clk(Clk), .clr(Clr));
  Register #(.width(1), .trigger("rising"), .Select("low")) register_20 (
    .D(multiplexer_20_out), .en(\使能 ), .Q(BGTZ_2), .clk(Clk), .clr(Clr));
  Register #(.width(1), .trigger("rising"), .Select("low")) register_21 (
    .D(multiplexer_21_out), .en(\使能 ), .Q(LHU_2), .clk(Clk), .clr(Clr));
  Register #(.width(1), .trigger("rising"), .Select("low")) register_22 (
    .D(multiplexer_22_out), .en(\使能 ), .Q(PredJmp_out_Eret_in), .clk(Clk), .clr(Clr));
endmodule

module EX_MEM (
  input  Syscall_in,
  input  MemToReg_in,
  input  MemWrite_in,
  input  RegWrite_in,
  input  JAL_in,
  input  RegDst_in,
  input  equal_in,
  input  [31:0] IR_in,
  input  [31:0] OldPC_in,
  input  [31:0] PC_in,
  input  [31:0] AluOut_in,
  input  [31:0] R2_in,
  input  LHU,
  input  pause_in,
  input  Eret_in,
  input  \气泡高电平有效 ,
  input  \使能 ,
  input  Clk,
  input  Clr,
  output Syscall_out,
  output MemToReg_out,
  output MemWrite_out,
  output RegWrite_out,
  output JAL_out,
  output RegDst_out,
  output equal_out,
  output [31:0] IR_out,
  output [31:0] OldPC_out,
  output [31:0] PC_out,
  output [31:0] AluOut_out,
  output [31:0] R2_out,
  output LHU_2,
  output pause_out,
  output Eret_in_2
);

  wire multiplexer_1_out, multiplexer_2_out, multiplexer_3_out, multiplexer_4_out, multiplexer_5_out,
       multiplexer_6_out, multiplexer_7_out, multiplexer_13_out, multiplexer_14_out, multiplexer_15_out;
  wire [31:0] multiplexer_8_out, multiplexer_9_out, multiplexer_10_out, multiplexer_11_out,
       multiplexer_12_out;

  Multiplexer #(.select(1), .width(1), .disabled("Z"), .enable("false")) multiplexer_1 (
    .in0(Syscall_in), .in1(1'b0), .out(multiplexer_1_out), .sel(\气泡高电平有效 ));
  Multiplexer #(.select(1), .width(1), .disabled("Z"), .enable("false")) multiplexer_2 (
    .in0(MemToReg_in), .in1(1'b0), .out(multiplexer_2_out), .sel(\气泡高电平有效 ));
  Multiplexer #(.select(1), .width(1), .disabled("Z"), .enable("false")) multiplexer_3 (
    .in0(MemWrite_in), .in1(1'b0), .out(multiplexer_3_out), .sel(\气泡高电平有效 ));
  Multiplexer #(.select(1), .width(1), .disabled("Z"), .enable("false")) multiplexer_4 (
    .in0(RegWrite_in), .in1(1'b0), .out(multiplexer_4_out), .sel(\气泡高电平有效 ));
  Multiplexer #(.select(1), .width(1), .disabled("Z"), .enable("false")) multiplexer_5 (
    .in0(JAL_in), .in1(1'b0), .out(multiplexer_5_out), .sel(\气泡高电平有效 ));
  Multiplexer #(.select(1), .width(1), .disabled("Z"), .enable("false")) multiplexer_6 (
    .in0(RegDst_in), .in1(1'b0), .out(multiplexer_6_out), .sel(\气泡高电平有效 ));
  Multiplexer #(.select(1), .width(1), .disabled("Z"), .enable("false")) multiplexer_7 (
    .in0(equal_in), .in1(1'b0), .out(multiplexer_7_out), .sel(\气泡高电平有效 ));
  Multiplexer #(.select(1), .width(32), .disabled("Z"), .enable("false")) multiplexer_8 (
    .in0(IR_in), .in1({32{1'b0}}), .out(multiplexer_8_out), .sel(\气泡高电平有效 ));
  Multiplexer #(.select(1), .width(32), .disabled("Z"), .enable("false")) multiplexer_9 (
    .in0(OldPC_in), .in1({32{1'b0}}), .out(multiplexer_9_out), .sel(\气泡高电平有效 ));
  Multiplexer #(.select(1), .width(32), .disabled("Z"), .enable("false")) multiplexer_10 (
    .in0(PC_in), .in1({32{1'b0}}), .out(multiplexer_10_out), .sel(\气泡高电平有效 ));
  Multiplexer #(.select(1), .width(32), .disabled("Z"), .enable("false")) multiplexer_11 (
    .in0(AluOut_in), .in1({32{1'b0}}), .out(multiplexer_11_out), .sel(\气泡高电平有效 ));
  Multiplexer #(.select(1), .width(32), .disabled("Z"), .enable("false")) multiplexer_12 (
    .in0(R2_in), .in1({32{1'b0}}), .out(multiplexer_12_out), .sel(\气泡高电平有效 ));
  Multiplexer #(.select(1), .width(1), .disabled("Z"), .enable("false")) multiplexer_13 (
    .in0(LHU), .in1(1'b0), .out(multiplexer_13_out), .sel(\气泡高电平有效 ));
  Multiplexer #(.select(1), .width(1), .disabled("Z"), .enable("false")) multiplexer_14 (
    .in0(pause_in), .in1(1'b0), .out(multiplexer_14_out), .sel(\气泡高电平有效 ));
  Multiplexer #(.select(1), .width(1), .disabled("Z"), .enable("false")) multiplexer_15 (
    .in0(Eret_in), .in1(1'b0), .out(multiplexer_15_out), .sel(\气泡高电平有效 ));
  Register #(.width(1), .trigger("rising"), .Select("low")) register_1 (
    .D(multiplexer_1_out), .en(\使能 ), .Q(Syscall_out), .clk(Clk), .clr(Clr));
  Register #(.width(1), .trigger("rising"), .Select("low")) register_2 (
    .D(multiplexer_2_out), .en(\使能 ), .Q(MemToReg_out), .clk(Clk), .clr(Clr));
  Register #(.width(1), .trigger("rising"), .Select("low")) register_3 (
    .D(multiplexer_3_out), .en(\使能 ), .Q(MemWrite_out), .clk(Clk), .clr(Clr));
  Register #(.width(1), .trigger("rising"), .Select("low")) register_4 (
    .D(multiplexer_4_out), .en(\使能 ), .Q(RegWrite_out), .clk(Clk), .clr(Clr));
  Register #(.width(1), .trigger("rising"), .Select("low")) register_5 (
    .D(multiplexer_5_out), .en(\使能 ), .Q(JAL_out), .clk(Clk), .clr(Clr));
  Register #(.width(1), .trigger("rising"), .Select("low")) register_6 (
    .D(multiplexer_6_out), .en(\使能 ), .Q(RegDst_out), .clk(Clk), .clr(Clr));
  Register #(.width(1), .trigger("rising"), .Select("low")) register_7 (
    .D(multiplexer_7_out), .en(\使能 ), .Q(equal_out), .clk(Clk), .clr(Clr));
  Register #(.width(32), .trigger("rising"), .Select("low")) register_8 (
    .D(multiplexer_8_out), .en(\使能 ), .Q(IR_out), .clk(Clk), .clr(Clr));
  Register #(.width(32), .trigger("rising"), .Select("low")) register_9 (
    .D(multiplexer_9_out), .en(\使能 ), .Q(OldPC_out), .clk(Clk), .clr(Clr));
  Register #(.width(32), .trigger("rising"), .Select("low")) register_10 (
    .D(multiplexer_10_out), .en(\使能 ), .Q(PC_out), .clk(Clk), .clr(Clr));
  Register #(.width(32), .trigger("rising"), .Select("low")) register_11 (
    .D(multiplexer_11_out), .en(\使能 ), .Q(AluOut_out), .clk(Clk), .clr(Clr));
  Register #(.width(32), .trigger("rising"), .Select("low")) register_12 (
    .D(multiplexer_12_out), .en(\使能 ), .Q(R2_out), .clk(Clk), .clr(Clr));
  Register #(.width(1), .trigger("rising"), .Select("low")) register_13 (
    .D(multiplexer_13_out), .en(\使能 ), .Q(LHU_2), .clk(Clk), .clr(Clr));
  Register #(.width(1), .trigger("rising"), .Select("low")) register_14 (
    .D(multiplexer_14_out), .en(\使能 ), .Q(pause_out), .clk(Clk), .clr(Clr));
  Register #(.width(1), .trigger("rising"), .Select("low")) register_15 (
    .D(multiplexer_15_out), .en(\使能 ), .Q(Eret_in_2), .clk(Clk), .clr(Clr));
endmodule

module MEM_WB (
  input  Syscall_in,
  input  MemToReg_in,
  input  MemWrite_in,
  input  RegWrite_in,
  input  JAL_in,
  input  RegDst_in,
  input  equal_in,
  input  [31:0] IR_in,
  input  [31:0] OldPC_in,
  input  [31:0] PC_in,
  input  [31:0] AluOut_in,
  input  [31:0] MemOut_in,
  input  LHU,
  input  pause_in,
  input  Eret_in,
  input  \气泡高电平有效 ,
  input  \使能 ,
  input  Clk,
  input  Clr,
  output Syscall_out,
  output MemToReg_out,
  output MemWrite_out,
  output RegWrite_out,
  output JAL_out,
  output RegDst_out,
  output equal_out,
  output [31:0] IR_out,
  output [31:0] OldPC_out,
  output [31:0] PC_out,
  output [31:0] AluOut_out,
  output [31:0] MemOut_out,
  output LHU_2,
  output pause_out,
  output Eret_out
);

  wire multiplexer_1_out, multiplexer_2_out, multiplexer_3_out, multiplexer_4_out, multiplexer_5_out,
       multiplexer_6_out, multiplexer_7_out, multiplexer_13_out, multiplexer_14_out, multiplexer_15_out;
  wire [31:0] multiplexer_8_out, multiplexer_9_out, multiplexer_10_out, multiplexer_11_out,
       multiplexer_12_out;

  Multiplexer #(.select(1), .width(1), .disabled("Z"), .enable("false")) multiplexer_1 (
    .in0(Syscall_in), .in1(1'b0), .out(multiplexer_1_out), .sel(\气泡高电平有效 ));
  Multiplexer #(.select(1), .width(1), .disabled("Z"), .enable("false")) multiplexer_2 (
    .in0(MemToReg_in), .in1(1'b0), .out(multiplexer_2_out), .sel(\气泡高电平有效 ));
  Multiplexer #(.select(1), .width(1), .disabled("Z"), .enable("false")) multiplexer_3 (
    .in0(MemWrite_in), .in1(1'b0), .out(multiplexer_3_out), .sel(\气泡高电平有效 ));
  Multiplexer #(.select(1), .width(1), .disabled("Z"), .enable("false")) multiplexer_4 (
    .in0(RegWrite_in), .in1(1'b0), .out(multiplexer_4_out), .sel(\气泡高电平有效 ));
  Multiplexer #(.select(1), .width(1), .disabled("Z"), .enable("false")) multiplexer_5 (
    .in0(JAL_in), .in1(1'b0), .out(multiplexer_5_out), .sel(\气泡高电平有效 ));
  Multiplexer #(.select(1), .width(1), .disabled("Z"), .enable("false")) multiplexer_6 (
    .in0(RegDst_in), .in1(1'b0), .out(multiplexer_6_out), .sel(\气泡高电平有效 ));
  Multiplexer #(.select(1), .width(1), .disabled("Z"), .enable("false")) multiplexer_7 (
    .in0(equal_in), .in1(1'b0), .out(multiplexer_7_out), .sel(\气泡高电平有效 ));
  Multiplexer #(.select(1), .width(32), .disabled("Z"), .enable("false")) multiplexer_8 (
    .in0(IR_in), .in1({32{1'b0}}), .out(multiplexer_8_out), .sel(\气泡高电平有效 ));
  Multiplexer #(.select(1), .width(32), .disabled("Z"), .enable("false")) multiplexer_9 (
    .in0(OldPC_in), .in1({32{1'b0}}), .out(multiplexer_9_out), .sel(\气泡高电平有效 ));
  Multiplexer #(.select(1), .width(32), .disabled("Z"), .enable("false")) multiplexer_10 (
    .in0(PC_in), .in1({32{1'b0}}), .out(multiplexer_10_out), .sel(\气泡高电平有效 ));
  Multiplexer #(.select(1), .width(32), .disabled("Z"), .enable("false")) multiplexer_11 (
    .in0(AluOut_in), .in1({32{1'b0}}), .out(multiplexer_11_out), .sel(\气泡高电平有效 ));
  Multiplexer #(.select(1), .width(32), .disabled("Z"), .enable("false")) multiplexer_12 (
    .in0(MemOut_in), .in1({32{1'b0}}), .out(multiplexer_12_out), .sel(\气泡高电平有效 ));
  Multiplexer #(.select(1), .width(1), .disabled("Z"), .enable("false")) multiplexer_13 (
    .in0(LHU), .in1(1'b0), .out(multiplexer_13_out), .sel(\气泡高电平有效 ));
  Multiplexer #(.select(1), .width(1), .disabled("Z"), .enable("false")) multiplexer_14 (
    .in0(pause_in), .in1(1'b0), .out(multiplexer_14_out), .sel(\气泡高电平有效 ));
  Multiplexer #(.select(1), .width(1), .disabled("Z"), .enable("false")) multiplexer_15 (
    .in0(Eret_in), .in1(1'b0), .out(multiplexer_15_out), .sel(\气泡高电平有效 ));
  Register #(.width(1), .trigger("rising"), .Select("low")) register_1 (
    .D(multiplexer_1_out), .en(\使能 ), .Q(Syscall_out), .clk(Clk), .clr(Clr));
  Register #(.width(1), .trigger("rising"), .Select("low")) register_2 (
    .D(multiplexer_2_out), .en(\使能 ), .Q(MemToReg_out), .clk(Clk), .clr(Clr));
  Register #(.width(1), .trigger("rising"), .Select("low")) register_3 (
    .D(multiplexer_3_out), .en(\使能 ), .Q(MemWrite_out), .clk(Clk), .clr(Clr));
  Register #(.width(1), .trigger("rising"), .Select("low")) register_4 (
    .D(multiplexer_4_out), .en(\使能 ), .Q(RegWrite_out), .clk(Clk), .clr(Clr));
  Register #(.width(1), .trigger("rising"), .Select("low")) register_5 (
    .D(multiplexer_5_out), .en(\使能 ), .Q(JAL_out), .clk(Clk), .clr(Clr));
  Register #(.width(1), .trigger("rising"), .Select("low")) register_6 (
    .D(multiplexer_6_out), .en(\使能 ), .Q(RegDst_out), .clk(Clk), .clr(Clr));
  Register #(.width(1), .trigger("rising"), .Select("low")) register_7 (
    .D(multiplexer_7_out), .en(\使能 ), .Q(equal_out), .clk(Clk), .clr(Clr));
  Register #(.width(32), .trigger("rising"), .Select("low")) register_8 (
    .D(multiplexer_8_out), .en(\使能 ), .Q(IR_out), .clk(Clk), .clr(Clr));
  Register #(.width(32), .trigger("rising"), .Select("low")) register_9 (
    .D(multiplexer_9_out), .en(\使能 ), .Q(OldPC_out), .clk(Clk), .clr(Clr));
  Register #(.width(32), .trigger("rising"), .Select("low")) register_10 (
    .D(multiplexer_10_out), .en(\使能 ), .Q(PC_out), .clk(Clk), .clr(Clr));
  Register #(.width(32), .trigger("rising"), .Select("low")) register_11 (
    .D(multiplexer_11_out), .en(\使能 ), .Q(AluOut_out), .clk(Clk), .clr(Clr));
  Register #(.width(32), .trigger("rising"), .Select("low")) register_12 (
    .D(multiplexer_12_out), .en(\使能 ), .Q(MemOut_out), .clk(Clk), .clr(Clr));
  Register #(.width(1), .trigger("rising"), .Select("low")) register_13 (
    .D(multiplexer_13_out), .en(\使能 ), .Q(LHU_2), .clk(Clk), .clr(Clr));
  Register #(.width(1), .trigger("rising"), .Select("low")) register_14 (
    .D(multiplexer_14_out), .en(\使能 ), .Q(pause_out), .clk(Clk), .clr(Clr));
  Register #(.width(1), .trigger("rising"), .Select("low")) register_15 (
    .D(multiplexer_15_out), .en(\使能 ), .Q(Eret_out), .clk(Clk), .clr(Clr));
endmodule

module \理想流水线_差异化  (
  output RegWrite,
  output MemWrite,
  output [31:0] IF_PC,
  output [31:0] ID_PC,
  output [31:0] EX_PC,
  output [31:0] M_PC,
  output [31:0] WB_PC,
  output [31:0] RDin,
  output [31:0] MDin,
  output [31:0] LedData
);

  wire AluSrcB, and_1_out, and_2_out, Beq, BGTZ, BGTZ_flag, Bne, CLK, clock_2_out, comparator_1_gt,
       comparator_2_eq, comparator_2_lt, controlled_buffer_1_out, d_ff_1_q, equal, ex_mem_1_equal_out,
       ex_mem_1_jal_out, ex_mem_1_lhu_2, ex_mem_1_memtoreg_out, ex_mem_1_regdst_out, ex_mem_1_regwrite_out,
       ex_mem_1_syscall_out, Go, halt, id_ex_1_jal_out, id_ex_1_lhu_2, id_ex_1_memtoreg_out,
       id_ex_1_memwrite_out, id_ex_1_regdst_out, id_ex_1_regwrite_out, IR1, IR2, IR3, J, JMP, jmp_flag, JR,
       LED, LHU, mem_wb_1_equal_out, mem_wb_1_jal_out, mem_wb_1_memtoreg_out, mem_wb_1_syscall_out,
       multiplexer_4_out, nand_2_out, not_1_out, or_2_out, RegDst, RST, SignedExt, Syscall, W1, W2, W3,
       Write, \单周期硬布线控制器_差异化_1_alu_src , \单周期硬布线控制器_差异化_1_beq , \单周期硬布线控制器_差异化_1_bgtz ,
       \单周期硬布线控制器_差异化_1_bne , \单周期硬布线控制器_差异化_1_jal , \单周期硬布线控制器_差异化_1_jmp , \单周期硬布线控制器_差异化_1_jr ,
       \单周期硬布线控制器_差异化_1_lhu , \单周期硬布线控制器_差异化_1_memtoreg , \单周期硬布线控制器_差异化_1_memwrite ,
       \单周期硬布线控制器_差异化_1_regdst , \单周期硬布线控制器_差异化_1_regwrite , \单周期硬布线控制器_差异化_1_syscall ;
  wire [3:0] id_ex_1_aluop_out, \单周期硬布线控制器_差异化_1_alu_op ;
  wire [4:0] if_id_1_ir_out_3, if_id_1_ir_out_4, if_id_1_ir_out_5, multiplexer_5_out, multiplexer_6_out,
       multiplexer_10_out, w_num;
  wire [5:0] if_id_1_ir_out, if_id_1_ir_out_6;
  wire [10:6] if_id_1_ir_out_2;
  wire [12:0] CNT_num;
  wire [15:0] \LoadUse次数 , multiplexer_12_out, \总周期数 , \插入气泡数 , \无条件分支数 , \条件分支成功数 ;
  wire [27:0] shifter_1_out;
  wire [31:0] adder_1_out, bit_extender_1_out, bit_extender_2_out, bit_extender_3_out, EX_IR,
       ex_mem_1_aluout_out, ex_mem_1_ir_out, ex_mem_1_pc_out, ID_IR, if_id_1_pc_out, IF_IR, imme, IR, MEM_IR,
       mem_wb_1_aluout_out, mem_wb_1_ir_out, mem_wb_1_memout_out, mem_wb_1_pc_out, mips_alu_1_result,
       mips_regifile_1_r1, mips_regifile_1_r2, multiplexer_1_out, multiplexer_2_out, multiplexer_3_out,
       multiplexer_7_out, multiplexer_8_out, multiplexer_9_out, multiplexer_13_out, multiplexer_14_out, PC_4,
       PCBranch, R1, R2, ram_1_data, rom_1_data, shifter_2_out, WB_IR;

  Button \u_总复位  (.out(RST));
  Button _1 (.out(IR1));
  Button _2 (.out(IR2));
  Button _3 (.out(IR3));
  // Probe on \总周期数 
  // Probe on \总周期数 
  Button \u_继续运行  (.out(Go));
  LED #(.active("true")) led_1 (.in(W1));
  LED #(.active("true")) led_2 (.in(W2));
  LED #(.active("true")) led_3 (.in(W3));
  and and_1 (and_1_out, Bne, ~equal);  // AND_Gate
  and and_2 (and_2_out, equal, Beq);
  or or_1 (jmp_flag, and_1_out, and_2_out);
  Multiplexer #(.select(1), .width(32), .disabled("Z"), .enable("false")) multiplexer_1 (
    .in0(adder_1_out), .in1(PCBranch), .out(multiplexer_1_out), .sel(jmp_flag));
  Shifter #(.width(28), .shift("ll")) shifter_1 (.in(IR[27:0]), .\dist (5'b00010), .out(shifter_1_out));
  Hex_Digit_Display hex_digit_display_1 (.value(LedData[31:28]));  // open: dp
  // Probe on IF_PC[19:0]
  // Mips_Probe mips_probe_1: pin names not known; wires that end beside it: IF_IR
  Multiplexer #(.select(2), .width(32), .disabled("Z"), .enable("false")) multiplexer_2 (
    .in0(multiplexer_1_out), .in1(R1), .in2({PC_4[31:28], shifter_1_out}), .in3(R1), .out(multiplexer_2_out),
    .sel({JMP, JR}));
  Hex_Digit_Display hex_digit_display_2 (.value(LedData[23:20]));  // open: dp
  Hex_Digit_Display hex_digit_display_3 (.value(LedData[27:24]));  // open: dp
  // Probe on ID_PC[19:0]
  // Mips_Probe mips_probe_2: pin names not known; wires that end beside it: ID_IR
  Register #(.width(32), .trigger("rising"), .Select("low")) register_1 (
    .D(R2), .Q(LedData), .clk(LED), .clr(RST));  // open: en
  Comparator #(.width(32), .mode("twosComplement")) comparator_1 (
    .a(R1), .b({32{1'b0}}), .gt(comparator_1_gt));  // open: eq, lt
  and and_3 (BGTZ_flag, BGTZ, comparator_1_gt);
  Multiplexer #(.select(1), .width(32), .disabled("Z"), .enable("false")) multiplexer_3 (
    .in0(multiplexer_2_out), .in1(PCBranch), .out(multiplexer_3_out), .sel(BGTZ_flag));
  Hex_Digit_Display hex_digit_display_4 (.value(LedData[15:12]));  // open: dp
  Hex_Digit_Display hex_digit_display_5 (.value(LedData[19:16]));  // open: dp
  Multiplexer #(.select(1), .width(1), .disabled("Z"), .enable("false")) multiplexer_4 (
    .in0(1'b1), .in1(Go), .out(multiplexer_4_out), .sel(halt));
  Hex_Digit_Display hex_digit_display_6 (.value(LedData[7:4]));  // open: dp
  Hex_Digit_Display hex_digit_display_7 (.value(LedData[11:8]));  // open: dp
  Clock #(.highDuration(1), .lowDuration(1)) clock_1 (.out(CLK));
  // Probe on EX_PC[19:0]
  // Mips_Probe mips_probe_3: pin names not known; wires that end beside it: EX_IR
  Register #(.width(32), .trigger("rising"), .Select("low")) PC (
    .D(multiplexer_3_out), .en(multiplexer_4_out), .Q(IF_PC), .clk(CLK), .clr(RST));
  Counter #(.width(16), .max('hffff), .ongoal("wrap"), .trigger("rising"), .behavior("old")) counter_1 (
    .load(1'b0), .count(multiplexer_4_out), .Q(\总周期数 ), .clk(CLK), .clr(RST));  // open: D, carry, preset
  not not_1 (not_1_out, Go);
  nand nand_1 (Write, not_1_out, halt);
  Hex_Digit_Display hex_digit_display_8 (.value(LedData[3:0]));  // open: dp
  Adder #(.width(32)) adder_1 (.a(IF_PC), .b(32'h4), .out(adder_1_out));  // open: cin, cout
  // Probe on \总周期数 
  // Probe on M_PC[19:0]
  // Mips_Probe mips_probe_4: pin names not known; wires that end beside it: MEM_IR
  // Probe on \总周期数 
  // Probe on \无条件分支数 
  // Probe on \条件分支成功数 
  // Probe on \插入气泡数 
  // Probe on \LoadUse次数 
  ROM #(.addrWidth(10), .dataWidth(32), .Select("high")) rom_1 (.addr(IF_PC[11:2]), .data(rom_1_data));
  // Probe on IF_PC[11:0]
  // Probe on WB_PC[19:0]
  // Mips_Probe mips_probe_5: pin names not known; wires that end beside it: WB_IR
  // Mips_Probe mips_probe_6: pin names not known; wires that end beside it: rom_1_data
  // Probe on ID_PC[11:0]
  // Probe on EX_PC[11:0]
  IF_ID if_id_1 (
    .IR_in(rom_1_data), .OldPC_in(IF_PC), .PC_in(adder_1_out),
    .IR_out({if_id_1_ir_out_6, if_id_1_ir_out_5, if_id_1_ir_out_4, if_id_1_ir_out_3, if_id_1_ir_out_2, if_id_1_ir_out}),
    .OldPC_out(ID_PC), .PC_out(if_id_1_pc_out), .\气泡高电平有效 (1'b0), .\使能 (Write), .Clk(CLK), .Clr(RST));  // open: PredJmp_in, PredJmp_out
  // Probe on M_PC[11:0]
  D_Flip_Flop #(.trigger("high"), .Pre_Clr_Positions("LEGACY"), .NegatePresetClear("false"), .enable("true"), .NewFFLayout("false")) d_ff_1 (.Q(d_ff_1_q));  // open: clk, D, Qn, preset, en, reset
  // Probe on 13'hc
  // Probe on WB_PC[11:0]
  Comparator #(.width(13), .mode("twosComplement")) comparator_2 (
    .a(CNT_num), .b(13'hc), .eq(comparator_2_eq), .lt(comparator_2_lt));  // open: gt
  Clock #(.highDuration(1), .lowDuration(1)) clock_2 (.out(clock_2_out));
  nand nand_2 (nand_2_out, d_ff_1_q, comparator_2_eq);
  Counter #(.width(13), .max('h1fff), .ongoal("stay"), .trigger("rising"), .behavior("old")) counter_2 (
    .count(comparator_2_lt), .Q(CNT_num), .clk(clock_2_out));  // open: load, D, carry, clr, preset
  assign bit_extender_1_out = {{16{1'b0}}, {if_id_1_ir_out_3, if_id_1_ir_out_2, if_id_1_ir_out}};  // Bit_Extender bit_extender_1
  assign bit_extender_2_out = {{16{if_id_1_ir_out_3[4]}}, {if_id_1_ir_out_3, if_id_1_ir_out_2, if_id_1_ir_out}};  // Bit_Extender bit_extender_2
  assign controlled_buffer_1_out = nand_2_out ? clock_2_out : 1'bz;  // Controlled_Buffer controlled_buffer_1
  \单周期硬布线控制器_差异化  \u_单周期硬布线控制器_差异化_1  (
    .OP(if_id_1_ir_out_6), .Func(if_id_1_ir_out), .ALU_OP(\单周期硬布线控制器_差异化_1_alu_op ),
    .MemToReg(\单周期硬布线控制器_差异化_1_memtoreg ), .MemWrite(\单周期硬布线控制器_差异化_1_memwrite ),
    .ALU_SRC(\单周期硬布线控制器_差异化_1_alu_src ), .RegWrite(\单周期硬布线控制器_差异化_1_regwrite ),
    .SysCALL(\单周期硬布线控制器_差异化_1_syscall ), .SignedExt(SignedExt), .RegDst(\单周期硬布线控制器_差异化_1_regdst ),
    .Beq(\单周期硬布线控制器_差异化_1_beq ), .Bne(\单周期硬布线控制器_差异化_1_bne ), .JR(\单周期硬布线控制器_差异化_1_jr ),
    .JMP(\单周期硬布线控制器_差异化_1_jmp ), .JAL(\单周期硬布线控制器_差异化_1_jal ), .BGTZ(\单周期硬布线控制器_差异化_1_bgtz ),
    .LHU(\单周期硬布线控制器_差异化_1_lhu ));
  Multiplexer #(.select(1), .width(5), .disabled("Z"), .enable("false")) multiplexer_5 (
    .in0(if_id_1_ir_out_5), .in1(5'b00010), .out(multiplexer_5_out), .sel(\单周期硬布线控制器_差异化_1_syscall ));
  Multiplexer #(.select(1), .width(5), .disabled("Z"), .enable("false")) multiplexer_6 (
    .in0(if_id_1_ir_out_4), .in1(5'b00100), .out(multiplexer_6_out), .sel(\单周期硬布线控制器_差异化_1_syscall ));
  Multiplexer #(.select(1), .width(32), .disabled("Z"), .enable("false")) multiplexer_7 (
    .in0(bit_extender_1_out), .in1(bit_extender_2_out), .out(multiplexer_7_out), .sel(SignedExt));
  Pull_Resistor #(.pull(1)) pull_resistor_1 (.node(controlled_buffer_1_out));
  MIPS_Regifile mips_regifile_1 (
    .Din(RDin), .Clk(CLK), .R1(mips_regifile_1_r1), .R2(mips_regifile_1_r2), .WE(RegWrite), .W_num(w_num),
    .R1_num(multiplexer_5_out), .R2_num(multiplexer_6_out));
  ID_EX id_ex_1 (
    .Beq_in(\单周期硬布线控制器_差异化_1_beq ), .Bne_in(\单周期硬布线控制器_差异化_1_bne ), .MemToReg_in(\单周期硬布线控制器_差异化_1_memtoreg ),
    .MemWrite_in(\单周期硬布线控制器_差异化_1_memwrite ), .AluSrcB_in(\单周期硬布线控制器_差异化_1_alu_src ),
    .RegWrite_in(\单周期硬布线控制器_差异化_1_regwrite ), .JAL_in(\单周期硬布线控制器_差异化_1_jal ),
    .RegDst_in(\单周期硬布线控制器_差异化_1_regdst ), .JMP_in(\单周期硬布线控制器_差异化_1_jmp ), .JR_in(\单周期硬布线控制器_差异化_1_jr ),
    .SignedExt_in(SignedExt), .AluOP_in(\单周期硬布线控制器_差异化_1_alu_op ),
    .IR_in({if_id_1_ir_out_6, if_id_1_ir_out_5, if_id_1_ir_out_4, if_id_1_ir_out_3, if_id_1_ir_out_2, if_id_1_ir_out}),
    .OldPC_in(ID_PC), .PC_in(if_id_1_pc_out), .R1_in(mips_regifile_1_r1), .R2_in(mips_regifile_1_r2),
    .imm_in(multiplexer_7_out), .Beq_out(Beq), .Bne_out(Bne), .MemToReg_out(id_ex_1_memtoreg_out),
    .MemWrite_out(id_ex_1_memwrite_out), .AluSrcB_out(AluSrcB), .RegWrite_out(id_ex_1_regwrite_out),
    .JAL_out(id_ex_1_jal_out), .RegDst_out(id_ex_1_regdst_out), .JMP_out(JMP), .JR_out(JR),
    .AluOP_out(id_ex_1_aluop_out), .IR_out(IR), .OldPC_out(EX_PC), .PC_out(PC_4), .R1_out(R1), .R2_out(R2),
    .imm_out(imme), .\气泡高电平有效 (1'b0), .\使能 (Write), .Clk(CLK), .Clr(RST),
    .Syscall_in(\单周期硬布线控制器_差异化_1_syscall ), .Syscall_out(Syscall), .BGTZ(\单周期硬布线控制器_差异化_1_bgtz ),
    .BGTZ_2(BGTZ), .LHU(\单周期硬布线控制器_差异化_1_lhu ), .LHU_2(id_ex_1_lhu_2));  // open: SignedExt_out, PredJmp_in_Eret_in, PredJmp_out_Eret_in
  Multiplexer #(.select(1), .width(32), .disabled("Z"), .enable("false")) multiplexer_8 (
    .in0(R2), .in1(imme), .out(multiplexer_8_out), .sel(AluSrcB));
  Shifter #(.width(32), .shift("ll")) shifter_2 (.in(imme), .\dist (5'b00010), .out(shifter_2_out));
  Multiplexer #(.select(1), .width(32), .disabled("Z"), .enable("false")) multiplexer_9 (
    .in0(multiplexer_8_out), .in1(32'h22), .out(multiplexer_9_out), .sel(Syscall));
  Adder #(.width(32)) adder_2 (.a(shifter_2_out), .b(PC_4), .out(PCBranch));  // open: cin, cout
  or or_2 (or_2_out, BGTZ_flag, jmp_flag);
  MIPS_ALU mips_alu_1 (
    .X(R1), .Y(multiplexer_9_out), .AluOP(id_ex_1_aluop_out), .Equal(equal), .Result(mips_alu_1_result),
    .shamt(IR[10:6]));  // open: Result_2
  Counter #(.width(16), .max('hffff), .ongoal("wrap"), .trigger("rising"), .behavior("old")) counter_3 (
    .load(1'b0), .count(JMP), .Q(\无条件分支数 ), .clk(CLK), .clr(RST));  // open: D, carry, preset
  Counter #(.width(16), .max('hffff), .ongoal("wrap"), .trigger("rising"), .behavior("old")) counter_4 (
    .load(1'b0), .count(or_2_out), .Q(\条件分支成功数 ), .clk(CLK), .clr(RST));  // open: D, carry, preset
  or or_3 (J, or_2_out, JMP, JR);
  EX_MEM ex_mem_1 (
    .Syscall_in(Syscall), .MemToReg_in(id_ex_1_memtoreg_out), .MemWrite_in(id_ex_1_memwrite_out),
    .RegWrite_in(id_ex_1_regwrite_out), .JAL_in(id_ex_1_jal_out), .RegDst_in(id_ex_1_regdst_out),
    .equal_in(equal), .IR_in(IR), .OldPC_in(EX_PC), .PC_in(PC_4), .AluOut_in(mips_alu_1_result), .R2_in(R2),
    .Syscall_out(ex_mem_1_syscall_out), .MemToReg_out(ex_mem_1_memtoreg_out), .MemWrite_out(MemWrite),
    .RegWrite_out(ex_mem_1_regwrite_out), .JAL_out(ex_mem_1_jal_out), .RegDst_out(ex_mem_1_regdst_out),
    .equal_out(ex_mem_1_equal_out), .IR_out(ex_mem_1_ir_out), .OldPC_out(M_PC), .PC_out(ex_mem_1_pc_out),
    .AluOut_out(ex_mem_1_aluout_out), .R2_out(MDin), .\气泡高电平有效 (1'b0), .\使能 (Write), .Clk(CLK), .Clr(RST),
    .LHU_2(ex_mem_1_lhu_2), .LHU(id_ex_1_lhu_2));  // open: pause_in, pause_out, Eret_in, Eret_in_2
  RAM #(.addrWidth(10), .dataWidth(32), .bus("separate"), .Select("high")) ram_1 (
    .addr(ex_mem_1_aluout_out[11:2]), .din(MDin), .data(ram_1_data), .str(MemWrite), .clk(CLK), .clr(RST));  // open: sel, ld
  MEM_WB mem_wb_1 (
    .Syscall_in(ex_mem_1_syscall_out), .MemToReg_in(ex_mem_1_memtoreg_out), .MemWrite_in(MemWrite),
    .RegWrite_in(ex_mem_1_regwrite_out), .JAL_in(ex_mem_1_jal_out), .RegDst_in(ex_mem_1_regdst_out),
    .equal_in(ex_mem_1_equal_out), .IR_in(ex_mem_1_ir_out), .OldPC_in(M_PC), .PC_in(ex_mem_1_pc_out),
    .AluOut_in(ex_mem_1_aluout_out), .MemOut_in(ram_1_data), .Syscall_out(mem_wb_1_syscall_out),
    .MemToReg_out(mem_wb_1_memtoreg_out), .RegWrite_out(RegWrite), .JAL_out(mem_wb_1_jal_out),
    .RegDst_out(RegDst), .equal_out(mem_wb_1_equal_out), .IR_out(mem_wb_1_ir_out), .OldPC_out(WB_PC),
    .PC_out(mem_wb_1_pc_out), .AluOut_out(mem_wb_1_aluout_out), .MemOut_out(mem_wb_1_memout_out),
    .\气泡高电平有效 (1'b0), .\使能 (Write), .Clk(CLK), .Clr(RST), .LHU_2(LHU), .LHU(ex_mem_1_lhu_2));  // open: MemWrite_out, pause_in, pause_out, Eret_in, Eret_out
  Multiplexer #(.select(1), .width(5), .disabled("Z"), .enable("false")) multiplexer_10 (
    .in0(mem_wb_1_ir_out[20:16]), .in1(mem_wb_1_ir_out[15:11]), .out(multiplexer_10_out), .sel(RegDst));
  Multiplexer #(.select(1), .width(5), .disabled("Z"), .enable("false")) multiplexer_11 (
    .in0(multiplexer_10_out), .in1({5{1'b1}}), .out(w_num), .sel(mem_wb_1_jal_out));
  Multiplexer #(.select(1), .width(16), .disabled("Z"), .enable("false")) multiplexer_12 (
    .in0(mem_wb_1_memout_out[15:0]), .in1(mem_wb_1_memout_out[31:16]), .out(multiplexer_12_out),
    .sel(mem_wb_1_aluout_out[1]));
  Multiplexer #(.select(1), .width(32), .disabled("Z"), .enable("false")) multiplexer_13 (
    .in0(mem_wb_1_aluout_out), .in1(mem_wb_1_memout_out), .out(multiplexer_13_out),
    .sel(mem_wb_1_memtoreg_out));
  assign bit_extender_3_out = {{16{1'b0}}, multiplexer_12_out};  // Bit_Extender bit_extender_3
  Multiplexer #(.select(1), .width(32), .disabled("Z"), .enable("false")) multiplexer_14 (
    .in0(multiplexer_13_out), .in1(bit_extender_3_out), .out(multiplexer_14_out), .sel(LHU));
  Multiplexer #(.select(1), .width(32), .disabled("Z"), .enable("false")) multiplexer_15 (
    .in0(multiplexer_14_out), .in1(mem_wb_1_pc_out), .out(RDin), .sel(mem_wb_1_jal_out));
  and and_4 (halt, ~mem_wb_1_equal_out, mem_wb_1_syscall_out);  // AND_Gate
  and and_5 (LED, mem_wb_1_equal_out, Syscall);

  // Other names for the same wires on the sheet: MEM_PC[31:0] = M_PC; PC[31:0] = IF_PC

  // Notes on the sheet:
  //   中断源
  //   时空图监测，可删除
  //   中断等待指示
  //   数码管输出
  //   指令存储器
  //   PC+4
  //   contents of rom_1 (hex, n*v repeats v):
  //   20090000 200b0010 34118483 20120404 118c00 129400 36318281 22520404 ad310000 2328820 21290004
  //   216bffff 1560fffb 200b0020 20090000 95310000 112020 20020022 c 21290002 216bffff 1560fff9 2002000a c
  //   控制位
  //   流水调试日志用
  //   暂停节拍，不能为0
  //   指令字
  //   戳工具置1进入计数暂停模式，ctrl+k时钟自动运行到对应节拍暂停
  //   ctrl+k关闭时钟连续运行，将控制位置零，进入单步调试模式调试
  //   用这个时钟源需要去掉电路中的其他时钟源
  //   OP
  //   Func
  //   rs
  //   rt
  //   rd
  //   JMP
  //   JR
  //   OP
  //   Func
  //   可计数暂停的时钟源
  //   Beq
  //   Bne
  //   MemToReg
  //   MemWrite
  //   AluOP
  //   AluSrcB
  //   RegWrite
  //   JAL
  //   RegDst
  //   Syscall
  //   为方便自动评测，需要输出流水线各段保存的PC值，注意是PC不是PC+4，另外ID段寄存器写入信息，Mem段内存写入信息也要输出
  //   PCBranch
  //   rt
  //   rd
endmodule

// 单周期硬布线控制器
module \单周期硬布线控制器_差异化  (
  input  [5:0] OP,
  input  [5:0] Func,
  output [3:0] ALU_OP,
  output MemToReg,
  output MemWrite,
  output ALU_SRC,
  output RegWrite,
  output SysCALL,
  output SignedExt,
  output RegDst,
  output Beq,
  output Bne,
  output JR,
  output JMP,
  output JAL,
  output BGTZ,
  output LHU
);

  \运算控制器自动生成_差异化  \u_运算控制器自动生成_差异化_1  (
    .OP0(OP[0]), .OP1(OP[1]), .OP2(OP[2]), .OP3(OP[3]), .OP4(OP[4]), .OP5(OP[5]), .F0(Func[0]), .F1(Func[1]),
    .F2(Func[2]), .F3(Func[3]), .F4(Func[4]), .F5(Func[5]), .S0(ALU_OP[0]), .S1(ALU_OP[1]), .S2(ALU_OP[2]),
    .S3(ALU_OP[3]));
  \控制信号自动生成_差异化  \u_控制信号自动生成_差异化_1  (
    .OP0(OP[0]), .OP1(OP[1]), .OP2(OP[2]), .MemToReg(MemToReg), .OP3(OP[3]), .OP4(OP[4]), .OP5(OP[5]),
    .MemWrite(MemWrite), .F0(Func[0]), .F1(Func[1]), .F2(Func[2]), .F3(Func[3]), .F4(Func[4]), .F5(Func[5]),
    .ALU_SRC(ALU_SRC), .RegWrite(RegWrite), .BGTZ(BGTZ), .SysCALL(SysCALL), .SignedExt(SignedExt),
    .RegDst(RegDst), .BEQ(Beq), .BNE(Bne), .JR(JR), .JUMP(JMP), .JAL(JAL), .LHU(LHU));

  // Other names for the same wires on the sheet: OP_CODE[5:0] = OP

  // Notes on the sheet:
  //   运算器控制器，根据指令生成运算器功能选择信号
  //   控制信号生成，产生数据通路需要的其他控制信号
endmodule
module \运算控制器自动生成_差异化  (
  input  OP0,
  input  OP1,
  input  OP2,
  input  OP3,
  input  OP4,
  input  OP5,
  input  F0,
  input  F1,
  input  F2,
  input  F3,
  input  F4,
  input  F5,
  output S0,
  output S1,
  output S2,
  output S3
);

  wire and_1_out, and_2_out, and_3_out, and_4_out, and_5_out, and_6_out, and_7_out, and_8_out, and_9_out,
       and_10_out, and_11_out, and_12_out, and_13_out, and_14_out, and_15_out, and_16_out, and_17_out,
       and_18_out, and_19_out, and_20_out, and_21_out, and_22_out, and_23_out, and_24_out, and_25_out,
       and_26_out, and_27_out, and_28_out, and_29_out, and_30_out, and_31_out, and_32_out, and_33_out,
       and_34_out, and_35_out, and_36_out, and_37_out, and_38_out, and_39_out, and_40_out, not_1_out,
       not_2_out, not_3_out, not_4_out, not_5_out, not_6_out, not_7_out, not_8_out, not_9_out, not_10_out,
       not_11_out, not_12_out, not_13_out, not_14_out, not_15_out, not_16_out, not_17_out, not_18_out,
       not_19_out, not_20_out, not_21_out, not_22_out, not_23_out, not_24_out, not_25_out, not_26_out,
       not_27_out, not_28_out, not_29_out, not_30_out, not_31_out, not_32_out, not_33_out, not_34_out,
       not_35_out, not_36_out, not_37_out, not_38_out, not_39_out, not_40_out, not_41_out, not_42_out,
       not_43_out, not_44_out, not_45_out, not_46_out, not_47_out, not_48_out, not_49_out, not_50_out,
       not_51_out, not_52_out, not_53_out, not_54_out, not_55_out, not_56_out, not_57_out, not_58_out,
       not_59_out, not_60_out, not_61_out, not_62_out, not_63_out, not_64_out, not_65_out, not_66_out,
       not_67_out, not_68_out, not_69_out, not_70_out, not_71_out, not_72_out, not_73_out, not_74_out,
       not_75_out, not_76_out, not_77_out, not_78_out, not_79_out, not_80_out, not_81_out, not_82_out,
       not_83_out, not_84_out, not_85_out, not_86_out, not_87_out, not_88_out, not_89_out, not_90_out,
       not_91_out, not_92_out, not_93_out, not_94_out, not_95_out, not_96_out, not_97_out, not_98_out,
       not_99_out, not_100_out, not_101_out, not_102_out, not_103_out, not_104_out, not_105_out, not_106_out,
       not_107_out, not_108_out, not_109_out, not_110_out, not_111_out, not_112_out, not_113_out,
       not_114_out, not_115_out, not_116_out, not_117_out, not_118_out, not_119_out, not_120_out,
       not_121_out, not_122_out, not_123_out, not_124_out, not_125_out, not_126_out, not_127_out,
       not_128_out, not_129_out, not_130_out, not_131_out, not_132_out, not_133_out, not_134_out,
       not_135_out, not_136_out, not_137_out, not_138_out, not_139_out, not_140_out, not_141_out,
       not_142_out, not_143_out, not_144_out, not_145_out, not_146_out, not_147_out, not_148_out,
       not_149_out, not_150_out, not_151_out, not_152_out, not_153_out, not_154_out, not_155_out,
       not_156_out, not_157_out, not_158_out, not_159_out, not_160_out, not_161_out, not_162_out,
       not_163_out, not_164_out, not_165_out, not_166_out, not_167_out, not_168_out, not_169_out,
       not_170_out, not_171_out, not_172_out, not_173_out, not_174_out, not_175_out, not_176_out,
       not_177_out, not_178_out, not_179_out, not_180_out, not_181_out, not_182_out, not_183_out,
       not_184_out, not_185_out, not_186_out, not_187_out, not_188_out, not_189_out, not_190_out,
       not_191_out, not_192_out, not_193_out, not_194_out, not_195_out, not_196_out, not_197_out,
       not_198_out, not_199_out, not_200_out, not_201_out, not_202_out, not_203_out, not_204_out,
       not_205_out, not_206_out, not_207_out, not_208_out, not_209_out, not_210_out, not_211_out,
       not_212_out, not_213_out, not_214_out, not_215_out, not_216_out, not_217_out, not_218_out,
       not_219_out, not_220_out, not_221_out, not_222_out, not_223_out, not_224_out, not_225_out,
       not_226_out, not_227_out, not_228_out, not_229_out, not_230_out, not_231_out, not_232_out,
       not_233_out, not_234_out, not_235_out, not_236_out, not_237_out, not_238_out, not_239_out,
       not_240_out, not_241_out, not_242_out, not_243_out, not_244_out, not_245_out, not_246_out,
       not_247_out, not_248_out, not_249_out, not_250_out, not_251_out, not_252_out, not_253_out,
       not_254_out, not_255_out, not_256_out, not_257_out, not_258_out, not_259_out, not_260_out,
       not_261_out, not_262_out, not_263_out, not_264_out, not_265_out, not_266_out;

  not not_1 (not_1_out, OP5);
  not not_2 (not_2_out, OP4);
  not not_3 (not_3_out, OP3);
  not not_4 (not_4_out, OP2);
  not not_5 (not_5_out, OP1);
  not not_6 (not_6_out, OP0);
  not not_7 (not_7_out, F5);
  not not_8 (not_8_out, F4);
  not not_9 (not_9_out, F3);
  not not_10 (not_10_out, F2);
  not not_11 (not_11_out, OP5);
  not not_12 (not_12_out, OP4);
  not not_13 (not_13_out, OP3);
  not not_14 (not_14_out, OP2);
  not not_15 (not_15_out, OP1);
  not not_16 (not_16_out, OP0);
  not not_17 (not_17_out, F4);
  not not_18 (not_18_out, F3);
  not not_19 (not_19_out, F2);
  not not_20 (not_20_out, F1);
  not not_21 (not_21_out, F0);
  not not_22 (not_22_out, OP5);
  not not_23 (not_23_out, OP4);
  not not_24 (not_24_out, OP3);
  not not_25 (not_25_out, OP2);
  not not_26 (not_26_out, OP1);
  not not_27 (not_27_out, OP0);
  not not_28 (not_28_out, F4);
  not not_29 (not_29_out, F3);
  not not_30 (not_30_out, F2);
  not not_31 (not_31_out, F1);
  not not_32 (not_32_out, OP5);
  not not_33 (not_33_out, OP4);
  not not_34 (not_34_out, OP3);
  not not_35 (not_35_out, OP2);
  not not_36 (not_36_out, OP1);
  not not_37 (not_37_out, OP0);
  not not_38 (not_38_out, F4);
  not not_39 (not_39_out, F3);
  not not_40 (not_40_out, F1);
  not not_41 (not_41_out, F0);
  not not_42 (not_42_out, OP5);
  not not_43 (not_43_out, OP4);
  not not_44 (not_44_out, OP3);
  not not_45 (not_45_out, OP2);
  not not_46 (not_46_out, OP1);
  not not_47 (not_47_out, OP0);
  not not_48 (not_48_out, F4);
  not not_49 (not_49_out, F2);
  not not_50 (not_50_out, F0);
  not not_51 (not_51_out, OP5);
  not not_52 (not_52_out, OP4);
  not not_53 (not_53_out, OP2);
  not not_54 (not_54_out, OP1);
  not not_55 (not_55_out, OP0);
  not not_56 (not_56_out, OP5);
  not not_57 (not_57_out, OP4);
  not not_58 (not_58_out, OP1);
  not not_59 (not_59_out, OP0);
  not not_60 (not_60_out, OP5);
  not not_61 (not_61_out, OP4);
  not not_62 (not_62_out, OP2);
  not not_63 (not_63_out, OP1);
  not not_64 (not_64_out, OP5);
  not not_65 (not_65_out, OP4);
  not not_66 (not_66_out, OP2);
  not not_67 (not_67_out, OP0);
  not not_68 (not_68_out, OP4);
  not not_69 (not_69_out, OP3);
  not not_70 (not_70_out, OP2);
  not not_71 (not_71_out, OP4);
  not not_72 (not_72_out, OP2);
  not not_73 (not_73_out, OP5);
  not not_74 (not_74_out, OP4);
  not not_75 (not_75_out, OP3);
  not not_76 (not_76_out, OP2);
  not not_77 (not_77_out, OP1);
  not not_78 (not_78_out, OP0);
  not not_79 (not_79_out, F4);
  not not_80 (not_80_out, F3);
  not not_81 (not_81_out, F0);
  not not_82 (not_82_out, OP5);
  not not_83 (not_83_out, OP4);
  not not_84 (not_84_out, OP0);
  not not_85 (not_85_out, OP4);
  not not_86 (not_86_out, OP3);
  not not_87 (not_87_out, OP1);
  not not_88 (not_88_out, OP5);
  not not_89 (not_89_out, OP4);
  not not_90 (not_90_out, OP3);
  not not_91 (not_91_out, OP2);
  not not_92 (not_92_out, OP1);
  not not_93 (not_93_out, OP0);
  not not_94 (not_94_out, F5);
  not not_95 (not_95_out, F4);
  not not_96 (not_96_out, F3);
  not not_97 (not_97_out, F2);
  not not_98 (not_98_out, F0);
  not not_99 (not_99_out, OP5);
  not not_100 (not_100_out, OP4);
  not not_101 (not_101_out, OP3);
  not not_102 (not_102_out, OP2);
  not not_103 (not_103_out, OP1);
  not not_104 (not_104_out, OP0);
  not not_105 (not_105_out, F4);
  not not_106 (not_106_out, F3);
  not not_107 (not_107_out, F2);
  not not_108 (not_108_out, F0);
  not not_109 (not_109_out, OP5);
  not not_110 (not_110_out, OP4);
  not not_111 (not_111_out, OP3);
  not not_112 (not_112_out, OP2);
  not not_113 (not_113_out, OP1);
  not not_114 (not_114_out, OP0);
  not not_115 (not_115_out, F4);
  not not_116 (not_116_out, F3);
  not not_117 (not_117_out, F1);
  not not_118 (not_118_out, F0);
  not not_119 (not_119_out, OP5);
  not not_120 (not_120_out, OP4);
  not not_121 (not_121_out, OP3);
  not not_122 (not_122_out, OP2);
  not not_123 (not_123_out, OP1);
  not not_124 (not_124_out, OP0);
  not not_125 (not_125_out, F4);
  not not_126 (not_126_out, F3);
  not not_127 (not_127_out, OP5);
  not not_128 (not_128_out, OP4);
  not not_129 (not_129_out, OP3);
  not not_130 (not_130_out, OP2);
  not not_131 (not_131_out, OP1);
  not not_132 (not_132_out, OP0);
  not not_133 (not_133_out, F4);
  not not_134 (not_134_out, F2);
  not not_135 (not_135_out, F0);
  not not_136 (not_136_out, OP5);
  not not_137 (not_137_out, OP4);
  not not_138 (not_138_out, OP1);
  not not_139 (not_139_out, OP0);
  not not_140 (not_140_out, OP5);
  not not_141 (not_141_out, OP4);
  not not_142 (not_142_out, OP2);
  not not_143 (not_143_out, OP0);
  not not_144 (not_144_out, OP5);
  not not_145 (not_145_out, OP4);
  not not_146 (not_146_out, OP3);
  not not_147 (not_147_out, OP2);
  not not_148 (not_148_out, OP1);
  not not_149 (not_149_out, OP0);
  not not_150 (not_150_out, F4);
  not not_151 (not_151_out, F3);
  not not_152 (not_152_out, F2);
  not not_153 (not_153_out, F1);
  not not_154 (not_154_out, F0);
  not not_155 (not_155_out, OP5);
  not not_156 (not_156_out, OP4);
  not not_157 (not_157_out, OP3);
  not not_158 (not_158_out, OP2);
  not not_159 (not_159_out, OP1);
  not not_160 (not_160_out, OP0);
  not not_161 (not_161_out, F4);
  not not_162 (not_162_out, F3);
  not not_163 (not_163_out, F2);
  not not_164 (not_164_out, F1);
  not not_165 (not_165_out, OP5);
  not not_166 (not_166_out, OP4);
  not not_167 (not_167_out, OP3);
  not not_168 (not_168_out, OP2);
  not not_169 (not_169_out, OP1);
  not not_170 (not_170_out, OP0);
  not not_171 (not_171_out, F4);
  not not_172 (not_172_out, F3);
  not not_173 (not_173_out, F2);
  not not_174 (not_174_out, F0);
  not not_175 (not_175_out, OP5);
  not not_176 (not_176_out, OP4);
  not not_177 (not_177_out, OP3);
  not not_178 (not_178_out, OP2);
  not not_179 (not_179_out, OP1);
  not not_180 (not_180_out, OP0);
  not not_181 (not_181_out, F4);
  not not_182 (not_182_out, F3);
  not not_183 (not_183_out, F1);
  not not_184 (not_184_out, F0);
  not not_185 (not_185_out, OP5);
  not not_186 (not_186_out, OP4);
  not not_187 (not_187_out, OP3);
  not not_188 (not_188_out, OP2);
  not not_189 (not_189_out, OP1);
  not not_190 (not_190_out, OP0);
  not not_191 (not_191_out, F4);
  not not_192 (not_192_out, F2);
  not not_193 (not_193_out, OP5);
  not not_194 (not_194_out, OP4);
  not not_195 (not_195_out, OP2);
  not not_196 (not_196_out, OP1);
  not not_197 (not_197_out, OP0);
  not not_198 (not_198_out, OP5);
  not not_199 (not_199_out, OP4);
  not not_200 (not_200_out, OP1);
  not not_201 (not_201_out, OP0);
  not not_202 (not_202_out, OP5);
  not not_203 (not_203_out, OP4);
  not not_204 (not_204_out, OP2);
  not not_205 (not_205_out, OP1);
  not not_206 (not_206_out, OP4);
  not not_207 (not_207_out, OP3);
  not not_208 (not_208_out, OP2);
  not not_209 (not_209_out, OP4);
  not not_210 (not_210_out, OP2);
  not not_211 (not_211_out, OP4);
  not not_212 (not_212_out, OP3);
  not not_213 (not_213_out, OP1);
  not not_214 (not_214_out, OP5);
  not not_215 (not_215_out, OP4);
  not not_216 (not_216_out, OP3);
  not not_217 (not_217_out, OP2);
  not not_218 (not_218_out, OP1);
  not not_219 (not_219_out, OP0);
  not not_220 (not_220_out, F4);
  not not_221 (not_221_out, F3);
  not not_222 (not_222_out, F1);
  not not_223 (not_223_out, OP5);
  not not_224 (not_224_out, OP4);
  not not_225 (not_225_out, OP3);
  not not_226 (not_226_out, OP2);
  not not_227 (not_227_out, OP1);
  not not_228 (not_228_out, OP0);
  not not_229 (not_229_out, F4);
  not not_230 (not_230_out, F3);
  not not_231 (not_231_out, OP5);
  not not_232 (not_232_out, OP4);
  not not_233 (not_233_out, OP3);
  not not_234 (not_234_out, OP2);
  not not_235 (not_235_out, OP1);
  not not_236 (not_236_out, OP0);
  not not_237 (not_237_out, F4);
  not not_238 (not_238_out, F2);
  not not_239 (not_239_out, F0);
  not not_240 (not_240_out, OP5);
  not not_241 (not_241_out, OP4);
  not not_242 (not_242_out, OP3);
  not not_243 (not_243_out, OP2);
  not not_244 (not_244_out, OP1);
  not not_245 (not_245_out, OP0);
  not not_246 (not_246_out, F4);
  not not_247 (not_247_out, F2);
  not not_248 (not_248_out, OP5);
  not not_249 (not_249_out, OP4);
  not not_250 (not_250_out, OP2);
  not not_251 (not_251_out, OP0);
  not not_252 (not_252_out, OP5);
  not not_253 (not_253_out, OP4);
  not not_254 (not_254_out, OP1);
  not not_255 (not_255_out, OP5);
  not not_256 (not_256_out, OP4);
  not not_257 (not_257_out, OP3);
  not not_258 (not_258_out, OP2);
  not not_259 (not_259_out, OP1);
  not not_260 (not_260_out, OP0);
  not not_261 (not_261_out, F4);
  not not_262 (not_262_out, F3);
  not not_263 (not_263_out, F0);
  not not_264 (not_264_out, OP5);
  not not_265 (not_265_out, OP4);
  not not_266 (not_266_out, OP0);
  and and_1 (and_1_out, not_1_out, not_2_out, not_3_out, not_4_out, not_5_out, not_6_out, not_7_out, not_8_out, not_9_out, not_10_out, F1, F0);
  and and_2 (and_2_out, not_11_out, not_12_out, not_13_out, not_14_out, not_15_out, not_16_out, F5, not_17_out, not_18_out, not_19_out, not_20_out, not_21_out);
  and and_3 (and_3_out, not_22_out, not_23_out, not_24_out, not_25_out, not_26_out, not_27_out, F5, not_28_out, not_29_out, not_30_out, not_31_out, F0);
  and and_4 (and_4_out, not_32_out, not_33_out, not_34_out, not_35_out, not_36_out, not_37_out, F5, not_38_out, not_39_out, F2, not_40_out, not_41_out);
  and and_5 (and_5_out, not_42_out, not_43_out, not_44_out, not_45_out, not_46_out, not_47_out, F5, not_48_out, F3, not_49_out, F1, not_50_out);
  and and_6 (and_6_out, not_51_out, not_52_out, OP3, not_53_out, not_54_out, not_55_out);
  and and_7 (and_7_out, not_56_out, not_57_out, OP3, OP2, not_58_out, not_59_out);
  and and_8 (and_8_out, not_60_out, not_61_out, OP3, not_62_out, not_63_out, OP0);
  and and_9 (and_9_out, not_64_out, not_65_out, OP3, not_66_out, OP1, not_67_out);
  and and_10 (and_10_out, OP5, not_68_out, not_69_out, not_70_out, OP1, OP0);
  and and_11 (and_11_out, OP5, not_71_out, OP3, not_72_out, OP1, OP0);
  and and_12 (and_12_out, not_73_out, not_74_out, not_75_out, not_76_out, not_77_out, not_78_out, F5, not_79_out, not_80_out, F2, F1, not_81_out);
  and and_13 (and_13_out, not_82_out, not_83_out, OP3, OP2, OP1, not_84_out);
  and and_14 (and_14_out, OP5, not_85_out, not_86_out, OP2, not_87_out, OP0);
  and and_15 (and_15_out, not_88_out, not_89_out, not_90_out, not_91_out, not_92_out, not_93_out, not_94_out, not_95_out, not_96_out, not_97_out, F1, not_98_out);
  and and_16 (and_16_out, not_99_out, not_100_out, not_101_out, not_102_out, not_103_out, not_104_out, F5, not_105_out, not_106_out, not_107_out, F1, not_108_out);
  and and_17 (and_17_out, not_109_out, not_110_out, not_111_out, not_112_out, not_113_out, not_114_out, F5, not_115_out, not_116_out, F2, not_117_out, not_118_out);
  and and_18 (and_18_out, not_119_out, not_120_out, not_121_out, not_122_out, not_123_out, not_124_out, F5, not_125_out, not_126_out, F2, F1, F0);
  and and_19 (and_19_out, not_127_out, not_128_out, not_129_out, not_130_out, not_131_out, not_132_out, F5, not_133_out, F3, not_134_out, F1, not_135_out);
  and and_20 (and_20_out, not_136_out, not_137_out, OP3, OP2, not_138_out, not_139_out);
  and and_21 (and_21_out, not_140_out, not_141_out, OP3, not_142_out, OP1, not_143_out);
  and and_22 (and_22_out, not_144_out, not_145_out, not_146_out, not_147_out, not_148_out, not_149_out, F5, not_150_out, not_151_out, not_152_out, not_153_out, not_154_out);
  and and_23 (and_23_out, not_155_out, not_156_out, not_157_out, not_158_out, not_159_out, not_160_out, F5, not_161_out, not_162_out, not_163_out, not_164_out, F0);
  and and_24 (and_24_out, not_165_out, not_166_out, not_167_out, not_168_out, not_169_out, not_170_out, F5, not_171_out, not_172_out, not_173_out, F1, not_174_out);
  and and_25 (and_25_out, not_175_out, not_176_out, not_177_out, not_178_out, not_179_out, not_180_out, F5, not_181_out, not_182_out, F2, not_183_out, not_184_out);
  and and_26 (and_26_out, not_185_out, not_186_out, not_187_out, not_188_out, not_189_out, not_190_out, F5, not_191_out, F3, not_192_out, F1, F0);
  and and_27 (and_27_out, not_193_out, not_194_out, OP3, not_195_out, not_196_out, not_197_out);
  and and_28 (and_28_out, not_198_out, not_199_out, OP3, OP2, not_200_out, not_201_out);
  and and_29 (and_29_out, not_202_out, not_203_out, OP3, not_204_out, not_205_out, OP0);
  and and_30 (and_30_out, OP5, not_206_out, not_207_out, not_208_out, OP1, OP0);
  and and_31 (and_31_out, OP5, not_209_out, OP3, not_210_out, OP1, OP0);
  and and_32 (and_32_out, OP5, not_211_out, not_212_out, OP2, not_213_out, OP0);
  and and_33 (and_33_out, not_214_out, not_215_out, not_216_out, not_217_out, not_218_out, not_219_out, F5, not_220_out, not_221_out, F2, not_222_out, F0);
  and and_34 (and_34_out, not_223_out, not_224_out, not_225_out, not_226_out, not_227_out, not_228_out, F5, not_229_out, not_230_out, F2, F1, F0);
  and and_35 (and_35_out, not_231_out, not_232_out, not_233_out, not_234_out, not_235_out, not_236_out, F5, not_237_out, F3, not_238_out, F1, not_239_out);
  and and_36 (and_36_out, not_240_out, not_241_out, not_242_out, not_243_out, not_244_out, not_245_out, F5, not_246_out, F3, not_247_out, F1, F0);
  and and_37 (and_37_out, not_248_out, not_249_out, OP3, not_250_out, OP1, not_251_out);
  and and_38 (and_38_out, not_252_out, not_253_out, OP3, OP2, not_254_out, OP0);
  and and_39 (and_39_out, not_255_out, not_256_out, not_257_out, not_258_out, not_259_out, not_260_out, F5, not_261_out, not_262_out, F2, F1, not_263_out);
  and and_40 (and_40_out, not_264_out, not_265_out, OP3, OP2, OP1, not_266_out);
  or or_1 (S1, and_15_out, and_16_out, and_17_out, and_18_out, and_19_out, and_20_out, and_21_out);
  or or_2 (S2, and_22_out, and_23_out, and_24_out, and_25_out, and_26_out, and_27_out, and_28_out, and_29_out, and_30_out, and_31_out, and_32_out);
  or or_3 (S3, and_33_out, and_34_out, and_35_out, and_36_out, and_37_out, and_38_out, and_39_out, and_40_out);
  or or_4 (S0, and_1_out, and_2_out, and_3_out, and_4_out, and_5_out, and_6_out, and_7_out, and_8_out, and_9_out, and_10_out, and_11_out, and_12_out, and_13_out, and_14_out);
endmodule

module \控制信号自动生成_差异化  (
  input  OP0,
  input  OP1,
  input  OP2,
  input  OP3,
  input  OP4,
  input  OP5,
  input  F0,
  input  F1,
  input  F2,
  input  F3,
  input  F4,
  input  F5,
  output MemToReg,
  output MemWrite,
  output ALU_SRC,
  output RegWrite,
  output BGTZ,
  output SysCALL,
  output SignedExt,
  output RegDst,
  output BEQ,
  output BNE,
  output JR,
  output JUMP,
  output JAL,
  output LHU
);

  wire and_1_out, and_2_out, and_4_out, and_5_out, and_6_out, and_7_out, and_8_out, and_9_out, and_10_out,
       and_11_out, and_12_out, and_13_out, and_14_out, and_15_out, and_16_out, and_17_out, and_18_out,
       and_19_out, and_20_out, and_21_out, and_22_out, and_23_out, and_24_out, and_25_out, and_26_out,
       and_27_out, and_28_out, and_29_out, and_30_out, and_31_out, and_32_out, and_33_out, and_36_out,
       and_37_out, and_38_out, and_39_out, and_40_out, and_41_out, and_42_out, and_43_out, and_44_out,
       and_45_out, and_46_out, and_47_out, and_48_out, and_49_out, and_50_out, and_51_out, and_52_out,
       and_53_out, and_54_out, and_55_out, and_56_out, and_60_out, and_61_out, and_62_out, not_1_out,
       not_2_out, not_3_out, not_4_out, not_5_out, not_6_out, not_7_out, not_8_out, not_9_out, not_10_out,
       not_11_out, not_12_out, not_13_out, not_14_out, not_15_out, not_16_out, not_17_out, not_18_out,
       not_19_out, not_20_out, not_21_out, not_22_out, not_23_out, not_24_out, not_25_out, not_26_out,
       not_27_out, not_28_out, not_29_out, not_30_out, not_31_out, not_32_out, not_33_out, not_34_out,
       not_35_out, not_36_out, not_37_out, not_38_out, not_39_out, not_40_out, not_41_out, not_42_out,
       not_43_out, not_44_out, not_45_out, not_46_out, not_47_out, not_48_out, not_49_out, not_50_out,
       not_51_out, not_52_out, not_53_out, not_54_out, not_55_out, not_56_out, not_57_out, not_58_out,
       not_59_out, not_60_out, not_61_out, not_62_out, not_63_out, not_64_out, not_65_out, not_66_out,
       not_67_out, not_68_out, not_69_out, not_70_out, not_71_out, not_72_out, not_73_out, not_74_out,
       not_75_out, not_76_out, not_77_out, not_78_out, not_79_out, not_80_out, not_81_out, not_82_out,
       not_83_out, not_84_out, not_85_out, not_86_out, not_87_out, not_88_out, not_89_out, not_90_out,
       not_91_out, not_92_out, not_93_out, not_94_out, not_95_out, not_96_out, not_97_out, not_98_out,
       not_99_out, not_100_out, not_101_out, not_102_out, not_103_out, not_104_out, not_105_out, not_106_out,
       not_107_out, not_108_out, not_109_out, not_110_out, not_111_out, not_112_out, not_113_out,
       not_114_out, not_115_out, not_116_out, not_117_out, not_118_out, not_119_out, not_120_out,
       not_121_out, not_122_out, not_123_out, not_124_out, not_125_out, not_126_out, not_127_out,
       not_128_out, not_129_out, not_130_out, not_131_out, not_132_out, not_133_out, not_134_out,
       not_135_out, not_136_out, not_137_out, not_138_out, not_139_out, not_140_out, not_141_out,
       not_142_out, not_143_out, not_144_out, not_145_out, not_146_out, not_147_out, not_148_out,
       not_149_out, not_150_out, not_151_out, not_152_out, not_153_out, not_154_out, not_155_out,
       not_156_out, not_157_out, not_158_out, not_159_out, not_160_out, not_161_out, not_162_out,
       not_163_out, not_164_out, not_165_out, not_166_out, not_167_out, not_168_out, not_169_out,
       not_170_out, not_171_out, not_172_out, not_173_out, not_174_out, not_175_out, not_176_out,
       not_177_out, not_178_out, not_179_out, not_180_out, not_181_out, not_182_out, not_183_out,
       not_184_out, not_185_out, not_186_out, not_187_out, not_188_out, not_189_out, not_190_out,
       not_191_out, not_192_out, not_193_out, not_194_out, not_195_out, not_196_out, not_197_out,
       not_198_out, not_199_out, not_200_out, not_201_out, not_202_out, not_203_out, not_204_out,
       not_205_out, not_206_out, not_207_out, not_208_out, not_209_out, not_210_out, not_211_out,
       not_212_out, not_213_out, not_214_out, not_215_out, not_216_out, not_217_out, not_218_out,
       not_219_out, not_220_out, not_221_out, not_222_out, not_223_out, not_224_out, not_225_out,
       not_226_out, not_227_out, not_228_out, not_229_out, not_230_out, not_231_out, not_232_out,
       not_233_out, not_234_out, not_235_out, not_236_out, not_237_out, not_238_out, not_239_out,
       not_240_out, not_241_out, not_242_out, not_243_out, not_244_out, not_245_out, not_246_out,
       not_247_out, not_248_out, not_249_out, not_250_out, not_251_out, not_252_out, not_253_out,
       not_254_out, not_255_out, not_256_out, not_257_out, not_258_out, not_259_out, not_260_out,
       not_261_out, not_262_out, not_263_out, not_264_out, not_265_out, not_266_out, not_267_out,
       not_268_out, not_269_out, not_270_out, not_271_out, not_272_out, not_273_out, not_274_out,
       not_275_out, not_276_out, not_277_out, not_278_out, not_279_out, not_280_out, not_281_out,
       not_282_out, not_283_out, not_284_out, not_285_out, not_286_out, not_287_out, not_288_out,
       not_289_out, not_290_out, not_291_out, not_292_out, not_293_out, not_294_out, not_295_out,
       not_296_out, not_297_out, not_298_out, not_299_out, not_300_out, not_301_out, not_302_out,
       not_303_out, not_304_out, not_305_out, not_306_out, not_307_out, not_308_out, not_309_out,
       not_310_out, not_311_out, not_312_out, not_313_out, not_314_out, not_315_out, not_316_out,
       not_317_out, not_318_out, not_319_out, not_320_out, not_321_out, not_322_out, not_323_out,
       not_324_out, not_325_out, not_326_out, not_327_out, not_328_out, not_329_out, not_330_out,
       not_331_out, not_332_out, not_333_out, not_334_out, not_335_out, not_336_out, not_337_out,
       not_338_out, not_339_out, not_340_out, not_341_out, not_342_out, not_343_out, not_344_out,
       not_345_out, not_346_out, not_347_out, not_348_out, not_349_out, not_350_out, not_351_out,
       not_352_out, not_353_out, not_354_out, not_355_out, not_356_out, not_357_out, not_358_out,
       not_359_out, not_360_out, not_361_out, not_362_out, not_363_out, not_364_out, not_365_out,
       not_366_out, not_367_out, not_368_out, not_369_out, not_370_out, not_371_out, not_372_out,
       not_373_out, not_374_out, not_375_out, not_376_out, not_377_out, not_378_out, not_379_out,
       not_380_out, not_381_out, not_382_out, not_383_out, not_384_out, not_385_out, not_386_out,
       not_387_out, not_388_out, not_389_out, not_390_out, not_391_out, not_392_out, not_393_out,
       not_394_out, not_395_out, not_396_out, not_397_out, not_398_out, not_399_out;

  not not_1 (not_1_out, OP4);
  not not_2 (not_2_out, OP3);
  not not_3 (not_3_out, OP2);
  not not_4 (not_4_out, OP4);
  not not_5 (not_5_out, OP3);
  not not_6 (not_6_out, OP1);
  not not_7 (not_7_out, OP4);
  not not_8 (not_8_out, OP2);
  not not_9 (not_9_out, OP5);
  not not_10 (not_10_out, OP4);
  not not_11 (not_11_out, OP2);
  not not_12 (not_12_out, OP1);
  not not_13 (not_13_out, OP0);
  not not_14 (not_14_out, OP5);
  not not_15 (not_15_out, OP4);
  not not_16 (not_16_out, OP1);
  not not_17 (not_17_out, OP0);
  not not_18 (not_18_out, OP5);
  not not_19 (not_19_out, OP4);
  not not_20 (not_20_out, OP2);
  not not_21 (not_21_out, OP1);
  not not_22 (not_22_out, OP5);
  not not_23 (not_23_out, OP4);
  not not_24 (not_24_out, OP2);
  not not_25 (not_25_out, OP0);
  not not_26 (not_26_out, OP5);
  not not_27 (not_27_out, OP4);
  not not_28 (not_28_out, OP1);
  not not_29 (not_29_out, OP4);
  not not_30 (not_30_out, OP3);
  not not_31 (not_31_out, OP2);
  not not_32 (not_32_out, OP4);
  not not_33 (not_33_out, OP2);
  not not_34 (not_34_out, OP5);
  not not_35 (not_35_out, OP4);
  not not_36 (not_36_out, OP0);
  not not_37 (not_37_out, OP4);
  not not_38 (not_38_out, OP3);
  not not_39 (not_39_out, OP1);
  not not_40 (not_40_out, OP5);
  not not_41 (not_41_out, OP4);
  not not_42 (not_42_out, OP3);
  not not_43 (not_43_out, OP2);
  not not_44 (not_44_out, OP1);
  not not_45 (not_45_out, OP0);
  not not_46 (not_46_out, F5);
  not not_47 (not_47_out, F4);
  not not_48 (not_48_out, F3);
  not not_49 (not_49_out, F2);
  not not_50 (not_50_out, F1);
  not not_51 (not_51_out, F0);
  not not_52 (not_52_out, OP5);
  not not_53 (not_53_out, OP4);
  not not_54 (not_54_out, OP3);
  not not_55 (not_55_out, OP2);
  not not_56 (not_56_out, OP1);
  not not_57 (not_57_out, OP0);
  not not_58 (not_58_out, F5);
  not not_59 (not_59_out, F4);
  not not_60 (not_60_out, F3);
  not not_61 (not_61_out, F2);
  not not_62 (not_62_out, OP5);
  not not_63 (not_63_out, OP4);
  not not_64 (not_64_out, OP3);
  not not_65 (not_65_out, OP2);
  not not_66 (not_66_out, OP1);
  not not_67 (not_67_out, OP0);
  not not_68 (not_68_out, F5);
  not not_69 (not_69_out, F4);
  not not_70 (not_70_out, F3);
  not not_71 (not_71_out, F2);
  not not_72 (not_72_out, F0);
  not not_73 (not_73_out, OP5);
  not not_74 (not_74_out, OP4);
  not not_75 (not_75_out, OP3);
  not not_76 (not_76_out, OP2);
  not not_77 (not_77_out, OP1);
  not not_78 (not_78_out, OP0);
  not not_79 (not_79_out, F4);
  not not_80 (not_80_out, F3);
  not not_81 (not_81_out, F2);
  not not_82 (not_82_out, F1);
  not not_83 (not_83_out, F0);
  not not_84 (not_84_out, OP5);
  not not_85 (not_85_out, OP4);
  not not_86 (not_86_out, OP3);
  not not_87 (not_87_out, OP2);
  not not_88 (not_88_out, OP1);
  not not_89 (not_89_out, OP0);
  not not_90 (not_90_out, F4);
  not not_91 (not_91_out, F3);
  not not_92 (not_92_out, F2);
  not not_93 (not_93_out, F1);
  not not_94 (not_94_out, OP5);
  not not_95 (not_95_out, OP4);
  not not_96 (not_96_out, OP3);
  not not_97 (not_97_out, OP2);
  not not_98 (not_98_out, OP1);
  not not_99 (not_99_out, OP0);
  not not_100 (not_100_out, F4);
  not not_101 (not_101_out, F3);
  not not_102 (not_102_out, F2);
  not not_103 (not_103_out, F0);
  not not_104 (not_104_out, OP5);
  not not_105 (not_105_out, OP4);
  not not_106 (not_106_out, OP3);
  not not_107 (not_107_out, OP2);
  not not_108 (not_108_out, OP1);
  not not_109 (not_109_out, OP0);
  not not_110 (not_110_out, F4);
  not not_111 (not_111_out, F3);
  not not_112 (not_112_out, F1);
  not not_113 (not_113_out, F0);
  not not_114 (not_114_out, OP5);
  not not_115 (not_115_out, OP4);
  not not_116 (not_116_out, OP3);
  not not_117 (not_117_out, OP2);
  not not_118 (not_118_out, OP1);
  not not_119 (not_119_out, OP0);
  not not_120 (not_120_out, F4);
  not not_121 (not_121_out, F3);
  not not_122 (not_122_out, F1);
  not not_123 (not_123_out, OP5);
  not not_124 (not_124_out, OP4);
  not not_125 (not_125_out, OP3);
  not not_126 (not_126_out, OP2);
  not not_127 (not_127_out, OP1);
  not not_128 (not_128_out, OP0);
  not not_129 (not_129_out, F4);
  not not_130 (not_130_out, F3);
  not not_131 (not_131_out, OP5);
  not not_132 (not_132_out, OP4);
  not not_133 (not_133_out, OP3);
  not not_134 (not_134_out, OP2);
  not not_135 (not_135_out, OP1);
  not not_136 (not_136_out, OP0);
  not not_137 (not_137_out, F4);
  not not_138 (not_138_out, F2);
  not not_139 (not_139_out, F0);
  not not_140 (not_140_out, OP5);
  not not_141 (not_141_out, OP4);
  not not_142 (not_142_out, OP3);
  not not_143 (not_143_out, OP2);
  not not_144 (not_144_out, OP1);
  not not_145 (not_145_out, OP0);
  not not_146 (not_146_out, F4);
  not not_147 (not_147_out, F2);
  not not_148 (not_148_out, OP5);
  not not_149 (not_149_out, OP4);
  not not_150 (not_150_out, OP3);
  not not_151 (not_151_out, OP2);
  not not_152 (not_152_out, OP5);
  not not_153 (not_153_out, OP4);
  not not_154 (not_154_out, OP2);
  not not_155 (not_155_out, OP1);
  not not_156 (not_156_out, OP0);
  not not_157 (not_157_out, OP5);
  not not_158 (not_158_out, OP4);
  not not_159 (not_159_out, OP1);
  not not_160 (not_160_out, OP0);
  not not_161 (not_161_out, OP5);
  not not_162 (not_162_out, OP4);
  not not_163 (not_163_out, OP2);
  not not_164 (not_164_out, OP1);
  not not_165 (not_165_out, OP5);
  not not_166 (not_166_out, OP4);
  not not_167 (not_167_out, OP2);
  not not_168 (not_168_out, OP0);
  not not_169 (not_169_out, OP5);
  not not_170 (not_170_out, OP4);
  not not_171 (not_171_out, OP1);
  not not_172 (not_172_out, OP4);
  not not_173 (not_173_out, OP3);
  not not_174 (not_174_out, OP2);
  not not_175 (not_175_out, OP5);
  not not_176 (not_176_out, OP4);
  not not_177 (not_177_out, OP3);
  not not_178 (not_178_out, OP2);
  not not_179 (not_179_out, OP1);
  not not_180 (not_180_out, OP0);
  not not_181 (not_181_out, F4);
  not not_182 (not_182_out, F3);
  not not_183 (not_183_out, F0);
  not not_184 (not_184_out, OP5);
  not not_185 (not_185_out, OP4);
  not not_186 (not_186_out, OP0);
  not not_187 (not_187_out, OP4);
  not not_188 (not_188_out, OP3);
  not not_189 (not_189_out, OP1);
  not not_190 (not_190_out, OP5);
  not not_191 (not_191_out, OP4);
  not not_192 (not_192_out, OP3);
  not not_193 (not_193_out, OP5);
  not not_194 (not_194_out, OP4);
  not not_195 (not_195_out, OP3);
  not not_196 (not_196_out, OP2);
  not not_197 (not_197_out, OP1);
  not not_198 (not_198_out, OP0);
  not not_199 (not_199_out, F5);
  not not_200 (not_200_out, F4);
  not not_201 (not_201_out, F1);
  not not_202 (not_202_out, F0);
  not not_203 (not_203_out, OP5);
  not not_204 (not_204_out, OP4);
  not not_205 (not_205_out, OP3);
  not not_206 (not_206_out, OP1);
  not not_207 (not_207_out, OP0);
  not not_208 (not_208_out, OP5);
  not not_209 (not_209_out, OP4);
  not not_210 (not_210_out, OP3);
  not not_211 (not_211_out, OP1);
  not not_212 (not_212_out, OP5);
  not not_213 (not_213_out, OP4);
  not not_214 (not_214_out, OP2);
  not not_215 (not_215_out, OP1);
  not not_216 (not_216_out, OP0);
  not not_217 (not_217_out, OP5);
  not not_218 (not_218_out, OP4);
  not not_219 (not_219_out, OP2);
  not not_220 (not_220_out, OP1);
  not not_221 (not_221_out, OP5);
  not not_222 (not_222_out, OP4);
  not not_223 (not_223_out, OP2);
  not not_224 (not_224_out, OP0);
  not not_225 (not_225_out, OP4);
  not not_226 (not_226_out, OP3);
  not not_227 (not_227_out, OP2);
  not not_228 (not_228_out, OP4);
  not not_229 (not_229_out, OP2);
  not not_230 (not_230_out, OP4);
  not not_231 (not_231_out, OP3);
  not not_232 (not_232_out, OP1);
  not not_233 (not_233_out, OP5);
  not not_234 (not_234_out, OP4);
  not not_235 (not_235_out, OP3);
  not not_236 (not_236_out, OP5);
  not not_237 (not_237_out, OP4);
  not not_238 (not_238_out, OP3);
  not not_239 (not_239_out, OP2);
  not not_240 (not_240_out, OP1);
  not not_241 (not_241_out, OP0);
  not not_242 (not_242_out, F5);
  not not_243 (not_243_out, F4);
  not not_244 (not_244_out, F3);
  not not_245 (not_245_out, F2);
  not not_246 (not_246_out, F1);
  not not_247 (not_247_out, F0);
  not not_248 (not_248_out, OP5);
  not not_249 (not_249_out, OP4);
  not not_250 (not_250_out, OP3);
  not not_251 (not_251_out, OP2);
  not not_252 (not_252_out, OP1);
  not not_253 (not_253_out, OP0);
  not not_254 (not_254_out, F5);
  not not_255 (not_255_out, F4);
  not not_256 (not_256_out, F3);
  not not_257 (not_257_out, F2);
  not not_258 (not_258_out, OP5);
  not not_259 (not_259_out, OP4);
  not not_260 (not_260_out, OP3);
  not not_261 (not_261_out, OP2);
  not not_262 (not_262_out, OP1);
  not not_263 (not_263_out, OP0);
  not not_264 (not_264_out, F5);
  not not_265 (not_265_out, F4);
  not not_266 (not_266_out, F3);
  not not_267 (not_267_out, F2);
  not not_268 (not_268_out, F0);
  not not_269 (not_269_out, OP5);
  not not_270 (not_270_out, OP4);
  not not_271 (not_271_out, OP3);
  not not_272 (not_272_out, OP2);
  not not_273 (not_273_out, OP1);
  not not_274 (not_274_out, OP0);
  not not_275 (not_275_out, F4);
  not not_276 (not_276_out, F3);
  not not_277 (not_277_out, F2);
  not not_278 (not_278_out, F1);
  not not_279 (not_279_out, F0);
  not not_280 (not_280_out, OP5);
  not not_281 (not_281_out, OP4);
  not not_282 (not_282_out, OP3);
  not not_283 (not_283_out, OP2);
  not not_284 (not_284_out, OP1);
  not not_285 (not_285_out, OP0);
  not not_286 (not_286_out, F4);
  not not_287 (not_287_out, F3);
  not not_288 (not_288_out, F2);
  not not_289 (not_289_out, F1);
  not not_290 (not_290_out, OP5);
  not not_291 (not_291_out, OP4);
  not not_292 (not_292_out, OP3);
  not not_293 (not_293_out, OP2);
  not not_294 (not_294_out, OP1);
  not not_295 (not_295_out, OP0);
  not not_296 (not_296_out, F4);
  not not_297 (not_297_out, F3);
  not not_298 (not_298_out, F2);
  not not_299 (not_299_out, F0);
  not not_300 (not_300_out, OP5);
  not not_301 (not_301_out, OP4);
  not not_302 (not_302_out, OP3);
  not not_303 (not_303_out, OP2);
  not not_304 (not_304_out, OP1);
  not not_305 (not_305_out, OP0);
  not not_306 (not_306_out, F4);
  not not_307 (not_307_out, F3);
  not not_308 (not_308_out, F1);
  not not_309 (not_309_out, F0);
  not not_310 (not_310_out, OP5);
  not not_311 (not_311_out, OP4);
  not not_312 (not_312_out, OP3);
  not not_313 (not_313_out, OP2);
  not not_314 (not_314_out, OP1);
  not not_315 (not_315_out, OP0);
  not not_316 (not_316_out, F4);
  not not_317 (not_317_out, F3);
  not not_318 (not_318_out, F1);
  not not_319 (not_319_out, OP5);
  not not_320 (not_320_out, OP4);
  not not_321 (not_321_out, OP3);
  not not_322 (not_322_out, OP2);
  not not_323 (not_323_out, OP1);
  not not_324 (not_324_out, OP0);
  not not_325 (not_325_out, F4);
  not not_326 (not_326_out, F3);
  not not_327 (not_327_out, OP5);
  not not_328 (not_328_out, OP4);
  not not_329 (not_329_out, OP3);
  not not_330 (not_330_out, OP2);
  not not_331 (not_331_out, OP1);
  not not_332 (not_332_out, OP0);
  not not_333 (not_333_out, F4);
  not not_334 (not_334_out, F2);
  not not_335 (not_335_out, F0);
  not not_336 (not_336_out, OP5);
  not not_337 (not_337_out, OP4);
  not not_338 (not_338_out, OP3);
  not not_339 (not_339_out, OP2);
  not not_340 (not_340_out, OP1);
  not not_341 (not_341_out, OP0);
  not not_342 (not_342_out, F4);
  not not_343 (not_343_out, F2);
  not not_344 (not_344_out, OP5);
  not not_345 (not_345_out, OP4);
  not not_346 (not_346_out, OP3);
  not not_347 (not_347_out, OP2);
  not not_348 (not_348_out, OP1);
  not not_349 (not_349_out, OP0);
  not not_350 (not_350_out, F4);
  not not_351 (not_351_out, F3);
  not not_352 (not_352_out, F0);
  not not_353 (not_353_out, OP5);
  not not_354 (not_354_out, OP4);
  not not_355 (not_355_out, OP3);
  not not_356 (not_356_out, OP1);
  not not_357 (not_357_out, OP0);
  not not_358 (not_358_out, OP5);
  not not_359 (not_359_out, OP4);
  not not_360 (not_360_out, OP3);
  not not_361 (not_361_out, OP1);
  not not_362 (not_362_out, OP5);
  not not_363 (not_363_out, OP4);
  not not_364 (not_364_out, OP3);
  not not_365 (not_365_out, OP2);
  not not_366 (not_366_out, OP1);
  not not_367 (not_367_out, OP0);
  not not_368 (not_368_out, F5);
  not not_369 (not_369_out, F4);
  not not_370 (not_370_out, F2);
  not not_371 (not_371_out, F1);
  not not_372 (not_372_out, F0);
  not not_373 (not_373_out, OP5);
  not not_374 (not_374_out, OP4);
  not not_375 (not_375_out, OP3);
  not not_376 (not_376_out, OP2);
  not not_377 (not_377_out, OP1);
  not not_378 (not_378_out, OP0);
  not not_379 (not_379_out, F5);
  not not_380 (not_380_out, F4);
  not not_381 (not_381_out, F2);
  not not_382 (not_382_out, F1);
  not not_383 (not_383_out, F0);
  not not_384 (not_384_out, OP5);
  not not_385 (not_385_out, OP4);
  not not_386 (not_386_out, OP3);
  not not_387 (not_387_out, OP2);
  not not_388 (not_388_out, OP0);
  not not_389 (not_389_out, OP5);
  not not_390 (not_390_out, OP4);
  not not_391 (not_391_out, OP3);
  not not_392 (not_392_out, OP2);
  not not_393 (not_393_out, OP5);
  not not_394 (not_394_out, OP4);
  not not_395 (not_395_out, OP3);
  not not_396 (not_396_out, OP2);
  not not_397 (not_397_out, OP4);
  not not_398 (not_398_out, OP3);
  not not_399 (not_399_out, OP1);
  and and_1 (and_1_out, OP5, not_1_out, not_2_out, not_3_out, OP1, OP0);
  and and_2 (and_2_out, OP5, not_4_out, not_5_out, OP2, not_6_out, OP0);
  and and_3 (MemWrite, OP5, not_7_out, OP3, not_8_out, OP1, OP0);
  and and_4 (and_4_out, not_9_out, not_10_out, OP3, not_11_out, not_12_out, not_13_out);
  and and_5 (and_5_out, not_14_out, not_15_out, OP3, OP2, not_16_out, not_17_out);
  and and_6 (and_6_out, not_18_out, not_19_out, OP3, not_20_out, not_21_out, OP0);
  and and_7 (and_7_out, not_22_out, not_23_out, OP3, not_24_out, OP1, not_25_out);
  and and_8 (and_8_out, not_26_out, not_27_out, OP3, OP2, not_28_out, OP0);
  and and_9 (and_9_out, OP5, not_29_out, not_30_out, not_31_out, OP1, OP0);
  and and_10 (and_10_out, OP5, not_32_out, OP3, not_33_out, OP1, OP0);
  and and_11 (and_11_out, not_34_out, not_35_out, OP3, OP2, OP1, not_36_out);
  and and_12 (and_12_out, OP5, not_37_out, not_38_out, OP2, not_39_out, OP0);
  and and_13 (and_13_out, not_40_out, not_41_out, not_42_out, not_43_out, not_44_out, not_45_out, not_46_out, not_47_out, not_48_out, not_49_out, not_50_out, not_51_out);
  and and_14 (and_14_out, not_52_out, not_53_out, not_54_out, not_55_out, not_56_out, not_57_out, not_58_out, not_59_out, not_60_out, not_61_out, F1, F0);
  and and_15 (and_15_out, not_62_out, not_63_out, not_64_out, not_65_out, not_66_out, not_67_out, not_68_out, not_69_out, not_70_out, not_71_out, F1, not_72_out);
  and and_16 (and_16_out, not_73_out, not_74_out, not_75_out, not_76_out, not_77_out, not_78_out, F5, not_79_out, not_80_out, not_81_out, not_82_out, not_83_out);
  and and_17 (and_17_out, not_84_out, not_85_out, not_86_out, not_87_out, not_88_out, not_89_out, F5, not_90_out, not_91_out, not_92_out, not_93_out, F0);
  and and_18 (and_18_out, not_94_out, not_95_out, not_96_out, not_97_out, not_98_out, not_99_out, F5, not_100_out, not_101_out, not_102_out, F1, not_103_out);
  and and_19 (and_19_out, not_104_out, not_105_out, not_106_out, not_107_out, not_108_out, not_109_out, F5, not_110_out, not_111_out, F2, not_112_out, not_113_out);
  and and_20 (and_20_out, not_114_out, not_115_out, not_116_out, not_117_out, not_118_out, not_119_out, F5, not_120_out, not_121_out, F2, not_122_out, F0);
  and and_21 (and_21_out, not_123_out, not_124_out, not_125_out, not_126_out, not_127_out, not_128_out, F5, not_129_out, not_130_out, F2, F1, F0);
  and and_22 (and_22_out, not_131_out, not_132_out, not_133_out, not_134_out, not_135_out, not_136_out, F5, not_137_out, F3, not_138_out, F1, not_139_out);
  and and_23 (and_23_out, not_140_out, not_141_out, not_142_out, not_143_out, not_144_out, not_145_out, F5, not_146_out, F3, not_147_out, F1, F0);
  and and_24 (and_24_out, not_148_out, not_149_out, not_150_out, not_151_out, OP1, OP0);
  and and_25 (and_25_out, not_152_out, not_153_out, OP3, not_154_out, not_155_out, not_156_out);
  and and_26 (and_26_out, not_157_out, not_158_out, OP3, OP2, not_159_out, not_160_out);
  and and_27 (and_27_out, not_161_out, not_162_out, OP3, not_163_out, not_164_out, OP0);
  and and_28 (and_28_out, not_165_out, not_166_out, OP3, not_167_out, OP1, not_168_out);
  and and_29 (and_29_out, not_169_out, not_170_out, OP3, OP2, not_171_out, OP0);
  and and_30 (and_30_out, OP5, not_172_out, not_173_out, not_174_out, OP1, OP0);
  and and_31 (and_31_out, not_175_out, not_176_out, not_177_out, not_178_out, not_179_out, not_180_out, F5, not_181_out, not_182_out, F2, F1, not_183_out);
  and and_32 (and_32_out, not_184_out, not_185_out, OP3, OP2, OP1, not_186_out);
  and and_33 (and_33_out, OP5, not_187_out, not_188_out, OP2, not_189_out, OP0);
  and and_34 (BGTZ, not_190_out, not_191_out, not_192_out, OP2, OP1, OP0);
  and and_35 (SysCALL, not_193_out, not_194_out, not_195_out, not_196_out, not_197_out, not_198_out, not_199_out, not_200_out, F3, F2, not_201_out, not_202_out);
  and and_36 (and_36_out, not_203_out, not_204_out, not_205_out, OP2, not_206_out, not_207_out);
  and and_37 (and_37_out, not_208_out, not_209_out, not_210_out, OP2, not_211_out, OP0);
  and and_38 (and_38_out, not_212_out, not_213_out, OP3, not_214_out, not_215_out, not_216_out);
  and and_39 (and_39_out, not_217_out, not_218_out, OP3, not_219_out, not_220_out, OP0);
  and and_40 (and_40_out, not_221_out, not_222_out, OP3, not_223_out, OP1, not_224_out);
  and and_41 (and_41_out, OP5, not_225_out, not_226_out, not_227_out, OP1, OP0);
  and and_42 (and_42_out, OP5, not_228_out, OP3, not_229_out, OP1, OP0);
  and and_43 (and_43_out, OP5, not_230_out, not_231_out, OP2, not_232_out, OP0);
  and and_44 (and_44_out, not_233_out, not_234_out, not_235_out, OP2, OP1, OP0);
  and and_45 (and_45_out, not_236_out, not_237_out, not_238_out, not_239_out, not_240_out, not_241_out, not_242_out, not_243_out, not_244_out, not_245_out, not_246_out, not_247_out);
  and and_46 (and_46_out, not_248_out, not_249_out, not_250_out, not_251_out, not_252_out, not_253_out, not_254_out, not_255_out, not_256_out, not_257_out, F1, F0);
  and and_47 (and_47_out, not_258_out, not_259_out, not_260_out, not_261_out, not_262_out, not_263_out, not_264_out, not_265_out, not_266_out, not_267_out, F1, not_268_out);
  and and_48 (and_48_out, not_269_out, not_270_out, not_271_out, not_272_out, not_273_out, not_274_out, F5, not_275_out, not_276_out, not_277_out, not_278_out, not_279_out);
  and and_49 (and_49_out, not_280_out, not_281_out, not_282_out, not_283_out, not_284_out, not_285_out, F5, not_286_out, not_287_out, not_288_out, not_289_out, F0);
  and and_50 (and_50_out, not_290_out, not_291_out, not_292_out, not_293_out, not_294_out, not_295_out, F5, not_296_out, not_297_out, not_298_out, F1, not_299_out);
  and and_51 (and_51_out, not_300_out, not_301_out, not_302_out, not_303_out, not_304_out, not_305_out, F5, not_306_out, not_307_out, F2, not_308_out, not_309_out);
  and and_52 (and_52_out, not_310_out, not_311_out, not_312_out, not_313_out, not_314_out, not_315_out, F5, not_316_out, not_317_out, F2, not_318_out, F0);
  and and_53 (and_53_out, not_319_out, not_320_out, not_321_out, not_322_out, not_323_out, not_324_out, F5, not_325_out, not_326_out, F2, F1, F0);
  and and_54 (and_54_out, not_327_out, not_328_out, not_329_out, not_330_out, not_331_out, not_332_out, F5, not_333_out, F3, not_334_out, F1, not_335_out);
  and and_55 (and_55_out, not_336_out, not_337_out, not_338_out, not_339_out, not_340_out, not_341_out, F5, not_342_out, F3, not_343_out, F1, F0);
  and and_56 (and_56_out, not_344_out, not_345_out, not_346_out, not_347_out, not_348_out, not_349_out, F5, not_350_out, not_351_out, F2, F1, not_352_out);
  and and_57 (BEQ, not_353_out, not_354_out, not_355_out, OP2, not_356_out, not_357_out);
  and and_58 (BNE, not_358_out, not_359_out, not_360_out, OP2, not_361_out, OP0);
  and and_59 (JR, not_362_out, not_363_out, not_364_out, not_365_out, not_366_out, not_367_out, not_368_out, not_369_out, F3, not_370_out, not_371_out, not_372_out);
  and and_60 (and_60_out, not_373_out, not_374_out, not_375_out, not_376_out, not_377_out, not_378_out, not_379_out, not_380_out, F3, not_381_out, not_382_out, not_383_out);
  and and_61 (and_61_out, not_384_out, not_385_out, not_386_out, not_387_out, OP1, not_388_out);
  and and_62 (and_62_out, not_389_out, not_390_out, not_391_out, not_392_out, OP1, OP0);
  and and_63 (JAL, not_393_out, not_394_out, not_395_out, not_396_out, OP1, OP0);
  and and_64 (LHU, OP5, not_397_out, not_398_out, OP2, not_399_out, OP0);
  or or_1 (MemToReg, and_1_out, and_2_out);
  or or_2 (ALU_SRC, and_4_out, and_5_out, and_6_out, and_7_out, and_8_out, and_9_out, and_10_out, and_11_out, and_12_out);
  or or_3 (SignedExt, and_36_out, and_37_out, and_38_out, and_39_out, and_40_out, and_41_out, and_42_out, and_43_out, and_44_out);
  or or_4 (JUMP, and_60_out, and_61_out, and_62_out);
  or or_5 (RegWrite, and_13_out, and_14_out, and_15_out, and_16_out, and_17_out, and_18_out, and_19_out, and_20_out, and_21_out, and_22_out, and_23_out, and_24_out, and_25_out, and_26_out, and_27_out, and_28_out, and_29_out, and_30_out, and_31_out, and_32_out, and_33_out);
  or or_6 (RegDst, and_45_out, and_46_out, and_47_out, and_48_out, and_49_out, and_50_out, and_51_out, and_52_out, and_53_out, and_54_out, and_55_out, and_56_out);
endmodule

module \源寄存器使用判断逻辑  (
  input  OP0,
  input  OP1,
  input  OP2,
  input  OP3,
  input  OP4,
  input  OP5,
  input  F0,
  input  F1,
  input  F2,
  input  F3,
  input  F4,
  input  F5,
  output R1_USED,
  output R2_USED
);

  wire and_1_out, and_2_out, and_3_out, and_4_out, and_5_out, and_6_out, and_7_out, and_8_out, and_9_out,
       and_10_out, and_11_out, and_12_out, and_13_out, and_14_out, and_15_out, and_16_out, and_17_out,
       and_18_out, and_19_out, and_20_out, and_21_out, and_22_out, and_23_out, and_24_out, and_25_out,
       and_26_out, and_27_out, and_28_out, and_29_out, and_30_out, and_31_out, and_32_out, and_33_out,
       and_34_out, and_35_out, and_36_out, and_37_out, and_38_out, and_39_out, and_40_out, and_41_out,
       and_42_out, and_43_out, and_44_out, not_1_out, not_2_out, not_3_out, not_4_out, not_5_out, not_6_out,
       not_7_out, not_8_out, not_9_out, not_10_out, not_11_out, not_12_out, not_13_out, not_14_out,
       not_15_out, not_16_out, not_17_out, not_18_out, not_19_out, not_20_out, not_21_out, not_22_out,
       not_23_out, not_24_out, not_25_out, not_26_out, not_27_out, not_28_out, not_29_out, not_30_out,
       not_31_out, not_32_out, not_33_out, not_34_out, not_35_out, not_36_out, not_37_out, not_38_out,
       not_39_out, not_40_out, not_41_out, not_42_out, not_43_out, not_44_out, not_45_out, not_46_out,
       not_47_out, not_48_out, not_49_out, not_50_out, not_51_out, not_52_out, not_53_out, not_54_out,
       not_55_out, not_56_out, not_57_out, not_58_out, not_59_out, not_60_out, not_61_out, not_62_out,
       not_63_out, not_64_out, not_65_out, not_66_out, not_67_out, not_68_out, not_69_out, not_70_out,
       not_71_out, not_72_out, not_73_out, not_74_out, not_75_out, not_76_out, not_77_out, not_78_out,
       not_79_out, not_80_out, not_81_out, not_82_out, not_83_out, not_84_out, not_85_out, not_86_out,
       not_87_out, not_88_out, not_89_out, not_90_out, not_91_out, not_92_out, not_93_out, not_94_out,
       not_95_out, not_96_out, not_97_out, not_98_out, not_99_out, not_100_out, not_101_out, not_102_out,
       not_103_out, not_104_out, not_105_out, not_106_out, not_107_out, not_108_out, not_109_out,
       not_110_out, not_111_out, not_112_out, not_113_out, not_114_out, not_115_out, not_116_out,
       not_117_out, not_118_out, not_119_out, not_120_out, not_121_out, not_122_out, not_123_out,
       not_124_out, not_125_out, not_126_out, not_127_out, not_128_out, not_129_out, not_130_out,
       not_131_out, not_132_out, not_133_out, not_134_out, not_135_out, not_136_out, not_137_out,
       not_138_out, not_139_out, not_140_out, not_141_out, not_142_out, not_143_out, not_144_out,
       not_145_out, not_146_out, not_147_out, not_148_out, not_149_out, not_150_out, not_151_out,
       not_152_out, not_153_out, not_154_out, not_155_out, not_156_out, not_157_out, not_158_out,
       not_159_out, not_160_out, not_161_out, not_162_out, not_163_out, not_164_out, not_165_out,
       not_166_out, not_167_out, not_168_out, not_169_out, not_170_out, not_171_out, not_172_out,
       not_173_out, not_174_out, not_175_out, not_176_out, not_177_out, not_178_out, not_179_out,
       not_180_out, not_181_out, not_182_out, not_183_out, not_184_out, not_185_out, not_186_out,
       not_187_out, not_188_out, not_189_out, not_190_out, not_191_out, not_192_out, not_193_out,
       not_194_out, not_195_out, not_196_out, not_197_out, not_198_out, not_199_out, not_200_out,
       not_201_out, not_202_out, not_203_out, not_204_out, not_205_out, not_206_out, not_207_out,
       not_208_out, not_209_out, not_210_out, not_211_out, not_212_out, not_213_out, not_214_out,
       not_215_out, not_216_out, not_217_out, not_218_out, not_219_out, not_220_out, not_221_out,
       not_222_out, not_223_out, not_224_out, not_225_out, not_226_out, not_227_out, not_228_out,
       not_229_out, not_230_out, not_231_out, not_232_out, not_233_out, not_234_out, not_235_out,
       not_236_out, not_237_out, not_238_out, not_239_out, not_240_out, not_241_out, not_242_out,
       not_243_out, not_244_out, not_245_out, not_246_out, not_247_out, not_248_out, not_249_out,
       not_250_out, not_251_out, not_252_out, not_253_out, not_254_out, not_255_out, not_256_out,
       not_257_out, not_258_out, not_259_out, not_260_out, not_261_out, not_262_out, not_263_out,
       not_264_out, not_265_out, not_266_out, not_267_out, not_268_out, not_269_out, not_270_out,
       not_271_out, not_272_out, not_273_out, not_274_out, not_275_out, not_276_out, not_277_out,
       not_278_out, not_279_out, not_280_out, not_281_out, not_282_out, not_283_out, not_284_out,
       not_285_out, not_286_out, not_287_out, not_288_out, not_289_out, not_290_out, not_291_out,
       not_292_out, not_293_out, not_294_out, not_295_out, not_296_out, not_297_out, not_298_out,
       not_299_out, not_300_out, not_301_out, not_302_out, not_303_out, not_304_out, not_305_out,
       not_306_out, not_307_out, not_308_out, not_309_out, not_310_out, not_311_out, not_312_out,
       not_313_out, not_314_out, not_315_out, not_316_out, not_317_out, not_318_out, not_319_out,
       not_320_out, not_321_out, not_322_out, not_323_out, not_324_out, not_325_out;

  not not_1 (not_1_out, OP5);
  not not_2 (not_2_out, OP4);
  not not_3 (not_3_out, OP3);
  not not_4 (not_4_out, OP2);
  not not_5 (not_5_out, OP1);
  not not_6 (not_6_out, OP0);
  not not_7 (not_7_out, F5);
  not not_8 (not_8_out, F4);
  not not_9 (not_9_out, F3);
  not not_10 (not_10_out, F2);
  not not_11 (not_11_out, F1);
  not not_12 (not_12_out, F0);
  not not_13 (not_13_out, OP5);
  not not_14 (not_14_out, OP4);
  not not_15 (not_15_out, OP3);
  not not_16 (not_16_out, OP2);
  not not_17 (not_17_out, OP1);
  not not_18 (not_18_out, OP0);
  not not_19 (not_19_out, F5);
  not not_20 (not_20_out, F4);
  not not_21 (not_21_out, F3);
  not not_22 (not_22_out, F2);
  not not_23 (not_23_out, OP5);
  not not_24 (not_24_out, OP4);
  not not_25 (not_25_out, OP3);
  not not_26 (not_26_out, OP2);
  not not_27 (not_27_out, OP1);
  not not_28 (not_28_out, OP0);
  not not_29 (not_29_out, F5);
  not not_30 (not_30_out, F4);
  not not_31 (not_31_out, F3);
  not not_32 (not_32_out, F2);
  not not_33 (not_33_out, F0);
  not not_34 (not_34_out, OP5);
  not not_35 (not_35_out, OP4);
  not not_36 (not_36_out, OP3);
  not not_37 (not_37_out, OP2);
  not not_38 (not_38_out, OP1);
  not not_39 (not_39_out, OP0);
  not not_40 (not_40_out, F4);
  not not_41 (not_41_out, F3);
  not not_42 (not_42_out, F2);
  not not_43 (not_43_out, F1);
  not not_44 (not_44_out, F0);
  not not_45 (not_45_out, OP5);
  not not_46 (not_46_out, OP4);
  not not_47 (not_47_out, OP3);
  not not_48 (not_48_out, OP2);
  not not_49 (not_49_out, OP1);
  not not_50 (not_50_out, OP0);
  not not_51 (not_51_out, F4);
  not not_52 (not_52_out, F3);
  not not_53 (not_53_out, F2);
  not not_54 (not_54_out, F1);
  not not_55 (not_55_out, OP5);
  not not_56 (not_56_out, OP4);
  not not_57 (not_57_out, OP3);
  not not_58 (not_58_out, OP2);
  not not_59 (not_59_out, OP1);
  not not_60 (not_60_out, OP0);
  not not_61 (not_61_out, F4);
  not not_62 (not_62_out, F3);
  not not_63 (not_63_out, F2);
  not not_64 (not_64_out, F0);
  not not_65 (not_65_out, OP5);
  not not_66 (not_66_out, OP4);
  not not_67 (not_67_out, OP3);
  not not_68 (not_68_out, OP2);
  not not_69 (not_69_out, OP1);
  not not_70 (not_70_out, OP0);
  not not_71 (not_71_out, F4);
  not not_72 (not_72_out, F3);
  not not_73 (not_73_out, F1);
  not not_74 (not_74_out, F0);
  not not_75 (not_75_out, OP5);
  not not_76 (not_76_out, OP4);
  not not_77 (not_77_out, OP3);
  not not_78 (not_78_out, OP2);
  not not_79 (not_79_out, OP1);
  not not_80 (not_80_out, OP0);
  not not_81 (not_81_out, F4);
  not not_82 (not_82_out, F3);
  not not_83 (not_83_out, F1);
  not not_84 (not_84_out, OP5);
  not not_85 (not_85_out, OP4);
  not not_86 (not_86_out, OP3);
  not not_87 (not_87_out, OP2);
  not not_88 (not_88_out, OP1);
  not not_89 (not_89_out, OP0);
  not not_90 (not_90_out, F4);
  not not_91 (not_91_out, F3);
  not not_92 (not_92_out, OP5);
  not not_93 (not_93_out, OP4);
  not not_94 (not_94_out, OP3);
  not not_95 (not_95_out, OP2);
  not not_96 (not_96_out, OP1);
  not not_97 (not_97_out, OP0);
  not not_98 (not_98_out, F4);
  not not_99 (not_99_out, F2);
  not not_100 (not_100_out, F0);
  not not_101 (not_101_out, OP5);
  not not_102 (not_102_out, OP4);
  not not_103 (not_103_out, OP3);
  not not_104 (not_104_out, OP2);
  not not_105 (not_105_out, OP1);
  not not_106 (not_106_out, OP0);
  not not_107 (not_107_out, F4);
  not not_108 (not_108_out, F2);
  not not_109 (not_109_out, OP5);
  not not_110 (not_110_out, OP4);
  not not_111 (not_111_out, OP3);
  not not_112 (not_112_out, OP2);
  not not_113 (not_113_out, OP1);
  not not_114 (not_114_out, OP0);
  not not_115 (not_115_out, F5);
  not not_116 (not_116_out, F4);
  not not_117 (not_117_out, F2);
  not not_118 (not_118_out, F1);
  not not_119 (not_119_out, F0);
  not not_120 (not_120_out, OP5);
  not not_121 (not_121_out, OP4);
  not not_122 (not_122_out, OP3);
  not not_123 (not_123_out, OP2);
  not not_124 (not_124_out, OP1);
  not not_125 (not_125_out, OP0);
  not not_126 (not_126_out, F5);
  not not_127 (not_127_out, F4);
  not not_128 (not_128_out, F1);
  not not_129 (not_129_out, F0);
  not not_130 (not_130_out, OP5);
  not not_131 (not_131_out, OP4);
  not not_132 (not_132_out, OP3);
  not not_133 (not_133_out, OP1);
  not not_134 (not_134_out, OP0);
  not not_135 (not_135_out, OP5);
  not not_136 (not_136_out, OP4);
  not not_137 (not_137_out, OP3);
  not not_138 (not_138_out, OP1);
  not not_139 (not_139_out, OP5);
  not not_140 (not_140_out, OP4);
  not not_141 (not_141_out, OP2);
  not not_142 (not_142_out, OP1);
  not not_143 (not_143_out, OP0);
  not not_144 (not_144_out, OP5);
  not not_145 (not_145_out, OP4);
  not not_146 (not_146_out, OP1);
  not not_147 (not_147_out, OP0);
  not not_148 (not_148_out, OP5);
  not not_149 (not_149_out, OP4);
  not not_150 (not_150_out, OP2);
  not not_151 (not_151_out, OP1);
  not not_152 (not_152_out, OP5);
  not not_153 (not_153_out, OP4);
  not not_154 (not_154_out, OP2);
  not not_155 (not_155_out, OP0);
  not not_156 (not_156_out, OP5);
  not not_157 (not_157_out, OP4);
  not not_158 (not_158_out, OP1);
  not not_159 (not_159_out, OP4);
  not not_160 (not_160_out, OP3);
  not not_161 (not_161_out, OP2);
  not not_162 (not_162_out, OP4);
  not not_163 (not_163_out, OP2);
  not not_164 (not_164_out, OP5);
  not not_165 (not_165_out, OP4);
  not not_166 (not_166_out, OP3);
  not not_167 (not_167_out, OP2);
  not not_168 (not_168_out, OP1);
  not not_169 (not_169_out, OP0);
  not not_170 (not_170_out, F4);
  not not_171 (not_171_out, F3);
  not not_172 (not_172_out, F0);
  not not_173 (not_173_out, OP5);
  not not_174 (not_174_out, OP4);
  not not_175 (not_175_out, OP0);
  not not_176 (not_176_out, OP4);
  not not_177 (not_177_out, OP3);
  not not_178 (not_178_out, OP1);
  not not_179 (not_179_out, OP5);
  not not_180 (not_180_out, OP4);
  not not_181 (not_181_out, OP3);
  not not_182 (not_182_out, OP5);
  not not_183 (not_183_out, OP4);
  not not_184 (not_184_out, OP3);
  not not_185 (not_185_out, OP2);
  not not_186 (not_186_out, OP1);
  not not_187 (not_187_out, OP0);
  not not_188 (not_188_out, F5);
  not not_189 (not_189_out, F4);
  not not_190 (not_190_out, F3);
  not not_191 (not_191_out, F2);
  not not_192 (not_192_out, F1);
  not not_193 (not_193_out, F0);
  not not_194 (not_194_out, OP5);
  not not_195 (not_195_out, OP4);
  not not_196 (not_196_out, OP3);
  not not_197 (not_197_out, OP2);
  not not_198 (not_198_out, OP1);
  not not_199 (not_199_out, OP0);
  not not_200 (not_200_out, F5);
  not not_201 (not_201_out, F4);
  not not_202 (not_202_out, F3);
  not not_203 (not_203_out, F2);
  not not_204 (not_204_out, OP5);
  not not_205 (not_205_out, OP4);
  not not_206 (not_206_out, OP3);
  not not_207 (not_207_out, OP2);
  not not_208 (not_208_out, OP1);
  not not_209 (not_209_out, OP0);
  not not_210 (not_210_out, F5);
  not not_211 (not_211_out, F4);
  not not_212 (not_212_out, F3);
  not not_213 (not_213_out, F2);
  not not_214 (not_214_out, F0);
  not not_215 (not_215_out, OP5);
  not not_216 (not_216_out, OP4);
  not not_217 (not_217_out, OP3);
  not not_218 (not_218_out, OP2);
  not not_219 (not_219_out, OP1);
  not not_220 (not_220_out, OP0);
  not not_221 (not_221_out, F4);
  not not_222 (not_222_out, F3);
  not not_223 (not_223_out, F2);
  not not_224 (not_224_out, F1);
  not not_225 (not_225_out, F0);
  not not_226 (not_226_out, OP5);
  not not_227 (not_227_out, OP4);
  not not_228 (not_228_out, OP3);
  not not_229 (not_229_out, OP2);
  not not_230 (not_230_out, OP1);
  not not_231 (not_231_out, OP0);
  not not_232 (not_232_out, F4);
  not not_233 (not_233_out, F3);
  not not_234 (not_234_out, F2);
  not not_235 (not_235_out, F1);
  not not_236 (not_236_out, OP5);
  not not_237 (not_237_out, OP4);
  not not_238 (not_238_out, OP3);
  not not_239 (not_239_out, OP2);
  not not_240 (not_240_out, OP1);
  not not_241 (not_241_out, OP0);
  not not_242 (not_242_out, F4);
  not not_243 (not_243_out, F3);
  not not_244 (not_244_out, F2);
  not not_245 (not_245_out, F0);
  not not_246 (not_246_out, OP5);
  not not_247 (not_247_out, OP4);
  not not_248 (not_248_out, OP3);
  not not_249 (not_249_out, OP2);
  not not_250 (not_250_out, OP1);
  not not_251 (not_251_out, OP0);
  not not_252 (not_252_out, F4);
  not not_253 (not_253_out, F3);
  not not_254 (not_254_out, F1);
  not not_255 (not_255_out, F0);
  not not_256 (not_256_out, OP5);
  not not_257 (not_257_out, OP4);
  not not_258 (not_258_out, OP3);
  not not_259 (not_259_out, OP2);
  not not_260 (not_260_out, OP1);
  not not_261 (not_261_out, OP0);
  not not_262 (not_262_out, F4);
  not not_263 (not_263_out, F3);
  not not_264 (not_264_out, F1);
  not not_265 (not_265_out, OP5);
  not not_266 (not_266_out, OP4);
  not not_267 (not_267_out, OP3);
  not not_268 (not_268_out, OP2);
  not not_269 (not_269_out, OP1);
  not not_270 (not_270_out, OP0);
  not not_271 (not_271_out, F4);
  not not_272 (not_272_out, F3);
  not not_273 (not_273_out, OP5);
  not not_274 (not_274_out, OP4);
  not not_275 (not_275_out, OP3);
  not not_276 (not_276_out, OP2);
  not not_277 (not_277_out, OP1);
  not not_278 (not_278_out, OP0);
  not not_279 (not_279_out, F4);
  not not_280 (not_280_out, F2);
  not not_281 (not_281_out, F0);
  not not_282 (not_282_out, OP5);
  not not_283 (not_283_out, OP4);
  not not_284 (not_284_out, OP3);
  not not_285 (not_285_out, OP2);
  not not_286 (not_286_out, OP1);
  not not_287 (not_287_out, OP0);
  not not_288 (not_288_out, F4);
  not not_289 (not_289_out, F2);
  not not_290 (not_290_out, OP5);
  not not_291 (not_291_out, OP4);
  not not_292 (not_292_out, OP3);
  not not_293 (not_293_out, OP2);
  not not_294 (not_294_out, OP1);
  not not_295 (not_295_out, OP0);
  not not_296 (not_296_out, F5);
  not not_297 (not_297_out, F4);
  not not_298 (not_298_out, F1);
  not not_299 (not_299_out, F0);
  not not_300 (not_300_out, OP5);
  not not_301 (not_301_out, OP4);
  not not_302 (not_302_out, OP3);
  not not_303 (not_303_out, OP1);
  not not_304 (not_304_out, OP0);
  not not_305 (not_305_out, OP5);
  not not_306 (not_306_out, OP4);
  not not_307 (not_307_out, OP3);
  not not_308 (not_308_out, OP1);
  not not_309 (not_309_out, OP4);
  not not_310 (not_310_out, OP3);
  not not_311 (not_311_out, OP2);
  not not_312 (not_312_out, OP4);
  not not_313 (not_313_out, OP2);
  not not_314 (not_314_out, OP5);
  not not_315 (not_315_out, OP4);
  not not_316 (not_316_out, OP3);
  not not_317 (not_317_out, OP2);
  not not_318 (not_318_out, OP1);
  not not_319 (not_319_out, OP0);
  not not_320 (not_320_out, F4);
  not not_321 (not_321_out, F3);
  not not_322 (not_322_out, F0);
  not not_323 (not_323_out, OP4);
  not not_324 (not_324_out, OP3);
  not not_325 (not_325_out, OP1);
  and and_1 (and_1_out, not_1_out, not_2_out, not_3_out, not_4_out, not_5_out, not_6_out, not_7_out, not_8_out, not_9_out, not_10_out, not_11_out, not_12_out);
  and and_2 (and_2_out, not_13_out, not_14_out, not_15_out, not_16_out, not_17_out, not_18_out, not_19_out, not_20_out, not_21_out, not_22_out, F1, F0);
  and and_3 (and_3_out, not_23_out, not_24_out, not_25_out, not_26_out, not_27_out, not_28_out, not_29_out, not_30_out, not_31_out, not_32_out, F1, not_33_out);
  and and_4 (and_4_out, not_34_out, not_35_out, not_36_out, not_37_out, not_38_out, not_39_out, F5, not_40_out, not_41_out, not_42_out, not_43_out, not_44_out);
  and and_5 (and_5_out, not_45_out, not_46_out, not_47_out, not_48_out, not_49_out, not_50_out, F5, not_51_out, not_52_out, not_53_out, not_54_out, F0);
  and and_6 (and_6_out, not_55_out, not_56_out, not_57_out, not_58_out, not_59_out, not_60_out, F5, not_61_out, not_62_out, not_63_out, F1, not_64_out);
  and and_7 (and_7_out, not_65_out, not_66_out, not_67_out, not_68_out, not_69_out, not_70_out, F5, not_71_out, not_72_out, F2, not_73_out, not_74_out);
  and and_8 (and_8_out, not_75_out, not_76_out, not_77_out, not_78_out, not_79_out, not_80_out, F5, not_81_out, not_82_out, F2, not_83_out, F0);
  and and_9 (and_9_out, not_84_out, not_85_out, not_86_out, not_87_out, not_88_out, not_89_out, F5, not_90_out, not_91_out, F2, F1, F0);
  and and_10 (and_10_out, not_92_out, not_93_out, not_94_out, not_95_out, not_96_out, not_97_out, F5, not_98_out, F3, not_99_out, F1, not_100_out);
  and and_11 (and_11_out, not_101_out, not_102_out, not_103_out, not_104_out, not_105_out, not_106_out, F5, not_107_out, F3, not_108_out, F1, F0);
  and and_12 (and_12_out, not_109_out, not_110_out, not_111_out, not_112_out, not_113_out, not_114_out, not_115_out, not_116_out, F3, not_117_out, not_118_out, not_119_out);
  and and_13 (and_13_out, not_120_out, not_121_out, not_122_out, not_123_out, not_124_out, not_125_out, not_126_out, not_127_out, F3, F2, not_128_out, not_129_out);
  and and_14 (and_14_out, not_130_out, not_131_out, not_132_out, OP2, not_133_out, not_134_out);
  and and_15 (and_15_out, not_135_out, not_136_out, not_137_out, OP2, not_138_out, OP0);
  and and_16 (and_16_out, not_139_out, not_140_out, OP3, not_141_out, not_142_out, not_143_out);
  and and_17 (and_17_out, not_144_out, not_145_out, OP3, OP2, not_146_out, not_147_out);
  and and_18 (and_18_out, not_148_out, not_149_out, OP3, not_150_out, not_151_out, OP0);
  and and_19 (and_19_out, not_152_out, not_153_out, OP3, not_154_out, OP1, not_155_out);
  and and_20 (and_20_out, not_156_out, not_157_out, OP3, OP2, not_158_out, OP0);
  and and_21 (and_21_out, OP5, not_159_out, not_160_out, not_161_out, OP1, OP0);
  and and_22 (and_22_out, OP5, not_162_out, OP3, not_163_out, OP1, OP0);
  and and_23 (and_23_out, not_164_out, not_165_out, not_166_out, not_167_out, not_168_out, not_169_out, F5, not_170_out, not_171_out, F2, F1, not_172_out);
  and and_24 (and_24_out, not_173_out, not_174_out, OP3, OP2, OP1, not_175_out);
  and and_25 (and_25_out, OP5, not_176_out, not_177_out, OP2, not_178_out, OP0);
  and and_26 (and_26_out, not_179_out, not_180_out, not_181_out, OP2, OP1, OP0);
  and and_27 (and_27_out, not_182_out, not_183_out, not_184_out, not_185_out, not_186_out, not_187_out, not_188_out, not_189_out, not_190_out, not_191_out, not_192_out, not_193_out);
  and and_28 (and_28_out, not_194_out, not_195_out, not_196_out, not_197_out, not_198_out, not_199_out, not_200_out, not_201_out, not_202_out, not_203_out, F1, F0);
  and and_29 (and_29_out, not_204_out, not_205_out, not_206_out, not_207_out, not_208_out, not_209_out, not_210_out, not_211_out, not_212_out, not_213_out, F1, not_214_out);
  and and_30 (and_30_out, not_215_out, not_216_out, not_217_out, not_218_out, not_219_out, not_220_out, F5, not_221_out, not_222_out, not_223_out, not_224_out, not_225_out);
  and and_31 (and_31_out, not_226_out, not_227_out, not_228_out, not_229_out, not_230_out, not_231_out, F5, not_232_out, not_233_out, not_234_out, not_235_out, F0);
  and and_32 (and_32_out, not_236_out, not_237_out, not_238_out, not_239_out, not_240_out, not_241_out, F5, not_242_out, not_243_out, not_244_out, F1, not_245_out);
  and and_33 (and_33_out, not_246_out, not_247_out, not_248_out, not_249_out, not_250_out, not_251_out, F5, not_252_out, not_253_out, F2, not_254_out, not_255_out);
  and and_34 (and_34_out, not_256_out, not_257_out, not_258_out, not_259_out, not_260_out, not_261_out, F5, not_262_out, not_263_out, F2, not_264_out, F0);
  and and_35 (and_35_out, not_265_out, not_266_out, not_267_out, not_268_out, not_269_out, not_270_out, F5, not_271_out, not_272_out, F2, F1, F0);
  and and_36 (and_36_out, not_273_out, not_274_out, not_275_out, not_276_out, not_277_out, not_278_out, F5, not_279_out, F3, not_280_out, F1, not_281_out);
  and and_37 (and_37_out, not_282_out, not_283_out, not_284_out, not_285_out, not_286_out, not_287_out, F5, not_288_out, F3, not_289_out, F1, F0);
  and and_38 (and_38_out, not_290_out, not_291_out, not_292_out, not_293_out, not_294_out, not_295_out, not_296_out, not_297_out, F3, F2, not_298_out, not_299_out);
  and and_39 (and_39_out, not_300_out, not_301_out, not_302_out, OP2, not_303_out, not_304_out);
  and and_40 (and_40_out, not_305_out, not_306_out, not_307_out, OP2, not_308_out, OP0);
  and and_41 (and_41_out, OP5, not_309_out, not_310_out, not_311_out, OP1, OP0);
  and and_42 (and_42_out, OP5, not_312_out, OP3, not_313_out, OP1, OP0);
  and and_43 (and_43_out, not_314_out, not_315_out, not_316_out, not_317_out, not_318_out, not_319_out, F5, not_320_out, not_321_out, F2, F1, not_322_out);
  and and_44 (and_44_out, OP5, not_323_out, not_324_out, OP2, not_325_out, OP0);
  or or_1 (R1_USED, and_1_out, and_2_out, and_3_out, and_4_out, and_5_out, and_6_out, and_7_out, and_8_out, and_9_out, and_10_out, and_11_out, and_12_out, and_13_out, and_14_out, and_15_out, and_16_out, and_17_out, and_18_out, and_19_out, and_20_out, and_21_out, and_22_out, and_23_out, and_24_out, and_25_out, and_26_out);
  or or_2 (R2_USED, and_27_out, and_28_out, and_29_out, and_30_out, and_31_out, and_32_out, and_33_out, and_34_out, and_35_out, and_36_out, and_37_out, and_38_out, and_39_out, and_40_out, and_41_out, and_42_out, and_43_out, and_44_out);
endmodule

module \数据相关检测逻辑  (
  input  [4:0] EX_WriteReg_num,
  input  [5:0] OP,
  input  EX_RegWrite,
  input  [4:0] MEM_WriteReg_num,
  input  [5:0] Func,
  input  MEM_RegWrite,
  input  [4:0] ID_ReadReg1_num,
  input  [4:0] ID_ReadReg2_num,
  output \数据相关 
);

  wire and_1_out, and_2_out, and_3_out, and_4_out, and_5_out, and_6_out, and_7_out, and_8_out, and_9_out,
       and_10_out, comparator_1_eq, comparator_2_eq, comparator_3_eq, comparator_4_eq, comparator_5_eq,
       comparator_6_eq, comparator_7_eq, comparator_8_eq, or_1_out, or_2_out, R1_USED, R2_USED;

  \源寄存器使用判断逻辑  \u_源寄存器使用判断逻辑_1  (
    .OP0(OP[0]), .OP1(OP[1]), .OP2(OP[2]), .OP3(OP[3]), .OP4(OP[4]), .OP5(OP[5]), .F0(Func[0]), .F1(Func[1]),
    .F2(Func[2]), .F3(Func[3]), .F4(Func[4]), .F5(Func[5]), .R1_USED(R1_USED), .R2_USED(R2_USED));
  Comparator #(.width(5), .mode("twosComplement")) comparator_1 (
    .a({5{1'b0}}), .b(ID_ReadReg1_num), .eq(comparator_1_eq));  // open: gt, lt
  Comparator #(.width(5), .mode("twosComplement")) comparator_2 (
    .a(ID_ReadReg1_num), .b(EX_WriteReg_num), .eq(comparator_2_eq));  // open: gt, lt
  Comparator #(.width(5), .mode("twosComplement")) comparator_3 (
    .a({5{1'b0}}), .b(ID_ReadReg2_num), .eq(comparator_3_eq));  // open: gt, lt
  Comparator #(.width(5), .mode("twosComplement")) comparator_4 (
    .a(ID_ReadReg2_num), .b(EX_WriteReg_num), .eq(comparator_4_eq));  // open: gt, lt
  Comparator #(.width(5), .mode("twosComplement")) comparator_5 (
    .a({5{1'b0}}), .b(ID_ReadReg1_num), .eq(comparator_5_eq));  // open: gt, lt
  Comparator #(.width(5), .mode("twosComplement")) comparator_6 (
    .a(ID_ReadReg1_num), .b(MEM_WriteReg_num), .eq(comparator_6_eq));  // open: gt, lt
  Comparator #(.width(5), .mode("twosComplement")) comparator_7 (
    .a({5{1'b0}}), .b(ID_ReadReg2_num), .eq(comparator_7_eq));  // open: gt, lt
  Comparator #(.width(5), .mode("twosComplement")) comparator_8 (
    .a(ID_ReadReg2_num), .b(MEM_WriteReg_num), .eq(comparator_8_eq));  // open: gt, lt
  and and_1 (and_1_out, ~comparator_1_eq, comparator_2_eq);  // AND_Gate
  and and_2 (and_2_out, ~comparator_3_eq, comparator_4_eq);  // AND_Gate
  and and_3 (and_3_out, ~comparator_5_eq, comparator_6_eq);  // AND_Gate
  and and_4 (and_4_out, ~comparator_7_eq, comparator_8_eq);  // AND_Gate
  and and_5 (and_5_out, and_1_out, R1_USED);
  and and_6 (and_6_out, and_2_out, R2_USED);
  and and_7 (and_7_out, and_3_out, R1_USED);
  and and_8 (and_8_out, and_4_out, R2_USED);
  or or_1 (or_1_out, and_5_out, and_6_out);
  or or_2 (or_2_out, and_7_out, and_8_out);
  and and_9 (and_9_out, EX_RegWrite, or_1_out);
  and and_10 (and_10_out, MEM_RegWrite, or_2_out);
  or or_3 (\数据相关 , and_9_out, and_10_out);
endmodule

module \MIPS_Regfile_下降沿  (
  input  [31:0] Din,
  input  Clk,
  input  WE,
  input  [4:0] R1_num,
  input  [4:0] W_num,
  input  [4:0] R2_num,
  output [31:0] R1,
  output [31:0] R2
);

  // RegisterFile registerfile_1: pin names not known; wires that end beside it: Din, Clk, WE, W_num, R1_num, R2_num, R1, R2
endmodule

module \重定向控制逻辑  (
  input  [5:0] OP,
  input  [4:0] EX_WriteReg_num,
  input  EX_RegWrite,
  input  [5:0] FUNC,
  input  [4:0] MEM_WriteReg_num,
  input  MEM_RegWrite,
  input  [5:0] EX_OP,
  input  [4:0] ID_R1_num,
  input  MemToReg,
  input  [4:0] ID_R2_num,
  output load_use,
  output [1:0] Forward1,
  output [1:0] Forward2
);

  wire and_1_out, and_2_out, and_3_out, and_4_out, and_5_out, and_6_out, and_7_out, and_8_out, and_9_out,
       and_11_out, comparator_1_eq, comparator_2_eq, comparator_3_eq, comparator_4_eq, comparator_5_eq,
       comparator_6_eq, comparator_7_eq, comparator_8_eq, comparator_9_eq, comparator_10_eq, load_use1,
       load_use2, or_1_out, or_2_out, R1_USED, R2_USED;
  wire [1:0] and_14_out, and_16_out;

  \源寄存器使用判断逻辑  \u_源寄存器使用判断逻辑_1  (
    .OP0(OP[0]), .OP1(OP[1]), .OP2(OP[2]), .OP3(OP[3]), .OP4(OP[4]), .OP5(OP[5]), .F0(FUNC[0]), .F1(FUNC[1]),
    .F2(FUNC[2]), .F3(FUNC[3]), .F4(FUNC[4]), .F5(FUNC[5]), .R1_USED(R1_USED), .R2_USED(R2_USED));
  Comparator #(.width(5), .mode("twosComplement")) comparator_1 (
    .a(EX_WriteReg_num), .b(ID_R1_num), .eq(comparator_1_eq));  // open: gt, lt
  Comparator #(.width(5), .mode("twosComplement")) comparator_2 (
    .a(ID_R1_num), .b(MEM_WriteReg_num), .eq(comparator_2_eq));  // open: gt, lt
  Comparator #(.width(5), .mode("twosComplement")) comparator_3 (
    .a(ID_R1_num), .b({5{1'b0}}), .eq(comparator_3_eq));  // open: gt, lt
  Comparator #(.width(5), .mode("twosComplement")) comparator_4 (
    .a(EX_WriteReg_num), .b(ID_R2_num), .eq(comparator_4_eq));  // open: gt, lt
  Comparator #(.width(5), .mode("twosComplement")) comparator_5 (
    .a(ID_R2_num), .b(MEM_WriteReg_num), .eq(comparator_5_eq));  // open: gt, lt
  Comparator #(.width(5), .mode("twosComplement")) comparator_6 (
    .a(ID_R2_num), .b({5{1'b0}}), .eq(comparator_6_eq));  // open: gt, lt
  and and_1 (and_1_out, comparator_1_eq, ~comparator_3_eq);  // AND_Gate
  and and_2 (and_2_out, comparator_2_eq, ~comparator_3_eq);  // AND_Gate
  and and_3 (and_3_out, comparator_4_eq, ~comparator_6_eq);  // AND_Gate
  and and_4 (and_4_out, comparator_5_eq, ~comparator_6_eq);  // AND_Gate
  and and_5 (and_5_out, R1_USED, and_1_out);
  and and_6 (and_6_out, R1_USED, and_2_out);
  and and_7 (and_7_out, R2_USED, and_3_out);
  and and_8 (and_8_out, R2_USED, and_4_out);
  Comparator #(.width(6), .mode("twosComplement")) comparator_7 (
    .a(6'b100000), .b(EX_OP), .eq(comparator_7_eq));  // open: gt, lt
  Comparator #(.width(6), .mode("twosComplement")) comparator_8 (
    .a(EX_OP), .b(6'b100011), .eq(comparator_8_eq));  // open: gt, lt
  Comparator #(.width(6), .mode("twosComplement")) comparator_9 (
    .a(6'b100000), .b(EX_OP), .eq(comparator_9_eq));  // open: gt, lt
  Comparator #(.width(6), .mode("twosComplement")) comparator_10 (
    .a(EX_OP), .b(6'b100011), .eq(comparator_10_eq));  // open: gt, lt
  or or_1 (or_1_out, comparator_7_eq, comparator_8_eq);
  and and_9 (and_9_out, EX_RegWrite, and_5_out);
  and and_10 (and_14_out[1], MEM_RegWrite, and_6_out);
  or or_2 (or_2_out, comparator_9_eq, comparator_10_eq);
  and and_11 (and_11_out, EX_RegWrite, and_7_out);
  and and_12 (and_16_out[1], MEM_RegWrite, and_8_out);
  or or_3 (load_use, load_use1, load_use2);
  and and_13 (load_use1, or_1_out, and_9_out);
  and and_14 (and_14_out[0], ~or_1_out, and_9_out);  // AND_Gate
  and and_15 (load_use2, or_2_out, and_11_out);
  and and_16 (and_16_out[0], ~or_2_out, and_11_out);  // AND_Gate
  Multiplexer #(.select(3), .width(2), .disabled("Z"), .enable("false")) multiplexer_1 (
    .in0(2'b00), .in1(2'b01), .in2(2'b10), .in3(2'b01), .in4(2'b00), .in5(2'b01), .in6(2'b11), .in7(2'b01),
    .out(Forward1), .sel({MemToReg, and_14_out}));
  Multiplexer #(.select(3), .width(2), .disabled("Z"), .enable("false")) multiplexer_2 (
    .in0(2'b00), .in1(2'b01), .in2(2'b10), .in3(2'b01), .in4(2'b00), .in5(2'b01), .in6(2'b11), .in7(2'b01),
    .out(Forward2), .sel({MemToReg, and_16_out}));
endmodule
module BTB (
  input  Clk,
  input  EX_Branch,
  input  [31:0] PC,
  input  [31:0] EX_PC,
  input  [31:0] EX_BranchAddr,
  input  EX_Branched,
  output [31:0] JumpAddr,
  output PredictJump
);

  wire A0, A1, A2, A3, A4, A5, A6, A7, and_17_out, comparator_1_eq, comparator_2_eq, comparator_3_eq,
       comparator_4_eq, comparator_5_eq, comparator_6_eq, comparator_7_eq, comparator_8_eq, comparator_9_eq,
       comparator_10_eq, comparator_11_eq, comparator_12_eq, comparator_13_eq, comparator_14_eq,
       comparator_15_eq, comparator_16_eq, decoder_1_out0, decoder_1_out1, decoder_1_out2, decoder_1_out3,
       decoder_1_out4, decoder_1_out5, decoder_1_out6, decoder_1_out7, decoder_2_out0, decoder_2_out1,
       decoder_2_out2, decoder_2_out3, decoder_2_out4, decoder_2_out5, decoder_2_out6, decoder_2_out7,
       EX_Hit, EX_Miss, IF_Hit, IF_Miss, L0, L1, L2, L3, L4, L5, L6, L7, M0, M1, M2, M3, M4, M5, M6, M7,
       not_2_out, not_3_out, not_4_out, not_5_out, not_6_out, not_7_out, not_8_out, not_9_out, or_3_out,
       or_4_out, or_5_out, or_6_out, or_7_out, or_8_out, or_9_out, or_10_out, or_11_out, or_12_out,
       or_13_out, or_14_out, or_15_out, or_16_out, or_17_out, or_18_out, priority_encoder_1_gs, V0, V1, V2,
       V3, V4, V5, V6, V7, WriteL0, WriteL1, WriteL2, WriteL3, WriteL4, WriteL5, WriteL6, WriteL7;
  wire [0:0] controlled_buffer_9_out, controlled_buffer_10_out, controlled_buffer_11_out,
       controlled_buffer_12_out, controlled_buffer_13_out, controlled_buffer_14_out,
       controlled_buffer_15_out, controlled_buffer_16_out;
  wire [1:0] adder_1_out, adder_2_out, adder_3_out, adder_4_out, adder_5_out, adder_6_out, adder_7_out,
       adder_8_out, multiplexer_1_out, multiplexer_2_out, multiplexer_3_out, multiplexer_4_out,
       multiplexer_5_out, multiplexer_6_out, multiplexer_7_out, multiplexer_8_out, multiplexer_9_out,
       multiplexer_10_out, multiplexer_11_out, multiplexer_12_out, multiplexer_13_out, multiplexer_14_out,
       multiplexer_15_out, multiplexer_16_out, multiplexer_17_out, multiplexer_18_out, multiplexer_19_out,
       multiplexer_20_out, multiplexer_21_out, multiplexer_22_out, multiplexer_23_out, multiplexer_24_out,
       multiplexer_25_out, multiplexer_26_out, multiplexer_27_out, multiplexer_28_out, multiplexer_29_out,
       multiplexer_30_out, multiplexer_31_out, multiplexer_32_out, multiplexer_33_out, multiplexer_34_out,
       multiplexer_35_out, multiplexer_36_out, multiplexer_37_out, multiplexer_38_out, multiplexer_39_out,
       multiplexer_40_out, Predict0, Predict1, Predict2, Predict3, Predict4, Predict5, Predict6, Predict7;
  wire [2:0] max3_1_max_num, max3_2_max_num, max3_3_max_num, max3_4_max_num, max3_5_max_num, max3_6_max_num,
       max3_7_max_num, priority_encoder_1_out;
  wire [15:0] C0, C1, C2, C3, C4, C5, C6, C7, max3_1_max, max3_2_max, max3_3_max, max3_4_max, max3_5_max,
       max3_6_max;
  wire [31:0] Tag0, Tag1, Tag2, Tag3, Tag4, Tag5, Tag6, Tag7, \分支目标地址_2_q , \分支目标地址_3_q , \分支目标地址_4_q ,
       \分支目标地址_5_q , \分支目标地址_6_q , \分支目标地址_7_q , \分支目标地址_8_q , \分支目标地址_q ;

  Pull_Resistor #(.pull(0)) pull_resistor_1 (.node(PredictJump));
  Register #(.width(1), .trigger("rising"), .Select("low")) VALID (
    .D(1'b1), .en(WriteL0), .Q(V0), .clk(Clk));  // open: clr
  Register #(.width(1), .trigger("rising"), .Select("low")) VALID_2 (
    .D(1'b1), .en(WriteL1), .Q(V1), .clk(Clk));  // open: clr
  Register #(.width(1), .trigger("rising"), .Select("low")) VALID_3 (
    .D(1'b1), .en(WriteL2), .Q(V2), .clk(Clk));  // open: clr
  Register #(.width(1), .trigger("rising"), .Select("low")) VALID_4 (
    .D(1'b1), .en(WriteL3), .Q(V3), .clk(Clk));  // open: clr
  Register #(.width(1), .trigger("rising"), .Select("low")) VALID_5 (
    .D(1'b1), .en(WriteL4), .Q(V4), .clk(Clk));  // open: clr
  Register #(.width(1), .trigger("rising"), .Select("low")) VALID_6 (
    .D(1'b1), .en(WriteL5), .Q(V5), .clk(Clk));  // open: clr
  Register #(.width(1), .trigger("rising"), .Select("low")) VALID_7 (
    .D(1'b1), .en(WriteL6), .Q(V6), .clk(Clk));  // open: clr
  Register #(.width(1), .trigger("rising"), .Select("low")) VALID_8 (
    .D(1'b1), .en(WriteL7), .Q(V7), .clk(Clk));  // open: clr
  Comparator #(.width(32), .mode("twosComplement")) comparator_1 (
    .a(PC), .b(Tag0), .eq(comparator_1_eq));  // open: gt, lt
  Comparator #(.width(32), .mode("twosComplement")) comparator_2 (
    .a(PC), .b(Tag1), .eq(comparator_2_eq));  // open: gt, lt
  Comparator #(.width(32), .mode("twosComplement")) comparator_3 (
    .a(PC), .b(Tag2), .eq(comparator_3_eq));  // open: gt, lt
  Comparator #(.width(32), .mode("twosComplement")) comparator_4 (
    .a(PC), .b(Tag3), .eq(comparator_4_eq));  // open: gt, lt
  Comparator #(.width(32), .mode("twosComplement")) comparator_5 (
    .a(PC), .b(Tag4), .eq(comparator_5_eq));  // open: gt, lt
  Comparator #(.width(32), .mode("twosComplement")) comparator_6 (
    .a(PC), .b(Tag5), .eq(comparator_6_eq));  // open: gt, lt
  Comparator #(.width(32), .mode("twosComplement")) comparator_7 (
    .a(PC), .b(Tag6), .eq(comparator_7_eq));  // open: gt, lt
  Comparator #(.width(32), .mode("twosComplement")) comparator_8 (
    .a(PC), .b(Tag7), .eq(comparator_8_eq));  // open: gt, lt
  Register #(.width(32), .trigger("rising"), .Select("low")) \u_分支指令地址  (
    .D(EX_PC), .en(WriteL0), .Q(Tag0), .clk(Clk));  // open: clr
  Register #(.width(32), .trigger("rising"), .Select("low")) \u_分支指令地址_2  (
    .D(EX_PC), .en(WriteL1), .Q(Tag1), .clk(Clk));  // open: clr
  Register #(.width(32), .trigger("rising"), .Select("low")) \u_分支指令地址_3  (
    .D(EX_PC), .en(WriteL2), .Q(Tag2), .clk(Clk));  // open: clr
  Register #(.width(32), .trigger("rising"), .Select("low")) \u_分支指令地址_4  (
    .D(EX_PC), .en(WriteL3), .Q(Tag3), .clk(Clk));  // open: clr
  Register #(.width(32), .trigger("rising"), .Select("low")) \u_分支指令地址_5  (
    .D(EX_PC), .en(WriteL4), .Q(Tag4), .clk(Clk));  // open: clr
  Register #(.width(32), .trigger("rising"), .Select("low")) \u_分支指令地址_6  (
    .D(EX_PC), .en(WriteL5), .Q(Tag5), .clk(Clk));  // open: clr
  Register #(.width(32), .trigger("rising"), .Select("low")) \u_分支指令地址_7  (
    .D(EX_PC), .en(WriteL6), .Q(Tag6), .clk(Clk));  // open: clr
  Register #(.width(32), .trigger("rising"), .Select("low")) \u_分支指令地址_8  (
    .D(EX_PC), .en(WriteL7), .Q(Tag7), .clk(Clk));  // open: clr
  and and_1 (L0, comparator_1_eq, V0);
  and and_2 (L1, comparator_2_eq, V1);
  and and_3 (L2, comparator_3_eq, V2);
  and and_4 (L3, comparator_4_eq, V3);
  and and_5 (L4, comparator_5_eq, V4);
  and and_6 (L5, comparator_6_eq, V5);
  and and_7 (L6, comparator_7_eq, V6);
  and and_8 (L7, comparator_8_eq, V7);
  Counter #(.width(16), .max('hffff), .ongoal("wrap"), .trigger("rising"), .behavior("old")) \u_置换标记  (
    .count(A0), .Q(C0), .clk(Clk), .clr(L0));  // open: load, D, carry, preset
  Counter #(.width(16), .max('hffff), .ongoal("wrap"), .trigger("rising"), .behavior("old")) \u_置换标记_2  (
    .count(A1), .Q(C1), .clk(Clk), .clr(L1));  // open: load, D, carry, preset
  Counter #(.width(16), .max('hffff), .ongoal("wrap"), .trigger("rising"), .behavior("old")) \u_置换标记_3  (
    .count(A2), .Q(C2), .clk(Clk), .clr(L2));  // open: load, D, carry, preset
  Counter #(.width(16), .max('hffff), .ongoal("wrap"), .trigger("rising"), .behavior("old")) \u_置换标记_4  (
    .count(A3), .Q(C3), .clk(Clk), .clr(L3));  // open: load, D, carry, preset
  Counter #(.width(16), .max('hffff), .ongoal("wrap"), .trigger("rising"), .behavior("old")) \u_置换标记_5  (
    .count(A4), .Q(C4), .clk(Clk), .clr(L4));  // open: load, D, carry, preset
  Counter #(.width(16), .max('hffff), .ongoal("wrap"), .trigger("rising"), .behavior("old")) \u_置换标记_6  (
    .count(A5), .Q(C5), .clk(Clk), .clr(L5));  // open: load, D, carry, preset
  Counter #(.width(16), .max('hffff), .ongoal("wrap"), .trigger("rising"), .behavior("old")) \u_置换标记_7  (
    .count(A6), .Q(C6), .clk(Clk), .clr(L6));  // open: load, D, carry, preset
  Counter #(.width(16), .max('hffff), .ongoal("wrap"), .trigger("rising"), .behavior("old")) \u_置换标记_8  (
    .count(A7), .Q(C7), .clk(Clk), .clr(L7));  // open: load, D, carry, preset
  or or_1 (IF_Hit, L0, L1, L2, L3, L4, L5, L6, L7);
  not not_1 (IF_Miss, IF_Hit);
  Register #(.width(32), .trigger("rising"), .Select("low")) \u_分支目标地址  (
    .D(EX_BranchAddr), .en(WriteL0), .Q(\分支目标地址_q ), .clk(Clk));  // open: clr
  Register #(.width(32), .trigger("rising"), .Select("low")) \u_分支目标地址_2  (
    .D(EX_BranchAddr), .en(WriteL1), .Q(\分支目标地址_2_q ), .clk(Clk));  // open: clr
  Register #(.width(32), .trigger("rising"), .Select("low")) \u_分支目标地址_3  (
    .D(EX_BranchAddr), .en(WriteL2), .Q(\分支目标地址_3_q ), .clk(Clk));  // open: clr
  Register #(.width(32), .trigger("rising"), .Select("low")) \u_分支目标地址_4  (
    .D(EX_BranchAddr), .en(WriteL3), .Q(\分支目标地址_4_q ), .clk(Clk));  // open: clr
  Register #(.width(32), .trigger("rising"), .Select("low")) \u_分支目标地址_5  (
    .D(EX_BranchAddr), .en(WriteL4), .Q(\分支目标地址_5_q ), .clk(Clk));  // open: clr
  Register #(.width(32), .trigger("rising"), .Select("low")) \u_分支目标地址_6  (
    .D(EX_BranchAddr), .en(WriteL5), .Q(\分支目标地址_6_q ), .clk(Clk));  // open: clr
  Register #(.width(32), .trigger("rising"), .Select("low")) \u_分支目标地址_7  (
    .D(EX_BranchAddr), .en(WriteL6), .Q(\分支目标地址_7_q ), .clk(Clk));  // open: clr
  Register #(.width(32), .trigger("rising"), .Select("low")) \u_分支目标地址_8  (
    .D(EX_BranchAddr), .en(WriteL7), .Q(\分支目标地址_8_q ), .clk(Clk));  // open: clr
  assign JumpAddr = L0 ? \分支目标地址_q  : 32'bz;  // Controlled_Buffer controlled_buffer_1
  assign JumpAddr = L1 ? \分支目标地址_2_q  : 32'bz;  // Controlled_Buffer controlled_buffer_2
  assign JumpAddr = L2 ? \分支目标地址_3_q  : 32'bz;  // Controlled_Buffer controlled_buffer_3
  assign JumpAddr = L3 ? \分支目标地址_4_q  : 32'bz;  // Controlled_Buffer controlled_buffer_4
  assign JumpAddr = L4 ? \分支目标地址_5_q  : 32'bz;  // Controlled_Buffer controlled_buffer_5
  assign JumpAddr = L5 ? \分支目标地址_6_q  : 32'bz;  // Controlled_Buffer controlled_buffer_6
  assign JumpAddr = L6 ? \分支目标地址_7_q  : 32'bz;  // Controlled_Buffer controlled_buffer_7
  assign JumpAddr = L7 ? \分支目标地址_8_q  : 32'bz;  // Controlled_Buffer controlled_buffer_8
  Comparator #(.width(32), .mode("twosComplement")) comparator_9 (
    .a(EX_PC), .b(Tag0), .eq(comparator_9_eq));  // open: gt, lt
  Comparator #(.width(32), .mode("twosComplement")) comparator_10 (
    .a(EX_PC), .b(Tag1), .eq(comparator_10_eq));  // open: gt, lt
  Comparator #(.width(32), .mode("twosComplement")) comparator_11 (
    .a(EX_PC), .b(Tag2), .eq(comparator_11_eq));  // open: gt, lt
  Comparator #(.width(32), .mode("twosComplement")) comparator_12 (
    .a(EX_PC), .b(Tag3), .eq(comparator_12_eq));  // open: gt, lt
  Comparator #(.width(32), .mode("twosComplement")) comparator_13 (
    .a(EX_PC), .b(Tag4), .eq(comparator_13_eq));  // open: gt, lt
  Comparator #(.width(32), .mode("twosComplement")) comparator_14 (
    .a(EX_PC), .b(Tag5), .eq(comparator_14_eq));  // open: gt, lt
  Comparator #(.width(32), .mode("twosComplement")) comparator_15 (
    .a(EX_PC), .b(Tag6), .eq(comparator_15_eq));  // open: gt, lt
  Comparator #(.width(32), .mode("twosComplement")) comparator_16 (
    .a(EX_PC), .b(Tag7), .eq(comparator_16_eq));  // open: gt, lt
  and and_9 (M0, comparator_9_eq, V0);
  and and_10 (M1, comparator_10_eq, V1);
  and and_11 (M2, comparator_11_eq, V2);
  and and_12 (M3, comparator_12_eq, V3);
  and and_13 (M4, comparator_13_eq, V4);
  and and_14 (M5, comparator_14_eq, V5);
  and and_15 (M6, comparator_15_eq, V6);
  and and_16 (M7, comparator_16_eq, V7);
  not not_2 (not_2_out, V0);
  not not_3 (not_3_out, V1);
  not not_4 (not_4_out, V2);
  not not_5 (not_5_out, V3);
  not not_6 (not_6_out, V4);
  not not_7 (not_7_out, V5);
  not not_8 (not_8_out, V6);
  not not_9 (not_9_out, V7);
  MAX3 max3_1 (.Y(C1), .X(C0), .Y_num(3'b001), .X_num(3'b000), .MAX(max3_1_max), .Max_num(max3_1_max_num));
  MAX3 max3_2 (.Y(C3), .X(C2), .Y_num(3'b011), .X_num(3'b010), .MAX(max3_2_max), .Max_num(max3_2_max_num));
  MAX3 max3_3 (.Y(C5), .X(C4), .Y_num(3'b101), .X_num(3'b100), .MAX(max3_3_max), .Max_num(max3_3_max_num));
  MAX3 max3_4 (.Y(C7), .X(C6), .Y_num(3'b111), .X_num(3'b110), .MAX(max3_4_max), .Max_num(max3_4_max_num));
  and and_17 (and_17_out, V0, V1, V2, V3, V4, V5, V6, V7);
  Priority_Encoder #(.select(3), .disabled("Z")) priority_encoder_1 (
    .in0(not_2_out), .in1(not_3_out), .in2(not_4_out), .in3(not_5_out), .in4(not_6_out), .in5(not_7_out),
    .in6(not_8_out), .in7(not_9_out), .out(priority_encoder_1_out), .gs(priority_encoder_1_gs));  // open: en_out, en_in
  MAX3 max3_5 (
    .Y(max3_2_max), .X(max3_1_max), .Y_num(max3_2_max_num), .X_num(max3_1_max_num), .MAX(max3_5_max),
    .Max_num(max3_5_max_num));
  MAX3 max3_6 (
    .Y(max3_4_max), .X(max3_3_max), .Y_num(max3_4_max_num), .X_num(max3_3_max_num), .MAX(max3_6_max),
    .Max_num(max3_6_max_num));
  or or_2 (EX_Hit, M0, M1, M2, M3, M4, M5, M6, M7);
  not not_10 (EX_Miss, EX_Hit);
  Decoder #(.select(3), .tristate("false"), .disabled(0), .enable("true")) decoder_1 (
    .out0(decoder_1_out0), .out1(decoder_1_out1), .out2(decoder_1_out2), .out3(decoder_1_out3),
    .out4(decoder_1_out4), .out5(decoder_1_out5), .out6(decoder_1_out6), .out7(decoder_1_out7),
    .sel(priority_encoder_1_out), .en(priority_encoder_1_gs));
  Decoder #(.select(3), .tristate("false"), .disabled(0), .enable("true")) decoder_2 (
    .out0(decoder_2_out0), .out1(decoder_2_out1), .out2(decoder_2_out2), .out3(decoder_2_out3),
    .out4(decoder_2_out4), .out5(decoder_2_out5), .out6(decoder_2_out6), .out7(decoder_2_out7),
    .sel(max3_7_max_num), .en(and_17_out));
  MAX3 max3_7 (
    .Y(max3_6_max), .X(max3_5_max), .Y_num(max3_6_max_num), .X_num(max3_5_max_num), .Max_num(max3_7_max_num));  // open: MAX
  assign {PredictJump, controlled_buffer_9_out[0]} = L0 ? Predict0 : 2'bz;  // Controlled_Buffer controlled_buffer_9
  assign {PredictJump, controlled_buffer_10_out[0]} = L1 ? Predict1 : 2'bz;  // Controlled_Buffer controlled_buffer_10
  assign {PredictJump, controlled_buffer_11_out[0]} = L2 ? Predict2 : 2'bz;  // Controlled_Buffer controlled_buffer_11
  assign {PredictJump, controlled_buffer_12_out[0]} = L3 ? Predict3 : 2'bz;  // Controlled_Buffer controlled_buffer_12
  assign {PredictJump, controlled_buffer_13_out[0]} = L4 ? Predict4 : 2'bz;  // Controlled_Buffer controlled_buffer_13
  assign {PredictJump, controlled_buffer_14_out[0]} = L5 ? Predict5 : 2'bz;  // Controlled_Buffer controlled_buffer_14
  assign {PredictJump, controlled_buffer_15_out[0]} = L6 ? Predict6 : 2'bz;  // Controlled_Buffer controlled_buffer_15
  assign {PredictJump, controlled_buffer_16_out[0]} = L7 ? Predict7 : 2'bz;  // Controlled_Buffer controlled_buffer_16
  or or_3 (or_3_out, decoder_1_out0, decoder_2_out0);
  or or_4 (or_4_out, decoder_1_out1, decoder_2_out1);
  or or_5 (or_5_out, decoder_1_out2, decoder_2_out2);
  or or_6 (or_6_out, decoder_1_out3, decoder_2_out3);
  or or_7 (or_7_out, decoder_1_out4, decoder_2_out4);
  or or_8 (or_8_out, decoder_1_out5, decoder_2_out5);
  or or_9 (or_9_out, decoder_1_out6, decoder_2_out6);
  or or_10 (or_10_out, decoder_1_out7, decoder_2_out7);
  and and_18 (WriteL0, or_3_out, EX_Miss, EX_Branch);
  and and_19 (WriteL1, or_4_out, EX_Miss, EX_Branch);
  and and_20 (WriteL2, or_5_out, EX_Miss, EX_Branch);
  and and_21 (WriteL3, or_6_out, EX_Miss, EX_Branch);
  and and_22 (WriteL4, or_7_out, EX_Miss, EX_Branch);
  and and_23 (WriteL5, or_8_out, EX_Miss, EX_Branch);
  and and_24 (WriteL6, or_9_out, EX_Miss, EX_Branch);
  and and_25 (WriteL7, or_10_out, EX_Miss, EX_Branch);
  Multiplexer #(.select(1), .width(2), .disabled("Z"), .enable("false")) multiplexer_1 (
    .in0(2'b00), .in1(2'b01), .out(multiplexer_1_out), .sel(EX_Branched));
  Multiplexer #(.select(1), .width(2), .disabled("Z"), .enable("false")) multiplexer_2 (
    .in0(2'b11), .in1(2'b01), .out(multiplexer_2_out), .sel(EX_Branched));
  Multiplexer #(.select(1), .width(2), .disabled("Z"), .enable("false")) multiplexer_3 (
    .in0(2'b01), .in1(2'b00), .out(multiplexer_3_out), .sel(EX_Branched));
  Multiplexer #(.select(1), .width(2), .disabled("Z"), .enable("false")) multiplexer_4 (
    .in0(2'b01), .in1(2'b11), .out(multiplexer_4_out), .sel(EX_Branched));
  Multiplexer #(.select(1), .width(2), .disabled("Z"), .enable("false")) multiplexer_5 (
    .in0(2'b00), .in1(2'b01), .out(multiplexer_5_out), .sel(EX_Branched));
  Multiplexer #(.select(1), .width(2), .disabled("Z"), .enable("false")) multiplexer_6 (
    .in0(2'b11), .in1(2'b01), .out(multiplexer_6_out), .sel(EX_Branched));
  Multiplexer #(.select(1), .width(2), .disabled("Z"), .enable("false")) multiplexer_7 (
    .in0(2'b01), .in1(2'b00), .out(multiplexer_7_out), .sel(EX_Branched));
  Multiplexer #(.select(1), .width(2), .disabled("Z"), .enable("false")) multiplexer_8 (
    .in0(2'b01), .in1(2'b11), .out(multiplexer_8_out), .sel(EX_Branched));
  Multiplexer #(.select(2), .width(2), .disabled("Z"), .enable("false")) multiplexer_9 (
    .in0(multiplexer_1_out), .in1(multiplexer_2_out), .in2(multiplexer_3_out), .in3(multiplexer_4_out),
    .out(multiplexer_9_out), .sel(Predict0));
  Multiplexer #(.select(2), .width(2), .disabled("Z"), .enable("false")) multiplexer_10 (
    .in0(multiplexer_5_out), .in1(multiplexer_6_out), .in2(multiplexer_7_out), .in3(multiplexer_8_out),
    .out(multiplexer_10_out), .sel(Predict4));
  Adder #(.width(2)) adder_1 (.a(Predict0), .b(multiplexer_9_out), .out(adder_1_out));  // open: cin, cout
  Adder #(.width(2)) adder_2 (.a(Predict4), .b(multiplexer_10_out), .out(adder_2_out));  // open: cin, cout
  or or_11 (or_11_out, L1, L2, L3, L4, L5, L6, L7, WriteL1, WriteL2, WriteL3, WriteL4, WriteL5, WriteL6, WriteL7);
  or or_12 (or_12_out, L0, L1, L2, L3, L5, L6, L7, WriteL0, WriteL1, WriteL2, WriteL3, WriteL5, WriteL6, WriteL7);
  Register #(.width(2), .trigger("rising"), .Select("low")) \u_分支预测历史位  (
    .D(adder_1_out), .en(M0), .Q(Predict0), .clk(Clk));  // open: clr
  Register #(.width(2), .trigger("rising"), .Select("low")) \u_分支预测历史位_2  (
    .D(adder_2_out), .en(M4), .Q(Predict4), .clk(Clk));  // open: clr
  and and_26 (A0, or_11_out, V0);
  and and_27 (A4, or_12_out, V4);
  Multiplexer #(.select(1), .width(2), .disabled("Z"), .enable("false")) multiplexer_11 (
    .in0(2'b00), .in1(2'b01), .out(multiplexer_11_out), .sel(EX_Branched));
  Multiplexer #(.select(1), .width(2), .disabled("Z"), .enable("false")) multiplexer_12 (
    .in0(2'b11), .in1(2'b01), .out(multiplexer_12_out), .sel(EX_Branched));
  Multiplexer #(.select(1), .width(2), .disabled("Z"), .enable("false")) multiplexer_13 (
    .in0(2'b01), .in1(2'b00), .out(multiplexer_13_out), .sel(EX_Branched));
  Multiplexer #(.select(1), .width(2), .disabled("Z"), .enable("false")) multiplexer_14 (
    .in0(2'b01), .in1(2'b11), .out(multiplexer_14_out), .sel(EX_Branched));
  Multiplexer #(.select(1), .width(2), .disabled("Z"), .enable("false")) multiplexer_15 (
    .in0(2'b00), .in1(2'b01), .out(multiplexer_15_out), .sel(EX_Branched));
  Multiplexer #(.select(1), .width(2), .disabled("Z"), .enable("false")) multiplexer_16 (
    .in0(2'b11), .in1(2'b01), .out(multiplexer_16_out), .sel(EX_Branched));
  Multiplexer #(.select(1), .width(2), .disabled("Z"), .enable("false")) multiplexer_17 (
    .in0(2'b01), .in1(2'b00), .out(multiplexer_17_out), .sel(EX_Branched));
  Multiplexer #(.select(1), .width(2), .disabled("Z"), .enable("false")) multiplexer_18 (
    .in0(2'b01), .in1(2'b11), .out(multiplexer_18_out), .sel(EX_Branched));
  Multiplexer #(.select(2), .width(2), .disabled("Z"), .enable("false")) multiplexer_19 (
    .in0(multiplexer_11_out), .in1(multiplexer_12_out), .in2(multiplexer_13_out), .in3(multiplexer_14_out),
    .out(multiplexer_19_out), .sel(Predict1));
  Multiplexer #(.select(2), .width(2), .disabled("Z"), .enable("false")) multiplexer_20 (
    .in0(multiplexer_15_out), .in1(multiplexer_16_out), .in2(multiplexer_17_out), .in3(multiplexer_18_out),
    .out(multiplexer_20_out), .sel(Predict5));
  or or_13 (or_13_out, L0, L2, L3, L4, L5, L6, L7, WriteL0, WriteL2, WriteL3, WriteL4, WriteL5, WriteL6, WriteL7);
  or or_14 (or_14_out, L0, L1, L2, L3, L4, L6, L7, WriteL0, WriteL1, WriteL2, WriteL3, WriteL4, WriteL6, WriteL7);
  Register #(.width(2), .trigger("rising"), .Select("low")) \u_分支预测历史位_3  (
    .D(adder_3_out), .en(M1), .Q(Predict1), .clk(Clk));  // open: clr
  Adder #(.width(2)) adder_3 (.a(Predict1), .b(multiplexer_19_out), .out(adder_3_out));  // open: cin, cout
  Adder #(.width(2)) adder_4 (.a(Predict5), .b(multiplexer_20_out), .out(adder_4_out));  // open: cin, cout
  Register #(.width(2), .trigger("rising"), .Select("low")) \u_分支预测历史位_4  (
    .D(adder_4_out), .en(M5), .Q(Predict5), .clk(Clk));  // open: clr
  and and_28 (A1, or_13_out, V1);
  and and_29 (A5, or_14_out, V5);
  Multiplexer #(.select(1), .width(2), .disabled("Z"), .enable("false")) multiplexer_21 (
    .in0(2'b00), .in1(2'b01), .out(multiplexer_21_out), .sel(EX_Branched));
  Multiplexer #(.select(1), .width(2), .disabled("Z"), .enable("false")) multiplexer_22 (
    .in0(2'b11), .in1(2'b01), .out(multiplexer_22_out), .sel(EX_Branched));
  Multiplexer #(.select(1), .width(2), .disabled("Z"), .enable("false")) multiplexer_23 (
    .in0(2'b01), .in1(2'b00), .out(multiplexer_23_out), .sel(EX_Branched));
  Multiplexer #(.select(1), .width(2), .disabled("Z"), .enable("false")) multiplexer_24 (
    .in0(2'b01), .in1(2'b11), .out(multiplexer_24_out), .sel(EX_Branched));
  Multiplexer #(.select(1), .width(2), .disabled("Z"), .enable("false")) multiplexer_25 (
    .in0(2'b00), .in1(2'b01), .out(multiplexer_25_out), .sel(EX_Branched));
  Multiplexer #(.select(1), .width(2), .disabled("Z"), .enable("false")) multiplexer_26 (
    .in0(2'b11), .in1(2'b01), .out(multiplexer_26_out), .sel(EX_Branched));
  Multiplexer #(.select(1), .width(2), .disabled("Z"), .enable("false")) multiplexer_27 (
    .in0(2'b01), .in1(2'b00), .out(multiplexer_27_out), .sel(EX_Branched));
  Multiplexer #(.select(1), .width(2), .disabled("Z"), .enable("false")) multiplexer_28 (
    .in0(2'b01), .in1(2'b11), .out(multiplexer_28_out), .sel(EX_Branched));
  or or_15 (or_15_out, L0, L1, L3, L4, L5, L6, L7, WriteL0, WriteL1, WriteL3, WriteL4, WriteL5, WriteL6, WriteL7);
  or or_16 (or_16_out, L0, L1, L2, L3, L4, L5, L7, WriteL0, WriteL1, WriteL2, WriteL3, WriteL4, WriteL5, WriteL7);
  Adder #(.width(2)) adder_5 (.a(Predict2), .b(multiplexer_29_out), .out(adder_5_out));  // open: cin, cout
  Multiplexer #(.select(2), .width(2), .disabled("Z"), .enable("false")) multiplexer_29 (
    .in0(multiplexer_21_out), .in1(multiplexer_22_out), .in2(multiplexer_23_out), .in3(multiplexer_24_out),
    .out(multiplexer_29_out), .sel(Predict2));
  Adder #(.width(2)) adder_6 (.a(Predict6), .b(multiplexer_30_out), .out(adder_6_out));  // open: cin, cout
  Multiplexer #(.select(2), .width(2), .disabled("Z"), .enable("false")) multiplexer_30 (
    .in0(multiplexer_25_out), .in1(multiplexer_26_out), .in2(multiplexer_27_out), .in3(multiplexer_28_out),
    .out(multiplexer_30_out), .sel(Predict6));
  and and_30 (A2, or_15_out, V2);
  and and_31 (A6, or_16_out, V6);
  Register #(.width(2), .trigger("rising"), .Select("low")) \u_分支预测历史位_5  (
    .D(adder_5_out), .en(M2), .Q(Predict2), .clk(Clk));  // open: clr
  Register #(.width(2), .trigger("rising"), .Select("low")) \u_分支预测历史位_6  (
    .D(adder_6_out), .en(M6), .Q(Predict6), .clk(Clk));  // open: clr
  Multiplexer #(.select(1), .width(2), .disabled("Z"), .enable("false")) multiplexer_31 (
    .in0(2'b00), .in1(2'b01), .out(multiplexer_31_out), .sel(EX_Branched));
  Multiplexer #(.select(1), .width(2), .disabled("Z"), .enable("false")) multiplexer_32 (
    .in0(2'b11), .in1(2'b01), .out(multiplexer_32_out), .sel(EX_Branched));
  Multiplexer #(.select(1), .width(2), .disabled("Z"), .enable("false")) multiplexer_33 (
    .in0(2'b01), .in1(2'b00), .out(multiplexer_33_out), .sel(EX_Branched));
  Multiplexer #(.select(1), .width(2), .disabled("Z"), .enable("false")) multiplexer_34 (
    .in0(2'b01), .in1(2'b11), .out(multiplexer_34_out), .sel(EX_Branched));
  Multiplexer #(.select(1), .width(2), .disabled("Z"), .enable("false")) multiplexer_35 (
    .in0(2'b00), .in1(2'b01), .out(multiplexer_35_out), .sel(EX_Branched));
  Multiplexer #(.select(1), .width(2), .disabled("Z"), .enable("false")) multiplexer_36 (
    .in0(2'b11), .in1(2'b01), .out(multiplexer_36_out), .sel(EX_Branched));
  Multiplexer #(.select(1), .width(2), .disabled("Z"), .enable("false")) multiplexer_37 (
    .in0(2'b01), .in1(2'b00), .out(multiplexer_37_out), .sel(EX_Branched));
  Multiplexer #(.select(1), .width(2), .disabled("Z"), .enable("false")) multiplexer_38 (
    .in0(2'b01), .in1(2'b11), .out(multiplexer_38_out), .sel(EX_Branched));
  or or_17 (or_17_out, L0, L1, L2, L4, L5, L6, L7, WriteL0, WriteL1, WriteL2, WriteL4, WriteL5, WriteL6, WriteL7);
  or or_18 (or_18_out, L0, L1, L2, L3, L4, L5, L6, WriteL0, WriteL1, WriteL2, WriteL3, WriteL4, WriteL5, WriteL6);
  Multiplexer #(.select(2), .width(2), .disabled("Z"), .enable("false")) multiplexer_39 (
    .in0(multiplexer_31_out), .in1(multiplexer_32_out), .in2(multiplexer_33_out), .in3(multiplexer_34_out),
    .out(multiplexer_39_out), .sel(Predict3));
  Multiplexer #(.select(2), .width(2), .disabled("Z"), .enable("false")) multiplexer_40 (
    .in0(multiplexer_35_out), .in1(multiplexer_36_out), .in2(multiplexer_37_out), .in3(multiplexer_38_out),
    .out(multiplexer_40_out), .sel(Predict7));
  and and_32 (A3, or_17_out, V3);
  and and_33 (A7, or_18_out, V7);
  Adder #(.width(2)) adder_7 (.a(Predict3), .b(multiplexer_39_out), .out(adder_7_out));  // open: cin, cout
  Adder #(.width(2)) adder_8 (.a(Predict7), .b(multiplexer_40_out), .out(adder_8_out));  // open: cin, cout
  Register #(.width(2), .trigger("rising"), .Select("low")) \u_分支预测历史位_7  (
    .D(adder_7_out), .en(M3), .Q(Predict3), .clk(Clk));  // open: clr
  Register #(.width(2), .trigger("rising"), .Select("low")) \u_分支预测历史位_8  (
    .D(adder_8_out), .en(M7), .Q(Predict7), .clk(Clk));  // open: clr

  // Other names for the same wires on the sheet: Tag[31:0] = EX_PC
endmodule

module MAX3 (
  input  [15:0] Y,
  input  [15:0] X,
  input  [2:0] Y_num,
  input  [2:0] X_num,
  output [15:0] MAX,
  output [2:0] Max_num
);

  wire comparator_1_eq, comparator_1_gt, or_1_out;

  Multiplexer #(.select(1), .width(16), .disabled("Z"), .enable("false")) multiplexer_1 (
    .in0(Y), .in1(X), .out(MAX), .sel(or_1_out));
  Comparator #(.width(16), .mode("unsigned")) comparator_1 (
    .a(X), .b(Y), .gt(comparator_1_gt), .eq(comparator_1_eq));  // open: lt
  or or_1 (or_1_out, comparator_1_gt, comparator_1_eq);
  Multiplexer #(.select(1), .width(3), .disabled("Z"), .enable("false")) multiplexer_2 (
    .in0(Y_num), .in1(X_num), .out(Max_num), .sel(or_1_out));

  // Notes on the sheet:
  //   输出两个输入中的较大值，并输出较大值的3位编号
endmodule

module \动态分支预测  (
  output RegWrite,
  output MemWrite,
  output [31:0] IF_PC,
  output [31:0] ID_PC,
  output [31:0] EX_PC,
  output [31:0] M_PC,
  output [31:0] WB_PC,
  output [31:0] RDin,
  output [31:0] MDin,
  output [31:0] LedData
);

  wire AluSrcB, and_1_out, and_2_out, and_4_out, and_5_out, and_6_out, and_7_out, and_8_out, and_9_out, B,
       Beq, BGTZ, BGTZ_flag, Bne, CLK, clock_2_out, comparator_1_gt, comparator_2_eq, comparator_3_eq,
       comparator_3_lt, controlled_buffer_1_out, d_ff_1_q, equal, ex_mem_1_equal_out, ex_mem_1_jal_out,
       ex_mem_1_lhu_2, ex_mem_1_pause_out, ex_mem_1_regdst_out, ex_mem_1_syscall_out, EX_RegWrite, fail, Go,
       halt, id_ex_1_jal_out, id_ex_1_lhu_2, id_ex_1_memtoreg_out, id_ex_1_memwrite_out, id_ex_1_regdst_out,
       if_id_1_predjmp_out, IF_PredJmp, IR1, IR2, IR3, J, JMP, jmp_flag, JR, LED, LHU, load_use,
       MEM_RegWrite, mem_wb_1_jal_out, mem_wb_1_memtoreg_out, MemToReg, multiplexer_4_out, nand_1_out,
       not_2_out, or_2_out, or_3_out, or_4_out, or_7_out, or_8_out, pause, PredJmp, RegDst, RST, SignedExt,
       Syscall, V034, W1, W2, W3, Write, \单周期硬布线控制器_差异化_1_alu_src , \单周期硬布线控制器_差异化_1_beq ,
       \单周期硬布线控制器_差异化_1_bgtz , \单周期硬布线控制器_差异化_1_bne , \单周期硬布线控制器_差异化_1_jal , \单周期硬布线控制器_差异化_1_jmp ,
       \单周期硬布线控制器_差异化_1_jr , \单周期硬布线控制器_差异化_1_lhu , \单周期硬布线控制器_差异化_1_memtoreg , \单周期硬布线控制器_差异化_1_memwrite ,
       \单周期硬布线控制器_差异化_1_regdst , \单周期硬布线控制器_差异化_1_regwrite , \单周期硬布线控制器_差异化_1_syscall ;
  wire [1:0] Forward1, Forward2, ForwardRD1, ForwardRD2, multiplexer_15_out, multiplexer_16_out;
  wire [3:0] id_ex_1_aluop_out, \单周期硬布线控制器_差异化_1_alu_op ;
  wire [4:0] EX_WriteReg_num, ID_ReadReg1_num, ID_ReadReg2_num, MEM_WriteReg_num, multiplexer_13_out,
       multiplexer_17_out, multiplexer_21_out, w_num;
  wire [5:0] Func, OP;
  wire [12:0] CNT_num;
  wire [15:0] \LoadUse次数 , multiplexer_25_out, \总周期数 , \插入气泡数 , \无条件分支数 , \条件分支成功数 ;
  wire [25:6] if_id_1_ir_out;
  wire [27:0] shifter_1_out;
  wire [31:0] bit_extender_1_out, bit_extender_2_out, bit_extender_3_out, EX_IR, ex_mem_1_ir_out,
       ex_mem_1_pc_out, ID_IR, if_id_1_pc_out, IF_IR, IF_PC_4, imme, IR, MEM_AluOut, MEM_IR, Mem_MemData,
       mem_wb_1_ir_out, mem_wb_1_pc_out, mips_alu_1_result, \mips_regfile_下降沿_1_r1 , \mips_regfile_下降沿_1_r2 ,
       multiplexer_1_out, multiplexer_2_out, multiplexer_5_out, multiplexer_6_out, multiplexer_7_out,
       multiplexer_11_out, multiplexer_12_out, multiplexer_23_out, NewR1, NewR2, PC_4, PCBranch,
       PCBranchAddr, PCnext, PredAddr, R1, R2, ram_1_data, rom_1_data, shifter_2_out, WB_AluOut, WB_IR,
       WB_MemOut;

  Button \u_总复位  (.out(RST));
  Button _1 (.out(IR1));
  Button _2 (.out(IR2));
  Button _3 (.out(IR3));
  // Probe on \总周期数 
  // Probe on \总周期数 
  Button \u_继续运行  (.out(Go));
  LED #(.active("true")) led_1 (.in(W1));
  LED #(.active("true")) led_2 (.in(W2));
  LED #(.active("true")) led_3 (.in(W3));
  and and_1 (and_1_out, Bne, ~equal);  // AND_Gate
  or or_1 (jmp_flag, and_1_out, and_2_out);
  or or_2 (or_2_out, B, JMP);
  Hex_Digit_Display hex_digit_display_1 (.value(LedData[31:28]));  // open: dp
  // Probe on IF_PC[19:0]
  // Mips_Probe mips_probe_1: pin names not known; wires that end beside it: IF_IR
  and and_2 (and_2_out, equal, Beq);
  Multiplexer #(.select(1), .width(32), .disabled("Z"), .enable("false")) multiplexer_1 (
    .in0(IF_PC_4), .in1(PCBranch), .out(multiplexer_1_out), .sel(jmp_flag));
  Shifter #(.width(28), .shift("ll")) shifter_1 (.in(IR[27:0]), .\dist (5'b00010), .out(shifter_1_out));
  or or_3 (or_3_out, Beq, Bne, JMP, BGTZ);
  or or_4 (or_4_out, B, JMP);
  Hex_Digit_Display hex_digit_display_2 (.value(LedData[27:24]));  // open: dp
  Hex_Digit_Display hex_digit_display_3 (.value(LedData[23:20]));  // open: dp
  // Probe on ID_PC[19:0]
  // Mips_Probe mips_probe_2: pin names not known; wires that end beside it: ID_IR
  Comparator #(.width(32), .mode("twosComplement")) comparator_1 (
    .a(NewR1), .b({32{1'b0}}), .gt(comparator_1_gt));  // open: eq, lt
  and and_3 (BGTZ_flag, BGTZ, comparator_1_gt);
  Multiplexer #(.select(2), .width(32), .disabled("Z"), .enable("false")) multiplexer_2 (
    .in0(multiplexer_1_out), .in1(NewR1), .in2({PC_4[31:28], shifter_1_out}), .in3(NewR1),
    .out(multiplexer_2_out), .sel({JMP, JR}));
  and and_4 (and_4_out, or_3_out, ~JR);  // AND_Gate
  and and_5 (and_5_out, ~JR, or_2_out);  // AND_Gate
  and and_6 (and_6_out, or_4_out, ~JR);  // AND_Gate
  Hex_Digit_Display hex_digit_display_4 (.value(LedData[15:12]));  // open: dp
  Hex_Digit_Display hex_digit_display_5 (.value(LedData[19:16]));  // open: dp
  Multiplexer #(.select(1), .width(32), .disabled("Z"), .enable("false")) multiplexer_3 (
    .in0(multiplexer_2_out), .in1(PCBranch), .out(PCBranchAddr), .sel(BGTZ_flag));
  Comparator #(.width(1), .mode("twosComplement")) comparator_2 (
    .a(and_6_out), .b(PredJmp), .eq(comparator_2_eq));  // open: gt, lt
  Hex_Digit_Display hex_digit_display_6 (.value(LedData[7:4]));  // open: dp
  Hex_Digit_Display hex_digit_display_7 (.value(LedData[11:8]));  // open: dp
  Clock #(.highDuration(1), .lowDuration(1)) clock_1 (.out(CLK));
  // Probe on EX_PC[19:0]
  // Mips_Probe mips_probe_3: pin names not known; wires that end beside it: EX_IR
  Register #(.width(32), .trigger("rising"), .Select("low")) register_1 (
    .D(NewR2), .Q(LedData), .clk(LED), .clr(RST));  // open: en
  not not_1 (fail, comparator_2_eq);
  Hex_Digit_Display hex_digit_display_8 (.value(LedData[3:0]));  // open: dp
  and and_7 (and_7_out, ~load_use, multiplexer_4_out);  // AND_Gate
  Multiplexer #(.select(1), .width(1), .disabled("Z"), .enable("false")) multiplexer_4 (
    .in0(1'b1), .in1(Go), .out(multiplexer_4_out), .sel(halt));
  BTB btb_1 (
    .Clk(CLK), .EX_Branch(and_4_out), .PC(IF_PC), .EX_PC(EX_PC), .EX_BranchAddr(PCBranchAddr),
    .EX_Branched(and_5_out), .JumpAddr(PredAddr), .PredictJump(IF_PredJmp));
  // Probe on \总周期数 
  // Probe on M_PC[19:0]
  // Mips_Probe mips_probe_4: pin names not known; wires that end beside it: MEM_IR
  Register #(.width(32), .trigger("rising"), .Select("low")) PC (
    .D(PCnext), .en(and_7_out), .Q(IF_PC), .clk(CLK), .clr(RST));
  Counter #(.width(16), .max('hffff), .ongoal("wrap"), .trigger("rising"), .behavior("old")) counter_1 (
    .load(1'b0), .count(multiplexer_4_out), .Q(\总周期数 ), .clk(CLK), .clr(RST));  // open: D, carry, preset
  // Probe on \总周期数 
  // Probe on \无条件分支数 
  // Probe on \条件分支成功数 
  // Probe on \插入气泡数 
  // Probe on \LoadUse次数 
  Adder #(.width(32)) adder_1 (.a(IF_PC), .b(32'h4), .out(IF_PC_4));  // open: cin, cout
  // Probe on IF_PC[11:0]
  // Probe on WB_PC[19:0]
  // Mips_Probe mips_probe_5: pin names not known; wires that end beside it: WB_IR
  Multiplexer #(.select(1), .width(32), .disabled("Z"), .enable("false")) multiplexer_5 (
    .in0(IF_PC_4), .in1(PredAddr), .out(multiplexer_5_out), .sel(IF_PredJmp));
  Multiplexer #(.select(1), .width(32), .disabled("Z"), .enable("false")) multiplexer_6 (
    .in0(PC_4), .in1(PCBranchAddr), .out(multiplexer_6_out), .sel(and_5_out));
  // Probe on ID_PC[11:0]
  // Probe on EX_PC[11:0]
  ROM #(.addrWidth(10), .dataWidth(32), .Select("high")) rom_1 (.addr(IF_PC[11:2]), .data(rom_1_data));
  Multiplexer #(.select(1), .width(32), .disabled("Z"), .enable("false")) multiplexer_7 (
    .in0(multiplexer_5_out), .in1(multiplexer_6_out), .out(multiplexer_7_out), .sel(fail));
  // Probe on M_PC[11:0]
  D_Flip_Flop #(.trigger("high"), .Pre_Clr_Positions("LEGACY"), .NegatePresetClear("false"), .enable("true"), .NewFFLayout("false")) d_ff_1 (.Q(d_ff_1_q));  // open: clk, D, Qn, preset, en, reset
  // Probe on 13'h377
  // Mips_Probe mips_probe_6: pin names not known; wires that end beside it: rom_1_data
  and and_8 (and_8_out, Write, ~load_use);  // AND_Gate
  Multiplexer #(.select(1), .width(32), .disabled("Z"), .enable("false")) multiplexer_8 (
    .in0(multiplexer_7_out), .in1(NewR1), .out(PCnext), .sel(JR));
  // Probe on WB_PC[11:0]
  Comparator #(.width(13), .mode("twosComplement")) comparator_3 (
    .a(CNT_num), .b(13'h377), .eq(comparator_3_eq), .lt(comparator_3_lt));  // open: gt
  Clock #(.highDuration(1), .lowDuration(1)) clock_2 (.out(clock_2_out));
  IF_ID if_id_1 (
    .IR_in(rom_1_data), .OldPC_in(IF_PC), .PC_in(IF_PC_4), .IR_out({OP, if_id_1_ir_out, Func}),
    .OldPC_out(ID_PC), .PC_out(if_id_1_pc_out), .\气泡高电平有效 (fail), .\使能 (and_8_out), .Clk(CLK), .Clr(RST),
    .PredJmp_in(IF_PredJmp), .PredJmp_out(if_id_1_predjmp_out));
  nand nand_1 (nand_1_out, d_ff_1_q, comparator_3_eq);
  Counter #(.width(13), .max('h1fff), .ongoal("stay"), .trigger("rising"), .behavior("old")) counter_2 (
    .count(comparator_3_lt), .Q(CNT_num), .clk(clock_2_out));  // open: load, D, carry, clr, preset
  assign controlled_buffer_1_out = nand_1_out ? clock_2_out : 1'bz;  // Controlled_Buffer controlled_buffer_1
  Pull_Resistor #(.pull(1)) pull_resistor_1 (.node(controlled_buffer_1_out));
  assign bit_extender_1_out = {{16{1'b0}}, {if_id_1_ir_out[15:6], Func}};  // Bit_Extender bit_extender_1
  assign bit_extender_2_out = {{16{if_id_1_ir_out[15]}}, {if_id_1_ir_out[15:6], Func}};  // Bit_Extender bit_extender_2
  \单周期硬布线控制器_差异化  \u_单周期硬布线控制器_差异化_1  (
    .OP(OP), .Func(Func), .ALU_OP(\单周期硬布线控制器_差异化_1_alu_op ), .MemToReg(\单周期硬布线控制器_差异化_1_memtoreg ),
    .MemWrite(\单周期硬布线控制器_差异化_1_memwrite ), .ALU_SRC(\单周期硬布线控制器_差异化_1_alu_src ),
    .RegWrite(\单周期硬布线控制器_差异化_1_regwrite ), .SysCALL(\单周期硬布线控制器_差异化_1_syscall ), .SignedExt(SignedExt),
    .RegDst(\单周期硬布线控制器_差异化_1_regdst ), .Beq(\单周期硬布线控制器_差异化_1_beq ), .Bne(\单周期硬布线控制器_差异化_1_bne ),
    .JR(\单周期硬布线控制器_差异化_1_jr ), .JMP(\单周期硬布线控制器_差异化_1_jmp ), .JAL(\单周期硬布线控制器_差异化_1_jal ),
    .BGTZ(\单周期硬布线控制器_差异化_1_bgtz ), .LHU(\单周期硬布线控制器_差异化_1_lhu ));
  Multiplexer #(.select(1), .width(5), .disabled("Z"), .enable("false")) multiplexer_9 (
    .in0(if_id_1_ir_out[25:21]), .in1(5'b00010), .out(ID_ReadReg1_num), .sel(\单周期硬布线控制器_差异化_1_syscall ));
  Multiplexer #(.select(1), .width(5), .disabled("Z"), .enable("false")) multiplexer_10 (
    .in0(if_id_1_ir_out[20:16]), .in1(5'b00100), .out(ID_ReadReg2_num), .sel(\单周期硬布线控制器_差异化_1_syscall ));
  Multiplexer #(.select(1), .width(32), .disabled("Z"), .enable("false")) multiplexer_11 (
    .in0(bit_extender_1_out), .in1(bit_extender_2_out), .out(multiplexer_11_out), .sel(SignedExt));
  or or_5 (B, BGTZ_flag, jmp_flag);
  \MIPS_Regfile_下降沿  \mips_regfile_下降沿_1  (
    .Din(RDin), .Clk(CLK), .R1(\mips_regfile_下降沿_1_r1 ), .R2(\mips_regfile_下降沿_1_r2 ), .WE(RegWrite),
    .W_num(w_num), .R1_num(ID_ReadReg1_num), .R2_num(ID_ReadReg2_num));
  not not_2 (not_2_out, Go);
  Counter #(.width(16), .max('hffff), .ongoal("wrap"), .trigger("rising"), .behavior("old")) counter_3 (
    .load(1'b0), .count(JMP), .Q(\无条件分支数 ), .clk(CLK), .clr(RST));  // open: D, carry, preset
  Counter #(.width(16), .max('hffff), .ongoal("wrap"), .trigger("rising"), .behavior("old")) counter_4 (
    .load(1'b0), .count(B), .Q(\条件分支成功数 ), .clk(CLK), .clr(RST));  // open: D, carry, preset
  or or_6 (J, B, JMP, JR);
  nand nand_2 (Write, not_2_out, halt);
  or or_7 (or_7_out, fail, load_use);
  ID_EX id_ex_1 (
    .Beq_in(\单周期硬布线控制器_差异化_1_beq ), .Bne_in(\单周期硬布线控制器_差异化_1_bne ), .MemToReg_in(\单周期硬布线控制器_差异化_1_memtoreg ),
    .MemWrite_in(\单周期硬布线控制器_差异化_1_memwrite ), .AluSrcB_in(\单周期硬布线控制器_差异化_1_alu_src ),
    .RegWrite_in(\单周期硬布线控制器_差异化_1_regwrite ), .JAL_in(\单周期硬布线控制器_差异化_1_jal ),
    .RegDst_in(\单周期硬布线控制器_差异化_1_regdst ), .JMP_in(\单周期硬布线控制器_差异化_1_jmp ), .JR_in(\单周期硬布线控制器_差异化_1_jr ),
    .SignedExt_in(SignedExt), .AluOP_in(\单周期硬布线控制器_差异化_1_alu_op ), .IR_in({OP, if_id_1_ir_out, Func}),
    .OldPC_in(ID_PC), .PC_in(if_id_1_pc_out), .R1_in(\mips_regfile_下降沿_1_r1 ),
    .R2_in(\mips_regfile_下降沿_1_r2 ), .imm_in(multiplexer_11_out), .Beq_out(Beq), .Bne_out(Bne),
    .MemToReg_out(id_ex_1_memtoreg_out), .MemWrite_out(id_ex_1_memwrite_out), .AluSrcB_out(AluSrcB),
    .RegWrite_out(EX_RegWrite), .JAL_out(id_ex_1_jal_out), .RegDst_out(id_ex_1_regdst_out), .JMP_out(JMP),
    .JR_out(JR), .AluOP_out(id_ex_1_aluop_out), .IR_out(IR), .OldPC_out(EX_PC), .PC_out(PC_4), .R1_out(R1),
    .R2_out(R2), .imm_out(imme), .\气泡高电平有效 (or_7_out), .\使能 (Write), .Clk(CLK), .Clr(RST),
    .Syscall_in(\单周期硬布线控制器_差异化_1_syscall ), .Syscall_out(Syscall), .BGTZ(\单周期硬布线控制器_差异化_1_bgtz ),
    .BGTZ_2(BGTZ), .LHU(\单周期硬布线控制器_差异化_1_lhu ), .LHU_2(id_ex_1_lhu_2),
    .PredJmp_in_Eret_in(if_id_1_predjmp_out), .PredJmp_out_Eret_in(PredJmp));  // open: SignedExt_out
  Shifter #(.width(32), .shift("ll")) shifter_2 (.in(imme), .\dist (5'b00010), .out(shifter_2_out));
  Multiplexer #(.select(1), .width(32), .disabled("Z"), .enable("false")) multiplexer_12 (
    .in0(NewR2), .in1(imme), .out(multiplexer_12_out), .sel(AluSrcB));
  and and_9 (and_9_out, load_use, Write);
  Multiplexer #(.select(1), .width(5), .disabled("Z"), .enable("false")) multiplexer_13 (
    .in0(IR[20:16]), .in1(IR[15:11]), .out(multiplexer_13_out), .sel(id_ex_1_regdst_out));
  Multiplexer #(.select(1), .width(5), .disabled("Z"), .enable("false")) multiplexer_14 (
    .in0(multiplexer_13_out), .in1({5{1'b1}}), .out(EX_WriteReg_num), .sel(id_ex_1_jal_out));
  Adder #(.width(32)) adder_2 (.a(shifter_2_out), .b(PC_4), .out(PCBranch));  // open: cin, cout
  \重定向控制逻辑  \u_重定向控制逻辑_1  (
    .OP(OP), .EX_WriteReg_num(EX_WriteReg_num), .EX_RegWrite(EX_RegWrite), .FUNC(Func),
    .MEM_WriteReg_num(MEM_WriteReg_num), .MEM_RegWrite(MEM_RegWrite), .EX_OP(IR[31:26]),
    .ID_R1_num(ID_ReadReg1_num), .MemToReg(MemToReg), .ID_R2_num(ID_ReadReg2_num), .load_use(load_use),
    .Forward1(Forward1), .Forward2(Forward2));
  Counter #(.width(16), .max('hffff), .ongoal("wrap"), .trigger("rising"), .behavior("old")) counter_5 (
    .load(1'b0), .count(and_9_out), .Q(\LoadUse次数 ), .clk(CLK), .clr(RST));  // open: D, carry, preset
  MIPS_ALU mips_alu_1 (
    .X(NewR1), .Y(multiplexer_12_out), .AluOP(id_ex_1_aluop_out), .Equal(equal), .Result(mips_alu_1_result),
    .shamt(IR[10:6]));  // open: Result_2
  EX_MEM ex_mem_1 (
    .Syscall_in(Syscall), .MemToReg_in(id_ex_1_memtoreg_out), .MemWrite_in(id_ex_1_memwrite_out),
    .RegWrite_in(EX_RegWrite), .JAL_in(id_ex_1_jal_out), .RegDst_in(id_ex_1_regdst_out), .equal_in(equal),
    .IR_in(IR), .OldPC_in(EX_PC), .PC_in(PC_4), .AluOut_in(mips_alu_1_result), .R2_in(NewR2),
    .Syscall_out(ex_mem_1_syscall_out), .MemToReg_out(MemToReg), .MemWrite_out(MemWrite),
    .RegWrite_out(MEM_RegWrite), .JAL_out(ex_mem_1_jal_out), .RegDst_out(ex_mem_1_regdst_out),
    .equal_out(ex_mem_1_equal_out), .IR_out(ex_mem_1_ir_out), .OldPC_out(M_PC), .PC_out(ex_mem_1_pc_out),
    .AluOut_out(MEM_AluOut), .R2_out(MDin), .\气泡高电平有效 (1'b0), .\使能 (Write), .Clk(CLK), .Clr(RST),
    .LHU_2(ex_mem_1_lhu_2), .LHU(id_ex_1_lhu_2), .pause_in(pause), .pause_out(ex_mem_1_pause_out));  // open: Eret_in, Eret_in_2
  or or_8 (or_8_out, load_use, J);
  Multiplexer #(.select(1), .width(2), .disabled("Z"), .enable("false")) multiplexer_15 (
    .in0(Forward1), .in1(2'b00), .out(multiplexer_15_out), .sel(or_8_out));
  Multiplexer #(.select(1), .width(2), .disabled("Z"), .enable("false")) multiplexer_16 (
    .in0(Forward2), .in1(2'b00), .out(multiplexer_16_out), .sel(or_8_out));
  Register #(.width(2), .trigger("rising"), .Select("low")) register_2 (
    .D(multiplexer_15_out), .en(Write), .Q(ForwardRD1), .clk(CLK), .clr(RST));
  Register #(.width(2), .trigger("rising"), .Select("low")) register_3 (
    .D(multiplexer_16_out), .en(Write), .Q(ForwardRD2), .clk(CLK), .clr(RST));
  Multiplexer #(.select(1), .width(5), .disabled("Z"), .enable("false")) multiplexer_17 (
    .in0(ex_mem_1_ir_out[20:16]), .in1(ex_mem_1_ir_out[15:11]), .out(multiplexer_17_out),
    .sel(ex_mem_1_regdst_out));
  Multiplexer #(.select(1), .width(5), .disabled("Z"), .enable("false")) multiplexer_18 (
    .in0(multiplexer_17_out), .in1({5{1'b1}}), .out(MEM_WriteReg_num), .sel(ex_mem_1_jal_out));
  RAM #(.addrWidth(10), .dataWidth(32), .bus("separate"), .Select("high")) ram_1 (
    .addr(MEM_AluOut[11:2]), .din(MDin), .data(ram_1_data), .str(MemWrite), .clk(CLK), .clr(RST));  // open: sel, ld
  MEM_WB mem_wb_1 (
    .Syscall_in(ex_mem_1_syscall_out), .MemToReg_in(MemToReg), .MemWrite_in(MemWrite),
    .RegWrite_in(MEM_RegWrite), .JAL_in(ex_mem_1_jal_out), .RegDst_in(ex_mem_1_regdst_out),
    .equal_in(ex_mem_1_equal_out), .IR_in(ex_mem_1_ir_out), .OldPC_in(M_PC), .PC_in(ex_mem_1_pc_out),
    .AluOut_in(MEM_AluOut), .MemOut_in(ram_1_data), .MemToReg_out(mem_wb_1_memtoreg_out),
    .RegWrite_out(RegWrite), .JAL_out(mem_wb_1_jal_out), .RegDst_out(RegDst), .IR_out(mem_wb_1_ir_out),
    .OldPC_out(WB_PC), .PC_out(mem_wb_1_pc_out), .AluOut_out(WB_AluOut), .MemOut_out(WB_MemOut),
    .\气泡高电平有效 (1'b0), .\使能 (Write), .Clk(CLK), .Clr(RST), .LHU_2(LHU), .LHU(ex_mem_1_lhu_2),
    .pause_in(ex_mem_1_pause_out), .pause_out(halt));  // open: Syscall_out, MemWrite_out, equal_out, Eret_in, Eret_out
  Multiplexer #(.select(2), .width(32), .disabled("Z"), .enable("false")) multiplexer_19 (
    .in0(R1), .in1(MEM_AluOut), .in2(WB_AluOut), .in3(Mem_MemData), .out(NewR1), .sel(ForwardRD1));
  Multiplexer #(.select(2), .width(32), .disabled("Z"), .enable("false")) multiplexer_20 (
    .in0(R2), .in1(MEM_AluOut), .in2(WB_AluOut), .in3(Mem_MemData), .out(NewR2), .sel(ForwardRD2));
  Multiplexer #(.select(1), .width(5), .disabled("Z"), .enable("false")) multiplexer_21 (
    .in0(mem_wb_1_ir_out[20:16]), .in1(mem_wb_1_ir_out[15:11]), .out(multiplexer_21_out), .sel(RegDst));
  Multiplexer #(.select(1), .width(5), .disabled("Z"), .enable("false")) multiplexer_22 (
    .in0(multiplexer_21_out), .in1({5{1'b1}}), .out(w_num), .sel(mem_wb_1_jal_out));
  Multiplexer #(.select(1), .width(32), .disabled("Z"), .enable("false")) multiplexer_23 (
    .in0(WB_AluOut), .in1(Mem_MemData), .out(multiplexer_23_out), .sel(mem_wb_1_memtoreg_out));
  Comparator #(.width(32), .mode("twosComplement")) comparator_4 (.a(NewR1), .b(32'h22), .eq(V034));  // open: gt, lt
  Multiplexer #(.select(1), .width(32), .disabled("Z"), .enable("false")) multiplexer_24 (
    .in0(multiplexer_23_out), .in1(mem_wb_1_pc_out), .out(RDin), .sel(mem_wb_1_jal_out));
  Multiplexer #(.select(1), .width(16), .disabled("Z"), .enable("false")) multiplexer_25 (
    .in0(WB_MemOut[15:0]), .in1(WB_MemOut[31:16]), .out(multiplexer_25_out), .sel(WB_AluOut[1]));
  and and_10 (pause, ~V034, Syscall);  // AND_Gate
  and and_11 (LED, V034, Syscall);
  assign bit_extender_3_out = {{16{1'b0}}, multiplexer_25_out};  // Bit_Extender bit_extender_3
  Multiplexer #(.select(1), .width(32), .disabled("Z"), .enable("false")) multiplexer_26 (
    .in0(WB_MemOut), .in1(bit_extender_3_out), .out(Mem_MemData), .sel(LHU));

  // Other names for the same wires on the sheet: MEM_PC[31:0] = M_PC; PC[31:0] = IF_PC

  // Notes on the sheet:
  //   中断源
  //   时空图监测，可删除
  //   中断等待指示
  //   数码管输出
  //   指令存储器
  //   PC+4
  //   控制位
  //   contents of rom_1 (hex, n*v repeats v):
  //   20110001 8000c05 20110001 20120002 20130003 8000c09 20110001 20120002 20130003 8000c0d 20110001
  //   20120002 20130003 8000c11 20110001 20120002 20130003 c000cb8 20100001 20110001 118fc0 112020
  //   20020022 c 118882 12200001 8000c15 112020 20020022 c 20110001 118880 112020 20020022 c 12200001
  //   8000c1f 20110001 118fc0 112020 20020022 c 1188c3 112020 20020022 c 118903 112020 20020022 c 118903
  //   112020 20020022 c 118903 112020 20020022 c 118903 112020 20020022 c 118903 112020 20020022 c 118903
  //   112020 20020022 c 118903 112020 20020022 c 20100001 109fc0 139fc3 8021 2012000c 24160003 26100001
  //   3210000f 20080008 20090001 139900 2709825 132020 20020022 c 1094022 1500fff9 22100001 2018000f
  //   2188024 108700 20080008 20090001 139902 2709825 132021 20020022 c 1094022 1500fff9 108702 2c9b022
  //   12c00001 8000c50 4020 1084027 84400 3508ffff 82021 20020022 c 2010ffff 20110000 ae300000 22100001
  //   22310004 ae300000 22100001 22310004 ae300000 22100001 22310004 ae300000 22100001 22310004 ae300000
  //   22100001 22310004 ae300000 22100001 22310004 ae300000 22100001 22310004 ae300000 22100001 22310004
  //   ae300000 22100001 22310004 ae300000 22100001 22310004 ae300000 22100001 22310004 ae300000 22100001
  //   22310004 ae300000 22100001 22310004 ae300000 22100001 22310004 ae300000 22100001 22310004 ae300000
  //   22100001 22310004 22100001 8020 2011003c 8e130000 8e340000 274402a 11000002 ae330000 ae140000
  //   2231fffc 1611fff8 102020 20020022 c 22100004 2011003c 1611fff2 20020032 c 20100000 22100001 102020
  //   20020022 c 22100002 102020 20020022 c 22100003 102020 20020022 c 22100004 102020 20020022 c 22100005
  //   102020 20020022 c 22100006 102020 20020022 c 22100007 102020 20020022 c 22100008 102020 20020022
  //   20020022 c 3e00008
  //   流水调试日志用
  //   暂停节拍，不能为0
  //   戳工具置1进入计数暂停模式，ctrl+k时钟自动运行到对应节拍暂停
  //   ctrl+k关闭时钟连续运行，将控制位置零，进入单步调试模式调试
  //   指令字
  //   可计数暂停的时钟源
  //   OP
  //   Func
  //   rs
  //   rt
  //   rd
  //   JMP
  //   JR
  //   OP
  //   Func
  //   Beq
  //   Bne
  //   MemToReg
  //   MemWrite
  //   AluOP
  //   AluSrcB
  //   RegWrite
  //   JAL
  //   RegDst
  //   Syscall
  //   为方便自动评测，需要输出流水线各段保存的PC值，注意是PC不是PC+4，另外ID段寄存器写入信息，Mem段内存写入信息也要输出
  //   PCBranch
  //   rt
  //   rd
endmodule

module \流水中断  (
  output RegWrite,
  output MemWrite,
  output [31:0] IF_PC,
  output [31:0] ID_PC,
  output [31:0] EX_PC,
  output [31:0] M_PC,
  output [31:0] WB_PC,
  output [31:0] RDin,
  output [31:0] MDin,
  output [31:0] LedData
);

  wire AluSrcB, and_1_out, and_2_out, and_4_out, and_5_out, and_6_out, and_7_out, and_8_out, and_9_out, Beq,
       BGTZ, BGTZ_flag, Bne, CLK, clock_2_out, clock_3_out, clock_4_out, clock_5_out, comparator_1_gt,
       comparator_2_eq, comparator_4_eq, comparator_4_lt, controlled_buffer_1_out, d_ff_1_q, d_ff_2_q,
       d_ff_3_q, d_ff_4_q, equal, Eret, ex_mem_1_equal_out, ex_mem_1_eret_in_2, ex_mem_1_jal_out,
       ex_mem_1_lhu_2, ex_mem_1_pause_out, ex_mem_1_regdst_out, ex_mem_1_syscall_out, EX_RegWrite, Go, halt,
       ID_Eret, id_ex_1_jal_out, id_ex_1_lhu_2, id_ex_1_memtoreg_out, id_ex_1_memwrite_out,
       id_ex_1_predjmp_out_eret_in, id_ex_1_regdst_out, IE, Interrupt, IR1, IR1_2_q, IR1_3_q, IR1_q,
       IR1reset, IR2, IR2reset, IR3, IR3reset, J, JMP, jmp_flag, JR, LED, LHU, load_use, MEM_RegWrite,
       mem_wb_1_jal_out, mem_wb_1_memtoreg_out, MemToReg, multiplexer_4_out, nand_2_out, not_1_out,
       not_2_out, or_2_out, or_4_out, or_5_out, or_9_out, or_10_out, or_11_out, or_12_out, or_13_out,
       or_14_out, pause, priority_encoder_1_gs, RegDst, RST, SignedExt, Syscall, V034, W1, W2, W3, Write,
       \单周期硬布线控制器_差异化_1_alu_src , \单周期硬布线控制器_差异化_1_beq , \单周期硬布线控制器_差异化_1_bgtz , \单周期硬布线控制器_差异化_1_bne ,
       \单周期硬布线控制器_差异化_1_jal , \单周期硬布线控制器_差异化_1_jmp , \单周期硬布线控制器_差异化_1_jr , \单周期硬布线控制器_差异化_1_lhu ,
       \单周期硬布线控制器_差异化_1_memtoreg , \单周期硬布线控制器_差异化_1_memwrite , \单周期硬布线控制器_差异化_1_regdst ,
       \单周期硬布线控制器_差异化_1_regwrite , \单周期硬布线控制器_差异化_1_syscall ;
  wire [1:0] Forward1, Forward2, ForwardRD1, ForwardRD2, IRnumber, multiplexer_8_out, multiplexer_9_out,
       register_3_q;
  wire [3:0] id_ex_1_aluop_out, \单周期硬布线控制器_差异化_1_alu_op ;
  wire [4:0] EX_WriteReg_num, ID_ReadReg1_num, ID_ReadReg2_num, MEM_WriteReg_num, multiplexer_13_out,
       multiplexer_18_out, multiplexer_22_out, w_num;
  wire [5:0] Func;
  wire [12:0] CNT_num;
  wire [15:0] \LoadUse次数 , multiplexer_19_out, \总周期数 , \插入气泡数 , \无条件分支数 , \条件分支成功数 ;
  wire [27:0] shifter_1_out;
  wire [31:0] adder_1_out, bit_extender_1_out, bit_extender_2_out, bit_extender_3_out, EPC, EX_IR,
       ex_mem_1_ir_out, ex_mem_1_pc_out, if_id_1_pc_out, IF_IR, imme, IR, IRaddress, MEM_AluOut, MEM_IR,
       Mem_MemData, mem_wb_1_ir_out, mem_wb_1_pc_out, mips_alu_1_result, \mips_regfile_下降沿_1_r1 ,
       \mips_regfile_下降沿_1_r2 , multiplexer_1_out, multiplexer_2_out, multiplexer_7_out, multiplexer_11_out,
       multiplexer_12_out, multiplexer_24_out, NewR1, NewR2, PC_4, PCBranch, PCBranchAddr, PCnext, R1, R2,
       ram_1_data, rom_1_data, shifter_2_out, WB_AluOut, WB_IR, WB_MemOut;
  wire [31:6] ID_IR;

  Button \u_总复位  (.out(RST));
  Button _1 (.out(IR1));
  Button _2 (.out(IR2));
  Button _3 (.out(IR3));
  // Probe on \总周期数 
  // Probe on \总周期数 
  Button \u_继续运行  (.out(Go));
  LED #(.active("true")) led_1 (.in(W1));
  LED #(.active("true")) led_2 (.in(W2));
  LED #(.active("true")) led_3 (.in(W3));
  and and_1 (and_1_out, Bne, ~equal);  // AND_Gate
  or or_1 (jmp_flag, and_1_out, and_2_out);
  Hex_Digit_Display hex_digit_display_1 (.value(LedData[31:28]));  // open: dp
  // Probe on IF_PC[19:0]
  // Mips_Probe mips_probe_1: pin names not known; wires that end beside it: IF_IR
  and and_2 (and_2_out, equal, Beq);
  Multiplexer #(.select(1), .width(32), .disabled("Z"), .enable("false")) multiplexer_1 (
    .in0(adder_1_out), .in1(PCBranch), .out(multiplexer_1_out), .sel(jmp_flag));
  Shifter #(.width(28), .shift("ll")) shifter_1 (.in(IR[27:0]), .\dist (5'b00010), .out(shifter_1_out));
  Hex_Digit_Display hex_digit_display_2 (.value(LedData[23:20]));  // open: dp
  Hex_Digit_Display hex_digit_display_3 (.value(LedData[27:24]));  // open: dp
  // Probe on ID_PC[19:0]
  // Mips_Probe mips_probe_2: pin names not known; wires that end beside it: {ID_IR, Func}
  and and_3 (BGTZ_flag, BGTZ, comparator_1_gt);
  Multiplexer #(.select(2), .width(32), .disabled("Z"), .enable("false")) multiplexer_2 (
    .in0(multiplexer_1_out), .in1(NewR1), .in2({PC_4[31:28], shifter_1_out}), .in3(NewR1),
    .out(multiplexer_2_out), .sel({JMP, JR}));
  or or_2 (or_2_out, BGTZ_flag, jmp_flag);
  Hex_Digit_Display hex_digit_display_4 (.value(LedData[15:12]));  // open: dp
  Hex_Digit_Display hex_digit_display_5 (.value(LedData[19:16]));  // open: dp
  Comparator #(.width(32), .mode("twosComplement")) comparator_1 (
    .a(NewR1), .b({32{1'b0}}), .gt(comparator_1_gt));  // open: eq, lt
  Multiplexer #(.select(1), .width(32), .disabled("Z"), .enable("false")) multiplexer_3 (
    .in0(multiplexer_2_out), .in1(PCBranch), .out(PCBranchAddr), .sel(BGTZ_flag));
  not not_1 (not_1_out, Go);
  not not_2 (not_2_out, Interrupt);
  Comparator #(.width(16), .mode("twosComplement")) comparator_2 (
    .a(\总周期数 ), .b({16{1'b0}}), .eq(comparator_2_eq));  // open: gt, lt
  Comparator #(.width(32), .mode("twosComplement")) comparator_3 (
    .a({ID_IR, Func}), .b(32'h42000018), .eq(ID_Eret));  // open: gt, lt
  Hex_Digit_Display hex_digit_display_6 (.value(LedData[11:8]));  // open: dp
  Hex_Digit_Display hex_digit_display_7 (.value(LedData[7:4]));  // open: dp
  Clock #(.highDuration(1), .lowDuration(1)) clock_1 (.out(CLK));
  // Probe on EX_PC[19:0]
  // Mips_Probe mips_probe_3: pin names not known; wires that end beside it: EX_IR
  Register #(.width(32), .trigger("rising"), .Select("low")) register_1 (
    .D(NewR2), .Q(LedData), .clk(LED), .clr(RST));  // open: en
  nand nand_1 (Write, not_1_out, halt);
  Counter #(.width(16), .max('hffff), .ongoal("wrap"), .trigger("rising"), .behavior("old")) counter_1 (
    .load(1'b0), .count(JMP), .Q(\无条件分支数 ), .clk(CLK), .clr(RST));  // open: D, carry, preset
  Counter #(.width(16), .max('hffff), .ongoal("wrap"), .trigger("rising"), .behavior("old")) counter_2 (
    .load(1'b0), .count(or_2_out), .Q(\条件分支成功数 ), .clk(CLK), .clr(RST));  // open: D, carry, preset
  or or_3 (J, or_2_out, JMP, JR);
  Register #(.width(1), .trigger("rising"), .Select("low")) register_2 (
    .D(not_2_out), .en(or_4_out), .Q(IE), .clk(CLK));  // open: clr
  or or_4 (or_4_out, Interrupt, Eret, comparator_2_eq);
  Hex_Digit_Display hex_digit_display_8 (.value(LedData[3:0]));  // open: dp
  and and_4 (and_4_out, ~load_use, multiplexer_4_out);  // AND_Gate
  Multiplexer #(.select(1), .width(1), .disabled("Z"), .enable("false")) multiplexer_4 (
    .in0(1'b1), .in1(Go), .out(multiplexer_4_out), .sel(halt));
  // Probe on \总周期数 
  // Probe on M_PC[19:0]
  // Mips_Probe mips_probe_4: pin names not known; wires that end beside it: MEM_IR
  Register #(.width(32), .trigger("rising"), .Select("low")) PC (
    .D(PCnext), .en(and_4_out), .Q(IF_PC), .clk(CLK), .clr(RST));
  Counter #(.width(16), .max('hffff), .ongoal("wrap"), .trigger("rising"), .behavior("old")) counter_3 (
    .load(1'b0), .count(multiplexer_4_out), .Q(\总周期数 ), .clk(CLK), .clr(RST));  // open: D, carry, preset
  // Probe on \总周期数 
  // Probe on \无条件分支数 
  // Probe on \条件分支成功数 
  // Probe on \插入气泡数 
  // Probe on \LoadUse次数 
  Adder #(.width(32)) adder_1 (.a(IF_PC), .b(32'h4), .out(adder_1_out));  // open: cin, cout
  Demultiplexer #(.select(2), .width(1), .tristate("false"), .disabled("Z"), .enable("false")) demultiplexer_1 (
    .out1(IR1reset), .out2(IR2reset), .out3(IR3reset), .in(Eret), .sel(register_3_q));  // open: out0
  Register #(.width(2), .trigger("rising"), .Select("low")) register_3 (
    .D(IRnumber), .en(Interrupt), .Q(register_3_q), .clk(CLK), .clr(RST));
  Register #(.width(32), .trigger("rising"), .Select("low")) u_EPC (
    .D(WB_PC), .en(Interrupt), .Q(EPC), .clk(CLK), .clr(RST));
  // Probe on IF_PC[11:0]
  // Probe on WB_PC[19:0]
  // Mips_Probe mips_probe_5: pin names not known; wires that end beside it: WB_IR
  // Probe on EX_PC[11:0]
  // Probe on ID_PC[11:0]
  ROM #(.addrWidth(10), .dataWidth(32), .Select("high")) rom_1 (.addr(IF_PC[11:2]), .data(rom_1_data));
  and and_5 (and_5_out, load_use, Write);
  // Probe on M_PC[11:0]
  D_Flip_Flop #(.trigger("high"), .Pre_Clr_Positions("LEGACY"), .NegatePresetClear("false"), .enable("true"), .NewFFLayout("false")) d_ff_1 (.Q(d_ff_1_q));  // open: clk, D, Qn, preset, en, reset
  // Probe on 13'h377
  // Mips_Probe mips_probe_6: pin names not known; wires that end beside it: rom_1_data
  and and_6 (and_6_out, Write, ~load_use);  // AND_Gate
  \重定向控制逻辑  \u_重定向控制逻辑_1  (
    .OP(ID_IR[31:26]), .EX_WriteReg_num(EX_WriteReg_num), .EX_RegWrite(EX_RegWrite), .FUNC(Func),
    .MEM_WriteReg_num(MEM_WriteReg_num), .MEM_RegWrite(MEM_RegWrite), .EX_OP(IR[31:26]),
    .ID_R1_num(ID_ReadReg1_num), .MemToReg(MemToReg), .ID_R2_num(ID_ReadReg2_num), .load_use(load_use),
    .Forward1(Forward1), .Forward2(Forward2));
  Counter #(.width(16), .max('hffff), .ongoal("wrap"), .trigger("rising"), .behavior("old")) counter_4 (
    .load(1'b0), .count(and_5_out), .Q(\LoadUse次数 ), .clk(CLK), .clr(RST));  // open: D, carry, preset
  Clock #(.highDuration(1), .lowDuration(1)) clock_2 (.out(clock_2_out));
  LED #(.active("true")) \_1号中断等待指示灯  (.in(W1));
  Clock #(.highDuration(1), .lowDuration(1)) clock_3 (.out(clock_3_out));
  LED #(.active("true")) \_2号中断等待指示灯  (.in(W2));
  Clock #(.highDuration(1), .lowDuration(1)) clock_4 (.out(clock_4_out));
  LED #(.active("true")) \_3号中断等待指示灯  (.in(W3));
  // Probe on WB_PC[11:0]
  Comparator #(.width(13), .mode("twosComplement")) comparator_4 (
    .a(CNT_num), .b(13'h377), .eq(comparator_4_eq), .lt(comparator_4_lt));  // open: gt
  Clock #(.highDuration(1), .lowDuration(1)) clock_5 (.out(clock_5_out));
  or or_5 (or_5_out, J, Eret, Interrupt);
  IF_ID if_id_1 (
    .IR_in(rom_1_data), .OldPC_in(IF_PC), .PC_in(adder_1_out), .IR_out({ID_IR, Func}), .OldPC_out(ID_PC),
    .PC_out(if_id_1_pc_out), .\气泡高电平有效 (or_5_out), .\使能 (and_6_out), .Clk(CLK), .Clr(RST));  // open: PredJmp_in, PredJmp_out
  or or_6 (W1, IR1_q, d_ff_2_q);
  or or_7 (W2, IR1_2_q, d_ff_3_q);
  or or_8 (W3, IR1_3_q, d_ff_4_q);
  nand nand_2 (nand_2_out, d_ff_1_q, comparator_4_eq);
  Counter #(.width(13), .max('h1fff), .ongoal("stay"), .trigger("rising"), .behavior("old")) counter_5 (
    .count(comparator_4_lt), .Q(CNT_num), .clk(clock_5_out));  // open: load, D, carry, clr, preset
  D_Flip_Flop #(.trigger("rising"), .Pre_Clr_Positions("LEGACY"), .NegatePresetClear("false"), .enable("true"), .NewFFLayout("false")) d_ff_2 (
    .clk(IR1), .D(1'b1), .Q(d_ff_2_q), .reset(IR1_q));  // open: Qn, preset, en
  D_Flip_Flop #(.trigger("rising"), .Pre_Clr_Positions("LEGACY"), .NegatePresetClear("false"), .enable("true"), .NewFFLayout("false")) d_ff_3 (
    .clk(IR2), .D(1'b1), .Q(d_ff_3_q), .reset(IR1_2_q));  // open: Qn, preset, en
  D_Flip_Flop #(.trigger("rising"), .Pre_Clr_Positions("LEGACY"), .NegatePresetClear("false"), .enable("true"), .NewFFLayout("false")) d_ff_4 (
    .clk(IR3), .D(1'b1), .Q(d_ff_4_q), .reset(IR1_3_q));  // open: Qn, preset, en
  assign controlled_buffer_1_out = nand_2_out ? clock_5_out : 1'bz;  // Controlled_Buffer controlled_buffer_1
  or or_9 (or_9_out, d_ff_2_q, IR1_q);
  Pull_Resistor #(.pull(0)) pull_resistor_1 (.node(IR1reset));
  or or_10 (or_10_out, d_ff_3_q, IR1_2_q);
  Pull_Resistor #(.pull(0)) pull_resistor_2 (.node(IR2reset));
  or or_11 (or_11_out, d_ff_4_q, IR1_3_q);
  Pull_Resistor #(.pull(0)) pull_resistor_3 (.node(IR3reset));
  Pull_Resistor #(.pull(1)) pull_resistor_4 (.node(controlled_buffer_1_out));
  assign bit_extender_1_out = {{16{1'b0}}, {ID_IR[15:6], Func}};  // Bit_Extender bit_extender_1
  assign bit_extender_2_out = {{16{ID_IR[15]}}, {ID_IR[15:6], Func}};  // Bit_Extender bit_extender_2
  and and_7 (and_7_out, or_9_out, ~IR1reset);  // AND_Gate
  and and_8 (and_8_out, or_10_out, ~IR2reset);  // AND_Gate
  and and_9 (and_9_out, or_11_out, ~IR3reset);  // AND_Gate
  \单周期硬布线控制器_差异化  \u_单周期硬布线控制器_差异化_1  (
    .OP(ID_IR[31:26]), .Func(Func), .ALU_OP(\单周期硬布线控制器_差异化_1_alu_op ), .MemToReg(\单周期硬布线控制器_差异化_1_memtoreg ),
    .MemWrite(\单周期硬布线控制器_差异化_1_memwrite ), .ALU_SRC(\单周期硬布线控制器_差异化_1_alu_src ),
    .RegWrite(\单周期硬布线控制器_差异化_1_regwrite ), .SysCALL(\单周期硬布线控制器_差异化_1_syscall ), .SignedExt(SignedExt),
    .RegDst(\单周期硬布线控制器_差异化_1_regdst ), .Beq(\单周期硬布线控制器_差异化_1_beq ), .Bne(\单周期硬布线控制器_差异化_1_bne ),
    .JR(\单周期硬布线控制器_差异化_1_jr ), .JMP(\单周期硬布线控制器_差异化_1_jmp ), .JAL(\单周期硬布线控制器_差异化_1_jal ),
    .BGTZ(\单周期硬布线控制器_差异化_1_bgtz ), .LHU(\单周期硬布线控制器_差异化_1_lhu ));
  Multiplexer #(.select(1), .width(5), .disabled("Z"), .enable("false")) multiplexer_5 (
    .in0(ID_IR[25:21]), .in1(5'b00010), .out(ID_ReadReg1_num), .sel(\单周期硬布线控制器_差异化_1_syscall ));
  Multiplexer #(.select(1), .width(5), .disabled("Z"), .enable("false")) multiplexer_6 (
    .in0(ID_IR[20:16]), .in1(5'b00100), .out(ID_ReadReg2_num), .sel(\单周期硬布线控制器_差异化_1_syscall ));
  Multiplexer #(.select(1), .width(32), .disabled("Z"), .enable("false")) multiplexer_7 (
    .in0(bit_extender_1_out), .in1(bit_extender_2_out), .out(multiplexer_7_out), .sel(SignedExt));
  or or_12 (or_12_out, load_use, J);
  D_Flip_Flop #(.trigger("rising"), .Pre_Clr_Positions("LEGACY"), .NegatePresetClear("false"), .enable("true"), .NewFFLayout("false")) u_IR1 (
    .clk(clock_2_out), .D(and_7_out), .Q(IR1_q));  // open: Qn, preset, en, reset
  D_Flip_Flop #(.trigger("rising"), .Pre_Clr_Positions("LEGACY"), .NegatePresetClear("false"), .enable("true"), .NewFFLayout("false")) IR1_2 (
    .clk(clock_3_out), .D(and_8_out), .Q(IR1_2_q));  // open: Qn, preset, en, reset
  D_Flip_Flop #(.trigger("rising"), .Pre_Clr_Positions("LEGACY"), .NegatePresetClear("false"), .enable("true"), .NewFFLayout("false")) IR1_3 (
    .clk(clock_4_out), .D(and_9_out), .Q(IR1_3_q));  // open: Qn, preset, en, reset
  \MIPS_Regfile_下降沿  \mips_regfile_下降沿_1  (
    .Din(RDin), .Clk(CLK), .R1(\mips_regfile_下降沿_1_r1 ), .R2(\mips_regfile_下降沿_1_r2 ), .WE(RegWrite),
    .W_num(w_num), .R1_num(ID_ReadReg1_num), .R2_num(ID_ReadReg2_num));
  Multiplexer #(.select(1), .width(2), .disabled("Z"), .enable("false")) multiplexer_8 (
    .in0(Forward1), .in1(2'b00), .out(multiplexer_8_out), .sel(or_12_out));
  Multiplexer #(.select(1), .width(2), .disabled("Z"), .enable("false")) multiplexer_9 (
    .in0(Forward2), .in1(2'b00), .out(multiplexer_9_out), .sel(or_12_out));
  Priority_Encoder #(.select(2), .disabled("Z")) priority_encoder_1 (
    .in1(IR1_q), .in2(IR1_2_q), .in3(IR1_3_q), .out(IRnumber), .gs(priority_encoder_1_gs));  // open: in0, en_out, en_in
  Register #(.width(2), .trigger("rising"), .Select("low")) register_4 (
    .D(multiplexer_8_out), .en(Write), .Q(ForwardRD1), .clk(CLK), .clr(RST));
  Register #(.width(2), .trigger("rising"), .Select("low")) register_5 (
    .D(multiplexer_9_out), .en(Write), .Q(ForwardRD2), .clk(CLK), .clr(RST));
  Multiplexer #(.select(2), .width(32), .disabled("Z"), .enable("false")) multiplexer_10 (
    .in1(32'h30ac), .in2(32'h3150), .in3(32'h31f4), .out(IRaddress), .sel(IRnumber));  // open: in0
  and and_10 (Interrupt, priority_encoder_1_gs, IE);
  or or_13 (or_13_out, or_5_out, load_use);
  ID_EX id_ex_1 (
    .Beq_in(\单周期硬布线控制器_差异化_1_beq ), .Bne_in(\单周期硬布线控制器_差异化_1_bne ), .MemToReg_in(\单周期硬布线控制器_差异化_1_memtoreg ),
    .MemWrite_in(\单周期硬布线控制器_差异化_1_memwrite ), .AluSrcB_in(\单周期硬布线控制器_差异化_1_alu_src ),
    .RegWrite_in(\单周期硬布线控制器_差异化_1_regwrite ), .JAL_in(\单周期硬布线控制器_差异化_1_jal ),
    .RegDst_in(\单周期硬布线控制器_差异化_1_regdst ), .JMP_in(\单周期硬布线控制器_差异化_1_jmp ), .JR_in(\单周期硬布线控制器_差异化_1_jr ),
    .SignedExt_in(SignedExt), .AluOP_in(\单周期硬布线控制器_差异化_1_alu_op ), .IR_in({ID_IR, Func}), .OldPC_in(ID_PC),
    .PC_in(if_id_1_pc_out), .R1_in(\mips_regfile_下降沿_1_r1 ), .R2_in(\mips_regfile_下降沿_1_r2 ),
    .imm_in(multiplexer_7_out), .Beq_out(Beq), .Bne_out(Bne), .MemToReg_out(id_ex_1_memtoreg_out),
    .MemWrite_out(id_ex_1_memwrite_out), .AluSrcB_out(AluSrcB), .RegWrite_out(EX_RegWrite),
    .JAL_out(id_ex_1_jal_out), .RegDst_out(id_ex_1_regdst_out), .JMP_out(JMP), .JR_out(JR),
    .AluOP_out(id_ex_1_aluop_out), .IR_out(IR), .OldPC_out(EX_PC), .PC_out(PC_4), .R1_out(R1), .R2_out(R2),
    .imm_out(imme), .\气泡高电平有效 (or_13_out), .\使能 (Write), .Clk(CLK), .Clr(RST),
    .Syscall_in(\单周期硬布线控制器_差异化_1_syscall ), .Syscall_out(Syscall), .BGTZ(\单周期硬布线控制器_差异化_1_bgtz ),
    .BGTZ_2(BGTZ), .LHU(\单周期硬布线控制器_差异化_1_lhu ), .LHU_2(id_ex_1_lhu_2), .PredJmp_in_Eret_in(ID_Eret),
    .PredJmp_out_Eret_in(id_ex_1_predjmp_out_eret_in));  // open: SignedExt_out
  Shifter #(.width(32), .shift("ll")) shifter_2 (.in(imme), .\dist (5'b00010), .out(shifter_2_out));
  Multiplexer #(.select(1), .width(32), .disabled("Z"), .enable("false")) multiplexer_11 (
    .in0(NewR2), .in1(imme), .out(multiplexer_11_out), .sel(AluSrcB));
  Multiplexer #(.select(1), .width(32), .disabled("Z"), .enable("false")) multiplexer_12 (
    .in0(PCBranchAddr), .in1(IRaddress), .out(multiplexer_12_out), .sel(Interrupt));
  Multiplexer #(.select(1), .width(5), .disabled("Z"), .enable("false")) multiplexer_13 (
    .in0(IR[20:16]), .in1(IR[15:11]), .out(multiplexer_13_out), .sel(id_ex_1_regdst_out));
  Multiplexer #(.select(1), .width(5), .disabled("Z"), .enable("false")) multiplexer_14 (
    .in0(multiplexer_13_out), .in1({5{1'b1}}), .out(EX_WriteReg_num), .sel(id_ex_1_jal_out));
  Adder #(.width(32)) adder_2 (.a(shifter_2_out), .b(PC_4), .out(PCBranch));  // open: cin, cout
  Multiplexer #(.select(1), .width(32), .disabled("Z"), .enable("false")) multiplexer_15 (
    .in0(multiplexer_12_out), .in1(EPC), .out(PCnext), .sel(Eret));
  MIPS_ALU mips_alu_1 (
    .X(NewR1), .Y(multiplexer_11_out), .AluOP(id_ex_1_aluop_out), .Equal(equal), .Result(mips_alu_1_result),
    .shamt(IR[10:6]));  // open: Result_2
  Multiplexer #(.select(2), .width(32), .disabled("Z"), .enable("false")) multiplexer_16 (
    .in0(R1), .in1(MEM_AluOut), .in2(WB_AluOut), .in3(Mem_MemData), .out(NewR1), .sel(ForwardRD1));
  Multiplexer #(.select(2), .width(32), .disabled("Z"), .enable("false")) multiplexer_17 (
    .in0(R2), .in1(MEM_AluOut), .in2(WB_AluOut), .in3(Mem_MemData), .out(NewR2), .sel(ForwardRD2));
  or or_14 (or_14_out, Eret, Interrupt);
  EX_MEM ex_mem_1 (
    .Syscall_in(Syscall), .MemToReg_in(id_ex_1_memtoreg_out), .MemWrite_in(id_ex_1_memwrite_out),
    .RegWrite_in(EX_RegWrite), .JAL_in(id_ex_1_jal_out), .RegDst_in(id_ex_1_regdst_out), .equal_in(equal),
    .IR_in(IR), .OldPC_in(EX_PC), .PC_in(PC_4), .AluOut_in(mips_alu_1_result), .R2_in(NewR2),
    .Syscall_out(ex_mem_1_syscall_out), .MemToReg_out(MemToReg), .MemWrite_out(MemWrite),
    .RegWrite_out(MEM_RegWrite), .JAL_out(ex_mem_1_jal_out), .RegDst_out(ex_mem_1_regdst_out),
    .equal_out(ex_mem_1_equal_out), .IR_out(ex_mem_1_ir_out), .OldPC_out(M_PC), .PC_out(ex_mem_1_pc_out),
    .AluOut_out(MEM_AluOut), .R2_out(MDin), .\气泡高电平有效 (or_14_out), .\使能 (Write), .Clk(CLK), .Clr(RST),
    .LHU_2(ex_mem_1_lhu_2), .LHU(id_ex_1_lhu_2), .pause_in(pause), .pause_out(ex_mem_1_pause_out),
    .Eret_in(id_ex_1_predjmp_out_eret_in), .Eret_in_2(ex_mem_1_eret_in_2));
  Comparator #(.width(32), .mode("twosComplement")) comparator_5 (.a(NewR1), .b(32'h22), .eq(V034));  // open: gt, lt
  Multiplexer #(.select(1), .width(5), .disabled("Z"), .enable("false")) multiplexer_18 (
    .in0(ex_mem_1_ir_out[20:16]), .in1(ex_mem_1_ir_out[15:11]), .out(multiplexer_18_out),
    .sel(ex_mem_1_regdst_out));
  Multiplexer #(.select(1), .width(16), .disabled("Z"), .enable("false")) multiplexer_19 (
    .in0(WB_MemOut[15:0]), .in1(WB_MemOut[31:16]), .out(multiplexer_19_out), .sel(WB_AluOut[1]));
  and and_11 (pause, ~V034, Syscall);  // AND_Gate
  and and_12 (LED, V034, Syscall);
  Multiplexer #(.select(1), .width(5), .disabled("Z"), .enable("false")) multiplexer_20 (
    .in0(multiplexer_18_out), .in1({5{1'b1}}), .out(MEM_WriteReg_num), .sel(ex_mem_1_jal_out));
  RAM #(.addrWidth(10), .dataWidth(32), .bus("separate"), .Select("high")) ram_1 (
    .addr(MEM_AluOut[11:2]), .din(MDin), .data(ram_1_data), .str(MemWrite), .clk(CLK), .clr(RST));  // open: sel, ld
  assign bit_extender_3_out = {{16{1'b0}}, multiplexer_19_out};  // Bit_Extender bit_extender_3
  Multiplexer #(.select(1), .width(32), .disabled("Z"), .enable("false")) multiplexer_21 (
    .in0(WB_MemOut), .in1(bit_extender_3_out), .out(Mem_MemData), .sel(LHU));
  MEM_WB mem_wb_1 (
    .Syscall_in(ex_mem_1_syscall_out), .MemToReg_in(MemToReg), .MemWrite_in(MemWrite),
    .RegWrite_in(MEM_RegWrite), .JAL_in(ex_mem_1_jal_out), .RegDst_in(ex_mem_1_regdst_out),
    .equal_in(ex_mem_1_equal_out), .IR_in(ex_mem_1_ir_out), .OldPC_in(M_PC), .PC_in(ex_mem_1_pc_out),
    .AluOut_in(MEM_AluOut), .MemOut_in(ram_1_data), .MemToReg_out(mem_wb_1_memtoreg_out),
    .RegWrite_out(RegWrite), .JAL_out(mem_wb_1_jal_out), .RegDst_out(RegDst), .IR_out(mem_wb_1_ir_out),
    .OldPC_out(WB_PC), .PC_out(mem_wb_1_pc_out), .AluOut_out(WB_AluOut), .MemOut_out(WB_MemOut),
    .\气泡高电平有效 (Interrupt), .\使能 (Write), .Clk(CLK), .Clr(RST), .LHU_2(LHU), .LHU(ex_mem_1_lhu_2),
    .pause_in(ex_mem_1_pause_out), .pause_out(halt), .Eret_in(ex_mem_1_eret_in_2), .Eret_out(Eret));  // open: Syscall_out, MemWrite_out, equal_out
  Multiplexer #(.select(1), .width(5), .disabled("Z"), .enable("false")) multiplexer_22 (
    .in0(mem_wb_1_ir_out[20:16]), .in1(mem_wb_1_ir_out[15:11]), .out(multiplexer_22_out), .sel(RegDst));
  Multiplexer #(.select(1), .width(5), .disabled("Z"), .enable("false")) multiplexer_23 (
    .in0(multiplexer_22_out), .in1({5{1'b1}}), .out(w_num), .sel(mem_wb_1_jal_out));
  Multiplexer #(.select(1), .width(32), .disabled("Z"), .enable("false")) multiplexer_24 (
    .in0(WB_AluOut), .in1(Mem_MemData), .out(multiplexer_24_out), .sel(mem_wb_1_memtoreg_out));
  Multiplexer #(.select(1), .width(32), .disabled("Z"), .enable("false")) multiplexer_25 (
    .in0(multiplexer_24_out), .in1(mem_wb_1_pc_out), .out(RDin), .sel(mem_wb_1_jal_out));

  // Other names for the same wires on the sheet: ID_IR[5:0] = Func; OP[5:0] = ID_IR[31:26]; MEM_PC[31:0] = M_PC;
  //   PC[31:0] = IF_PC

  // Notes on the sheet:
  //   中断源
  //   时空图监测，可删除
  //   中断等待指示
  //   数码管输出
  //   IE
  //   指令存储器
  //   PC+4
  //   控制位
  //   contents of rom_1 (hex, n*v repeats v):
  //   20110001 8000c05 20110001 20120002 20130003 8000c09 20110001 20120002 20130003 8000c0d 20110001
  //   20120002 20130003 8000c11 20110001 20120002 20130003 c000cb8 20100001 20110001 118fc0 112020
  //   20020022 c 118882 12200001 8000c15 112020 20020022 c 20110001 118880 112020 20020022 c 12200001
  //   8000c1f 20110001 118fc0 112020 20020022 c 1188c3 112020 20020022 c 118903 112020 20020022 c 118903
  //   112020 20020022 c 118903 112020 20020022 c 118903 112020 20020022 c 118903 112020 20020022 c 118903
  //   112020 20020022 c 118903 112020 20020022 c 20100001 109fc0 139fc3 8021 2012000c 24160003 26100001
  //   3210000f 20080008 20090001 139900 2709825 132020 20020022 c 1094022 1500fff9 22100001 2018000f
  //   2188024 108700 20080008 20090001 139902 2709825 132021 20020022 c 1094022 1500fff9 108702 2c9b022
  //   12c00001 8000c50 4020 1084027 84400 3508ffff 82021 20020022 c 2010ffff 20110000 ae300000 22100001
  //   22310004 ae300000 22100001 22310004 ae300000 22100001 22310004 ae300000 22100001 22310004 ae300000
  //   22100001 22310004 ae300000 22100001 22310004 ae300000 22100001 22310004 ae300000 22100001 22310004
  //   ae300000 22100001 22310004 ae300000 22100001 22310004 ae300000 22100001 22310004 ae300000 22100001
  //   22310004 ae300000 22100001 22310004 ae300000 22100001 22310004 ae300000 22100001 22310004 ae300000
  //   22100001 22310004 22100001 8020 2011003c 8e130000 8e340000 274402a 11000002 ae330000 ae140000
  //   2231fffc 1611fff8 102020 20020022 c 22100004 2011003c 1611fff2 20020032 c 20100000 22100001 102020
  //   20020022 c 22100002 102020 20020022 c 22100003 102020 20020022 c 22100004 102020 20020022 c 22100005
  //   102020 20020022 c 22100006 102020 20020022 c 22100007 102020 20020022 c 22100008 102020 20020022
  //   20020022 c 3e00008
  //   流水调试日志用
  //   暂停节拍，不能为0
  //   戳工具置1进入计数暂停模式，ctrl+k时钟自动运行到对应节拍暂停
  //   ctrl+k关闭时钟连续运行，将控制位置零，进入单步调试模式调试
  //   指令字
  //   可计数暂停的时钟源
  //   OP
  //   Func
  //   rs
  //   rt
  //   rd
  //   JMP
  //   JR
  //   OP
  //   Func
  //   Reset 
  //   Reset 
  //   Reset 
  //   Beq
  //   Bne
  //   MemToReg
  //   MemWrite
  //   AluOP
  //   AluSrcB
  //   RegWrite
  //   JAL
  //   RegDst
  //   Syscall
  //   为方便自动评测，需要输出流水线各段保存的PC值，注意是PC不是PC+4，另外ID段寄存器写入信息，Mem段内存写入信息也要输出
  //   PCBranch
  //   rt
  //   rd
endmodule
